// Logisim project cpu24+4单级中断团队任务.circ as structural Verilog: 14 circuits, main circuit ◇单周期MIPS+单级中断
module \团队  (
);

  wire Body_ERROR, down, Go, left, or_1_out, right, RST, up, Wall_ERROR;
  wire [11:0] Score;
  wire [15:0] result_output_1_o1, result_output_1_o1_2, result_output_1_o1_3, result_output_1_o1_4,
       result_output_1_o1_5, result_output_1_o1_6, result_output_1_o1_7, result_output_1_o1_8,
       result_output_1_o1_9, result_output_1_o1_10, result_output_1_o1_11, result_output_1_o1_12,
       result_output_1_o1_13, result_output_1_o1_14, result_output_1_o1_15, result_output_1_o1_16,
       result_output_1_o1_17, result_output_1_o1_18, result_output_1_o1_19, result_output_1_o1_20,
       result_output_1_o1_21, result_output_1_o1_22, result_output_1_o1_23, result_output_1_o1_24,
       result_output_1_o1_25, result_output_1_o1_26, result_output_1_o1_27, result_output_1_o1_28,
       result_output_1_o1_29, result_output_1_o1_30, result_output_1_o1_31, result_output_1_o1_32;
  wire [31:0] \单周期mips_单级中断_1_o0 , \单周期mips_单级中断_1_o1 , \单周期mips_单级中断_1_o2 , \单周期mips_单级中断_1_o3 ,
       \单周期mips_单级中断_1_o4 , \单周期mips_单级中断_1_o5 , \单周期mips_单级中断_1_o6 , \单周期mips_单级中断_1_o7 ,
       \单周期mips_单级中断_1_o8 , \单周期mips_单级中断_1_o9 , \单周期mips_单级中断_1_o10 , \单周期mips_单级中断_1_o11 ,
       \单周期mips_单级中断_1_o12 , \单周期mips_单级中断_1_o13 , \单周期mips_单级中断_1_o14 , \单周期mips_单级中断_1_o15 ,
       \单周期mips_单级中断_1_o16 , \单周期mips_单级中断_1_o17 , \单周期mips_单级中断_1_o18 , \单周期mips_单级中断_1_o19 ,
       \单周期mips_单级中断_1_o20 , \单周期mips_单级中断_1_o21 , \单周期mips_单级中断_1_o22 , \单周期mips_单级中断_1_o23 ,
       \单周期mips_单级中断_1_o24 , \单周期mips_单级中断_1_o25 , \单周期mips_单级中断_1_o26 , \单周期mips_单级中断_1_o27 ,
       \单周期mips_单级中断_1_o28 , \单周期mips_单级中断_1_o29 , \单周期mips_单级中断_1_o30 , \单周期mips_单级中断_1_o31 ;

  or or_1 (or_1_out, Wall_ERROR, Body_ERROR);
  \单周期MIPS_单级中断  \u_单周期mips_单级中断_1  (
    .RST(RST), .GO(Go), .IR0(up), .IR1(left), .IR2(down), .IR3(right), .O0(\单周期mips_单级中断_1_o0 ),
    .O1(\单周期mips_单级中断_1_o1 ), .O2(\单周期mips_单级中断_1_o2 ), .O3(\单周期mips_单级中断_1_o3 ), .O4(\单周期mips_单级中断_1_o4 ),
    .O5(\单周期mips_单级中断_1_o5 ), .O6(\单周期mips_单级中断_1_o6 ), .O7(\单周期mips_单级中断_1_o7 ), .O8(\单周期mips_单级中断_1_o8 ),
    .O9(\单周期mips_单级中断_1_o9 ), .O10(\单周期mips_单级中断_1_o10 ), .O11(\单周期mips_单级中断_1_o11 ),
    .O12(\单周期mips_单级中断_1_o12 ), .O13(\单周期mips_单级中断_1_o13 ), .O14(\单周期mips_单级中断_1_o14 ),
    .O15(\单周期mips_单级中断_1_o15 ), .O16(\单周期mips_单级中断_1_o16 ), .O17(\单周期mips_单级中断_1_o17 ),
    .O18(\单周期mips_单级中断_1_o18 ), .O19(\单周期mips_单级中断_1_o19 ), .O20(\单周期mips_单级中断_1_o20 ),
    .O21(\单周期mips_单级中断_1_o21 ), .O22(\单周期mips_单级中断_1_o22 ), .O23(\单周期mips_单级中断_1_o23 ),
    .O24(\单周期mips_单级中断_1_o24 ), .O25(\单周期mips_单级中断_1_o25 ), .O26(\单周期mips_单级中断_1_o26 ),
    .O27(\单周期mips_单级中断_1_o27 ), .O28(\单周期mips_单级中断_1_o28 ), .O29(\单周期mips_单级中断_1_o29 ),
    .O30(\单周期mips_单级中断_1_o30 ), .O31(\单周期mips_单级中断_1_o31 ), .Wall_ERROR(Wall_ERROR), .Body_ERROR(Body_ERROR),
    .Score(Score));
  Button button_1 (.out(Go));
  Button button_2 (.out(RST));
  DotMatrix #(.inputtype("column"), .matrixcols(32), .matrixrows(16), .persist(0), .dotshape("square")) dotmatrix_1 (
    .col0(result_output_1_o1), .col1(result_output_1_o1_2), .col2(result_output_1_o1_3),
    .col3(result_output_1_o1_4), .col4(result_output_1_o1_5), .col5(result_output_1_o1_6),
    .col6(result_output_1_o1_7), .col7(result_output_1_o1_8), .col8(result_output_1_o1_9),
    .col9(result_output_1_o1_10), .col10(result_output_1_o1_11), .col11(result_output_1_o1_12),
    .col12(result_output_1_o1_13), .col13(result_output_1_o1_14), .col14(result_output_1_o1_15),
    .col15(result_output_1_o1_16), .col16(result_output_1_o1_17), .col17(result_output_1_o1_18),
    .col18(result_output_1_o1_19), .col19(result_output_1_o1_20), .col20(result_output_1_o1_21),
    .col21(result_output_1_o1_22), .col22(result_output_1_o1_23), .col23(result_output_1_o1_24),
    .col24(result_output_1_o1_25), .col25(result_output_1_o1_26), .col26(result_output_1_o1_27),
    .col27(result_output_1_o1_28), .col28(result_output_1_o1_29), .col29(result_output_1_o1_30),
    .col30(result_output_1_o1_31), .col31(result_output_1_o1_32));
  Result_OutPut result_output_1 (
    .O1(result_output_1_o1), .O1_2(result_output_1_o1_2), .O1_3(result_output_1_o1_3),
    .O1_4(result_output_1_o1_4), .O1_5(result_output_1_o1_5), .O1_6(result_output_1_o1_6),
    .O1_7(result_output_1_o1_7), .O1_8(result_output_1_o1_8), .O1_9(result_output_1_o1_9),
    .O1_10(result_output_1_o1_10), .O1_11(result_output_1_o1_11), .O1_12(result_output_1_o1_12),
    .O1_13(result_output_1_o1_13), .O1_14(result_output_1_o1_14), .O1_15(result_output_1_o1_15),
    .O1_16(result_output_1_o1_16), .O1_17(result_output_1_o1_17), .O1_18(result_output_1_o1_18),
    .O1_19(result_output_1_o1_19), .O1_20(result_output_1_o1_20), .O1_21(result_output_1_o1_21),
    .O1_22(result_output_1_o1_22), .O1_23(result_output_1_o1_23), .O1_24(result_output_1_o1_24),
    .O1_25(result_output_1_o1_25), .O1_26(result_output_1_o1_26), .O1_27(result_output_1_o1_27),
    .O1_28(result_output_1_o1_28), .O1_29(result_output_1_o1_29), .O1_30(result_output_1_o1_30),
    .O1_31(result_output_1_o1_31), .O1_32(result_output_1_o1_32), .ERROR(or_1_out), .Score(Score));
  DotMatrix #(.inputtype("row"), .matrixcols(32), .matrixrows(32), .persist(0), .dotshape("square")) dotmatrix_2 (
    .row0(\单周期mips_单级中断_1_o0 ), .row1(\单周期mips_单级中断_1_o1 ), .row2(\单周期mips_单级中断_1_o2 ),
    .row3(\单周期mips_单级中断_1_o3 ), .row4(\单周期mips_单级中断_1_o4 ), .row5(\单周期mips_单级中断_1_o5 ),
    .row6(\单周期mips_单级中断_1_o6 ), .row7(\单周期mips_单级中断_1_o7 ), .row8(\单周期mips_单级中断_1_o8 ),
    .row9(\单周期mips_单级中断_1_o9 ), .row10(\单周期mips_单级中断_1_o10 ), .row11(\单周期mips_单级中断_1_o11 ),
    .row12(\单周期mips_单级中断_1_o12 ), .row13(\单周期mips_单级中断_1_o13 ), .row14(\单周期mips_单级中断_1_o14 ),
    .row15(\单周期mips_单级中断_1_o15 ), .row16(\单周期mips_单级中断_1_o16 ), .row17(\单周期mips_单级中断_1_o17 ),
    .row18(\单周期mips_单级中断_1_o18 ), .row19(\单周期mips_单级中断_1_o19 ), .row20(\单周期mips_单级中断_1_o20 ),
    .row21(\单周期mips_单级中断_1_o21 ), .row22(\单周期mips_单级中断_1_o22 ), .row23(\单周期mips_单级中断_1_o23 ),
    .row24(\单周期mips_单级中断_1_o24 ), .row25(\单周期mips_单级中断_1_o25 ), .row26(\单周期mips_单级中断_1_o26 ),
    .row27(\单周期mips_单级中断_1_o27 ), .row28(\单周期mips_单级中断_1_o28 ), .row29(\单周期mips_单级中断_1_o29 ),
    .row30(\单周期mips_单级中断_1_o30 ), .row31(\单周期mips_单级中断_1_o31 ));
  LED #(.active("true")) led_1 (.in(left));
  Button button_3 (.out(left));
  Button button_4 (.out(up));
  LED #(.active("true")) led_2 (.in(up));
  Button button_5 (.out(right));
  LED #(.active("true")) led_3 (.in(right));
  LED #(.active("true")) led_4 (.in(down));
  Button button_6 (.out(down));
  Hex_Digit_Display hex_digit_display_1 (.value(Score[7:4]));  // open: dp
  Hex_Digit_Display hex_digit_display_2 (.value(Score[11:8]));  // open: dp
  Hex_Digit_Display hex_digit_display_3 (.value(Score[3:0]));  // open: dp
  LED #(.active("true")) led_5 (.in(Wall_ERROR));
  LED #(.active("true")) led_6 (.in(Body_ERROR));

  // Notes on the sheet:
  //   Go
  //   RST
  //   Push Go to start
  //   Push RST to clear
  //   Control
endmodule

module \单周期MIPS_单级中断  (
  input  RST,
  input  GO,
  input  IR0,
  input  IR1,
  input  IR2,
  input  IR3,
  output [31:0] O0,
  output [31:0] O1,
  output [31:0] O2,
  output [31:0] O3,
  output [31:0] O4,
  output [31:0] O5,
  output [31:0] O6,
  output [31:0] O7,
  output [31:0] O8,
  output [31:0] O9,
  output [31:0] O10,
  output [31:0] O11,
  output [31:0] O12,
  output [31:0] O13,
  output [31:0] O14,
  output [31:0] O15,
  output [31:0] O16,
  output [11:0] Score,
  output [31:0] O17,
  output [31:0] O18,
  output [31:0] O19,
  output [31:0] O20,
  output [31:0] O21,
  output Wall_ERROR,
  output Body_ERROR,
  output [31:0] O22,
  output [31:0] O23,
  output [31:0] O24,
  output [31:0] O25,
  output [31:0] O26,
  output [31:0] O27,
  output [31:0] O28,
  output [31:0] O29,
  output [31:0] O30,
  output [31:0] O31
);

  wire and_1_out, and_2_out, and_3_out, and_4_out, and_12_out, and_13_out, and_14_out, and_15_out,
       and_16_out, and_17_out, and_18_out, and_19_out, and_20_out, and_21_out, and_22_out, and_23_out,
       and_24_out, and_25_out, and_26_out, and_27_out, and_28_out, and_29_out, and_30_out, and_31_out,
       and_32_out, and_33_out, and_34_out, and_35_out, and_36_out, and_37_out, and_38_out, and_39_out,
       and_40_out, and_41_out, and_42_out, and_43_out, and_44_out, and_45_out, and_46_out, Beq_Bnq_Y, CLK,
       clock_2_out, comparator_1_eq, comparator_2_eq, comparator_3_eq, comparator_4_eq, comparator_5_eq,
       comparator_6_eq, comparator_6_lt, comparator_7_eq, comparator_9_lt, controlled_buffer_1_out, d_ff_1_q,
       d_ff_2_q, d_ff_3_q, d_ff_4_q, d_ff_5_q, demultiplexer_1_out0, demultiplexer_1_out1,
       demultiplexer_1_out2, demultiplexer_1_out3, ERET, Halt, IE, IE_q, INT, IR0_q, IR1_q, IR2_q, IR3_q,
       JMP, JR, LBU, MemToReg, MemWrite, MFC0, mips_alu_1_equal, MTC0, multiplexer_15_out, nand_1_out,
       not_1_out, or_1_out, or_6_out, or_7_out, or_8_out, or_9_out, or_10_out, or_11_out, or_12_out,
       or_13_out, or_14_out, out, RegWrite, SignedExt, Syscall, Upadte_score, W0, w0_t, W1, w1_t, W2, w2_t,
       W3, w3_t, w4, w5, w6, w7, w8, w9, w10, w11, w12, w13, w14, w15, w16, w17, w18, w19, w20, w21, w22,
       w23, w24, w25, w26, w27, w28, w29, w30, w31, Write_random, \单周期硬布线控制器_1_alu_src , \单周期硬布线控制器_1_beq ,
       \单周期硬布线控制器_1_blez , \单周期硬布线控制器_1_bne , \单周期硬布线控制器_1_jal , \单周期硬布线控制器_1_regdst ;
  wire [1:0] INT_num, priority_encoder_1_out;
  wire [3:0] \单周期硬布线控制器_1_alu_op ;
  wire [4:0] multiplexer_6_out, multiplexer_7_out, multiplexer_8_out, multiplexer_9_out, multiplexer_12_out,
       Random_Row;
  wire [9:0] Addr;
  wire [12:0] CNT_num;
  wire [15:0] \总周期数 ;
  wire [25:0] instr_index;
  wire [31:0] A0, bit_extender_1_out, bit_extender_2_out, Din_Random, LB_2_q, LB_3_q, LB_4_q, LB_5_q, LB_6_q,
       LB_7_q, LB_8_q, LB_9_q, LB_10_q, LB_12_q, LB_13_q, LB_14_q, LB_15_q, LB_16_q, LB_17_q, LB_18_q,
       LB_19_q, LB_20_q, LB_21_q, LB_22_q, LB_23_q, LB_24_q, LB_25_q, LB_26_q, LB_27_q, LB_28_q, LB_29_q,
       LB_30_q, LB_31_q, LB_32_q, LB_33_q, LB_q, mips_alu_1_result, multiplexer_1_out, multiplexer_2_out,
       multiplexer_4_out, multiplexer_10_out, multiplexer_13_out, multiplexer_16_out, multiplexer_18_out, PC,
       PC_4, PC_BEQ_BNQ, PC_ERET, PC_INT, PC_JR, PC_result, PC_TO_EPC, ram_1_data, Random_Col, RDin,
       shifter_1_out, WriteBackData;
  wire [31:12] score_q;
  wire [31:26] IR;

  Clock #(.highDuration(1), .lowDuration(1)) clock_1 (.out(CLK));
  Multiplexer #(.select(1), .width(32), .disabled("Z"), .enable("false")) multiplexer_1 (
    .in0({PC[31:28], instr_index, 2'b00}), .in1(PC_JR), .out(multiplexer_1_out), .sel(JR));
  LED #(.active("true")) led_1 (.in(W0));
  LED #(.active("true")) led_2 (.in(W1));
  LED #(.active("true")) led_3 (.in(W2));
  LED #(.active("true")) led_4 (.in(W3));
  Demultiplexer #(.select(2), .width(1), .tristate("false"), .disabled("Z"), .enable("false")) demultiplexer_1 (
    .out0(demultiplexer_1_out0), .out1(demultiplexer_1_out1), .out2(demultiplexer_1_out2),
    .out3(demultiplexer_1_out3), .in(ERET), .sel(INT_num));
  or or_1 (or_1_out, ~Halt, GO);  // OR_Gate
  Multiplexer #(.select(1), .width(32), .disabled("Z"), .enable("false")) multiplexer_2 (
    .in0(PC_4), .in1(multiplexer_1_out), .out(multiplexer_2_out), .sel(JMP));
  not not_1 (not_1_out, Halt);
  Register #(.width(32), .trigger("rising"), .Select("low")) u_PC (
    .D(PC_result), .en(or_1_out), .Q(PC), .clk(CLK), .clr(RST));
  Multiplexer #(.select(1), .width(32), .disabled("Z"), .enable("false")) multiplexer_3 (
    .in0(multiplexer_2_out), .in1(PC_BEQ_BNQ), .out(PC_TO_EPC), .sel(Beq_Bnq_Y));
  Counter #(.width(16), .max('hffff), .ongoal("continue"), .trigger("rising"), .behavior("old")) counter_1 (
    .count(not_1_out), .Q(\总周期数 ), .clk(CLK), .clr(RST));  // open: load, D, carry, preset
  Multiplexer #(.select(1), .width(32), .disabled("Z"), .enable("false")) multiplexer_4 (
    .in0(PC_TO_EPC), .in1(PC_ERET), .out(multiplexer_4_out), .sel(ERET));
  // Probe on \总周期数 
  ROM #(.addrWidth(10), .dataWidth(32), .Select("high")) rom_1 (.addr(PC[11:2]), .data({IR, instr_index}));
  Adder #(.width(32)) adder_1 (.a(PC), .b(32'h4), .out(PC_4));  // open: cin, cout
  Multiplexer #(.select(1), .width(32), .disabled("Z"), .enable("false")) multiplexer_5 (
    .in0(multiplexer_4_out), .in1(PC_INT), .out(PC_result), .sel(INT));
  or or_2 (W0, IR0_q, d_ff_1_q);
  or or_3 (W1, IR1_q, d_ff_2_q);
  or or_4 (W2, IR2_q, d_ff_3_q);
  or or_5 (W3, IR3_q, d_ff_4_q);
  // Mips_Probe mips_probe_1: pin names not known; wires that end beside it: {IR, instr_index}
  D_Flip_Flop #(.trigger("rising"), .Pre_Clr_Positions("LEGACY"), .NegatePresetClear("false"), .enable("true"), .NewFFLayout("false")) d_ff_1 (
    .clk(IR0), .D(1'b1), .Q(d_ff_1_q), .reset(IR0_q));  // open: Qn, preset, en
  D_Flip_Flop #(.trigger("rising"), .Pre_Clr_Positions("LEGACY"), .NegatePresetClear("false"), .enable("true"), .NewFFLayout("false")) d_ff_2 (
    .clk(IR1), .D(1'b1), .Q(d_ff_2_q), .reset(IR1_q));  // open: Qn, preset, en
  D_Flip_Flop #(.trigger("rising"), .Pre_Clr_Positions("LEGACY"), .NegatePresetClear("false"), .enable("true"), .NewFFLayout("false")) d_ff_3 (
    .clk(IR2), .D(1'b1), .Q(d_ff_3_q), .reset(IR2_q));  // open: Qn, preset, en
  D_Flip_Flop #(.trigger("rising"), .Pre_Clr_Positions("LEGACY"), .NegatePresetClear("false"), .enable("true"), .NewFFLayout("false")) d_ff_4 (
    .clk(IR3), .D(1'b1), .Q(d_ff_4_q), .reset(IR3_q));  // open: Qn, preset, en
  or or_6 (or_6_out, d_ff_1_q, IR0_q);
  or or_7 (or_7_out, d_ff_2_q, IR1_q);
  or or_8 (or_8_out, d_ff_3_q, IR2_q);
  or or_9 (or_9_out, d_ff_4_q, IR3_q);
  \单周期硬布线控制器  \u_单周期硬布线控制器_1  (
    .Func(instr_index[5:0]), .OP(IR), .ALU_OP(\单周期硬布线控制器_1_alu_op ), .MemToReg(MemToReg),
    .MemWrite(MemWrite), .ALU_SRC(\单周期硬布线控制器_1_alu_src ), .RegWrite(RegWrite), .SysCALL(Syscall),
    .SignedExt(SignedExt), .RegDst(\单周期硬布线控制器_1_regdst ), .JR(JR), .JMP(JMP), .Beq(\单周期硬布线控制器_1_beq ),
    .JAL(\单周期硬布线控制器_1_jal ), .Bne(\单周期硬布线控制器_1_bne ), .BLEZ(\单周期硬布线控制器_1_blez ), .LBU(LBU), .ERET(ERET),
    ._21_25(instr_index[25:21]), .MTC0(MTC0), .MFC0(MFC0));
  Multiplexer #(.select(1), .width(5), .disabled("Z"), .enable("false")) multiplexer_6 (
    .in0(instr_index[25:21]), .in1(5'b00010), .out(multiplexer_6_out), .sel(Syscall));
  Multiplexer #(.select(1), .width(5), .disabled("Z"), .enable("false")) multiplexer_7 (
    .in0(instr_index[20:16]), .in1(5'b00100), .out(multiplexer_7_out), .sel(Syscall));
  Multiplexer #(.select(1), .width(5), .disabled("Z"), .enable("false")) multiplexer_8 (
    .in0(instr_index[20:16]), .in1(instr_index[15:11]), .out(multiplexer_8_out), .sel(\单周期硬布线控制器_1_regdst ));
  assign bit_extender_1_out = {{16{instr_index[15]}}, instr_index[15:0]};  // Bit_Extender bit_extender_1
  assign bit_extender_2_out = {{16{1'b0}}, instr_index[15:0]};  // Bit_Extender bit_extender_2
  and and_1 (and_1_out, or_6_out, ~demultiplexer_1_out0);  // AND_Gate
  and and_2 (and_2_out, or_7_out, ~demultiplexer_1_out1);  // AND_Gate
  and and_3 (and_3_out, or_8_out, ~demultiplexer_1_out2);  // AND_Gate
  and and_4 (and_4_out, or_9_out, ~demultiplexer_1_out3);  // AND_Gate
  Multiplexer #(.select(1), .width(5), .disabled("Z"), .enable("false")) multiplexer_9 (
    .in0(multiplexer_8_out), .in1({5{1'b1}}), .out(multiplexer_9_out), .sel(\单周期硬布线控制器_1_jal ));
  Shifter #(.width(32), .shift("ll")) shifter_1 (.in(bit_extender_1_out), .\dist (5'b00010), .out(shifter_1_out));
  Multiplexer #(.select(1), .width(32), .disabled("Z"), .enable("false")) multiplexer_10 (
    .in0(bit_extender_2_out), .in1(bit_extender_1_out), .out(multiplexer_10_out), .sel(SignedExt));
  D_Flip_Flop #(.trigger("rising"), .Pre_Clr_Positions("LEGACY"), .NegatePresetClear("false"), .enable("true"), .NewFFLayout("false")) u_IR0 (
    .clk(CLK), .D(and_1_out), .Q(IR0_q));  // open: Qn, preset, en, reset
  D_Flip_Flop #(.trigger("rising"), .Pre_Clr_Positions("LEGACY"), .NegatePresetClear("false"), .enable("true"), .NewFFLayout("false")) u_IR1 (
    .clk(CLK), .D(and_2_out), .Q(IR1_q));  // open: Qn, preset, en, reset
  D_Flip_Flop #(.trigger("rising"), .Pre_Clr_Positions("LEGACY"), .NegatePresetClear("false"), .enable("true"), .NewFFLayout("false")) u_IR2 (
    .clk(CLK), .D(and_3_out), .Q(IR2_q));  // open: Qn, preset, en, reset
  D_Flip_Flop #(.trigger("rising"), .Pre_Clr_Positions("LEGACY"), .NegatePresetClear("false"), .enable("true"), .NewFFLayout("false")) u_IR3 (
    .clk(CLK), .D(and_4_out), .Q(IR3_q));  // open: Qn, preset, en, reset
  D_Flip_Flop #(.trigger("high"), .Pre_Clr_Positions("LEGACY"), .NegatePresetClear("false"), .enable("true"), .NewFFLayout("false")) d_ff_5 (.Q(d_ff_5_q));  // open: clk, D, Qn, preset, en, reset
  // Probe on 13'hc
  Multiplexer #(.select(1), .width(32), .disabled("Z"), .enable("false")) multiplexer_11 (
    .in0(WriteBackData), .in1(PC_4), .out(RDin), .sel(\单周期硬布线控制器_1_jal ));
  Adder #(.width(32)) adder_2 (.a(PC_4), .b(shifter_1_out), .out(PC_BEQ_BNQ));  // open: cin, cout
  Register #(.width(32), .trigger("rising"), .Select("low")) u_score (
    .D(A0), .en(Upadte_score), .Q({score_q, Score}), .clk(CLK), .clr(RST));
  Comparator #(.width(32), .mode("unsigned")) comparator_1 (
    .a(PC_JR), .b(32'h21), .eq(comparator_1_eq));  // open: gt, lt
  Comparator #(.width(32), .mode("unsigned")) comparator_2 (
    .a(PC_JR), .b(32'h20), .eq(comparator_2_eq));  // open: gt, lt
  Comparator #(.width(32), .mode("unsigned")) comparator_3 (
    .a(PC_JR), .b(32'h22), .eq(comparator_3_eq));  // open: gt, lt
  Comparator #(.width(32), .mode("unsigned")) comparator_4 (
    .a(PC_JR), .b(32'h10), .eq(comparator_4_eq));  // open: gt, lt
  Comparator #(.width(32), .mode("unsigned")) comparator_5 (
    .a(PC_JR), .b(32'h11), .eq(comparator_5_eq));  // open: gt, lt
  or or_10 (or_10_out, IR0_q, IR1_q, IR2_q, IR3_q);
  Comparator #(.width(13), .mode("twosComplement")) comparator_6 (
    .a(CNT_num), .b(13'hc), .eq(comparator_6_eq), .lt(comparator_6_lt));  // open: gt
  Clock #(.highDuration(1), .lowDuration(1)) clock_2 (.out(clock_2_out));
  Multiplexer #(.select(1), .width(5), .disabled("Z"), .enable("false")) multiplexer_12 (
    .in0(multiplexer_9_out), .in1(5'b00011), .out(multiplexer_12_out), .sel(Write_random));
  and and_5 (Upadte_score, comparator_1_eq, Syscall);
  and and_6 (Write_random, comparator_2_eq, Syscall);
  and and_7 (Halt, Syscall, ~comparator_1_eq, ~comparator_2_eq, ~comparator_3_eq);  // AND_Gate
  and and_8 (out, Syscall, comparator_3_eq);
  and and_9 (Wall_ERROR, Syscall, comparator_4_eq);
  and and_10 (Body_ERROR, Syscall, comparator_5_eq);
  and and_11 (INT, or_10_out, IE);
  nand nand_1 (nand_1_out, d_ff_5_q, comparator_6_eq);
  Counter #(.width(13), .max('h1fff), .ongoal("stay"), .trigger("rising"), .behavior("old")) counter_2 (
    .count(comparator_6_lt), .Q(CNT_num), .clk(clock_2_out));  // open: load, D, carry, clr, preset
  Multiplexer #(.select(1), .width(32), .disabled("Z"), .enable("false")) multiplexer_13 (
    .in0(RDin), .in1(Din_Random), .out(multiplexer_13_out), .sel(Write_random));
  Priority_Encoder #(.select(2), .disabled("Z")) priority_encoder_1 (
    .in0(IR0_q), .in1(IR1_q), .in2(IR2_q), .in3(IR3_q), .out(priority_encoder_1_out));  // open: gs, en_out, en_in
  or or_11 (or_11_out, ERET, MFC0);
  assign controlled_buffer_1_out = nand_1_out ? clock_2_out : 1'bz;  // Controlled_Buffer controlled_buffer_1
  or or_12 (or_12_out, Write_random, RegWrite);
  Multiplexer #(.select(2), .width(32), .disabled("Z"), .enable("false")) multiplexer_14 (
    .in0(32'h3280), .in1(32'h3290), .in2(32'h32a0), .in3(32'h32b0), .out(PC_INT), .sel(priority_encoder_1_out));
  Multiplexer #(.select(1), .width(1), .disabled("Z"), .enable("false")) multiplexer_15 (
    .in0(INT), .in1(1'b0), .out(multiplexer_15_out), .sel(or_11_out));
  or or_13 (or_13_out, or_11_out, INT);
  Pull_Resistor #(.pull(1)) pull_resistor_1 (.node(controlled_buffer_1_out));
  MIPS_Regifile mips_regifile_1 (
    .Din(multiplexer_13_out), .Clk(CLK), .R1(PC_JR), .R2(A0), .WE(or_12_out), .W_num(multiplexer_12_out),
    .R1_num(multiplexer_6_out), .R2_num(multiplexer_7_out));
  Register #(.width(32), .trigger("falling"), .Select("low")) EPC (
    .D(PC_TO_EPC), .en(INT), .Q(PC_ERET), .clk(CLK), .clr(RST));
  Register #(.width(1), .trigger("rising"), .Select("low")) u_IE (
    .D(multiplexer_15_out), .en(or_13_out), .Q(IE_q), .clk(CLK), .clr(RST), .preset(MTC0));  // open: cs
  Multiplexer #(.select(1), .width(32), .disabled("Z"), .enable("false")) multiplexer_16 (
    .in0(A0), .in1(multiplexer_10_out), .out(multiplexer_16_out), .sel(\单周期硬布线控制器_1_alu_src ));
  Register #(.width(2), .trigger("rising"), .Select("low")) LOCAL_NUM (
    .D(priority_encoder_1_out), .en(INT), .Q(INT_num), .clk(CLK), .clr(RST));
  not not_2 (IE, IE_q);
  or or_14 (or_14_out, mips_alu_1_equal, mips_alu_1_result[0]);
  MIPS_ALU mips_alu_1 (
    .X(PC_JR), .Y(multiplexer_16_out), .AluOP(\单周期硬布线控制器_1_alu_op ), .Equal(mips_alu_1_equal),
    .Result({mips_alu_1_result[31:12], Addr, mips_alu_1_result[1:0]}), .shamt(instr_index[10:6]));  // open: Result_2
  Comparator #(.width(32), .mode("unsigned")) comparator_7 (.a(A0), .b(32'h1), .eq(comparator_7_eq));  // open: gt, lt
  Comparator #(.width(32), .mode("unsigned")) comparator_8 (.a(A0), .b({32{1'b0}}));  // open: gt, eq, lt
  Random #(.width(5), .seed(0), .trigger("rising")) random_1 (
    .clk(CLK), .next(Write_random), .out(Random_Row));  // open: clr
  and and_12 (and_12_out, \单周期硬布线控制器_1_blez , or_14_out);
  and and_13 (and_13_out, \单周期硬布线控制器_1_beq , mips_alu_1_equal);
  and and_14 (and_14_out, \单周期硬布线控制器_1_bne , ~mips_alu_1_equal);  // AND_Gate
  or or_15 (Beq_Bnq_Y, and_12_out, and_13_out, and_14_out);
  Multiplexer #(.select(1), .width(32), .disabled("Z"), .enable("false")) multiplexer_17 (
    .in0({{27{1'b0}}, Random_Row}), .in1(Random_Col), .out(Din_Random), .sel(comparator_7_eq));
  Shifter #(.width(32), .shift("ll")) shifter_2 (.in(32'h1), .\dist (Random_Row), .out(Random_Col));
  Demultiplexer #(.select(5), .width(1), .tristate("false"), .disabled("Z"), .enable("false")) demultiplexer_2 (
    .out0(w0_t), .out1(w1_t), .out2(w2_t), .out3(w3_t), .out4(w4), .out5(w5), .out6(w6), .out7(w7),
    .out8(w8), .out9(w9), .out10(w10), .out11(w11), .out12(w12), .out13(w13), .out14(w14), .out15(w15),
    .out16(w16), .out17(w17), .out18(w18), .out19(w19), .out20(w20), .out21(w21), .out22(w22), .out23(w23),
    .out24(w24), .out25(w25), .out26(w26), .out27(w27), .out28(w28), .out29(w29), .out30(w30), .out31(w31),
    .in(comparator_9_lt), .sel(Addr[4:0]));
  RAM #(.addrWidth(10), .dataWidth(32), .bus("separate"), .Select("high")) ram_1 (
    .addr(Addr), .din(A0), .data(ram_1_data), .str(MemWrite), .clk(CLK), .clr(RST));  // open: sel, ld
  Multiplexer #(.select(1), .width(32), .disabled("Z"), .enable("false")) multiplexer_18 (
    .in0(ram_1_data), .in1({{24{1'b0}}, ram_1_data[7:0]}), .out(multiplexer_18_out), .sel(LBU));
  Comparator #(.width(10), .mode("unsigned")) comparator_9 (
    .a(Addr), .b(10'h20), .lt(comparator_9_lt));  // open: gt, eq
  Multiplexer #(.select(1), .width(32), .disabled("Z"), .enable("false")) multiplexer_19 (
    .in0({mips_alu_1_result[31:12], Addr, mips_alu_1_result[1:0]}), .in1(multiplexer_18_out),
    .out(WriteBackData), .sel(MemToReg));
  and and_15 (and_15_out, MemWrite, w0_t);
  and and_16 (and_16_out, MemWrite, w1_t);
  and and_17 (and_17_out, MemWrite, w2_t);
  and and_18 (and_18_out, MemWrite, w3_t);
  and and_19 (and_19_out, MemWrite, w4);
  and and_20 (and_20_out, MemWrite, w5);
  and and_21 (and_21_out, MemWrite, w6);
  and and_22 (and_22_out, MemWrite, w7);
  and and_23 (and_23_out, MemWrite, w8);
  and and_24 (and_24_out, MemWrite, w9);
  and and_25 (and_25_out, MemWrite, w10);
  and and_26 (and_26_out, MemWrite, w11);
  and and_27 (and_27_out, MemWrite, w12);
  and and_28 (and_28_out, MemWrite, w13);
  and and_29 (and_29_out, MemWrite, w14);
  and and_30 (and_30_out, MemWrite, w15);
  and and_31 (and_31_out, MemWrite, w16);
  and and_32 (and_32_out, MemWrite, w17);
  and and_33 (and_33_out, MemWrite, w18);
  and and_34 (and_34_out, MemWrite, w19);
  and and_35 (and_35_out, MemWrite, w20);
  and and_36 (and_36_out, MemWrite, w21);
  and and_37 (and_37_out, MemWrite, w22);
  and and_38 (and_38_out, MemWrite, w23);
  and and_39 (and_39_out, MemWrite, w24);
  and and_40 (and_40_out, MemWrite, w25);
  and and_41 (and_41_out, MemWrite, w26);
  and and_42 (and_42_out, MemWrite, w27);
  and and_43 (and_43_out, MemWrite, w28);
  and and_44 (and_44_out, MemWrite, w29);
  and and_45 (and_45_out, MemWrite, w30);
  and and_46 (and_46_out, MemWrite, w31);
  Register #(.width(32), .trigger("rising"), .Select("low")) LB (
    .D(A0), .en(and_15_out), .Q(LB_q), .clk(CLK), .clr(RST));
  Register #(.width(32), .trigger("rising"), .Select("low")) LB_2 (
    .D(A0), .en(and_16_out), .Q(LB_2_q), .clk(CLK), .clr(RST));
  Register #(.width(32), .trigger("rising"), .Select("low")) LB_3 (
    .D(A0), .en(and_17_out), .Q(LB_3_q), .clk(CLK), .clr(RST));
  Register #(.width(32), .trigger("rising"), .Select("low")) LB_4 (
    .D(A0), .en(and_18_out), .Q(LB_4_q), .clk(CLK), .clr(RST));
  Register #(.width(32), .trigger("rising"), .Select("low")) LB_5 (
    .D(A0), .en(and_19_out), .Q(LB_5_q), .clk(CLK), .clr(RST));
  Register #(.width(32), .trigger("rising"), .Select("low")) LB_6 (
    .D(A0), .en(and_20_out), .Q(LB_6_q), .clk(CLK), .clr(RST));
  Register #(.width(32), .trigger("rising"), .Select("low")) LB_7 (
    .D(A0), .en(and_21_out), .Q(LB_7_q), .clk(CLK), .clr(RST));
  Register #(.width(32), .trigger("rising"), .Select("low")) LB_8 (
    .D(A0), .en(and_22_out), .Q(LB_8_q), .clk(CLK), .clr(RST));
  Register #(.width(32), .trigger("rising"), .Select("low")) LB_9 (
    .D(A0), .en(and_23_out), .Q(LB_9_q), .clk(CLK), .clr(RST));
  Register #(.width(32), .trigger("rising"), .Select("low")) LB_10 (
    .D(A0), .en(and_24_out), .Q(LB_10_q), .clk(CLK), .clr(RST));
  Register #(.width(32), .trigger("rising"), .Select("low")) LB_11 (.en(CLK), .clk(RST), .clr(RST));  // open: D, Q
  Register #(.width(32), .trigger("rising"), .Select("low")) LB_12 (
    .D(A0), .en(and_25_out), .Q(LB_12_q), .clk(CLK), .clr(RST));
  Register #(.width(32), .trigger("rising"), .Select("low")) LB_13 (
    .D(A0), .en(and_26_out), .Q(LB_13_q), .clk(CLK), .clr(RST));
  Register #(.width(32), .trigger("rising"), .Select("low")) LB_14 (
    .D(A0), .en(and_27_out), .Q(LB_14_q), .clk(CLK), .clr(RST));
  Register #(.width(32), .trigger("rising"), .Select("low")) LB_15 (
    .D(A0), .en(and_28_out), .Q(LB_15_q), .clk(CLK), .clr(RST));
  Register #(.width(32), .trigger("rising"), .Select("low")) LB_16 (
    .D(A0), .en(and_29_out), .Q(LB_16_q), .clk(CLK), .clr(RST));
  Register #(.width(32), .trigger("rising"), .Select("low")) LB_17 (
    .D(A0), .en(and_30_out), .Q(LB_17_q), .clk(CLK), .clr(RST));
  Register #(.width(32), .trigger("rising"), .Select("low")) LB_18 (
    .D(A0), .en(and_31_out), .Q(LB_18_q), .clk(CLK), .clr(RST));
  Register #(.width(32), .trigger("rising"), .Select("low")) LB_19 (
    .D(A0), .en(and_32_out), .Q(LB_19_q), .clk(CLK), .clr(RST));
  Register #(.width(32), .trigger("rising"), .Select("low")) LB_20 (
    .D(A0), .en(and_33_out), .Q(LB_20_q), .clk(CLK), .clr(RST));
  Register #(.width(32), .trigger("rising"), .Select("low")) LB_21 (
    .D(A0), .en(and_34_out), .Q(LB_21_q), .clk(CLK), .clr(RST));
  Register #(.width(32), .trigger("rising"), .Select("low")) LB_22 (
    .D(A0), .en(and_35_out), .Q(LB_22_q), .clk(CLK), .clr(RST));
  Register #(.width(32), .trigger("rising"), .Select("low")) LB_23 (
    .D(A0), .en(and_36_out), .Q(LB_23_q), .clk(CLK), .clr(RST));
  Register #(.width(32), .trigger("rising"), .Select("low")) LB_24 (
    .D(A0), .en(and_37_out), .Q(LB_24_q), .clk(CLK), .clr(RST));
  Register #(.width(32), .trigger("rising"), .Select("low")) LB_25 (
    .D(A0), .en(and_38_out), .Q(LB_25_q), .clk(CLK), .clr(RST));
  Register #(.width(32), .trigger("rising"), .Select("low")) LB_26 (
    .D(A0), .en(and_39_out), .Q(LB_26_q), .clk(CLK), .clr(RST));
  Register #(.width(32), .trigger("rising"), .Select("low")) LB_27 (
    .D(A0), .en(and_40_out), .Q(LB_27_q), .clk(CLK), .clr(RST));
  Register #(.width(32), .trigger("rising"), .Select("low")) LB_28 (
    .D(A0), .en(and_41_out), .Q(LB_28_q), .clk(CLK), .clr(RST));
  Register #(.width(32), .trigger("rising"), .Select("low")) LB_29 (
    .D(A0), .en(and_42_out), .Q(LB_29_q), .clk(CLK), .clr(RST));
  Register #(.width(32), .trigger("rising"), .Select("low")) LB_30 (
    .D(A0), .en(and_43_out), .Q(LB_30_q), .clk(CLK), .clr(RST));
  Register #(.width(32), .trigger("rising"), .Select("low")) LB_31 (
    .D(A0), .en(and_44_out), .Q(LB_31_q), .clk(CLK), .clr(RST));
  Register #(.width(32), .trigger("rising"), .Select("low")) LB_32 (
    .D(A0), .en(and_45_out), .Q(LB_32_q), .clk(CLK), .clr(RST));
  Register #(.width(32), .trigger("rising"), .Select("low")) LB_33 (
    .D(A0), .en(and_46_out), .Q(LB_33_q), .clk(CLK), .clr(RST));
  Register #(.width(32), .trigger("rising"), .Select("low")) LB_34 (.D(LB_q), .en(out), .Q(O0), .clk(CLK), .clr(RST));
  Register #(.width(32), .trigger("rising"), .Select("low")) LB_35 (.D(LB_2_q), .en(out), .Q(O1), .clk(CLK), .clr(RST));
  Register #(.width(32), .trigger("rising"), .Select("low")) LB_36 (.D(LB_3_q), .en(out), .Q(O2), .clk(CLK), .clr(RST));
  Register #(.width(32), .trigger("rising"), .Select("low")) LB_37 (.D(LB_4_q), .en(out), .Q(O3), .clk(CLK), .clr(RST));
  Register #(.width(32), .trigger("rising"), .Select("low")) LB_38 (.D(LB_5_q), .en(out), .Q(O4), .clk(CLK), .clr(RST));
  Register #(.width(32), .trigger("rising"), .Select("low")) LB_39 (.D(LB_6_q), .en(out), .Q(O5), .clk(CLK), .clr(RST));
  Register #(.width(32), .trigger("rising"), .Select("low")) LB_40 (.D(LB_7_q), .en(out), .Q(O6), .clk(CLK), .clr(RST));
  Register #(.width(32), .trigger("rising"), .Select("low")) LB_41 (.D(LB_8_q), .en(out), .Q(O7), .clk(CLK), .clr(RST));
  Register #(.width(32), .trigger("rising"), .Select("low")) LB_42 (.D(LB_9_q), .en(out), .Q(O8), .clk(CLK), .clr(RST));
  Register #(.width(32), .trigger("rising"), .Select("low")) LB_43 (
    .D(LB_10_q), .en(out), .Q(O9), .clk(CLK), .clr(RST));
  Register #(.width(32), .trigger("rising"), .Select("low")) LB_44 (
    .D(LB_12_q), .en(out), .Q(O10), .clk(CLK), .clr(RST));
  Register #(.width(32), .trigger("rising"), .Select("low")) LB_45 (
    .D(LB_13_q), .en(out), .Q(O11), .clk(CLK), .clr(RST));
  Register #(.width(32), .trigger("rising"), .Select("low")) LB_46 (
    .D(LB_14_q), .en(out), .Q(O12), .clk(CLK), .clr(RST));
  Register #(.width(32), .trigger("rising"), .Select("low")) LB_47 (
    .D(LB_15_q), .en(out), .Q(O13), .clk(CLK), .clr(RST));
  Register #(.width(32), .trigger("rising"), .Select("low")) LB_48 (
    .D(LB_16_q), .en(out), .Q(O14), .clk(CLK), .clr(RST));
  Register #(.width(32), .trigger("rising"), .Select("low")) LB_49 (
    .D(LB_17_q), .en(out), .Q(O15), .clk(CLK), .clr(RST));
  Register #(.width(32), .trigger("rising"), .Select("low")) LB_50 (
    .D(LB_18_q), .en(out), .Q(O16), .clk(CLK), .clr(RST));
  Register #(.width(32), .trigger("rising"), .Select("low")) LB_51 (
    .D(LB_19_q), .en(out), .Q(O17), .clk(CLK), .clr(RST));
  Register #(.width(32), .trigger("rising"), .Select("low")) LB_52 (
    .D(LB_20_q), .en(out), .Q(O18), .clk(CLK), .clr(RST));
  Register #(.width(32), .trigger("rising"), .Select("low")) LB_53 (
    .D(LB_21_q), .en(out), .Q(O19), .clk(CLK), .clr(RST));
  Register #(.width(32), .trigger("rising"), .Select("low")) LB_54 (
    .D(LB_22_q), .en(out), .Q(O20), .clk(CLK), .clr(RST));
  Register #(.width(32), .trigger("rising"), .Select("low")) LB_55 (
    .D(LB_23_q), .en(out), .Q(O21), .clk(CLK), .clr(RST));
  Register #(.width(32), .trigger("rising"), .Select("low")) LB_56 (
    .D(LB_24_q), .en(out), .Q(O22), .clk(CLK), .clr(RST));
  Register #(.width(32), .trigger("rising"), .Select("low")) LB_57 (
    .D(LB_25_q), .en(out), .Q(O23), .clk(CLK), .clr(RST));
  Register #(.width(32), .trigger("rising"), .Select("low")) LB_58 (
    .D(LB_26_q), .en(out), .Q(O24), .clk(CLK), .clr(RST));
  Register #(.width(32), .trigger("rising"), .Select("low")) LB_59 (
    .D(LB_27_q), .en(out), .Q(O25), .clk(CLK), .clr(RST));
  Register #(.width(32), .trigger("rising"), .Select("low")) LB_60 (
    .D(LB_28_q), .en(out), .Q(O26), .clk(CLK), .clr(RST));
  Register #(.width(32), .trigger("rising"), .Select("low")) LB_61 (
    .D(LB_29_q), .en(out), .Q(O27), .clk(CLK), .clr(RST));
  Register #(.width(32), .trigger("rising"), .Select("low")) LB_62 (
    .D(LB_30_q), .en(out), .Q(O28), .clk(CLK), .clr(RST));
  Register #(.width(32), .trigger("rising"), .Select("low")) LB_63 (
    .D(LB_31_q), .en(out), .Q(O29), .clk(CLK), .clr(RST));
  Register #(.width(32), .trigger("rising"), .Select("low")) LB_64 (
    .D(LB_32_q), .en(out), .Q(O30), .clk(CLK), .clr(RST));
  Register #(.width(32), .trigger("rising"), .Select("low")) LB_65 (
    .D(LB_33_q), .en(out), .Q(O31), .clk(CLK), .clr(RST));

  // Other names for the same wires on the sheet: IR[25:0] = instr_index; PC_J[31:2] = {PC[31:28], instr_index};
  //   Shamt[4:0] = instr_index[10:6]; MDin[31:0] = A0; Reset = RST; V0[31:0] = PC_JR

  // Notes on the sheet:
  //   PC逻辑
  //   指令存储器
  //   contents of rom_1 (hex, n*v repeats v):
  //   3c010000 3421ff00 18020 108100 2011003c ae300000 2013000f 20141000 2015000f 20160008 16b400 2017004d
  //   200e0014 200f0100 e8880 ae2f0000 20020022 c 200d0000 20020000 c 22710020 118880 22720040 129080
  //   40800000 20100048 12170006 2010004b 12170011 20100050 1217001c 2010004d 12170025 40000000 20100000
  //   12700075 8e300000 2148025 ae300000 148827 8e500000 2118024 ae500000 20100001 2709822 8000c53
  //   40000000 20100001 1087c0 12900067 8e500000 2148025 ae500000 149027 8e300000 2128024 ae300000 14a040
  //   8000c53 40000000 2010001f 1270005b 8e300000 2148025 ae300000 8e500000 2148025 ae500000 22730001
  //   8000c53 40000000 20100001 12900050 145027 8e300000 20a8024 ae300000 8e500000 20a8024 ae500000 14a042
  //   8000c53 166e000c 168f000b 138880 8e300000 2148025 ae300000 21ad0001 d2020 20020021 c 20100400
  //   120d003e 8000c86 138880 8e300000 2148024 12000003 20020011 c 8000c00 138880 8e300000 2148025
  //   ae300000 158880 8e300000 169027 2128024 ae300000 22b10020 118880 8e300000 22b10040 118880 2168024
  //   12000008 8e300000 2168024 12000002 22b50001 8000c97 20100001 2b0a822 8000c97 8e300000 2168024
  //   12000002 16b040 8000c97 16b042 8000c97 20020020 20040000 c 35820 b8880 8e300000 20020020 20040001 c
  //   708024 1600fff5 b7020 37820 e8880 8e300000 20f8025 ae300000 20020022 c 8000c15 20020010 c 8000c00
  //   20020000 c 8000c00 20080050 11170001 20170048 42000018 2008004d 11170001 2017004b 42000018 20080048
  //   11170001 20170050 42000018 2008004b 11170001 2017004d 42000018
  //   OP
  //   Func
  //   rs
  //   指令字
  //   rt
  //   rd
  //   JMP
  //   JR
  //   OP
  //   Func
  //   Blez
  //   Beq
  //   Bne
  //   MemToReg
  //   MemWrite
  //   AluOP
  //   AluSrcB
  //   RegWrite
  //   JAL
  //   RegDst
  //   Syscall
  //   Syscall逻辑
  //   Reset 
  //   Reset 
  //   Reset 
  //   Reset 
  //   控制位
  //   暂停节拍，不能为0
  //   戳工具置1进入计数暂停模式，ctrl+k时钟自动运行到对应节拍暂停
  //   ctrl+k关闭时钟连续运行，将控制位置零，进入单步调试模式调试
  //   可计数暂停的时钟源
  //   获取随机数逻辑
  //   $a0 == 1 时 返回列随机，否则返回行随机到v1
endmodule

// 单周期硬布线控制器
module \单周期硬布线控制器  (
  input  [5:0] OP,
  input  [5:0] Func,
  input  [4:0] _21_25,
  output [3:0] ALU_OP,
  output MemToReg,
  output MemWrite,
  output ALU_SRC,
  output RegWrite,
  output SysCALL,
  output SignedExt,
  output RegDst,
  output Beq,
  output Bne,
  output JR,
  output JMP,
  output JAL,
  output BLEZ,
  output LBU,
  output ERET,
  output MTC0,
  output MFC0
);

  wire and_1_out, comparator_1_eq, comparator_2_eq;

  \运算控制器自动生成  \u_运算控制器自动生成_1  (
    .OP0(OP[0]), .OP1(OP[1]), .OP2(OP[2]), .OP3(OP[3]), .OP4(OP[4]), .OP5(OP[5]), .F0(Func[0]), .F1(Func[1]),
    .F2(Func[2]), .F3(Func[3]), .F4(Func[4]), .F5(Func[5]), .S0(ALU_OP[0]), .S1(ALU_OP[1]), .S2(ALU_OP[2]),
    .S3(ALU_OP[3]));
  \控制信号自动生成  \u_控制信号自动生成_1  (
    .OP0(OP[0]), .OP1(OP[1]), .OP2(OP[2]), .MemToReg(MemToReg), .OP3(OP[3]), .OP4(OP[4]), .OP5(OP[5]),
    .MemWrite(MemWrite), .F0(Func[0]), .F1(Func[1]), .F2(Func[2]), .F3(Func[3]), .F4(Func[4]), .F5(Func[5]),
    .ALU_SRC(ALU_SRC), .RegWrite(RegWrite), .SysCALL(SysCALL), .SignedExt(SignedExt), .RegDst(RegDst),
    .BEQ(Beq), .BNE(Bne), .JR(JR), .JUMP(JMP), .JAL(JAL), .BLEZ(BLEZ), .LBU(LBU), .ERET(ERET));
  and and_1 (and_1_out, ~OP[0], ~OP[1], ~OP[2], ~OP[3], OP[4], ~OP[5]);  // AND_Gate
  Comparator #(.width(5), .mode("unsigned")) comparator_1 (
    .a(_21_25), .b(5'b00100), .eq(comparator_1_eq));  // open: gt, lt
  Comparator #(.width(5), .mode("unsigned")) comparator_2 (
    .a(_21_25), .b({5{1'b0}}), .eq(comparator_2_eq));  // open: gt, lt
  and and_2 (MTC0, and_1_out, comparator_1_eq);
  and and_3 (MFC0, and_1_out, comparator_2_eq);

  // Other names for the same wires on the sheet: OP_CODE[5:0] = OP

  // Notes on the sheet:
  //   运算器控制器，根据指令生成运算器功能选择信号
  //   控制信号生成，产生数据通路需要的其他控制信号
endmodule

// 运算器控制器
module \运算控制器自动生成  (
  input  OP0,
  input  OP1,
  input  OP2,
  input  OP3,
  input  OP4,
  input  OP5,
  input  F0,
  input  F1,
  input  F2,
  input  F3,
  input  F4,
  input  F5,
  output S0,
  output S1,
  output S2,
  output S3
);

  wire and_1_out, and_2_out, and_3_out, and_4_out, and_5_out, and_6_out, and_7_out, and_8_out, and_9_out,
       and_10_out, and_11_out, and_12_out, and_13_out, and_14_out, and_15_out, and_16_out, and_17_out,
       and_18_out, and_19_out, and_20_out, and_21_out, and_22_out, and_23_out, and_24_out, and_25_out,
       and_26_out, and_27_out, and_28_out, and_29_out, and_30_out, and_31_out, and_32_out, and_33_out,
       and_34_out, and_35_out, and_36_out, and_37_out, and_38_out, and_39_out, and_40_out, and_41_out,
       and_42_out, and_43_out, not_1_out, not_2_out, not_3_out, not_4_out, not_5_out, not_6_out, not_7_out,
       not_8_out, not_9_out, not_10_out, not_11_out, not_12_out, not_13_out, not_14_out, not_15_out,
       not_16_out, not_17_out, not_18_out, not_19_out, not_20_out, not_21_out, not_22_out, not_23_out,
       not_24_out, not_25_out, not_26_out, not_27_out, not_28_out, not_29_out, not_30_out, not_31_out,
       not_32_out, not_33_out, not_34_out, not_35_out, not_36_out, not_37_out, not_38_out, not_39_out,
       not_40_out, not_41_out, not_42_out, not_43_out, not_44_out, not_45_out, not_46_out, not_47_out,
       not_48_out, not_49_out, not_50_out, not_51_out, not_52_out, not_53_out, not_54_out, not_55_out,
       not_56_out, not_57_out, not_58_out, not_59_out, not_60_out, not_61_out, not_62_out, not_63_out,
       not_64_out, not_65_out, not_66_out, not_67_out, not_68_out, not_69_out, not_70_out, not_71_out,
       not_72_out, not_73_out, not_74_out, not_75_out, not_76_out, not_77_out, not_78_out, not_79_out,
       not_80_out, not_81_out, not_82_out, not_83_out, not_84_out, not_85_out, not_86_out, not_87_out,
       not_88_out, not_89_out, not_90_out, not_91_out, not_92_out, not_93_out, not_94_out, not_95_out,
       not_96_out, not_97_out, not_98_out, not_99_out, not_100_out, not_101_out, not_102_out, not_103_out,
       not_104_out, not_105_out, not_106_out, not_107_out, not_108_out, not_109_out, not_110_out,
       not_111_out, not_112_out, not_113_out, not_114_out, not_115_out, not_116_out, not_117_out,
       not_118_out, not_119_out, not_120_out, not_121_out, not_122_out, not_123_out, not_124_out,
       not_125_out, not_126_out, not_127_out, not_128_out, not_129_out, not_130_out, not_131_out,
       not_132_out, not_133_out, not_134_out, not_135_out, not_136_out, not_137_out, not_138_out,
       not_139_out, not_140_out, not_141_out, not_142_out, not_143_out, not_144_out, not_145_out,
       not_146_out, not_147_out, not_148_out, not_149_out, not_150_out, not_151_out, not_152_out,
       not_153_out, not_154_out, not_155_out, not_156_out, not_157_out, not_158_out, not_159_out,
       not_160_out, not_161_out, not_162_out, not_163_out, not_164_out, not_165_out, not_166_out,
       not_167_out, not_168_out, not_169_out, not_170_out, not_171_out, not_172_out, not_173_out,
       not_174_out, not_175_out, not_176_out, not_177_out, not_178_out, not_179_out, not_180_out,
       not_181_out, not_182_out, not_183_out, not_184_out, not_185_out, not_186_out, not_187_out,
       not_188_out, not_189_out, not_190_out, not_191_out, not_192_out, not_193_out, not_194_out,
       not_195_out, not_196_out, not_197_out, not_198_out, not_199_out, not_200_out, not_201_out,
       not_202_out, not_203_out, not_204_out, not_205_out, not_206_out, not_207_out, not_208_out,
       not_209_out, not_210_out, not_211_out, not_212_out, not_213_out, not_214_out, not_215_out,
       not_216_out, not_217_out, not_218_out, not_219_out, not_220_out, not_221_out, not_222_out,
       not_223_out, not_224_out, not_225_out, not_226_out, not_227_out, not_228_out, not_229_out,
       not_230_out, not_231_out, not_232_out, not_233_out, not_234_out, not_235_out, not_236_out,
       not_237_out, not_238_out, not_239_out, not_240_out, not_241_out, not_242_out, not_243_out,
       not_244_out, not_245_out, not_246_out, not_247_out, not_248_out, not_249_out, not_250_out,
       not_251_out, not_252_out, not_253_out, not_254_out, not_255_out, not_256_out, not_257_out,
       not_258_out, not_259_out, not_260_out, not_261_out, not_262_out, not_263_out, not_264_out,
       not_265_out, not_266_out, not_267_out, not_268_out;

  not not_1 (not_1_out, OP5);
  not not_2 (not_2_out, OP4);
  not not_3 (not_3_out, OP3);
  not not_4 (not_4_out, OP2);
  not not_5 (not_5_out, OP1);
  not not_6 (not_6_out, OP0);
  not not_7 (not_7_out, F5);
  not not_8 (not_8_out, F4);
  not not_9 (not_9_out, F3);
  not not_10 (not_10_out, F2);
  not not_11 (not_11_out, OP5);
  not not_12 (not_12_out, OP4);
  not not_13 (not_13_out, OP3);
  not not_14 (not_14_out, OP2);
  not not_15 (not_15_out, OP1);
  not not_16 (not_16_out, OP0);
  not not_17 (not_17_out, F4);
  not not_18 (not_18_out, F3);
  not not_19 (not_19_out, F2);
  not not_20 (not_20_out, F1);
  not not_21 (not_21_out, F0);
  not not_22 (not_22_out, OP5);
  not not_23 (not_23_out, OP4);
  not not_24 (not_24_out, OP3);
  not not_25 (not_25_out, OP2);
  not not_26 (not_26_out, OP1);
  not not_27 (not_27_out, OP0);
  not not_28 (not_28_out, F4);
  not not_29 (not_29_out, F3);
  not not_30 (not_30_out, F2);
  not not_31 (not_31_out, F1);
  not not_32 (not_32_out, OP5);
  not not_33 (not_33_out, OP4);
  not not_34 (not_34_out, OP3);
  not not_35 (not_35_out, OP2);
  not not_36 (not_36_out, OP1);
  not not_37 (not_37_out, OP0);
  not not_38 (not_38_out, F4);
  not not_39 (not_39_out, F3);
  not not_40 (not_40_out, F1);
  not not_41 (not_41_out, F0);
  not not_42 (not_42_out, OP5);
  not not_43 (not_43_out, OP4);
  not not_44 (not_44_out, OP3);
  not not_45 (not_45_out, OP2);
  not not_46 (not_46_out, OP1);
  not not_47 (not_47_out, OP0);
  not not_48 (not_48_out, F4);
  not not_49 (not_49_out, F2);
  not not_50 (not_50_out, F0);
  not not_51 (not_51_out, OP5);
  not not_52 (not_52_out, OP4);
  not not_53 (not_53_out, OP2);
  not not_54 (not_54_out, OP1);
  not not_55 (not_55_out, OP0);
  not not_56 (not_56_out, OP5);
  not not_57 (not_57_out, OP4);
  not not_58 (not_58_out, OP1);
  not not_59 (not_59_out, OP0);
  not not_60 (not_60_out, OP5);
  not not_61 (not_61_out, OP4);
  not not_62 (not_62_out, OP2);
  not not_63 (not_63_out, OP1);
  not not_64 (not_64_out, OP5);
  not not_65 (not_65_out, OP4);
  not not_66 (not_66_out, OP2);
  not not_67 (not_67_out, OP0);
  not not_68 (not_68_out, OP4);
  not not_69 (not_69_out, OP3);
  not not_70 (not_70_out, OP2);
  not not_71 (not_71_out, OP4);
  not not_72 (not_72_out, OP2);
  not not_73 (not_73_out, OP5);
  not not_74 (not_74_out, OP4);
  not not_75 (not_75_out, OP0);
  not not_76 (not_76_out, OP4);
  not not_77 (not_77_out, OP3);
  not not_78 (not_78_out, OP1);
  not not_79 (not_79_out, OP0);
  not not_80 (not_80_out, OP5);
  not not_81 (not_81_out, OP4);
  not not_82 (not_82_out, OP3);
  not not_83 (not_83_out, OP0);
  not not_84 (not_84_out, OP5);
  not not_85 (not_85_out, OP4);
  not not_86 (not_86_out, OP3);
  not not_87 (not_87_out, OP2);
  not not_88 (not_88_out, OP1);
  not not_89 (not_89_out, OP0);
  not not_90 (not_90_out, F5);
  not not_91 (not_91_out, F4);
  not not_92 (not_92_out, F3);
  not not_93 (not_93_out, F2);
  not not_94 (not_94_out, F0);
  not not_95 (not_95_out, OP5);
  not not_96 (not_96_out, OP4);
  not not_97 (not_97_out, OP3);
  not not_98 (not_98_out, OP2);
  not not_99 (not_99_out, OP1);
  not not_100 (not_100_out, OP0);
  not not_101 (not_101_out, F4);
  not not_102 (not_102_out, F3);
  not not_103 (not_103_out, F2);
  not not_104 (not_104_out, F0);
  not not_105 (not_105_out, OP5);
  not not_106 (not_106_out, OP4);
  not not_107 (not_107_out, OP3);
  not not_108 (not_108_out, OP2);
  not not_109 (not_109_out, OP1);
  not not_110 (not_110_out, OP0);
  not not_111 (not_111_out, F4);
  not not_112 (not_112_out, F3);
  not not_113 (not_113_out, F1);
  not not_114 (not_114_out, F0);
  not not_115 (not_115_out, OP5);
  not not_116 (not_116_out, OP4);
  not not_117 (not_117_out, OP3);
  not not_118 (not_118_out, OP2);
  not not_119 (not_119_out, OP1);
  not not_120 (not_120_out, OP0);
  not not_121 (not_121_out, F4);
  not not_122 (not_122_out, F3);
  not not_123 (not_123_out, OP5);
  not not_124 (not_124_out, OP4);
  not not_125 (not_125_out, OP3);
  not not_126 (not_126_out, OP2);
  not not_127 (not_127_out, OP1);
  not not_128 (not_128_out, OP0);
  not not_129 (not_129_out, F4);
  not not_130 (not_130_out, F2);
  not not_131 (not_131_out, F0);
  not not_132 (not_132_out, OP5);
  not not_133 (not_133_out, OP4);
  not not_134 (not_134_out, OP1);
  not not_135 (not_135_out, OP0);
  not not_136 (not_136_out, OP5);
  not not_137 (not_137_out, OP4);
  not not_138 (not_138_out, OP2);
  not not_139 (not_139_out, OP0);
  not not_140 (not_140_out, OP5);
  not not_141 (not_141_out, OP4);
  not not_142 (not_142_out, OP3);
  not not_143 (not_143_out, OP0);
  not not_144 (not_144_out, OP5);
  not not_145 (not_145_out, OP4);
  not not_146 (not_146_out, OP3);
  not not_147 (not_147_out, OP2);
  not not_148 (not_148_out, OP1);
  not not_149 (not_149_out, OP0);
  not not_150 (not_150_out, F4);
  not not_151 (not_151_out, F3);
  not not_152 (not_152_out, F2);
  not not_153 (not_153_out, F1);
  not not_154 (not_154_out, F0);
  not not_155 (not_155_out, OP5);
  not not_156 (not_156_out, OP4);
  not not_157 (not_157_out, OP3);
  not not_158 (not_158_out, OP2);
  not not_159 (not_159_out, OP1);
  not not_160 (not_160_out, OP0);
  not not_161 (not_161_out, F4);
  not not_162 (not_162_out, F3);
  not not_163 (not_163_out, F2);
  not not_164 (not_164_out, F1);
  not not_165 (not_165_out, OP5);
  not not_166 (not_166_out, OP4);
  not not_167 (not_167_out, OP3);
  not not_168 (not_168_out, OP2);
  not not_169 (not_169_out, OP1);
  not not_170 (not_170_out, OP0);
  not not_171 (not_171_out, F4);
  not not_172 (not_172_out, F3);
  not not_173 (not_173_out, F2);
  not not_174 (not_174_out, F0);
  not not_175 (not_175_out, OP5);
  not not_176 (not_176_out, OP4);
  not not_177 (not_177_out, OP3);
  not not_178 (not_178_out, OP2);
  not not_179 (not_179_out, OP1);
  not not_180 (not_180_out, OP0);
  not not_181 (not_181_out, F4);
  not not_182 (not_182_out, F3);
  not not_183 (not_183_out, F1);
  not not_184 (not_184_out, F0);
  not not_185 (not_185_out, OP5);
  not not_186 (not_186_out, OP4);
  not not_187 (not_187_out, OP3);
  not not_188 (not_188_out, OP2);
  not not_189 (not_189_out, OP1);
  not not_190 (not_190_out, OP0);
  not not_191 (not_191_out, F4);
  not not_192 (not_192_out, F2);
  not not_193 (not_193_out, OP5);
  not not_194 (not_194_out, OP4);
  not not_195 (not_195_out, OP2);
  not not_196 (not_196_out, OP1);
  not not_197 (not_197_out, OP0);
  not not_198 (not_198_out, OP5);
  not not_199 (not_199_out, OP4);
  not not_200 (not_200_out, OP1);
  not not_201 (not_201_out, OP0);
  not not_202 (not_202_out, OP5);
  not not_203 (not_203_out, OP4);
  not not_204 (not_204_out, OP2);
  not not_205 (not_205_out, OP1);
  not not_206 (not_206_out, OP4);
  not not_207 (not_207_out, OP3);
  not not_208 (not_208_out, OP2);
  not not_209 (not_209_out, OP4);
  not not_210 (not_210_out, OP2);
  not not_211 (not_211_out, OP5);
  not not_212 (not_212_out, OP4);
  not not_213 (not_213_out, OP2);
  not not_214 (not_214_out, OP4);
  not not_215 (not_215_out, OP3);
  not not_216 (not_216_out, OP1);
  not not_217 (not_217_out, OP0);
  not not_218 (not_218_out, OP5);
  not not_219 (not_219_out, OP4);
  not not_220 (not_220_out, OP3);
  not not_221 (not_221_out, OP2);
  not not_222 (not_222_out, OP1);
  not not_223 (not_223_out, OP0);
  not not_224 (not_224_out, F4);
  not not_225 (not_225_out, F3);
  not not_226 (not_226_out, F1);
  not not_227 (not_227_out, OP5);
  not not_228 (not_228_out, OP4);
  not not_229 (not_229_out, OP3);
  not not_230 (not_230_out, OP2);
  not not_231 (not_231_out, OP1);
  not not_232 (not_232_out, OP0);
  not not_233 (not_233_out, F4);
  not not_234 (not_234_out, F3);
  not not_235 (not_235_out, OP5);
  not not_236 (not_236_out, OP4);
  not not_237 (not_237_out, OP3);
  not not_238 (not_238_out, OP2);
  not not_239 (not_239_out, OP1);
  not not_240 (not_240_out, OP0);
  not not_241 (not_241_out, F4);
  not not_242 (not_242_out, F2);
  not not_243 (not_243_out, F0);
  not not_244 (not_244_out, OP5);
  not not_245 (not_245_out, OP4);
  not not_246 (not_246_out, OP3);
  not not_247 (not_247_out, OP2);
  not not_248 (not_248_out, OP1);
  not not_249 (not_249_out, OP0);
  not not_250 (not_250_out, F4);
  not not_251 (not_251_out, F2);
  not not_252 (not_252_out, OP5);
  not not_253 (not_253_out, OP4);
  not not_254 (not_254_out, OP2);
  not not_255 (not_255_out, OP0);
  not not_256 (not_256_out, OP5);
  not not_257 (not_257_out, OP4);
  not not_258 (not_258_out, OP1);
  not not_259 (not_259_out, OP5);
  not not_260 (not_260_out, OP4);
  not not_261 (not_261_out, OP0);
  not not_262 (not_262_out, OP5);
  not not_263 (not_263_out, OP4);
  not not_264 (not_264_out, OP2);
  not not_265 (not_265_out, OP5);
  not not_266 (not_266_out, OP4);
  not not_267 (not_267_out, OP3);
  not not_268 (not_268_out, OP0);
  and and_1 (and_1_out, not_1_out, not_2_out, not_3_out, not_4_out, not_5_out, not_6_out, not_7_out, not_8_out, not_9_out, not_10_out, F1, F0);
  and and_2 (and_2_out, not_11_out, not_12_out, not_13_out, not_14_out, not_15_out, not_16_out, F5, not_17_out, not_18_out, not_19_out, not_20_out, not_21_out);
  and and_3 (and_3_out, not_22_out, not_23_out, not_24_out, not_25_out, not_26_out, not_27_out, F5, not_28_out, not_29_out, not_30_out, not_31_out, F0);
  and and_4 (and_4_out, not_32_out, not_33_out, not_34_out, not_35_out, not_36_out, not_37_out, F5, not_38_out, not_39_out, F2, not_40_out, not_41_out);
  and and_5 (and_5_out, not_42_out, not_43_out, not_44_out, not_45_out, not_46_out, not_47_out, F5, not_48_out, F3, not_49_out, F1, not_50_out);
  and and_6 (and_6_out, not_51_out, not_52_out, OP3, not_53_out, not_54_out, not_55_out);
  and and_7 (and_7_out, not_56_out, not_57_out, OP3, OP2, not_58_out, not_59_out);
  and and_8 (and_8_out, not_60_out, not_61_out, OP3, not_62_out, not_63_out, OP0);
  and and_9 (and_9_out, not_64_out, not_65_out, OP3, not_66_out, OP1, not_67_out);
  and and_10 (and_10_out, OP5, not_68_out, not_69_out, not_70_out, OP1, OP0);
  and and_11 (and_11_out, OP5, not_71_out, OP3, not_72_out, OP1, OP0);
  and and_12 (and_12_out, not_73_out, not_74_out, OP3, OP2, OP1, not_75_out);
  and and_13 (and_13_out, OP5, not_76_out, not_77_out, OP2, not_78_out, not_79_out);
  and and_14 (and_14_out, not_80_out, not_81_out, not_82_out, OP2, OP1, not_83_out);
  and and_15 (and_15_out, not_84_out, not_85_out, not_86_out, not_87_out, not_88_out, not_89_out, not_90_out, not_91_out, not_92_out, not_93_out, F1, not_94_out);
  and and_16 (and_16_out, not_95_out, not_96_out, not_97_out, not_98_out, not_99_out, not_100_out, F5, not_101_out, not_102_out, not_103_out, F1, not_104_out);
  and and_17 (and_17_out, not_105_out, not_106_out, not_107_out, not_108_out, not_109_out, not_110_out, F5, not_111_out, not_112_out, F2, not_113_out, not_114_out);
  and and_18 (and_18_out, not_115_out, not_116_out, not_117_out, not_118_out, not_119_out, not_120_out, F5, not_121_out, not_122_out, F2, F1, F0);
  and and_19 (and_19_out, not_123_out, not_124_out, not_125_out, not_126_out, not_127_out, not_128_out, F5, not_129_out, F3, not_130_out, F1, not_131_out);
  and and_20 (and_20_out, not_132_out, not_133_out, OP3, OP2, not_134_out, not_135_out);
  and and_21 (and_21_out, not_136_out, not_137_out, OP3, not_138_out, OP1, not_139_out);
  and and_22 (and_22_out, not_140_out, not_141_out, not_142_out, OP2, OP1, not_143_out);
  and and_23 (and_23_out, not_144_out, not_145_out, not_146_out, not_147_out, not_148_out, not_149_out, F5, not_150_out, not_151_out, not_152_out, not_153_out, not_154_out);
  and and_24 (and_24_out, not_155_out, not_156_out, not_157_out, not_158_out, not_159_out, not_160_out, F5, not_161_out, not_162_out, not_163_out, not_164_out, F0);
  and and_25 (and_25_out, not_165_out, not_166_out, not_167_out, not_168_out, not_169_out, not_170_out, F5, not_171_out, not_172_out, not_173_out, F1, not_174_out);
  and and_26 (and_26_out, not_175_out, not_176_out, not_177_out, not_178_out, not_179_out, not_180_out, F5, not_181_out, not_182_out, F2, not_183_out, not_184_out);
  and and_27 (and_27_out, not_185_out, not_186_out, not_187_out, not_188_out, not_189_out, not_190_out, F5, not_191_out, F3, not_192_out, F1, F0);
  and and_28 (and_28_out, not_193_out, not_194_out, OP3, not_195_out, not_196_out, not_197_out);
  and and_29 (and_29_out, not_198_out, not_199_out, OP3, OP2, not_200_out, not_201_out);
  and and_30 (and_30_out, not_202_out, not_203_out, OP3, not_204_out, not_205_out, OP0);
  and and_31 (and_31_out, OP5, not_206_out, not_207_out, not_208_out, OP1, OP0);
  and and_32 (and_32_out, OP5, not_209_out, OP3, not_210_out, OP1, OP0);
  and and_33 (and_33_out, not_211_out, not_212_out, OP3, not_213_out, OP1, OP0);
  and and_34 (and_34_out, OP5, not_214_out, not_215_out, OP2, not_216_out, not_217_out);
  and and_35 (and_35_out, not_218_out, not_219_out, not_220_out, not_221_out, not_222_out, not_223_out, F5, not_224_out, not_225_out, F2, not_226_out, F0);
  and and_36 (and_36_out, not_227_out, not_228_out, not_229_out, not_230_out, not_231_out, not_232_out, F5, not_233_out, not_234_out, F2, F1, F0);
  and and_37 (and_37_out, not_235_out, not_236_out, not_237_out, not_238_out, not_239_out, not_240_out, F5, not_241_out, F3, not_242_out, F1, not_243_out);
  and and_38 (and_38_out, not_244_out, not_245_out, not_246_out, not_247_out, not_248_out, not_249_out, F5, not_250_out, F3, not_251_out, F1, F0);
  and and_39 (and_39_out, not_252_out, not_253_out, OP3, not_254_out, OP1, not_255_out);
  and and_40 (and_40_out, not_256_out, not_257_out, OP3, OP2, not_258_out, OP0);
  and and_41 (and_41_out, not_259_out, not_260_out, OP3, OP2, OP1, not_261_out);
  and and_42 (and_42_out, not_262_out, not_263_out, OP3, not_264_out, OP1, OP0);
  and and_43 (and_43_out, not_265_out, not_266_out, not_267_out, OP2, OP1, not_268_out);
  or or_1 (S1, and_15_out, and_16_out, and_17_out, and_18_out, and_19_out, and_20_out, and_21_out, and_22_out);
  or or_2 (S3, and_35_out, and_36_out, and_37_out, and_38_out, and_39_out, and_40_out, and_41_out, and_42_out, and_43_out);
  or or_3 (S0, and_1_out, and_2_out, and_3_out, and_4_out, and_5_out, and_6_out, and_7_out, and_8_out, and_9_out, and_10_out, and_11_out, and_12_out, and_13_out, and_14_out);
  or or_4 (S2, and_23_out, and_24_out, and_25_out, and_26_out, and_27_out, and_28_out, and_29_out, and_30_out, and_31_out, and_32_out, and_33_out, and_34_out);
endmodule

// 控制信号生成
module \控制信号自动生成  (
  input  OP0,
  input  OP1,
  input  OP2,
  input  OP3,
  input  OP4,
  input  OP5,
  input  F0,
  input  F1,
  input  F2,
  input  F3,
  input  F4,
  input  F5,
  output MemToReg,
  output MemWrite,
  output ALU_SRC,
  output RegWrite,
  output SysCALL,
  output SignedExt,
  output RegDst,
  output BEQ,
  output BNE,
  output JR,
  output JUMP,
  output JAL,
  output BLEZ,
  output LBU,
  output ERET
);

  wire and_1_out, and_2_out, and_4_out, and_5_out, and_6_out, and_7_out, and_8_out, and_9_out, and_10_out,
       and_11_out, and_12_out, and_13_out, and_14_out, and_15_out, and_16_out, and_17_out, and_18_out,
       and_20_out, and_21_out, and_22_out, and_23_out, and_24_out, and_25_out, and_26_out, and_27_out,
       and_31_out, and_32_out, not_1_out, not_2_out, not_3_out, not_4_out, not_5_out, not_6_out, not_7_out,
       not_8_out, not_9_out, not_10_out, not_11_out, not_12_out, not_13_out, not_14_out, not_15_out,
       not_16_out, not_17_out, not_18_out, not_19_out, not_20_out, not_21_out, not_22_out, not_23_out,
       not_24_out, not_25_out, not_26_out, not_27_out, not_28_out, not_29_out, not_30_out, not_31_out,
       not_32_out, not_33_out, not_34_out, not_35_out, not_36_out, not_37_out, not_38_out, not_39_out,
       not_40_out, not_41_out, not_42_out, not_43_out, not_44_out, not_45_out, not_46_out, not_47_out,
       not_48_out, not_49_out, not_50_out, not_51_out, not_52_out, not_53_out, not_54_out, not_55_out,
       not_56_out, not_57_out, not_58_out, not_59_out, not_60_out, not_61_out, not_62_out, not_63_out,
       not_64_out, not_65_out, not_66_out, not_67_out, not_68_out, not_69_out, not_70_out, not_71_out,
       not_72_out, not_73_out, not_74_out, not_75_out, not_76_out, not_77_out, not_78_out, not_79_out,
       not_80_out, not_81_out, not_82_out, not_83_out, not_84_out, not_85_out, not_86_out, not_87_out,
       not_88_out, not_89_out, not_90_out, not_91_out, not_92_out, not_93_out, not_94_out, not_95_out,
       not_96_out, not_97_out, not_98_out, not_99_out, not_100_out, not_101_out, not_102_out, not_103_out,
       not_104_out, not_105_out, not_106_out, not_107_out, not_108_out, not_109_out, not_110_out,
       not_111_out, not_112_out, not_113_out, not_114_out, not_115_out, not_116_out, not_117_out,
       not_118_out, not_119_out, not_120_out, not_121_out, not_122_out, not_123_out, not_124_out,
       not_125_out, not_126_out, not_127_out, not_128_out, not_129_out, not_130_out, not_131_out,
       not_132_out, not_133_out, not_134_out, not_135_out, not_136_out, not_137_out, not_138_out,
       not_139_out, not_140_out, not_141_out, not_142_out, not_143_out, not_144_out, not_145_out,
       not_146_out, not_147_out, not_148_out, not_149_out, not_150_out, not_151_out, not_152_out,
       not_153_out, not_154_out, not_155_out, not_156_out, not_157_out, not_158_out, not_159_out,
       not_160_out, not_161_out, not_162_out, not_163_out, not_164_out, not_165_out, not_166_out,
       not_167_out, not_168_out, not_169_out, not_170_out, not_171_out, not_172_out, not_173_out,
       not_174_out, not_175_out, not_176_out, not_177_out, not_178_out, not_179_out, not_180_out,
       not_181_out, not_182_out, not_183_out, not_184_out, not_185_out, not_186_out, not_187_out,
       not_188_out, not_189_out, not_190_out, not_191_out, not_192_out, not_193_out, not_194_out,
       not_195_out, not_196_out, not_197_out, not_198_out, not_199_out;

  not not_1 (not_1_out, OP0);
  not not_2 (not_2_out, OP1);
  not not_3 (not_3_out, OP3);
  not not_4 (not_4_out, OP4);
  not not_5 (not_5_out, OP2);
  not not_6 (not_6_out, OP3);
  not not_7 (not_7_out, OP4);
  not not_8 (not_8_out, OP2);
  not not_9 (not_9_out, OP4);
  not not_10 (not_10_out, OP0);
  not not_11 (not_11_out, OP4);
  not not_12 (not_12_out, OP5);
  not not_13 (not_13_out, OP1);
  not not_14 (not_14_out, OP4);
  not not_15 (not_15_out, OP5);
  not not_16 (not_16_out, OP2);
  not not_17 (not_17_out, OP4);
  not not_18 (not_18_out, OP5);
  not not_19 (not_19_out, OP0);
  not not_20 (not_20_out, OP1);
  not not_21 (not_21_out, OP3);
  not not_22 (not_22_out, OP4);
  not not_23 (not_23_out, OP2);
  not not_24 (not_24_out, OP4);
  not not_25 (not_25_out, OP0);
  not not_26 (not_26_out, OP1);
  not not_27 (not_27_out, OP2);
  not not_28 (not_28_out, OP4);
  not not_29 (not_29_out, OP5);
  not not_30 (not_30_out, F0);
  not not_31 (not_31_out, F2);
  not not_32 (not_32_out, F3);
  not not_33 (not_33_out, F4);
  not not_34 (not_34_out, OP0);
  not not_35 (not_35_out, OP1);
  not not_36 (not_36_out, OP2);
  not not_37 (not_37_out, OP4);
  not not_38 (not_38_out, OP5);
  not not_39 (not_39_out, F1);
  not not_40 (not_40_out, F3);
  not not_41 (not_41_out, F4);
  not not_42 (not_42_out, OP0);
  not not_43 (not_43_out, OP1);
  not not_44 (not_44_out, OP2);
  not not_45 (not_45_out, OP4);
  not not_46 (not_46_out, OP5);
  not not_47 (not_47_out, F2);
  not not_48 (not_48_out, F3);
  not not_49 (not_49_out, F4);
  not not_50 (not_50_out, F5);
  not not_51 (not_51_out, OP0);
  not not_52 (not_52_out, OP1);
  not not_53 (not_53_out, OP2);
  not not_54 (not_54_out, OP4);
  not not_55 (not_55_out, OP5);
  not not_56 (not_56_out, F2);
  not not_57 (not_57_out, F4);
  not not_58 (not_58_out, OP0);
  not not_59 (not_59_out, OP1);
  not not_60 (not_60_out, OP2);
  not not_61 (not_61_out, OP4);
  not not_62 (not_62_out, OP5);
  not not_63 (not_63_out, F3);
  not not_64 (not_64_out, F4);
  not not_65 (not_65_out, OP0);
  not not_66 (not_66_out, OP4);
  not not_67 (not_67_out, OP5);
  not not_68 (not_68_out, OP1);
  not not_69 (not_69_out, OP4);
  not not_70 (not_70_out, OP5);
  not not_71 (not_71_out, OP2);
  not not_72 (not_72_out, OP4);
  not not_73 (not_73_out, OP5);
  not not_74 (not_74_out, OP0);
  not not_75 (not_75_out, OP1);
  not not_76 (not_76_out, OP3);
  not not_77 (not_77_out, OP4);
  not not_78 (not_78_out, OP2);
  not not_79 (not_79_out, OP3);
  not not_80 (not_80_out, OP4);
  not not_81 (not_81_out, OP0);
  not not_82 (not_82_out, OP1);
  not not_83 (not_83_out, OP2);
  not not_84 (not_84_out, OP3);
  not not_85 (not_85_out, OP4);
  not not_86 (not_86_out, OP5);
  not not_87 (not_87_out, F0);
  not not_88 (not_88_out, F1);
  not not_89 (not_89_out, F4);
  not not_90 (not_90_out, F5);
  not not_91 (not_91_out, OP2);
  not not_92 (not_92_out, OP4);
  not not_93 (not_93_out, OP5);
  not not_94 (not_94_out, OP0);
  not not_95 (not_95_out, OP1);
  not not_96 (not_96_out, OP3);
  not not_97 (not_97_out, OP4);
  not not_98 (not_98_out, OP2);
  not not_99 (not_99_out, OP4);
  not not_100 (not_100_out, OP0);
  not not_101 (not_101_out, OP1);
  not not_102 (not_102_out, OP2);
  not not_103 (not_103_out, OP3);
  not not_104 (not_104_out, OP4);
  not not_105 (not_105_out, OP5);
  not not_106 (not_106_out, F0);
  not not_107 (not_107_out, F2);
  not not_108 (not_108_out, F3);
  not not_109 (not_109_out, F4);
  not not_110 (not_110_out, OP0);
  not not_111 (not_111_out, OP1);
  not not_112 (not_112_out, OP2);
  not not_113 (not_113_out, OP3);
  not not_114 (not_114_out, OP4);
  not not_115 (not_115_out, OP5);
  not not_116 (not_116_out, F1);
  not not_117 (not_117_out, F3);
  not not_118 (not_118_out, F4);
  not not_119 (not_119_out, OP0);
  not not_120 (not_120_out, OP1);
  not not_121 (not_121_out, OP2);
  not not_122 (not_122_out, OP3);
  not not_123 (not_123_out, OP4);
  not not_124 (not_124_out, OP5);
  not not_125 (not_125_out, F2);
  not not_126 (not_126_out, F3);
  not not_127 (not_127_out, F4);
  not not_128 (not_128_out, F5);
  not not_129 (not_129_out, OP0);
  not not_130 (not_130_out, OP1);
  not not_131 (not_131_out, OP2);
  not not_132 (not_132_out, OP3);
  not not_133 (not_133_out, OP4);
  not not_134 (not_134_out, OP5);
  not not_135 (not_135_out, F2);
  not not_136 (not_136_out, F4);
  not not_137 (not_137_out, OP0);
  not not_138 (not_138_out, OP1);
  not not_139 (not_139_out, OP2);
  not not_140 (not_140_out, OP3);
  not not_141 (not_141_out, OP4);
  not not_142 (not_142_out, OP5);
  not not_143 (not_143_out, F3);
  not not_144 (not_144_out, F4);
  not not_145 (not_145_out, OP0);
  not not_146 (not_146_out, OP1);
  not not_147 (not_147_out, OP3);
  not not_148 (not_148_out, OP4);
  not not_149 (not_149_out, OP5);
  not not_150 (not_150_out, OP1);
  not not_151 (not_151_out, OP3);
  not not_152 (not_152_out, OP4);
  not not_153 (not_153_out, OP5);
  not not_154 (not_154_out, OP0);
  not not_155 (not_155_out, OP1);
  not not_156 (not_156_out, OP2);
  not not_157 (not_157_out, OP3);
  not not_158 (not_158_out, OP4);
  not not_159 (not_159_out, OP5);
  not not_160 (not_160_out, F0);
  not not_161 (not_161_out, F1);
  not not_162 (not_162_out, F2);
  not not_163 (not_163_out, F4);
  not not_164 (not_164_out, F5);
  not not_165 (not_165_out, OP0);
  not not_166 (not_166_out, OP2);
  not not_167 (not_167_out, OP3);
  not not_168 (not_168_out, OP4);
  not not_169 (not_169_out, OP5);
  not not_170 (not_170_out, F0);
  not not_171 (not_171_out, F1);
  not not_172 (not_172_out, F2);
  not not_173 (not_173_out, F4);
  not not_174 (not_174_out, F5);
  not not_175 (not_175_out, OP2);
  not not_176 (not_176_out, OP3);
  not not_177 (not_177_out, OP4);
  not not_178 (not_178_out, OP5);
  not not_179 (not_179_out, OP2);
  not not_180 (not_180_out, OP3);
  not not_181 (not_181_out, OP4);
  not not_182 (not_182_out, OP5);
  not not_183 (not_183_out, OP0);
  not not_184 (not_184_out, OP3);
  not not_185 (not_185_out, OP4);
  not not_186 (not_186_out, OP5);
  not not_187 (not_187_out, OP0);
  not not_188 (not_188_out, OP1);
  not not_189 (not_189_out, OP3);
  not not_190 (not_190_out, OP4);
  not not_191 (not_191_out, OP5);
  not not_192 (not_192_out, OP3);
  not not_193 (not_193_out, OP2);
  not not_194 (not_194_out, OP1);
  not not_195 (not_195_out, OP0);
  not not_196 (not_196_out, F5);
  not not_197 (not_197_out, F2);
  not not_198 (not_198_out, F1);
  not not_199 (not_199_out, F0);
  and and_1 (and_1_out, not_1_out, not_2_out, OP2, not_3_out, not_4_out, OP5);
  and and_2 (and_2_out, OP0, OP1, not_5_out, not_6_out, not_7_out, OP5);
  and and_3 (MemWrite, OP0, OP1, not_8_out, OP3, not_9_out, OP5);
  and and_4 (and_4_out, not_10_out, OP3, not_11_out, not_12_out);
  and and_5 (and_5_out, not_13_out, OP3, not_14_out, not_15_out);
  and and_6 (and_6_out, not_16_out, OP3, not_17_out, not_18_out);
  and and_7 (and_7_out, not_19_out, not_20_out, OP2, not_21_out, not_22_out, OP5);
  and and_8 (and_8_out, OP0, OP1, not_23_out, not_24_out, OP5);
  and and_9 (and_9_out, not_25_out, not_26_out, not_27_out, not_28_out, not_29_out, not_30_out, not_31_out, not_32_out, not_33_out);
  and and_10 (and_10_out, not_34_out, not_35_out, not_36_out, not_37_out, not_38_out, not_39_out, not_40_out, not_41_out, F5);
  and and_11 (and_11_out, not_42_out, not_43_out, not_44_out, not_45_out, not_46_out, F1, not_47_out, not_48_out, not_49_out, not_50_out);
  and and_12 (and_12_out, not_51_out, not_52_out, not_53_out, not_54_out, not_55_out, F1, not_56_out, F3, not_57_out, F5);
  and and_13 (and_13_out, not_58_out, not_59_out, not_60_out, not_61_out, not_62_out, F0, F2, not_63_out, not_64_out, F5);
  and and_14 (and_14_out, not_65_out, OP3, not_66_out, not_67_out);
  and and_15 (and_15_out, not_68_out, OP3, not_69_out, not_70_out);
  and and_16 (and_16_out, not_71_out, OP3, not_72_out, not_73_out);
  and and_17 (and_17_out, not_74_out, not_75_out, OP2, not_76_out, not_77_out, OP5);
  and and_18 (and_18_out, OP0, OP1, not_78_out, not_79_out, not_80_out);
  and and_19 (SysCALL, not_81_out, not_82_out, not_83_out, not_84_out, not_85_out, not_86_out, not_87_out, not_88_out, F2, F3, not_89_out, not_90_out);
  and and_20 (and_20_out, not_91_out, OP3, not_92_out, not_93_out);
  and and_21 (and_21_out, not_94_out, not_95_out, OP2, not_96_out, not_97_out, OP5);
  and and_22 (and_22_out, OP0, OP1, not_98_out, not_99_out, OP5);
  and and_23 (and_23_out, not_100_out, not_101_out, not_102_out, not_103_out, not_104_out, not_105_out, not_106_out, not_107_out, not_108_out, not_109_out);
  and and_24 (and_24_out, not_110_out, not_111_out, not_112_out, not_113_out, not_114_out, not_115_out, not_116_out, not_117_out, not_118_out, F5);
  and and_25 (and_25_out, not_119_out, not_120_out, not_121_out, not_122_out, not_123_out, not_124_out, F1, not_125_out, not_126_out, not_127_out, not_128_out);
  and and_26 (and_26_out, not_129_out, not_130_out, not_131_out, not_132_out, not_133_out, not_134_out, F1, not_135_out, F3, not_136_out, F5);
  and and_27 (and_27_out, not_137_out, not_138_out, not_139_out, not_140_out, not_141_out, not_142_out, F0, F2, not_143_out, not_144_out, F5);
  and and_28 (BEQ, not_145_out, not_146_out, OP2, not_147_out, not_148_out, not_149_out);
  and and_29 (BNE, OP0, not_150_out, OP2, not_151_out, not_152_out, not_153_out);
  and and_30 (JR, not_154_out, not_155_out, not_156_out, not_157_out, not_158_out, not_159_out, not_160_out, not_161_out, not_162_out, F3, not_163_out, not_164_out);
  and and_31 (and_31_out, not_165_out, not_166_out, not_167_out, not_168_out, not_169_out, not_170_out, not_171_out, not_172_out, F3, not_173_out, not_174_out);
  and and_32 (and_32_out, OP1, not_175_out, not_176_out, not_177_out, not_178_out);
  and and_33 (JAL, OP0, OP1, not_179_out, not_180_out, not_181_out, not_182_out);
  and and_34 (BLEZ, not_183_out, OP1, OP2, not_184_out, not_185_out, not_186_out);
  and and_35 (LBU, not_187_out, not_188_out, OP2, not_189_out, not_190_out, OP5);
  and and_36 (ERET, not_191_out, OP4, not_192_out, not_193_out, not_194_out, not_195_out, not_196_out, F4, F3, not_197_out, not_198_out, not_199_out);
  or or_1 (MemToReg, and_1_out, and_2_out);
  or or_2 (ALU_SRC, and_4_out, and_5_out, and_6_out, and_7_out, and_8_out);
  or or_3 (RegWrite, and_9_out, and_10_out, and_11_out, and_12_out, and_13_out, and_14_out, and_15_out, and_16_out, and_17_out, and_18_out);
  or or_4 (SignedExt, and_20_out, and_21_out, and_22_out);
  or or_5 (RegDst, and_23_out, and_24_out, and_25_out, and_26_out, and_27_out);
  or or_6 (JUMP, and_31_out, and_32_out);
endmodule

// ALU
module MIPS_ALU (
  input  [4:0] shamt,
  input  [31:0] X,
  input  [31:0] Y,
  input  [3:0] AluOP,
  output Equal,
  output [31:0] Result,
  output [31:0] Result_2
);

  wire [0:0] comparator_1_lt, comparator_2_lt;
  wire [31:0] adder_1_out, AND_out, divider_1_out, divider_1_rem, multiplier_1_cout, multiplier_1_out,
       NOR_out, OR_out, shifter_1_out, shifter_2_out, shifter_3_out, subtractor_1_out, XOR_out;

  assign AND_out = X & Y;  // AND_Gate AND, 32 bits wide
  assign OR_out = X | Y;  // OR_Gate OR, 32 bits wide
  Shifter #(.width(32), .shift("ll")) shifter_1 (.in(Y), .\dist (shamt), .out(shifter_1_out));
  Shifter #(.width(32), .shift("ar")) shifter_2 (.in(Y), .\dist (shamt), .out(shifter_2_out));
  Shifter #(.width(32), .shift("lr")) shifter_3 (.in(Y), .\dist (shamt), .out(shifter_3_out));
  Multiplier #(.width(32)) multiplier_1 (.a(X), .b(Y), .out(multiplier_1_out), .cout(multiplier_1_cout));  // open: cin
  Divider #(.width(32)) divider_1 (.a(X), .b(Y), .out(divider_1_out), .rem(divider_1_rem));  // open: upper
  Adder #(.width(32)) adder_1 (.a(X), .b(Y), .out(adder_1_out));  // open: cin, cout
  Subtractor #(.width(32)) subtractor_1 (.a(X), .b(Y), .out(subtractor_1_out));  // open: bin, bout
  assign XOR_out = X ^ Y;  // XOR_Gate XOR, 32 bits wide
  assign NOR_out = ~(X | Y);  // NOR_Gate NOR, 32 bits wide
  Comparator #(.width(32), .mode("twosComplement")) comparator_1 (
    .a(X), .b(Y), .eq(Equal), .lt(comparator_1_lt[0]));  // open: gt
  Comparator #(.width(32), .mode("unsigned")) comparator_2 (.a(X), .b(Y), .lt(comparator_2_lt[0]));  // open: gt, eq
  Multiplexer #(.select(4), .width(32), .disabled("Z"), .enable("false")) multiplexer_1 (
    .in0(shifter_1_out), .in1(shifter_2_out), .in2(shifter_3_out), .in3(multiplier_1_out),
    .in4(divider_1_out), .in5(adder_1_out), .in6(subtractor_1_out), .in7(AND_out), .in8(OR_out),
    .in9(XOR_out), .in10(NOR_out), .in11({{31{1'b0}}, comparator_1_lt[0]}),
    .in12({{31{1'b0}}, comparator_2_lt[0]}), .in13({32{1'b0}}), .in14({32{1'b0}}), .in15({32{1'b0}}),
    .out(Result), .sel(AluOP));
  Multiplexer #(.select(4), .width(32), .disabled("Z"), .enable("false")) multiplexer_2 (
    .in0({32{1'b0}}), .in1({32{1'b0}}), .in2({32{1'b0}}), .in3(multiplier_1_cout), .in4(divider_1_rem),
    .in5({32{1'b0}}), .in6({32{1'b0}}), .in7({32{1'b0}}), .in8({32{1'b0}}), .in9({32{1'b0}}),
    .in10({32{1'b0}}), .in11({32{1'b0}}), .in12({32{1'b0}}), .in13({32{1'b0}}), .in14({32{1'b0}}),
    .in15({32{1'b0}}), .out(Result_2), .sel(AluOP));
  Comparator #(.width(32), .mode("twosComplement")) comparator_3 (
    .a({32{1'b0}}), .b(32'h80000000));  // open: gt, eq, lt

  // Other names for the same wires on the sheet: Result2[31:0] = Result_2; S[3:0] = AluOP

  // Notes on the sheet:
  //   不要改变此引脚区域内容，也不要改变ALU封装形式
  //   输入引脚
  //   输出引脚
endmodule

module MIPS_Regifile (
  input  [31:0] Din,
  input  Clk,
  input  WE,
  input  [4:0] R1_num,
  input  [4:0] W_num,
  input  [4:0] R2_num,
  output [31:0] R1,
  output [31:0] R2
);

  // RegisterFile registerfile_1: pin names not known; wires that end beside it: Din, Clk, WE, W_num, R1_num, R2_num, R1, R2
endmodule

module \理想流水线  (
  output RegWrite,
  output MemWrite,
  output [31:0] IF_PC,
  output [31:0] ID_PC,
  output [31:0] EX_PC,
  output [31:0] M_PC,
  output [31:0] WB_PC,
  output [31:0] RDin,
  output [31:0] MDin,
  output [31:0] LedData
);

  wire CLK, clock_1_out, clock_2_out, comparator_1_eq, comparator_1_lt, d_ff_1_q, Go, IR1, IR2, IR3,
       nand_1_out, RST, W1, W2, W3;
  wire [12:0] CNT_num;
  wire [15:0] \LoadUse次数 , \总周期数 , \插入气泡数 , \无条件分支数 , \条件分支成功数 ;
  wire [31:0] EX_IR, ID_IR, IF_IR, MEM_IR, WB_IR;

  Button \u_总复位  (.out(RST));
  Button _1 (.out(IR1));
  Button _2 (.out(IR2));
  Button _3 (.out(IR3));
  // Probe on \总周期数 
  // Probe on \总周期数 
  Button \u_继续运行  (.out(Go));
  LED #(.active("true")) led_1 (.in(W1));
  LED #(.active("true")) led_2 (.in(W2));
  LED #(.active("true")) led_3 (.in(W3));
  Hex_Digit_Display hex_digit_display_1 (.value(LedData[31:28]));  // open: dp
  // Probe on IF_PC[19:0]
  // Mips_Probe mips_probe_1: pin names not known; wires that end beside it: IF_IR
  Hex_Digit_Display hex_digit_display_2 (.value(LedData[23:20]));  // open: dp
  Hex_Digit_Display hex_digit_display_3 (.value(LedData[27:24]));  // open: dp
  // Probe on ID_PC[19:0]
  // Mips_Probe mips_probe_2: pin names not known; wires that end beside it: ID_IR
  Hex_Digit_Display hex_digit_display_4 (.value(LedData[19:16]));  // open: dp
  Hex_Digit_Display hex_digit_display_5 (.value(LedData[15:12]));  // open: dp
  Hex_Digit_Display hex_digit_display_6 (.value(LedData[11:8]));  // open: dp
  Hex_Digit_Display hex_digit_display_7 (.value(LedData[7:4]));  // open: dp
  Clock #(.highDuration(1), .lowDuration(1)) clock_1 (.out(clock_1_out));
  // Probe on EX_PC[19:0]
  // Mips_Probe mips_probe_3: pin names not known; wires that end beside it: clock_1_out, EX_IR, CLK
  Hex_Digit_Display hex_digit_display_8 (.value(LedData[3:0]));  // open: dp
  // Probe on \总周期数 
  // Probe on M_PC[19:0]
  // Mips_Probe mips_probe_4: pin names not known; wires that end beside it: MEM_IR
  // Probe on \总周期数 
  // Probe on \无条件分支数 
  // Probe on \条件分支成功数 
  // Probe on \插入气泡数 
  // Probe on \LoadUse次数 
  // Probe on IF_PC[11:0]
  // Probe on WB_PC[19:0]
  // Mips_Probe mips_probe_5: pin names not known; wires that end beside it: WB_IR
  // Probe on EX_PC[11:0]
  // Probe on ID_PC[11:0]
  // Probe on M_PC[11:0]
  D_Flip_Flop #(.trigger("high"), .Pre_Clr_Positions("LEGACY"), .NegatePresetClear("false"), .enable("true"), .NewFFLayout("false")) d_ff_1 (.Q(d_ff_1_q));  // open: clk, D, Qn, preset, en, reset
  // Probe on 13'hc
  // Probe on WB_PC[11:0]
  Comparator #(.width(13), .mode("twosComplement")) comparator_1 (
    .a(CNT_num), .b(13'hc), .eq(comparator_1_eq), .lt(comparator_1_lt));  // open: gt
  Clock #(.highDuration(1), .lowDuration(1)) clock_2 (.out(clock_2_out));
  nand nand_1 (nand_1_out, d_ff_1_q, comparator_1_eq);
  Counter #(.width(13), .max('h1fff), .ongoal("stay"), .trigger("rising"), .behavior("old")) counter_1 (
    .count(comparator_1_lt), .Q(CNT_num), .clk(clock_2_out));  // open: load, D, carry, clr, preset
  assign CLK = nand_1_out ? clock_2_out : 1'bz;  // Controlled_Buffer controlled_buffer_1
  Pull_Resistor #(.pull(1)) pull_resistor_1 (.node(CLK));

  // Other names for the same wires on the sheet: MEM_PC[31:0] = M_PC

  // Notes on the sheet:
  //   中断源
  //   时空图监测，可删除
  //   中断等待指示
  //   数码管输出
  //   控制位
  //   流水调试日志用
  //   暂停节拍，不能为0
  //   戳工具置1进入计数暂停模式，ctrl+k时钟自动运行到对应节拍暂停
  //   ctrl+k关闭时钟连续运行，将控制位置零，进入单步调试模式调试
  //   用这个时钟源需要去掉电路中的其他时钟源
  //   可计数暂停的时钟源
  //   为方便自动评测，需要输出流水线各段保存的PC值，注意是PC不是PC+4，另外ID段寄存器写入信息，Mem段内存写入信息也要输出
endmodule

module \气泡流水线  (
  output RegWrite,
  output MemWrite,
  output [31:0] IF_PC,
  output [31:0] ID_PC,
  output [31:0] EX_PC,
  output [31:0] M_PC,
  output [31:0] WB_PC,
  output [31:0] RDin,
  output [31:0] MDin,
  output [31:0] LedData
);

  wire CLK, clock_2_out, comparator_1_eq, comparator_1_lt, d_ff_1_q, Go, IR1, IR2, IR3, nand_1_out, RST, W1,
       W2, W3;
  wire [12:0] CNT_num;
  wire [15:0] \LoadUse次数 , \总周期数 , \插入气泡数 , \无条件分支数 , \条件分支成功数 ;
  wire [31:0] EX_IR, ID_IR, IF_IR, MEM_IR, WB_IR;

  Button \u_总复位  (.out(RST));
  Button _1 (.out(IR1));
  Button _2 (.out(IR2));
  Button _3 (.out(IR3));
  // Probe on \总周期数 
  // Probe on \总周期数 
  Button \u_继续运行  (.out(Go));
  LED #(.active("true")) led_1 (.in(W1));
  LED #(.active("true")) led_2 (.in(W2));
  LED #(.active("true")) led_3 (.in(W3));
  Hex_Digit_Display hex_digit_display_1 (.value(LedData[31:28]));  // open: dp
  // Probe on IF_PC[19:0]
  // Mips_Probe mips_probe_1: pin names not known; wires that end beside it: IF_IR
  Hex_Digit_Display hex_digit_display_2 (.value(LedData[27:24]));  // open: dp
  Hex_Digit_Display hex_digit_display_3 (.value(LedData[23:20]));  // open: dp
  // Probe on ID_PC[19:0]
  // Mips_Probe mips_probe_2: pin names not known; wires that end beside it: ID_IR
  Hex_Digit_Display hex_digit_display_4 (.value(LedData[19:16]));  // open: dp
  Hex_Digit_Display hex_digit_display_5 (.value(LedData[15:12]));  // open: dp
  Hex_Digit_Display hex_digit_display_6 (.value(LedData[7:4]));  // open: dp
  Hex_Digit_Display hex_digit_display_7 (.value(LedData[11:8]));  // open: dp
  Clock #(.highDuration(1), .lowDuration(1)) clock_1 (.out(CLK));
  // Probe on EX_PC[19:0]
  // Mips_Probe mips_probe_3: pin names not known; wires that end beside it: EX_IR
  Hex_Digit_Display hex_digit_display_8 (.value(LedData[3:0]));  // open: dp
  // Probe on \总周期数 
  // Probe on M_PC[19:0]
  // Mips_Probe mips_probe_4: pin names not known; wires that end beside it: MEM_IR
  // Probe on \总周期数 
  // Probe on \无条件分支数 
  // Probe on \条件分支成功数 
  // Probe on \插入气泡数 
  // Probe on \LoadUse次数 
  // Probe on IF_PC[11:0]
  // Probe on WB_PC[19:0]
  // Mips_Probe mips_probe_5: pin names not known; wires that end beside it: WB_IR
  // Probe on EX_PC[11:0]
  // Probe on ID_PC[11:0]
  // Probe on M_PC[11:0]
  D_Flip_Flop #(.trigger("high"), .Pre_Clr_Positions("LEGACY"), .NegatePresetClear("false"), .enable("true"), .NewFFLayout("false")) d_ff_1 (.Q(d_ff_1_q));  // open: clk, D, Qn, preset, en, reset
  // Probe on 13'hc
  // Probe on WB_PC[11:0]
  Comparator #(.width(13), .mode("twosComplement")) comparator_1 (
    .a(CNT_num), .b(13'hc), .eq(comparator_1_eq), .lt(comparator_1_lt));  // open: gt
  Clock #(.highDuration(1), .lowDuration(1)) clock_2 (.out(clock_2_out));
  nand nand_1 (nand_1_out, d_ff_1_q, comparator_1_eq);
  Counter #(.width(13), .max('h1fff), .ongoal("stay"), .trigger("rising"), .behavior("old")) counter_1 (
    .count(comparator_1_lt), .Q(CNT_num), .clk(clock_2_out));  // open: load, D, carry, clr, preset
  assign CLK = nand_1_out ? clock_2_out : 1'bz;  // Controlled_Buffer controlled_buffer_1
  Pull_Resistor #(.pull(1)) pull_resistor_1 (.node(CLK));

  // Other names for the same wires on the sheet: MEM_PC[31:0] = M_PC

  // Notes on the sheet:
  //   中断源
  //   时空图监测，可删除
  //   中断等待指示
  //   数码管输出
  //   控制位
  //   流水调试日志用
  //   暂停节拍，不能为0
  //   戳工具置1进入计数暂停模式，ctrl+k时钟自动运行到对应节拍暂停
  //   ctrl+k关闭时钟连续运行，将控制位置零，进入单步调试模式调试
  //   可计数暂停的时钟源
  //   为方便自动评测，需要输出流水线各段保存的PC值，注意是PC不是PC+4，另外ID段寄存器写入信息，Mem段内存写入信息也要输出
endmodule

module \重定向流水线  (
  output RegWrite,
  output MemWrite,
  output [31:0] IF_PC,
  output [31:0] ID_PC,
  output [31:0] EX_PC,
  output [31:0] M_PC,
  output [31:0] WB_PC,
  output [31:0] RDin,
  output [31:0] MDin,
  output [31:0] LedData
);

  wire CLK, clock_2_out, comparator_1_eq, comparator_1_lt, d_ff_1_q, Go, IR1, IR2, IR3, nand_1_out, RST, W1,
       W2, W3;
  wire [12:0] CNT_num;
  wire [15:0] \LoadUse次数 , \总周期数 , \插入气泡数 , \无条件分支数 , \条件分支成功数 ;
  wire [31:0] EX_IR, ID_IR, IF_IR, MEM_IR, WB_IR;

  Button \u_总复位  (.out(RST));
  Button _1 (.out(IR1));
  Button _2 (.out(IR2));
  Button _3 (.out(IR3));
  // Probe on \总周期数 
  // Probe on \总周期数 
  Button \u_继续运行  (.out(Go));
  LED #(.active("true")) led_1 (.in(W1));
  LED #(.active("true")) led_2 (.in(W2));
  LED #(.active("true")) led_3 (.in(W3));
  Hex_Digit_Display hex_digit_display_1 (.value(LedData[31:28]));  // open: dp
  // Probe on IF_PC[19:0]
  // Mips_Probe mips_probe_1: pin names not known; wires that end beside it: IF_IR
  Hex_Digit_Display hex_digit_display_2 (.value(LedData[27:24]));  // open: dp
  Hex_Digit_Display hex_digit_display_3 (.value(LedData[23:20]));  // open: dp
  // Probe on ID_PC[19:0]
  // Mips_Probe mips_probe_2: pin names not known; wires that end beside it: ID_IR
  Hex_Digit_Display hex_digit_display_4 (.value(LedData[19:16]));  // open: dp
  Hex_Digit_Display hex_digit_display_5 (.value(LedData[15:12]));  // open: dp
  Hex_Digit_Display hex_digit_display_6 (.value(LedData[7:4]));  // open: dp
  Hex_Digit_Display hex_digit_display_7 (.value(LedData[11:8]));  // open: dp
  Clock #(.highDuration(1), .lowDuration(1)) clock_1 (.out(CLK));
  // Probe on EX_PC[19:0]
  // Mips_Probe mips_probe_3: pin names not known; wires that end beside it: EX_IR
  Hex_Digit_Display hex_digit_display_8 (.value(LedData[3:0]));  // open: dp
  // Probe on \总周期数 
  // Probe on M_PC[19:0]
  // Mips_Probe mips_probe_4: pin names not known; wires that end beside it: MEM_IR
  // Probe on \总周期数 
  // Probe on \无条件分支数 
  // Probe on \条件分支成功数 
  // Probe on \插入气泡数 
  // Probe on \LoadUse次数 
  // Probe on IF_PC[11:0]
  // Probe on WB_PC[19:0]
  // Mips_Probe mips_probe_5: pin names not known; wires that end beside it: WB_IR
  // Probe on EX_PC[11:0]
  // Probe on ID_PC[11:0]
  // Probe on M_PC[11:0]
  D_Flip_Flop #(.trigger("high"), .Pre_Clr_Positions("LEGACY"), .NegatePresetClear("false"), .enable("true"), .NewFFLayout("false")) d_ff_1 (.Q(d_ff_1_q));  // open: clk, D, Qn, preset, en, reset
  // Probe on 13'hc
  // Probe on WB_PC[11:0]
  Comparator #(.width(13), .mode("twosComplement")) comparator_1 (
    .a(CNT_num), .b(13'hc), .eq(comparator_1_eq), .lt(comparator_1_lt));  // open: gt
  Clock #(.highDuration(1), .lowDuration(1)) clock_2 (.out(clock_2_out));
  nand nand_1 (nand_1_out, d_ff_1_q, comparator_1_eq);
  Counter #(.width(13), .max('h1fff), .ongoal("stay"), .trigger("rising"), .behavior("old")) counter_1 (
    .count(comparator_1_lt), .Q(CNT_num), .clk(clock_2_out));  // open: load, D, carry, clr, preset
  assign CLK = nand_1_out ? clock_2_out : 1'bz;  // Controlled_Buffer controlled_buffer_1
  Pull_Resistor #(.pull(1)) pull_resistor_1 (.node(CLK));

  // Other names for the same wires on the sheet: MEM_PC[31:0] = M_PC

  // Notes on the sheet:
  //   中断源
  //   时空图监测，可删除
  //   中断等待指示
  //   数码管输出
  //   控制位
  //   流水调试日志用
  //   暂停节拍，不能为0
  //   戳工具置1进入计数暂停模式，ctrl+k时钟自动运行到对应节拍暂停
  //   ctrl+k关闭时钟连续运行，将控制位置零，进入单步调试模式调试
  //   可计数暂停的时钟源
  //   为方便自动评测，需要输出流水线各段保存的PC值，注意是PC不是PC+4，另外ID段寄存器写入信息，Mem段内存写入信息也要输出
endmodule

module \中断按键参考电路  (
  input  \同步清零信号 ,
  output \与中断屏蔽位与 
);

  wire \_1号中断_out , and_1_out, clock_1_out, d_ff_1_q, or_1_out, or_2_out;

  Clock #(.highDuration(1), .lowDuration(1)) clock_1 (.out(clock_1_out));
  Button \_1号中断  (.out(\_1号中断_out ));
  LED #(.active("true")) \_1号中断等待指示灯  (.in(or_1_out));
  or or_1 (or_1_out, \与中断屏蔽位与 , d_ff_1_q);
  D_Flip_Flop #(.trigger("rising"), .Pre_Clr_Positions("LEGACY"), .NegatePresetClear("false"), .enable("true"), .NewFFLayout("false")) d_ff_1 (
    .clk(\_1号中断_out ), .D(1'b1), .Q(d_ff_1_q), .reset(\与中断屏蔽位与 ));  // open: Qn, preset, en
  or or_2 (or_2_out, d_ff_1_q, \与中断屏蔽位与 );
  and and_1 (and_1_out, or_2_out, ~\同步清零信号 );  // AND_Gate
  D_Flip_Flop #(.trigger("rising"), .Pre_Clr_Positions("LEGACY"), .NegatePresetClear("false"), .enable("true"), .NewFFLayout("false")) IR1 (
    .clk(clock_1_out), .D(and_1_out), .Q(\与中断屏蔽位与 ));  // open: Qn, preset, en, reset

  // Notes on the sheet:
  //   中断信号采样参考电路
  //   Reset 
endmodule

module \单周期MIPS_多级中断  (
  input  IR1,
  input  IR2,
  input  IR3,
  output RegWrite,
  output MemWrite,
  output [31:0] PC,
  output [31:0] IR,
  output [31:0] RDin,
  output [31:0] MDin,
  output [31:0] LedData
);

  wire CLK, comparator_1_eq, comparator_2_eq, comparator_3_eq, comparator_4_eq, comparator_5_eq, Go, IR1_t,
       IR2_t, IR3_t, IRA, IRB, IRC, or_1_out, or_2_out, W1, W2, W3;
  wire [15:0] \总周期数 ;

  Clock #(.highDuration(1), .lowDuration(1)) clock_1 (.out(CLK));
  Button _1 ();  // open: out
  Button _2 ();  // open: out
  Button _3 ();  // open: out
  Button \u_继续运行  (.out(Go));
  LED #(.active("true")) led_1 (.in(W1));
  LED #(.active("true")) led_2 (.in(W2));
  LED #(.active("true")) led_3 (.in(W3));
  Hex_Digit_Display hex_digit_display_1 (.value(LedData[31:28]));  // open: dp
  Comparator #(.width(16), .mode("twosComplement")) comparator_1 (
    .a(\总周期数 ), .b(16'h7), .eq(comparator_1_eq));  // open: gt, lt
  Comparator #(.width(16), .mode("twosComplement")) comparator_2 (
    .a(\总周期数 ), .b(16'h241), .eq(comparator_2_eq));  // open: gt, lt
  Hex_Digit_Display hex_digit_display_2 (.value(LedData[27:24]));  // open: dp
  Hex_Digit_Display hex_digit_display_3 (.value(LedData[23:20]));  // open: dp
  Comparator #(.width(16), .mode("twosComplement")) comparator_3 (
    .a(16'h258), .b(\总周期数 ), .eq(comparator_3_eq));  // open: gt, lt
  or or_1 (or_1_out, comparator_3_eq, comparator_4_eq);
  Comparator #(.width(16), .mode("twosComplement")) comparator_4 (
    .a(\总周期数 ), .b(16'h1), .eq(comparator_4_eq));  // open: gt, lt
  Comparator #(.width(16), .mode("twosComplement")) comparator_5 (
    .a(\总周期数 ), .b(16'h4), .eq(comparator_5_eq));  // open: gt, lt
  or or_2 (or_2_out, comparator_1_eq, comparator_2_eq);
  Hex_Digit_Display hex_digit_display_4 (.value(LedData[15:12]));  // open: dp
  Hex_Digit_Display hex_digit_display_5 (.value(LedData[19:16]));  // open: dp
  Pull_Resistor #(.pull(0)) pull_resistor_1 (.node(IRA));
  assign IRA = or_1_out ? ~CLK : 1'bz;  // Controlled_Inverter controlled_inverter_1
  Pull_Resistor #(.pull(0)) pull_resistor_2 (.node(IRB));
  assign IRB = comparator_5_eq ? ~CLK : 1'bz;  // Controlled_Inverter controlled_inverter_2
  Pull_Resistor #(.pull(0)) pull_resistor_3 (.node(IRC));
  assign IRC = or_2_out ? ~CLK : 1'bz;  // Controlled_Inverter controlled_inverter_3
  Hex_Digit_Display hex_digit_display_6 (.value(LedData[11:8]));  // open: dp
  Hex_Digit_Display hex_digit_display_7 (.value(LedData[7:4]));  // open: dp
  // Probe on \总周期数 
  Hex_Digit_Display hex_digit_display_8 (.value(LedData[3:0]));  // open: dp
  or or_3 (IR1_t, IR1, IRA);
  or or_4 (IR2_t, IR2, IRB);
  or or_5 (IR3_t, IR3, IRC);

  // Notes on the sheet:
  //   中断源
  //   中断等待指示
  //   总复位信号应将除ROM以外所有存储组件全部清零
  //   多级中断测试信号模拟器
  //   数码管输出
  //   数码管输出应该用寄存器锁存，否则显示数据只能一闪而过
  //   为方便自动评测，需要输出PC，IR，寄存器堆写如数据RDin
  //   RAM写使能MemWrite、RAM写入数据MDin等信号
endmodule

module \封装正确性测试  (
);

  wire IR1, IR2, IR3, MemW, RegW;
  wire [31:0] EX_PC, ID_PC, IF_PC, IR, LED, MDin, MDinr, MEM_PC, PC, RDin, RDinr, WB_PC;

  \气泡流水线  \u_气泡流水线_1  (
    .RegWrite(RegW), .MemWrite(MemW), .IF_PC(IF_PC), .ID_PC(ID_PC), .EX_PC(EX_PC), .M_PC(MEM_PC),
    .WB_PC(WB_PC), .RDin(RDinr), .MDin(MDinr), .LedData(LED));
  // 单周期MIPS_单级中断 单周期mips_单级中断_1: pin names not known; wires that end beside it: IR1, IR2, IR3, RegW, MemW, PC, IR, RDin, MDin, LED
  \理想流水线  \u_理想流水线_1  (
    .RegWrite(RegW), .MemWrite(MemW), .IF_PC(IF_PC), .ID_PC(ID_PC), .EX_PC(EX_PC), .M_PC(MEM_PC),
    .WB_PC(WB_PC), .RDin(RDinr), .MDin(MDinr), .LedData(LED));
  \重定向流水线  \u_重定向流水线_1  (
    .RegWrite(RegW), .MemWrite(MemW), .IF_PC(IF_PC), .ID_PC(ID_PC), .EX_PC(EX_PC), .M_PC(MEM_PC),
    .WB_PC(WB_PC), .RDin(RDinr), .MDin(MDinr), .LedData(LED));
  \单周期MIPS_多级中断  \u_单周期mips_多级中断_1  (
    .IR1(IR1), .IR2(IR2), .IR3(IR3), .RegWrite(RegW), .MemWrite(MemW), .PC(PC), .IR(IR), .RDin(RDin),
    .MDin(MDin), .LedData(LED));

  // Notes on the sheet:
  //   气泡流水封装测试
  //   单周期+单级中断封装测试
  //   请检查上面封装有无位宽不匹配，引脚标签是否和连接的标签相对应，否则无法在educoder平台上正确测试
  //   理想流水封装测试
  //   重定向流水封装测试
  //   单周期+多级中断封装测试
endmodule

module Result_OutPut (
  input  ERROR,
  input  [11:0] Score,
  output [15:0] O1,
  output [15:0] O1_2,
  output [15:0] O1_3,
  output [15:0] O1_4,
  output [15:0] O1_5,
  output [15:0] O1_6,
  output [15:0] O1_7,
  output [15:0] O1_8,
  output [15:0] O1_9,
  output [15:0] O1_10,
  output [15:0] O1_11,
  output [15:0] O1_12,
  output [15:0] O1_13,
  output [15:0] O1_14,
  output [15:0] O1_15,
  output [15:0] O1_16,
  output [15:0] O1_17,
  output [15:0] O1_18,
  output [15:0] O1_19,
  output [15:0] O1_20,
  output [15:0] O1_21,
  output [15:0] O1_22,
  output [15:0] O1_23,
  output [15:0] O1_24,
  output [15:0] O1_25,
  output [15:0] O1_26,
  output [15:0] O1_27,
  output [15:0] O1_28,
  output [15:0] O1_29,
  output [15:0] O1_30,
  output [15:0] O1_31,
  output [15:0] O1_32
);

  wire comparator_1_eq, comparator_1_lt;
  wire [1:0] Control;

  Comparator #(.width(12), .mode("unsigned")) comparator_1 (
    .a(Score), .b(12'h400), .eq(comparator_1_eq), .lt(comparator_1_lt));  // open: gt
  Priority_Encoder #(.select(2), .disabled("Z")) priority_encoder_1 (
    .in0(comparator_1_lt), .in1(comparator_1_eq), .in2(ERROR), .out(Control));  // open: in3, gs, en_out, en_in
  Multiplexer #(.select(2), .width(16), .disabled("Z"), .enable("false")) multiplexer_1 (
    .in0({16{1'b0}}), .in1({16{1'b0}}), .in2({16{1'b0}}), .out(O1), .sel(Control));  // open: in3
  Multiplexer #(.select(2), .width(16), .disabled("Z"), .enable("false")) multiplexer_2 (
    .in0(16'h100), .in1(16'h1800), .in2(16'h1ff8), .out(O1_2), .sel(Control));  // open: in3
  Multiplexer #(.select(2), .width(16), .disabled("Z"), .enable("false")) multiplexer_3 (
    .in0(16'h300), .in1(16'he00), .in2(16'h8), .out(O1_3), .sel(Control));  // open: in3
  Multiplexer #(.select(2), .width(16), .disabled("Z"), .enable("false")) multiplexer_4 (
    .in0(16'h600), .in1(16'h3c0), .in2(16'h8), .out(O1_4), .sel(Control));  // open: in3
  Multiplexer #(.select(2), .width(16), .disabled("Z"), .enable("false")) multiplexer_5 (
    .in0(16'h600), .in1(16'hf8), .in2(16'h8), .out(O1_5), .sel(Control));  // open: in3
  Multiplexer #(.select(2), .width(16), .disabled("Z"), .enable("false")) multiplexer_6 (
    .in0(16'h300), .in1(16'h3c0), .in2(16'h8), .out(O1_6), .sel(Control));  // open: in3
  Multiplexer #(.select(2), .width(16), .disabled("Z"), .enable("false")) multiplexer_7 (
    .in0(16'h380), .in1(16'he00), .in2({16{1'b0}}), .out(O1_7), .sel(Control));  // open: in3
  Multiplexer #(.select(2), .width(16), .disabled("Z"), .enable("false")) multiplexer_8 (
    .in0(16'h1c0), .in1(16'h3c0), .in2(16'h1ff8), .out(O1_8), .sel(Control));  // open: in3
  Multiplexer #(.select(2), .width(16), .disabled("Z"), .enable("false")) multiplexer_9 (
    .in0(16'h1c0), .in1(16'hf8), .in2(16'h1008), .out(O1_9), .sel(Control));  // open: in3
  Multiplexer #(.select(2), .width(16), .disabled("Z"), .enable("false")) multiplexer_10 (
    .in0(16'h380), .in1(16'h3c0), .in2(16'h1008), .out(O1_10), .sel(Control));  // open: in3
  Multiplexer #(.select(2), .width(16), .disabled("Z"), .enable("false")) multiplexer_11 (
    .in0(16'h780), .in1(16'he00), .in2(16'h1008), .out(O1_11), .sel(Control));  // open: in3
  Multiplexer #(.select(2), .width(16), .disabled("Z"), .enable("false")) multiplexer_12 (
    .in0(16'hf80), .in1(16'h1800), .in2(16'h1ff8), .out(O1_12), .sel(Control));  // open: in3
  Multiplexer #(.select(2), .width(16), .disabled("Z"), .enable("false")) multiplexer_13 (
    .in0(16'h7c0), .in1({16{1'b0}}), .in2({16{1'b0}}), .out(O1_13), .sel(Control));  // open: in3
  Multiplexer #(.select(2), .width(16), .disabled("Z"), .enable("false")) multiplexer_14 (
    .in0(16'h7c0), .in1({16{1'b0}}), .in2(16'h620), .out(O1_14), .sel(Control));  // open: in3
  Multiplexer #(.select(2), .width(16), .disabled("Z"), .enable("false")) multiplexer_15 (
    .in0(16'h3e0), .in1(16'h1008), .in2(16'h930), .out(O1_15), .sel(Control));  // open: in3
  Multiplexer #(.select(2), .width(16), .disabled("Z"), .enable("false")) multiplexer_16 (
    .in0(16'h3e0), .in1(16'h1ff8), .in2(16'h1898), .out(O1_16), .sel(Control));  // open: in3
  Multiplexer #(.select(2), .width(16), .disabled("Z"), .enable("false")) multiplexer_17 (
    .in0(16'h7c0), .in1(16'h1008), .in2(16'h1918), .out(O1_17), .sel(Control));  // open: in3
  Multiplexer #(.select(2), .width(16), .disabled("Z"), .enable("false")) multiplexer_18 (
    .in0(16'h7e0), .in1({16{1'b0}}), .in2(16'hc90), .out(O1_18), .sel(Control));  // open: in3
  Multiplexer #(.select(2), .width(16), .disabled("Z"), .enable("false")) multiplexer_19 (
    .in0(16'hff0), .in1({16{1'b0}}), .in2(16'h460), .out(O1_19), .sel(Control));  // open: in3
  Multiplexer #(.select(2), .width(16), .disabled("Z"), .enable("false")) multiplexer_20 (
    .in0(16'h1ff8), .in1(16'h1ff8), .in2({16{1'b0}}), .out(O1_20), .sel(Control));  // open: in3
  Multiplexer #(.select(2), .width(16), .disabled("Z"), .enable("false")) multiplexer_21 (
    .in0(16'h1e78), .in1(16'he00), .in2(16'h1ff8), .out(O1_21), .sel(Control));  // open: in3
  Multiplexer #(.select(2), .width(16), .disabled("Z"), .enable("false")) multiplexer_22 (
    .in0(16'h1898), .in1(16'h380), .in2(16'h1108), .out(O1_22), .sel(Control));  // open: in3
  Multiplexer #(.select(2), .width(16), .disabled("Z"), .enable("false")) multiplexer_23 (
    .in0(16'h1918), .in1(16'hc0), .in2(16'h1108), .out(O1_23), .sel(Control));  // open: in3
  Multiplexer #(.select(2), .width(16), .disabled("Z"), .enable("false")) multiplexer_24 (
    .in0(16'hcb0), .in1(16'h70), .in2(16'h1108), .out(O1_24), .sel(Control));  // open: in3
  Multiplexer #(.select(2), .width(16), .disabled("Z"), .enable("false")) multiplexer_25 (
    .in0(16'h420), .in1(16'h1ff8), .in2(16'h1108), .out(O1_25), .sel(Control));  // open: in3
  Multiplexer #(.select(2), .width(16), .disabled("Z"), .enable("false")) multiplexer_26 (
    .in0({16{1'b0}}), .in1({16{1'b0}}), .in2({16{1'b0}}), .out(O1_26), .sel(Control));  // open: in3
  Multiplexer #(.select(2), .width(16), .disabled("Z"), .enable("false")) multiplexer_27 (
    .in0({16{1'b0}}), .in1({16{1'b0}}), .in2({16{1'b0}}), .out(O1_27), .sel(Control));  // open: in3
  Multiplexer #(.select(2), .width(16), .disabled("Z"), .enable("false")) multiplexer_28 (
    .in0(16'h180), .in1({16{1'b0}}), .in2({16{1'b0}}), .out(O1_28), .sel(Control));  // open: in3
  Multiplexer #(.select(2), .width(16), .disabled("Z"), .enable("false")) multiplexer_29 (
    .in0(16'h3c0), .in1({16{1'b0}}), .in2({16{1'b0}}), .out(O1_29), .sel(Control));  // open: in3
  Multiplexer #(.select(2), .width(16), .disabled("Z"), .enable("false")) multiplexer_30 (
    .in0(16'h180), .in1(16'h1fc8), .in2(16'h1fc8), .out(O1_30), .sel(Control));  // open: in3
  Multiplexer #(.select(2), .width(16), .disabled("Z"), .enable("false")) multiplexer_31 (
    .in0({16{1'b0}}), .in1({16{1'b0}}), .in2({16{1'b0}}), .out(O1_31), .sel(Control));  // open: in3
  Multiplexer #(.select(2), .width(16), .disabled("Z"), .enable("false")) multiplexer_32 (
    .in0({16{1'b0}}), .in1({16{1'b0}}), .in2({16{1'b0}}), .out(O1_32), .sel(Control));  // open: in3

  // Other names for the same wires on the sheet: R0[15:0] = O1; R1[15:0] = O1_2; R2[15:0] = O1_3; R3[15:0] = O1_4;
  //   R4[15:0] = O1_5; R5[15:0] = O1_6; R6[15:0] = O1_7; R7[15:0] = O1_8; R8[15:0] = O1_9; R9[15:0] = O1_10;
  //   R10[15:0] = O1_11; R11[15:0] = O1_12; R12[15:0] = O1_13; R13[15:0] = O1_14; R14[15:0] = O1_15;
  //   R15[15:0] = O1_16; R16[15:0] = O1_17; R17[15:0] = O1_18; R18[15:0] = O1_19; R19[15:0] = O1_20;
  //   R20[15:0] = O1_21; R21[15:0] = O1_22; R22[15:0] = O1_23; R23[15:0] = O1_24; R24[15:0] = O1_25;
  //   R25[15:0] = O1_26; R26[15:0] = O1_27; R27[15:0] = O1_28; R28[15:0] = O1_29; R29[15:0] = O1_30;
  //   R30[15:0] = O1_31; R31[15:0] = O1_32
endmodule
