// Logisim project cpu24.circ as structural Verilog: 25 circuits, main circuit ◇单周期MIPS
module \单周期MIPS  (
  input  IR1,
  input  IR2,
  input  IR3,
  output RegWrite,
  output MemWrite,
  output [31:0] PC,
  output [31:0] IR,
  output [31:0] RDin,
  output [31:0] MDin,
  output [31:0] LedData
);

  wire AluSrcB, and_1_out, and_2_out, and_3_out, and_4_out, and_5_out, Beq, BLEZ, Bne, CLK, clock_2_out,
       comparator_1_eq, comparator_1_lt, comparator_2_eq, controlled_buffer_1_out, d_ff_1_q, Go, Halt, IR1_t,
       IR2_t, IR3_t, IRA, IRB, IRC, JAL, JMP, JR, LBU, MemToReg, mips_alu_1_equal, nand_1_out, not_1_out,
       not_2_out, not_3_out, not_4_out, or_4_out, PCSrc, RegDst, Reset, SignedExt, SRLV, Syscall, W1, W2, W3;
  wire [3:0] AluOP;
  wire [4:0] multiplexer_2_out, multiplexer_3_out, multiplexer_4_out, multiplexer_5_out, multiplexer_9_out;
  wire [12:0] CNT_num;
  wire [15:0] \总周期数 ;
  wire [31:0] bit_extender_1_out, bit_extender_2_out, mips_alu_1_result, multiplexer_1_out,
       multiplexer_7_out, multiplexer_8_out, multiplexer_10_out, PC_4, PC_imm, PC_rst, ram_1_data,
       shifter_1_out, WriteBackData;

  Clock #(.highDuration(1), .lowDuration(1)) clock_1 (.out(CLK));
  Button _1 (.out(IRA));
  Button _2 (.out(IRB));
  Button _3 (.out(IRC));
  Button \u_继续运行  (.out(Go));
  LED #(.active("true")) led_1 (.in(W1));
  LED #(.active("true")) led_2 (.in(W2));
  LED #(.active("true")) led_3 (.in(W3));
  D_Flip_Flop #(.trigger("high"), .Pre_Clr_Positions("LEGACY"), .NegatePresetClear("false"), .enable("true"), .NewFFLayout("false")) d_ff_1 (.Q(d_ff_1_q));  // open: clk, D, Qn, preset, en, reset
  Hex_Digit_Display hex_digit_display_1 (.value(LedData[31:28]));  // open: dp
  Button button_1 (.out(Reset));
  Multiplexer #(.select(3), .width(32), .disabled("Z"), .enable("false")) multiplexer_1 (
    .in0(PC_4), .in1(PC_imm), .in2({PC[31:28], IR[25:0], 2'b00}), .in6(PC_rst), .out(multiplexer_1_out),
    .sel({JR, JMP, PCSrc}));  // open: in3, in4, in5, in7
  not not_1 (not_1_out, Halt);
  // Probe on 13'hc
  Hex_Digit_Display hex_digit_display_2 (.value(LedData[23:20]));  // open: dp
  Hex_Digit_Display hex_digit_display_3 (.value(LedData[27:24]));  // open: dp
  Register #(.width(32), .trigger("rising"), .Select("low")) u_PC (
    .D(multiplexer_1_out), .en(not_1_out), .Q(PC), .clk(CLK), .clr(Reset));
  Comparator #(.width(13), .mode("twosComplement")) comparator_1 (
    .a(CNT_num), .b(13'hc), .eq(comparator_1_eq), .lt(comparator_1_lt));  // open: gt
  Clock #(.highDuration(1), .lowDuration(1)) clock_2 (.out(clock_2_out));
  Hex_Digit_Display hex_digit_display_4 (.value(LedData[19:16]));  // open: dp
  Hex_Digit_Display hex_digit_display_5 (.value(LedData[15:12]));  // open: dp
  Counter #(.width(16), .max('hffff), .ongoal("wrap"), .trigger("rising"), .behavior("old")) counter_1 (
    .count(not_2_out), .Q(\总周期数 ), .clk(CLK));  // open: load, D, carry, clr, preset
  not not_2 (not_2_out, Halt);
  Adder #(.width(32)) adder_1 (.a(PC), .b(32'h4), .out(PC_4));  // open: cin, cout
  nand nand_1 (nand_1_out, d_ff_1_q, comparator_1_eq);
  Counter #(.width(13), .max('h1fff), .ongoal("stay"), .trigger("rising"), .behavior("old")) counter_2 (
    .count(comparator_1_lt), .Q(CNT_num), .clk(clock_2_out));  // open: load, D, carry, clr, preset
  Hex_Digit_Display hex_digit_display_6 (.value(LedData[7:4]));  // open: dp
  Hex_Digit_Display hex_digit_display_7 (.value(LedData[11:8]));  // open: dp
  // Probe on \总周期数 
  assign controlled_buffer_1_out = nand_1_out ? clock_2_out : 1'bz;  // Controlled_Buffer controlled_buffer_1
  Pull_Resistor #(.pull(1)) pull_resistor_1 (.node(controlled_buffer_1_out));
  Hex_Digit_Display hex_digit_display_8 (.value(LedData[3:0]));  // open: dp
  // Mips_Probe mips_probe_1: pin names not known; wires that end beside it: IR
  ROM #(.addrWidth(10), .dataWidth(32), .Select("high")) rom_1 (.addr(PC[11:2]), .data(IR));
  or or_1 (IR1_t, IR1, IRA);
  \单周期硬布线控制器  \u_单周期硬布线控制器_1  (
    .Func(IR[5:0]), .OP(IR[31:26]), .ALU_OP(AluOP), .MemToReg(MemToReg), .MemWrite(MemWrite),
    .ALU_SRC(AluSrcB), .RegWrite(RegWrite), .SysCALL(Syscall), .SignedExt(SignedExt), .RegDst(RegDst),
    .JR(JR), .JMP(JMP), .Beq(Beq), .JAL(JAL), .Bne(Bne), .BLEZ(BLEZ), .SRLV(SRLV), .LBU(LBU));
  Multiplexer #(.select(1), .width(5), .disabled("Z"), .enable("false")) multiplexer_2 (
    .in0(IR[25:21]), .in1(5'b00010), .out(multiplexer_2_out), .sel(Syscall));
  Multiplexer #(.select(1), .width(5), .disabled("Z"), .enable("false")) multiplexer_3 (
    .in0(IR[20:16]), .in1(5'b00100), .out(multiplexer_3_out), .sel(Syscall));
  Multiplexer #(.select(1), .width(5), .disabled("Z"), .enable("false")) multiplexer_4 (
    .in0(IR[20:16]), .in1(IR[15:11]), .out(multiplexer_4_out), .sel(RegDst));
  Multiplexer #(.select(1), .width(5), .disabled("Z"), .enable("false")) multiplexer_5 (
    .in0(multiplexer_4_out), .in1({5{1'b1}}), .out(multiplexer_5_out), .sel(JAL));
  assign bit_extender_1_out = {{16{1'b0}}, IR[15:0]};  // Bit_Extender bit_extender_1
  assign bit_extender_2_out = {{16{IR[15]}}, IR[15:0]};  // Bit_Extender bit_extender_2
  or or_2 (IR2_t, IR2, IRB);
  Multiplexer #(.select(1), .width(32), .disabled("Z"), .enable("false")) multiplexer_6 (
    .in0(WriteBackData), .in1(PC_4), .out(RDin), .sel(JAL));
  Multiplexer #(.select(1), .width(32), .disabled("Z"), .enable("false")) multiplexer_7 (
    .in0(bit_extender_1_out), .in1(bit_extender_2_out), .out(multiplexer_7_out), .sel(SignedExt));
  MIPS_Regifile mips_regifile_1 (
    .Din(RDin), .Clk(CLK), .R1(PC_rst), .R2(MDin), .WE(RegWrite), .W_num(multiplexer_5_out),
    .R1_num(multiplexer_2_out), .R2_num(multiplexer_3_out));
  Shifter #(.width(32), .shift("ll")) shifter_1 (.in(bit_extender_2_out), .\dist (5'b00010), .out(shifter_1_out));
  or or_3 (IR3_t, IR3, IRC);
  Adder #(.width(32)) adder_2 (.a(shifter_1_out), .b(PC_4), .out(PC_imm));  // open: cin, cout
  Comparator #(.width(32), .mode("twosComplement")) comparator_2 (
    .a(PC_rst), .b(32'h22), .eq(comparator_2_eq));  // open: gt, lt
  Multiplexer #(.select(1), .width(32), .disabled("Z"), .enable("false")) multiplexer_8 (
    .in0(MDin), .in1(multiplexer_7_out), .out(multiplexer_8_out), .sel(AluSrcB));
  Multiplexer #(.select(1), .width(5), .disabled("Z"), .enable("false")) multiplexer_9 (
    .in0(IR[10:6]), .in1(PC_rst[4:0]), .out(multiplexer_9_out), .sel(SRLV));
  not not_3 (not_3_out, comparator_2_eq);
  not not_4 (not_4_out, mips_alu_1_equal);
  and and_1 (and_1_out, not_4_out, Bne);
  and and_2 (and_2_out, Beq, mips_alu_1_equal);
  or or_4 (or_4_out, mips_alu_1_equal, mips_alu_1_result[0]);
  MIPS_ALU mips_alu_1 (
    .X(PC_rst), .Y(multiplexer_8_out), .AluOP(AluOP), .Equal(mips_alu_1_equal), .Result(mips_alu_1_result),
    .shamt(multiplexer_9_out));  // open: Result_2
  and and_3 (and_3_out, Syscall, comparator_2_eq);
  and and_4 (and_4_out, Syscall, not_3_out);
  or or_5 (PCSrc, and_1_out, and_2_out, and_5_out);
  and and_5 (and_5_out, BLEZ, or_4_out);
  Register #(.width(1), .trigger("rising"), .Select("low")) register_1 (
    .D(and_4_out), .en(and_4_out), .Q(Halt), .clk(CLK), .clr(Go));
  RAM #(.addrWidth(10), .dataWidth(32), .bus("separate"), .Select("high")) ram_1 (
    .addr(mips_alu_1_result[11:2]), .din(MDin), .data(ram_1_data), .str(MemWrite), .clk(CLK), .clr(Reset));  // open: sel, ld
  Register #(.width(32), .trigger("rising"), .Select("low")) register_2 (
    .D(MDin), .en(and_3_out), .Q(LedData), .clk(CLK), .clr(Reset));
  Multiplexer #(.select(1), .width(32), .disabled("Z"), .enable("false")) multiplexer_10 (
    .in0(ram_1_data), .in1({{24{1'b0}}, ram_1_data[7:0]}), .out(multiplexer_10_out), .sel(LBU));
  Multiplexer #(.select(1), .width(32), .disabled("Z"), .enable("false")) multiplexer_11 (
    .in0(mips_alu_1_result), .in1(multiplexer_10_out), .out(WriteBackData), .sel(MemToReg));

  // Other names for the same wires on the sheet: a0[31:0] = MDin; addr[25:0] = IR[25:0];
  //   PC_J[31:2] = {PC[31:28], IR[25:0]}; shamt[4:0] = IR[10:6]; v0[31:0] = PC_rst

  // Notes on the sheet:
  //   中断源
  //   中断等待指示
  //   总复位信号应将除ROM以外所有存储组件全部清零
  //   控制位
  //   暂停节拍，不能为0
  //   用这个时钟源需要去掉电路中的其他时钟源
  //   戳工具置1进入计数暂停模式，ctrl+k时钟自动运行到对应节拍暂停
  //   ctrl+k关闭时钟连续运行，将控制位置零，进入单步调试模式调试
  //   数码管输出
  //   数码管输出应该用寄存器锁存，否则显示数据只能一闪而过
  //   指令存储器
  //   可计数暂停的时钟源
  //   指令字
  //   contents of rom_1 (hex, n*v repeats v):
  //   20110001 8000c05 20110001 20120002 20130003 8000c09 20110001 20120002 20130003 8000c0d 20110001
  //   20120002 20130003 8000c11 20110001 20120002 20130003 c000cb8 20100001 20110001 118fc0 112020
  //   20020022 c 118882 12200001 8000c15 112020 20020022 c 20110001 118880 112020 20020022 c 12200001
  //   8000c1f 20110001 118fc0 112020 20020022 c 1188c3 112020 20020022 c 118903 112020 20020022 c 118903
  //   112020 20020022 c 118903 112020 20020022 c 118903 112020 20020022 c 118903 112020 20020022 c 118903
  //   112020 20020022 c 118903 112020 20020022 c 20100001 109fc0 139fc3 8021 2012000c 24160003 26100001
  //   3210000f 20080008 20090001 139900 2709825 132020 20020022 c 1094022 1500fff9 22100001 2018000f
  //   2188024 108700 20080008 20090001 139902 2709825 132021 20020022 c 1094022 1500fff9 108702 2c9b022
  //   12c00001 8000c50 4020 1084027 84400 3508ffff 82021 20020022 c 2010ffff 20110000 ae300000 22100001
  //   22310004 ae300000 22100001 22310004 ae300000 22100001 22310004 ae300000 22100001 22310004 ae300000
  //   22100001 22310004 ae300000 22100001 22310004 ae300000 22100001 22310004 ae300000 22100001 22310004
  //   ae300000 22100001 22310004 ae300000 22100001 22310004 ae300000 22100001 22310004 ae300000 22100001
  //   22310004 ae300000 22100001 22310004 ae300000 22100001 22310004 ae300000 22100001 22310004 ae300000
  //   22100001 22310004 22100001 8020 2011003c 8e130000 8e340000 274402a 11000002 ae330000 ae140000
  //   2231fffc 1611fff8 102020 20020022 c 22100004 2011003c 1611fff2 20020032 c 20100000 22100001 102020
  //   20020022 c 22100002 102020 20020022 c 22100003 102020 20020022 c 22100004 102020 20020022 c 22100005
  //   102020 20020022 c 22100006 102020 20020022 c 22100007 102020 20020022 c 22100008 102020 20020022
  //   20020022 c 3e00008
  //   OP
  //   Func
  //   rs
  //   rt
  //   rd
  //   Beq
  //   JMP
  //   JR
  //   Bne
  //   OP
  //   JAL
  //   Func
  //   Syscall
  //   v0
  //   a0
  //   MemToReg
  //   MemWrite
  //   AluOP
  //   AluSrcB
  //   RegWrite
  //   RegDst
  //   为方便自动评测，需要输出PC，IR，寄存器堆写如数据RDin
  //   RAM写使能MemWrite、RAM写入数据MDin等信号
endmodule

// 单周期硬布线控制器
module \单周期硬布线控制器  (
  input  [5:0] OP,
  input  [5:0] Func,
  output [3:0] ALU_OP,
  output MemToReg,
  output MemWrite,
  output ALU_SRC,
  output RegWrite,
  output SysCALL,
  output SignedExt,
  output RegDst,
  output Beq,
  output Bne,
  output JR,
  output JMP,
  output JAL,
  output BLEZ,
  output SRLV,
  output LBU
);

  \运算控制器自动生成  \u_运算控制器自动生成_1  (
    .OP0(OP[0]), .OP1(OP[1]), .OP2(OP[2]), .OP3(OP[3]), .OP4(OP[4]), .OP5(OP[5]), .F0(Func[0]), .F1(Func[1]),
    .F2(Func[2]), .F3(Func[3]), .F4(Func[4]), .F5(Func[5]), .S0(ALU_OP[0]), .S1(ALU_OP[1]), .S2(ALU_OP[2]),
    .S3(ALU_OP[3]));
  \控制信号自动生成  \u_控制信号自动生成_1  (
    .OP0(OP[0]), .OP1(OP[1]), .OP2(OP[2]), .MemToReg(MemToReg), .OP3(OP[3]), .OP4(OP[4]), .OP5(OP[5]),
    .MemWrite(MemWrite), .F0(Func[0]), .F1(Func[1]), .F2(Func[2]), .F3(Func[3]), .F4(Func[4]),
    .ALU_SRC(ALU_SRC), .F5(Func[5]), .RegWrite(RegWrite), .SysCALL(SysCALL), .SignedExt(SignedExt),
    .RegDst(RegDst), .BEQ(Beq), .BNE(Bne), .JR(JR), .JUMP(JMP), .JAL(JAL), .BLEZ(BLEZ), .SRLV(SRLV), .LBU(LBU));

  // Other names for the same wires on the sheet: OP_CODE[5:0] = OP

  // Notes on the sheet:
  //   运算器控制器，根据指令生成运算器功能选择信号
  //   控制信号生成，产生数据通路需要的其他控制信号
endmodule

// 运算器控制器
module \运算控制器自动生成  (
  input  OP0,
  input  OP1,
  input  OP2,
  input  OP3,
  input  OP4,
  input  OP5,
  input  F0,
  input  F1,
  input  F2,
  input  F3,
  input  F4,
  input  F5,
  output S0,
  output S1,
  output S2,
  output S3
);

  wire and_1_out, and_2_out, and_3_out, and_4_out, and_5_out, and_6_out, and_7_out, and_8_out, and_9_out,
       and_10_out, and_11_out, and_12_out, and_13_out, and_14_out, and_15_out, and_16_out, and_17_out,
       and_18_out, and_19_out, and_20_out, and_21_out, and_22_out, and_23_out, and_24_out, and_25_out,
       and_26_out, and_27_out, and_28_out, and_29_out, and_30_out, and_31_out, and_32_out, and_33_out,
       and_34_out, and_35_out, and_36_out, and_37_out, and_38_out, and_39_out, and_40_out, and_41_out,
       and_42_out, not_1_out, not_2_out, not_3_out, not_4_out, not_5_out, not_6_out, not_7_out, not_8_out,
       not_9_out, not_10_out, not_11_out, not_12_out, not_13_out, not_14_out, not_15_out, not_16_out,
       not_17_out, not_18_out, not_19_out, not_20_out, not_21_out, not_22_out, not_23_out, not_24_out,
       not_25_out, not_26_out, not_27_out, not_28_out, not_29_out, not_30_out, not_31_out, not_32_out,
       not_33_out, not_34_out, not_35_out, not_36_out, not_37_out, not_38_out, not_39_out, not_40_out,
       not_41_out, not_42_out, not_43_out, not_44_out, not_45_out, not_46_out, not_47_out, not_48_out,
       not_49_out, not_50_out, not_51_out, not_52_out, not_53_out, not_54_out, not_55_out, not_56_out,
       not_57_out, not_58_out, not_59_out, not_60_out, not_61_out, not_62_out, not_63_out, not_64_out,
       not_65_out, not_66_out, not_67_out, not_68_out, not_69_out, not_70_out, not_71_out, not_72_out,
       not_73_out, not_74_out, not_75_out, not_76_out, not_77_out, not_78_out, not_79_out, not_80_out,
       not_81_out, not_82_out, not_83_out, not_84_out, not_85_out, not_86_out, not_87_out, not_88_out,
       not_89_out, not_90_out, not_91_out, not_92_out, not_93_out, not_94_out, not_95_out, not_96_out,
       not_97_out, not_98_out, not_99_out, not_100_out, not_101_out, not_102_out, not_103_out, not_104_out,
       not_105_out, not_106_out, not_107_out, not_108_out, not_109_out, not_110_out, not_111_out,
       not_112_out, not_113_out, not_114_out, not_115_out, not_116_out, not_117_out, not_118_out,
       not_119_out, not_120_out, not_121_out, not_122_out, not_123_out, not_124_out, not_125_out,
       not_126_out, not_127_out, not_128_out, not_129_out, not_130_out, not_131_out, not_132_out,
       not_133_out, not_134_out, not_135_out, not_136_out, not_137_out, not_138_out, not_139_out,
       not_140_out, not_141_out, not_142_out, not_143_out, not_144_out, not_145_out, not_146_out,
       not_147_out, not_148_out, not_149_out, not_150_out, not_151_out, not_152_out, not_153_out,
       not_154_out, not_155_out, not_156_out, not_157_out, not_158_out, not_159_out, not_160_out,
       not_161_out, not_162_out, not_163_out, not_164_out, not_165_out, not_166_out, not_167_out,
       not_168_out, not_169_out, not_170_out, not_171_out, not_172_out, not_173_out, not_174_out,
       not_175_out, not_176_out, not_177_out, not_178_out, not_179_out, not_180_out, not_181_out,
       not_182_out, not_183_out, not_184_out, not_185_out, not_186_out, not_187_out, not_188_out,
       not_189_out, not_190_out, not_191_out, not_192_out, not_193_out, not_194_out, not_195_out,
       not_196_out, not_197_out, not_198_out, not_199_out, not_200_out, not_201_out, not_202_out,
       not_203_out, not_204_out, not_205_out, not_206_out, not_207_out, not_208_out, not_209_out,
       not_210_out, not_211_out, not_212_out, not_213_out, not_214_out, not_215_out, not_216_out,
       not_217_out, not_218_out, not_219_out, not_220_out, not_221_out, not_222_out, not_223_out,
       not_224_out, not_225_out, not_226_out, not_227_out, not_228_out, not_229_out, not_230_out,
       not_231_out, not_232_out, not_233_out, not_234_out, not_235_out, not_236_out, not_237_out,
       not_238_out, not_239_out, not_240_out, not_241_out, not_242_out, not_243_out, not_244_out,
       not_245_out, not_246_out, not_247_out, not_248_out, not_249_out, not_250_out, not_251_out,
       not_252_out, not_253_out, not_254_out, not_255_out, not_256_out, not_257_out, not_258_out,
       not_259_out, not_260_out, not_261_out, not_262_out, not_263_out, not_264_out, not_265_out,
       not_266_out, not_267_out, not_268_out, not_269_out, not_270_out, not_271_out, not_272_out;

  not not_1 (not_1_out, OP5);
  not not_2 (not_2_out, OP4);
  not not_3 (not_3_out, OP3);
  not not_4 (not_4_out, OP2);
  not not_5 (not_5_out, OP1);
  not not_6 (not_6_out, OP0);
  not not_7 (not_7_out, F5);
  not not_8 (not_8_out, F4);
  not not_9 (not_9_out, F3);
  not not_10 (not_10_out, F2);
  not not_11 (not_11_out, OP5);
  not not_12 (not_12_out, OP4);
  not not_13 (not_13_out, OP3);
  not not_14 (not_14_out, OP2);
  not not_15 (not_15_out, OP1);
  not not_16 (not_16_out, OP0);
  not not_17 (not_17_out, F4);
  not not_18 (not_18_out, F3);
  not not_19 (not_19_out, F2);
  not not_20 (not_20_out, F1);
  not not_21 (not_21_out, F0);
  not not_22 (not_22_out, OP5);
  not not_23 (not_23_out, OP4);
  not not_24 (not_24_out, OP3);
  not not_25 (not_25_out, OP2);
  not not_26 (not_26_out, OP1);
  not not_27 (not_27_out, OP0);
  not not_28 (not_28_out, F4);
  not not_29 (not_29_out, F3);
  not not_30 (not_30_out, F2);
  not not_31 (not_31_out, F1);
  not not_32 (not_32_out, OP5);
  not not_33 (not_33_out, OP4);
  not not_34 (not_34_out, OP3);
  not not_35 (not_35_out, OP2);
  not not_36 (not_36_out, OP1);
  not not_37 (not_37_out, OP0);
  not not_38 (not_38_out, F4);
  not not_39 (not_39_out, F3);
  not not_40 (not_40_out, F1);
  not not_41 (not_41_out, F0);
  not not_42 (not_42_out, OP5);
  not not_43 (not_43_out, OP4);
  not not_44 (not_44_out, OP3);
  not not_45 (not_45_out, OP2);
  not not_46 (not_46_out, OP1);
  not not_47 (not_47_out, OP0);
  not not_48 (not_48_out, F4);
  not not_49 (not_49_out, F2);
  not not_50 (not_50_out, F0);
  not not_51 (not_51_out, OP5);
  not not_52 (not_52_out, OP4);
  not not_53 (not_53_out, OP2);
  not not_54 (not_54_out, OP1);
  not not_55 (not_55_out, OP0);
  not not_56 (not_56_out, OP5);
  not not_57 (not_57_out, OP4);
  not not_58 (not_58_out, OP1);
  not not_59 (not_59_out, OP0);
  not not_60 (not_60_out, OP5);
  not not_61 (not_61_out, OP4);
  not not_62 (not_62_out, OP2);
  not not_63 (not_63_out, OP1);
  not not_64 (not_64_out, OP5);
  not not_65 (not_65_out, OP4);
  not not_66 (not_66_out, OP2);
  not not_67 (not_67_out, OP0);
  not not_68 (not_68_out, OP4);
  not not_69 (not_69_out, OP3);
  not not_70 (not_70_out, OP2);
  not not_71 (not_71_out, OP4);
  not not_72 (not_72_out, OP2);
  not not_73 (not_73_out, OP4);
  not not_74 (not_74_out, OP3);
  not not_75 (not_75_out, OP1);
  not not_76 (not_76_out, OP0);
  not not_77 (not_77_out, OP5);
  not not_78 (not_78_out, OP4);
  not not_79 (not_79_out, OP3);
  not not_80 (not_80_out, OP0);
  not not_81 (not_81_out, OP5);
  not not_82 (not_82_out, OP4);
  not not_83 (not_83_out, OP3);
  not not_84 (not_84_out, OP2);
  not not_85 (not_85_out, OP1);
  not not_86 (not_86_out, OP0);
  not not_87 (not_87_out, F5);
  not not_88 (not_88_out, F4);
  not not_89 (not_89_out, F3);
  not not_90 (not_90_out, F2);
  not not_91 (not_91_out, F0);
  not not_92 (not_92_out, OP5);
  not not_93 (not_93_out, OP4);
  not not_94 (not_94_out, OP3);
  not not_95 (not_95_out, OP2);
  not not_96 (not_96_out, OP1);
  not not_97 (not_97_out, OP0);
  not not_98 (not_98_out, F4);
  not not_99 (not_99_out, F3);
  not not_100 (not_100_out, F2);
  not not_101 (not_101_out, F0);
  not not_102 (not_102_out, OP5);
  not not_103 (not_103_out, OP4);
  not not_104 (not_104_out, OP3);
  not not_105 (not_105_out, OP2);
  not not_106 (not_106_out, OP1);
  not not_107 (not_107_out, OP0);
  not not_108 (not_108_out, F4);
  not not_109 (not_109_out, F3);
  not not_110 (not_110_out, F1);
  not not_111 (not_111_out, F0);
  not not_112 (not_112_out, OP5);
  not not_113 (not_113_out, OP4);
  not not_114 (not_114_out, OP3);
  not not_115 (not_115_out, OP2);
  not not_116 (not_116_out, OP1);
  not not_117 (not_117_out, OP0);
  not not_118 (not_118_out, F4);
  not not_119 (not_119_out, F3);
  not not_120 (not_120_out, OP5);
  not not_121 (not_121_out, OP4);
  not not_122 (not_122_out, OP3);
  not not_123 (not_123_out, OP2);
  not not_124 (not_124_out, OP1);
  not not_125 (not_125_out, OP0);
  not not_126 (not_126_out, F4);
  not not_127 (not_127_out, F2);
  not not_128 (not_128_out, F0);
  not not_129 (not_129_out, OP5);
  not not_130 (not_130_out, OP4);
  not not_131 (not_131_out, OP1);
  not not_132 (not_132_out, OP0);
  not not_133 (not_133_out, OP5);
  not not_134 (not_134_out, OP4);
  not not_135 (not_135_out, OP2);
  not not_136 (not_136_out, OP0);
  not not_137 (not_137_out, OP5);
  not not_138 (not_138_out, OP4);
  not not_139 (not_139_out, OP3);
  not not_140 (not_140_out, OP2);
  not not_141 (not_141_out, OP1);
  not not_142 (not_142_out, OP0);
  not not_143 (not_143_out, F5);
  not not_144 (not_144_out, F4);
  not not_145 (not_145_out, F3);
  not not_146 (not_146_out, F0);
  not not_147 (not_147_out, OP5);
  not not_148 (not_148_out, OP4);
  not not_149 (not_149_out, OP3);
  not not_150 (not_150_out, OP0);
  not not_151 (not_151_out, OP5);
  not not_152 (not_152_out, OP4);
  not not_153 (not_153_out, OP3);
  not not_154 (not_154_out, OP2);
  not not_155 (not_155_out, OP1);
  not not_156 (not_156_out, OP0);
  not not_157 (not_157_out, F4);
  not not_158 (not_158_out, F3);
  not not_159 (not_159_out, F2);
  not not_160 (not_160_out, F1);
  not not_161 (not_161_out, F0);
  not not_162 (not_162_out, OP5);
  not not_163 (not_163_out, OP4);
  not not_164 (not_164_out, OP3);
  not not_165 (not_165_out, OP2);
  not not_166 (not_166_out, OP1);
  not not_167 (not_167_out, OP0);
  not not_168 (not_168_out, F4);
  not not_169 (not_169_out, F3);
  not not_170 (not_170_out, F2);
  not not_171 (not_171_out, F1);
  not not_172 (not_172_out, OP5);
  not not_173 (not_173_out, OP4);
  not not_174 (not_174_out, OP3);
  not not_175 (not_175_out, OP2);
  not not_176 (not_176_out, OP1);
  not not_177 (not_177_out, OP0);
  not not_178 (not_178_out, F4);
  not not_179 (not_179_out, F3);
  not not_180 (not_180_out, F2);
  not not_181 (not_181_out, F0);
  not not_182 (not_182_out, OP5);
  not not_183 (not_183_out, OP4);
  not not_184 (not_184_out, OP3);
  not not_185 (not_185_out, OP2);
  not not_186 (not_186_out, OP1);
  not not_187 (not_187_out, OP0);
  not not_188 (not_188_out, F4);
  not not_189 (not_189_out, F3);
  not not_190 (not_190_out, F1);
  not not_191 (not_191_out, F0);
  not not_192 (not_192_out, OP5);
  not not_193 (not_193_out, OP4);
  not not_194 (not_194_out, OP3);
  not not_195 (not_195_out, OP2);
  not not_196 (not_196_out, OP1);
  not not_197 (not_197_out, OP0);
  not not_198 (not_198_out, F4);
  not not_199 (not_199_out, F2);
  not not_200 (not_200_out, OP5);
  not not_201 (not_201_out, OP4);
  not not_202 (not_202_out, OP2);
  not not_203 (not_203_out, OP1);
  not not_204 (not_204_out, OP0);
  not not_205 (not_205_out, OP5);
  not not_206 (not_206_out, OP4);
  not not_207 (not_207_out, OP1);
  not not_208 (not_208_out, OP0);
  not not_209 (not_209_out, OP5);
  not not_210 (not_210_out, OP4);
  not not_211 (not_211_out, OP2);
  not not_212 (not_212_out, OP1);
  not not_213 (not_213_out, OP4);
  not not_214 (not_214_out, OP3);
  not not_215 (not_215_out, OP2);
  not not_216 (not_216_out, OP4);
  not not_217 (not_217_out, OP2);
  not not_218 (not_218_out, OP5);
  not not_219 (not_219_out, OP4);
  not not_220 (not_220_out, OP2);
  not not_221 (not_221_out, OP4);
  not not_222 (not_222_out, OP3);
  not not_223 (not_223_out, OP1);
  not not_224 (not_224_out, OP0);
  not not_225 (not_225_out, OP5);
  not not_226 (not_226_out, OP4);
  not not_227 (not_227_out, OP3);
  not not_228 (not_228_out, OP2);
  not not_229 (not_229_out, OP1);
  not not_230 (not_230_out, OP0);
  not not_231 (not_231_out, F4);
  not not_232 (not_232_out, F3);
  not not_233 (not_233_out, F1);
  not not_234 (not_234_out, OP5);
  not not_235 (not_235_out, OP4);
  not not_236 (not_236_out, OP3);
  not not_237 (not_237_out, OP2);
  not not_238 (not_238_out, OP1);
  not not_239 (not_239_out, OP0);
  not not_240 (not_240_out, F4);
  not not_241 (not_241_out, F3);
  not not_242 (not_242_out, OP5);
  not not_243 (not_243_out, OP4);
  not not_244 (not_244_out, OP3);
  not not_245 (not_245_out, OP2);
  not not_246 (not_246_out, OP1);
  not not_247 (not_247_out, OP0);
  not not_248 (not_248_out, F4);
  not not_249 (not_249_out, F2);
  not not_250 (not_250_out, F0);
  not not_251 (not_251_out, OP5);
  not not_252 (not_252_out, OP4);
  not not_253 (not_253_out, OP3);
  not not_254 (not_254_out, OP2);
  not not_255 (not_255_out, OP1);
  not not_256 (not_256_out, OP0);
  not not_257 (not_257_out, F4);
  not not_258 (not_258_out, F2);
  not not_259 (not_259_out, OP5);
  not not_260 (not_260_out, OP4);
  not not_261 (not_261_out, OP2);
  not not_262 (not_262_out, OP0);
  not not_263 (not_263_out, OP5);
  not not_264 (not_264_out, OP4);
  not not_265 (not_265_out, OP1);
  not not_266 (not_266_out, OP5);
  not not_267 (not_267_out, OP4);
  not not_268 (not_268_out, OP2);
  not not_269 (not_269_out, OP5);
  not not_270 (not_270_out, OP4);
  not not_271 (not_271_out, OP3);
  not not_272 (not_272_out, OP0);
  and and_1 (and_1_out, not_1_out, not_2_out, not_3_out, not_4_out, not_5_out, not_6_out, not_7_out, not_8_out, not_9_out, not_10_out, F1, F0);
  and and_2 (and_2_out, not_11_out, not_12_out, not_13_out, not_14_out, not_15_out, not_16_out, F5, not_17_out, not_18_out, not_19_out, not_20_out, not_21_out);
  and and_3 (and_3_out, not_22_out, not_23_out, not_24_out, not_25_out, not_26_out, not_27_out, F5, not_28_out, not_29_out, not_30_out, not_31_out, F0);
  and and_4 (and_4_out, not_32_out, not_33_out, not_34_out, not_35_out, not_36_out, not_37_out, F5, not_38_out, not_39_out, F2, not_40_out, not_41_out);
  and and_5 (and_5_out, not_42_out, not_43_out, not_44_out, not_45_out, not_46_out, not_47_out, F5, not_48_out, F3, not_49_out, F1, not_50_out);
  and and_6 (and_6_out, not_51_out, not_52_out, OP3, not_53_out, not_54_out, not_55_out);
  and and_7 (and_7_out, not_56_out, not_57_out, OP3, OP2, not_58_out, not_59_out);
  and and_8 (and_8_out, not_60_out, not_61_out, OP3, not_62_out, not_63_out, OP0);
  and and_9 (and_9_out, not_64_out, not_65_out, OP3, not_66_out, OP1, not_67_out);
  and and_10 (and_10_out, OP5, not_68_out, not_69_out, not_70_out, OP1, OP0);
  and and_11 (and_11_out, OP5, not_71_out, OP3, not_72_out, OP1, OP0);
  and and_12 (and_12_out, OP5, not_73_out, not_74_out, OP2, not_75_out, not_76_out);
  and and_13 (and_13_out, not_77_out, not_78_out, not_79_out, OP2, OP1, not_80_out);
  and and_14 (and_14_out, not_81_out, not_82_out, not_83_out, not_84_out, not_85_out, not_86_out, not_87_out, not_88_out, not_89_out, not_90_out, F1, not_91_out);
  and and_15 (and_15_out, not_92_out, not_93_out, not_94_out, not_95_out, not_96_out, not_97_out, F5, not_98_out, not_99_out, not_100_out, F1, not_101_out);
  and and_16 (and_16_out, not_102_out, not_103_out, not_104_out, not_105_out, not_106_out, not_107_out, F5, not_108_out, not_109_out, F2, not_110_out, not_111_out);
  and and_17 (and_17_out, not_112_out, not_113_out, not_114_out, not_115_out, not_116_out, not_117_out, F5, not_118_out, not_119_out, F2, F1, F0);
  and and_18 (and_18_out, not_120_out, not_121_out, not_122_out, not_123_out, not_124_out, not_125_out, F5, not_126_out, F3, not_127_out, F1, not_128_out);
  and and_19 (and_19_out, not_129_out, not_130_out, OP3, OP2, not_131_out, not_132_out);
  and and_20 (and_20_out, not_133_out, not_134_out, OP3, not_135_out, OP1, not_136_out);
  and and_21 (and_21_out, not_137_out, not_138_out, not_139_out, not_140_out, not_141_out, not_142_out, not_143_out, not_144_out, not_145_out, F2, F1, not_146_out);
  and and_22 (and_22_out, not_147_out, not_148_out, not_149_out, OP2, OP1, not_150_out);
  and and_23 (and_23_out, not_151_out, not_152_out, not_153_out, not_154_out, not_155_out, not_156_out, F5, not_157_out, not_158_out, not_159_out, not_160_out, not_161_out);
  and and_24 (and_24_out, not_162_out, not_163_out, not_164_out, not_165_out, not_166_out, not_167_out, F5, not_168_out, not_169_out, not_170_out, not_171_out, F0);
  and and_25 (and_25_out, not_172_out, not_173_out, not_174_out, not_175_out, not_176_out, not_177_out, F5, not_178_out, not_179_out, not_180_out, F1, not_181_out);
  and and_26 (and_26_out, not_182_out, not_183_out, not_184_out, not_185_out, not_186_out, not_187_out, F5, not_188_out, not_189_out, F2, not_190_out, not_191_out);
  and and_27 (and_27_out, not_192_out, not_193_out, not_194_out, not_195_out, not_196_out, not_197_out, F5, not_198_out, F3, not_199_out, F1, F0);
  and and_28 (and_28_out, not_200_out, not_201_out, OP3, not_202_out, not_203_out, not_204_out);
  and and_29 (and_29_out, not_205_out, not_206_out, OP3, OP2, not_207_out, not_208_out);
  and and_30 (and_30_out, not_209_out, not_210_out, OP3, not_211_out, not_212_out, OP0);
  and and_31 (and_31_out, OP5, not_213_out, not_214_out, not_215_out, OP1, OP0);
  and and_32 (and_32_out, OP5, not_216_out, OP3, not_217_out, OP1, OP0);
  and and_33 (and_33_out, not_218_out, not_219_out, OP3, not_220_out, OP1, OP0);
  and and_34 (and_34_out, OP5, not_221_out, not_222_out, OP2, not_223_out, not_224_out);
  and and_35 (and_35_out, not_225_out, not_226_out, not_227_out, not_228_out, not_229_out, not_230_out, F5, not_231_out, not_232_out, F2, not_233_out, F0);
  and and_36 (and_36_out, not_234_out, not_235_out, not_236_out, not_237_out, not_238_out, not_239_out, F5, not_240_out, not_241_out, F2, F1, F0);
  and and_37 (and_37_out, not_242_out, not_243_out, not_244_out, not_245_out, not_246_out, not_247_out, F5, not_248_out, F3, not_249_out, F1, not_250_out);
  and and_38 (and_38_out, not_251_out, not_252_out, not_253_out, not_254_out, not_255_out, not_256_out, F5, not_257_out, F3, not_258_out, F1, F0);
  and and_39 (and_39_out, not_259_out, not_260_out, OP3, not_261_out, OP1, not_262_out);
  and and_40 (and_40_out, not_263_out, not_264_out, OP3, OP2, not_265_out, OP0);
  and and_41 (and_41_out, not_266_out, not_267_out, OP3, not_268_out, OP1, OP0);
  and and_42 (and_42_out, not_269_out, not_270_out, not_271_out, OP2, OP1, not_272_out);
  or or_1 (S1, and_14_out, and_15_out, and_16_out, and_17_out, and_18_out, and_19_out, and_20_out, and_21_out, and_22_out);
  or or_2 (S3, and_35_out, and_36_out, and_37_out, and_38_out, and_39_out, and_40_out, and_41_out, and_42_out);
  or or_3 (S0, and_1_out, and_2_out, and_3_out, and_4_out, and_5_out, and_6_out, and_7_out, and_8_out, and_9_out, and_10_out, and_11_out, and_12_out, and_13_out);
  or or_4 (S2, and_23_out, and_24_out, and_25_out, and_26_out, and_27_out, and_28_out, and_29_out, and_30_out, and_31_out, and_32_out, and_33_out, and_34_out);
endmodule

// 控制信号生成
module \控制信号自动生成  (
  input  OP0,
  input  OP1,
  input  OP2,
  input  OP3,
  input  OP4,
  input  OP5,
  input  F0,
  input  F1,
  input  F2,
  input  F3,
  input  F4,
  input  F5,
  output MemToReg,
  output MemWrite,
  output ALU_SRC,
  output RegWrite,
  output SysCALL,
  output SignedExt,
  output RegDst,
  output BEQ,
  output BNE,
  output JR,
  output JUMP,
  output JAL,
  output BLEZ,
  output SRLV,
  output LBU
);

  wire and_1_out, and_2_out, and_4_out, and_5_out, and_6_out, and_7_out, and_8_out, and_9_out, and_10_out,
       and_11_out, and_12_out, and_13_out, and_14_out, and_15_out, and_16_out, and_17_out, and_19_out,
       and_20_out, and_21_out, and_22_out, and_23_out, and_24_out, and_25_out, and_26_out, and_27_out,
       and_31_out, and_32_out, not_1_out, not_2_out, not_3_out, not_4_out, not_5_out, not_6_out, not_7_out,
       not_8_out, not_9_out, not_10_out, not_11_out, not_12_out, not_13_out, not_14_out, not_15_out,
       not_16_out, not_17_out, not_18_out, not_19_out, not_20_out, not_21_out, not_22_out, not_23_out,
       not_24_out, not_25_out, not_26_out, not_27_out, not_28_out, not_29_out, not_30_out, not_31_out,
       not_32_out, not_33_out, not_34_out, not_35_out, not_36_out, not_37_out, not_38_out, not_39_out,
       not_40_out, not_41_out, not_42_out, not_43_out, not_44_out, not_45_out, not_46_out, not_47_out,
       not_48_out, not_49_out, not_50_out, not_51_out, not_52_out, not_53_out, not_54_out, not_55_out,
       not_56_out, not_57_out, not_58_out, not_59_out, not_60_out, not_61_out, not_62_out, not_63_out,
       not_64_out, not_65_out, not_66_out, not_67_out, not_68_out, not_69_out, not_70_out, not_71_out,
       not_72_out, not_73_out, not_74_out, not_75_out, not_76_out, not_77_out, not_78_out, not_79_out,
       not_80_out, not_81_out, not_82_out, not_83_out, not_84_out, not_85_out, not_86_out, not_87_out,
       not_88_out, not_89_out, not_90_out, not_91_out, not_92_out, not_93_out, not_94_out, not_95_out,
       not_96_out, not_97_out, not_98_out, not_99_out, not_100_out, not_101_out, not_102_out, not_103_out,
       not_104_out, not_105_out, not_106_out, not_107_out, not_108_out, not_109_out, not_110_out,
       not_111_out, not_112_out, not_113_out, not_114_out, not_115_out, not_116_out, not_117_out,
       not_118_out, not_119_out, not_120_out, not_121_out, not_122_out, not_123_out, not_124_out,
       not_125_out, not_126_out, not_127_out, not_128_out, not_129_out, not_130_out, not_131_out,
       not_132_out, not_133_out, not_134_out, not_135_out, not_136_out, not_137_out, not_138_out,
       not_139_out, not_140_out, not_141_out, not_142_out, not_143_out, not_144_out, not_145_out,
       not_146_out, not_147_out, not_148_out, not_149_out, not_150_out, not_151_out, not_152_out,
       not_153_out, not_154_out, not_155_out, not_156_out, not_157_out, not_158_out, not_159_out,
       not_160_out, not_161_out, not_162_out, not_163_out, not_164_out, not_165_out, not_166_out,
       not_167_out, not_168_out, not_169_out, not_170_out, not_171_out, not_172_out, not_173_out,
       not_174_out, not_175_out, not_176_out, not_177_out, not_178_out, not_179_out, not_180_out,
       not_181_out, not_182_out, not_183_out, not_184_out, not_185_out, not_186_out, not_187_out,
       not_188_out, not_189_out, not_190_out, not_191_out, not_192_out, not_193_out, not_194_out,
       not_195_out, not_196_out, not_197_out, not_198_out, not_199_out, not_200_out, not_201_out,
       not_202_out, not_203_out, not_204_out, not_205_out, not_206_out, not_207_out, not_208_out,
       not_209_out, not_210_out, not_211_out, not_212_out, not_213_out, not_214_out, not_215_out;

  not not_1 (not_1_out, OP4);
  not not_2 (not_2_out, OP3);
  not not_3 (not_3_out, OP2);
  not not_4 (not_4_out, OP4);
  not not_5 (not_5_out, OP3);
  not not_6 (not_6_out, OP1);
  not not_7 (not_7_out, OP0);
  not not_8 (not_8_out, OP2);
  not not_9 (not_9_out, OP4);
  not not_10 (not_10_out, OP1);
  not not_11 (not_11_out, OP4);
  not not_12 (not_12_out, OP5);
  not not_13 (not_13_out, OP2);
  not not_14 (not_14_out, OP4);
  not not_15 (not_15_out, OP5);
  not not_16 (not_16_out, OP0);
  not not_17 (not_17_out, OP1);
  not not_18 (not_18_out, OP3);
  not not_19 (not_19_out, OP4);
  not not_20 (not_20_out, OP2);
  not not_21 (not_21_out, OP4);
  not not_22 (not_22_out, OP0);
  not not_23 (not_23_out, OP1);
  not not_24 (not_24_out, OP2);
  not not_25 (not_25_out, OP4);
  not not_26 (not_26_out, OP5);
  not not_27 (not_27_out, F0);
  not not_28 (not_28_out, F2);
  not not_29 (not_29_out, F3);
  not not_30 (not_30_out, F4);
  not not_31 (not_31_out, OP0);
  not not_32 (not_32_out, OP1);
  not not_33 (not_33_out, OP2);
  not not_34 (not_34_out, OP4);
  not not_35 (not_35_out, OP5);
  not not_36 (not_36_out, F1);
  not not_37 (not_37_out, F3);
  not not_38 (not_38_out, F4);
  not not_39 (not_39_out, OP0);
  not not_40 (not_40_out, OP1);
  not not_41 (not_41_out, OP2);
  not not_42 (not_42_out, OP4);
  not not_43 (not_43_out, OP5);
  not not_44 (not_44_out, F0);
  not not_45 (not_45_out, F3);
  not not_46 (not_46_out, F4);
  not not_47 (not_47_out, F5);
  not not_48 (not_48_out, OP0);
  not not_49 (not_49_out, OP1);
  not not_50 (not_50_out, OP2);
  not not_51 (not_51_out, OP4);
  not not_52 (not_52_out, OP5);
  not not_53 (not_53_out, F2);
  not not_54 (not_54_out, F3);
  not not_55 (not_55_out, F4);
  not not_56 (not_56_out, F5);
  not not_57 (not_57_out, OP0);
  not not_58 (not_58_out, OP1);
  not not_59 (not_59_out, OP2);
  not not_60 (not_60_out, OP4);
  not not_61 (not_61_out, OP5);
  not not_62 (not_62_out, F2);
  not not_63 (not_63_out, F4);
  not not_64 (not_64_out, OP0);
  not not_65 (not_65_out, OP1);
  not not_66 (not_66_out, OP2);
  not not_67 (not_67_out, OP4);
  not not_68 (not_68_out, OP5);
  not not_69 (not_69_out, F3);
  not not_70 (not_70_out, F4);
  not not_71 (not_71_out, OP1);
  not not_72 (not_72_out, OP4);
  not not_73 (not_73_out, OP5);
  not not_74 (not_74_out, OP2);
  not not_75 (not_75_out, OP4);
  not not_76 (not_76_out, OP5);
  not not_77 (not_77_out, OP0);
  not not_78 (not_78_out, OP1);
  not not_79 (not_79_out, OP3);
  not not_80 (not_80_out, OP4);
  not not_81 (not_81_out, OP2);
  not not_82 (not_82_out, OP3);
  not not_83 (not_83_out, OP4);
  not not_84 (not_84_out, OP0);
  not not_85 (not_85_out, OP1);
  not not_86 (not_86_out, OP2);
  not not_87 (not_87_out, OP3);
  not not_88 (not_88_out, OP4);
  not not_89 (not_89_out, OP5);
  not not_90 (not_90_out, F0);
  not not_91 (not_91_out, F1);
  not not_92 (not_92_out, F4);
  not not_93 (not_93_out, F5);
  not not_94 (not_94_out, OP2);
  not not_95 (not_95_out, OP4);
  not not_96 (not_96_out, OP5);
  not not_97 (not_97_out, OP0);
  not not_98 (not_98_out, OP3);
  not not_99 (not_99_out, OP4);
  not not_100 (not_100_out, OP5);
  not not_101 (not_101_out, OP1);
  not not_102 (not_102_out, OP3);
  not not_103 (not_103_out, OP4);
  not not_104 (not_104_out, OP5);
  not not_105 (not_105_out, OP0);
  not not_106 (not_106_out, OP1);
  not not_107 (not_107_out, OP2);
  not not_108 (not_108_out, OP3);
  not not_109 (not_109_out, OP4);
  not not_110 (not_110_out, OP5);
  not not_111 (not_111_out, F0);
  not not_112 (not_112_out, F2);
  not not_113 (not_113_out, F3);
  not not_114 (not_114_out, F4);
  not not_115 (not_115_out, OP0);
  not not_116 (not_116_out, OP1);
  not not_117 (not_117_out, OP2);
  not not_118 (not_118_out, OP3);
  not not_119 (not_119_out, OP4);
  not not_120 (not_120_out, OP5);
  not not_121 (not_121_out, F1);
  not not_122 (not_122_out, F3);
  not not_123 (not_123_out, F4);
  not not_124 (not_124_out, OP0);
  not not_125 (not_125_out, OP1);
  not not_126 (not_126_out, OP2);
  not not_127 (not_127_out, OP3);
  not not_128 (not_128_out, OP4);
  not not_129 (not_129_out, OP5);
  not not_130 (not_130_out, F0);
  not not_131 (not_131_out, F3);
  not not_132 (not_132_out, F4);
  not not_133 (not_133_out, F5);
  not not_134 (not_134_out, OP0);
  not not_135 (not_135_out, OP1);
  not not_136 (not_136_out, OP2);
  not not_137 (not_137_out, OP3);
  not not_138 (not_138_out, OP4);
  not not_139 (not_139_out, OP5);
  not not_140 (not_140_out, F2);
  not not_141 (not_141_out, F3);
  not not_142 (not_142_out, F4);
  not not_143 (not_143_out, F5);
  not not_144 (not_144_out, OP0);
  not not_145 (not_145_out, OP1);
  not not_146 (not_146_out, OP2);
  not not_147 (not_147_out, OP3);
  not not_148 (not_148_out, OP4);
  not not_149 (not_149_out, OP5);
  not not_150 (not_150_out, F2);
  not not_151 (not_151_out, F4);
  not not_152 (not_152_out, OP0);
  not not_153 (not_153_out, OP1);
  not not_154 (not_154_out, OP2);
  not not_155 (not_155_out, OP3);
  not not_156 (not_156_out, OP4);
  not not_157 (not_157_out, OP5);
  not not_158 (not_158_out, F3);
  not not_159 (not_159_out, F4);
  not not_160 (not_160_out, OP0);
  not not_161 (not_161_out, OP1);
  not not_162 (not_162_out, OP3);
  not not_163 (not_163_out, OP4);
  not not_164 (not_164_out, OP5);
  not not_165 (not_165_out, OP1);
  not not_166 (not_166_out, OP3);
  not not_167 (not_167_out, OP4);
  not not_168 (not_168_out, OP5);
  not not_169 (not_169_out, OP0);
  not not_170 (not_170_out, OP1);
  not not_171 (not_171_out, OP2);
  not not_172 (not_172_out, OP3);
  not not_173 (not_173_out, OP4);
  not not_174 (not_174_out, OP5);
  not not_175 (not_175_out, F0);
  not not_176 (not_176_out, F1);
  not not_177 (not_177_out, F2);
  not not_178 (not_178_out, F4);
  not not_179 (not_179_out, F5);
  not not_180 (not_180_out, OP0);
  not not_181 (not_181_out, OP2);
  not not_182 (not_182_out, OP3);
  not not_183 (not_183_out, OP4);
  not not_184 (not_184_out, OP5);
  not not_185 (not_185_out, F0);
  not not_186 (not_186_out, F1);
  not not_187 (not_187_out, F2);
  not not_188 (not_188_out, F4);
  not not_189 (not_189_out, F5);
  not not_190 (not_190_out, OP2);
  not not_191 (not_191_out, OP3);
  not not_192 (not_192_out, OP4);
  not not_193 (not_193_out, OP5);
  not not_194 (not_194_out, OP2);
  not not_195 (not_195_out, OP3);
  not not_196 (not_196_out, OP4);
  not not_197 (not_197_out, OP5);
  not not_198 (not_198_out, OP0);
  not not_199 (not_199_out, OP3);
  not not_200 (not_200_out, OP4);
  not not_201 (not_201_out, OP5);
  not not_202 (not_202_out, OP0);
  not not_203 (not_203_out, OP1);
  not not_204 (not_204_out, OP2);
  not not_205 (not_205_out, OP3);
  not not_206 (not_206_out, OP4);
  not not_207 (not_207_out, OP5);
  not not_208 (not_208_out, F0);
  not not_209 (not_209_out, F3);
  not not_210 (not_210_out, F4);
  not not_211 (not_211_out, F5);
  not not_212 (not_212_out, OP0);
  not not_213 (not_213_out, OP1);
  not not_214 (not_214_out, OP3);
  not not_215 (not_215_out, OP4);
  and and_1 (and_1_out, OP5, not_1_out, not_2_out, not_3_out, OP1, OP0);
  and and_2 (and_2_out, OP5, not_4_out, not_5_out, OP2, not_6_out, not_7_out);
  and and_3 (MemWrite, OP0, OP1, not_8_out, OP3, not_9_out, OP5);
  and and_4 (and_4_out, not_10_out, OP3, not_11_out, not_12_out);
  and and_5 (and_5_out, not_13_out, OP3, not_14_out, not_15_out);
  and and_6 (and_6_out, not_16_out, not_17_out, OP2, not_18_out, not_19_out, OP5);
  and and_7 (and_7_out, OP0, OP1, not_20_out, not_21_out, OP5);
  and and_8 (and_8_out, not_22_out, not_23_out, not_24_out, not_25_out, not_26_out, not_27_out, not_28_out, not_29_out, not_30_out);
  and and_9 (and_9_out, not_31_out, not_32_out, not_33_out, not_34_out, not_35_out, not_36_out, not_37_out, not_38_out, F5);
  and and_10 (and_10_out, not_39_out, not_40_out, not_41_out, not_42_out, not_43_out, not_44_out, F1, not_45_out, not_46_out, not_47_out);
  and and_11 (and_11_out, not_48_out, not_49_out, not_50_out, not_51_out, not_52_out, F1, not_53_out, not_54_out, not_55_out, not_56_out);
  and and_12 (and_12_out, not_57_out, not_58_out, not_59_out, not_60_out, not_61_out, F1, not_62_out, F3, not_63_out, F5);
  and and_13 (and_13_out, not_64_out, not_65_out, not_66_out, not_67_out, not_68_out, F0, F2, not_69_out, not_70_out, F5);
  and and_14 (and_14_out, not_71_out, OP3, not_72_out, not_73_out);
  and and_15 (and_15_out, not_74_out, OP3, not_75_out, not_76_out);
  and and_16 (and_16_out, not_77_out, not_78_out, OP2, not_79_out, not_80_out, OP5);
  and and_17 (and_17_out, OP0, OP1, not_81_out, not_82_out, not_83_out);
  and and_18 (SysCALL, not_84_out, not_85_out, not_86_out, not_87_out, not_88_out, not_89_out, not_90_out, not_91_out, F2, F3, not_92_out, not_93_out);
  and and_19 (and_19_out, not_94_out, OP3, not_95_out, not_96_out);
  and and_20 (and_20_out, not_97_out, OP1, OP2, not_98_out, not_99_out, not_100_out);
  and and_21 (and_21_out, OP0, not_101_out, OP2, not_102_out, not_103_out, not_104_out);
  and and_22 (and_22_out, not_105_out, not_106_out, not_107_out, not_108_out, not_109_out, not_110_out, not_111_out, not_112_out, not_113_out, not_114_out);
  and and_23 (and_23_out, not_115_out, not_116_out, not_117_out, not_118_out, not_119_out, not_120_out, not_121_out, not_122_out, not_123_out, F5);
  and and_24 (and_24_out, not_124_out, not_125_out, not_126_out, not_127_out, not_128_out, not_129_out, not_130_out, F1, not_131_out, not_132_out, not_133_out);
  and and_25 (and_25_out, not_134_out, not_135_out, not_136_out, not_137_out, not_138_out, not_139_out, F1, not_140_out, not_141_out, not_142_out, not_143_out);
  and and_26 (and_26_out, not_144_out, not_145_out, not_146_out, not_147_out, not_148_out, not_149_out, F1, not_150_out, F3, not_151_out, F5);
  and and_27 (and_27_out, not_152_out, not_153_out, not_154_out, not_155_out, not_156_out, not_157_out, F0, F2, not_158_out, not_159_out, F5);
  and and_28 (BEQ, not_160_out, not_161_out, OP2, not_162_out, not_163_out, not_164_out);
  and and_29 (BNE, OP0, not_165_out, OP2, not_166_out, not_167_out, not_168_out);
  and and_30 (JR, not_169_out, not_170_out, not_171_out, not_172_out, not_173_out, not_174_out, not_175_out, not_176_out, not_177_out, F3, not_178_out, not_179_out);
  and and_31 (and_31_out, not_180_out, not_181_out, not_182_out, not_183_out, not_184_out, not_185_out, not_186_out, not_187_out, F3, not_188_out, not_189_out);
  and and_32 (and_32_out, OP1, not_190_out, not_191_out, not_192_out, not_193_out);
  and and_33 (JAL, OP0, OP1, not_194_out, not_195_out, not_196_out, not_197_out);
  and and_34 (BLEZ, not_198_out, OP1, OP2, not_199_out, not_200_out, not_201_out);
  and and_35 (SRLV, not_202_out, not_203_out, not_204_out, not_205_out, not_206_out, not_207_out, not_208_out, F1, F2, not_209_out, not_210_out, not_211_out);
  and and_36 (LBU, not_212_out, not_213_out, OP2, not_214_out, not_215_out, OP5);
  or or_1 (MemToReg, and_1_out, and_2_out);
  or or_2 (ALU_SRC, and_4_out, and_5_out, and_6_out, and_7_out);
  or or_3 (RegWrite, and_8_out, and_9_out, and_10_out, and_11_out, and_12_out, and_13_out, and_14_out, and_15_out, and_16_out, and_17_out);
  or or_4 (SignedExt, and_19_out, and_20_out, and_21_out);
  or or_5 (RegDst, and_22_out, and_23_out, and_24_out, and_25_out, and_26_out, and_27_out);
  or or_6 (JUMP, and_31_out, and_32_out);
endmodule

// ALU
module MIPS_ALU (
  input  [4:0] shamt,
  input  [31:0] X,
  input  [31:0] Y,
  input  [3:0] AluOP,
  output Equal,
  output [31:0] Result,
  output [31:0] Result_2
);

  wire [0:0] comparator_1_lt, comparator_2_lt;
  wire [31:0] adder_1_out, AND_out, divider_1_out, divider_1_rem, multiplier_1_cout, multiplier_1_out,
       NOR_out, OR_out, shifter_1_out, shifter_2_out, shifter_3_out, subtractor_1_out, XOR_out;

  assign AND_out = X & Y;  // AND_Gate AND, 32 bits wide
  assign OR_out = X | Y;  // OR_Gate OR, 32 bits wide
  Shifter #(.width(32), .shift("ll")) shifter_1 (.in(Y), .\dist (shamt), .out(shifter_1_out));
  Shifter #(.width(32), .shift("ar")) shifter_2 (.in(Y), .\dist (shamt), .out(shifter_2_out));
  Shifter #(.width(32), .shift("lr")) shifter_3 (.in(Y), .\dist (shamt), .out(shifter_3_out));
  Multiplier #(.width(32)) multiplier_1 (.a(X), .b(Y), .out(multiplier_1_out), .cout(multiplier_1_cout));  // open: cin
  Divider #(.width(32)) divider_1 (.a(X), .b(Y), .out(divider_1_out), .rem(divider_1_rem));  // open: upper
  Adder #(.width(32)) adder_1 (.a(X), .b(Y), .out(adder_1_out));  // open: cin, cout
  Subtractor #(.width(32)) subtractor_1 (.a(X), .b(Y), .out(subtractor_1_out));  // open: bin, bout
  assign XOR_out = X ^ Y;  // XOR_Gate XOR, 32 bits wide
  assign NOR_out = ~(X | Y);  // NOR_Gate NOR, 32 bits wide
  Comparator #(.width(32), .mode("twosComplement")) comparator_1 (
    .a(X), .b(Y), .eq(Equal), .lt(comparator_1_lt[0]));  // open: gt
  Comparator #(.width(32), .mode("unsigned")) comparator_2 (.a(X), .b(Y), .lt(comparator_2_lt[0]));  // open: gt, eq
  Multiplexer #(.select(4), .width(32), .disabled("Z"), .enable("false")) multiplexer_1 (
    .in0(shifter_1_out), .in1(shifter_2_out), .in2(shifter_3_out), .in3(multiplier_1_out),
    .in4(divider_1_out), .in5(adder_1_out), .in6(subtractor_1_out), .in7(AND_out), .in8(OR_out),
    .in9(XOR_out), .in10(NOR_out), .in11({{31{1'b0}}, comparator_1_lt[0]}),
    .in12({{31{1'b0}}, comparator_2_lt[0]}), .in13({32{1'b0}}), .in14({32{1'b0}}), .in15({32{1'b0}}),
    .out(Result), .sel(AluOP));
  Multiplexer #(.select(4), .width(32), .disabled("Z"), .enable("false")) multiplexer_2 (
    .in0({32{1'b0}}), .in1({32{1'b0}}), .in2({32{1'b0}}), .in3(multiplier_1_cout), .in4(divider_1_rem),
    .in5({32{1'b0}}), .in6({32{1'b0}}), .in7({32{1'b0}}), .in8({32{1'b0}}), .in9({32{1'b0}}),
    .in10({32{1'b0}}), .in11({32{1'b0}}), .in12({32{1'b0}}), .in13({32{1'b0}}), .in14({32{1'b0}}),
    .in15({32{1'b0}}), .out(Result_2), .sel(AluOP));

  // Other names for the same wires on the sheet: Result2[31:0] = Result_2; S[3:0] = AluOP

  // Notes on the sheet:
  //   不要改变此引脚区域内容，也不要改变ALU封装形式
  //   输入引脚
  //   输出引脚
endmodule

module MIPS_Regifile (
  input  [31:0] Din,
  input  Clk,
  input  WE,
  input  [4:0] R1_num,
  input  [4:0] W_num,
  input  [4:0] R2_num,
  output [31:0] R1,
  output [31:0] R2
);

  // RegisterFile registerfile_1: pin names not known; wires that end beside it: Din, Clk, WE, W_num, R1_num, R2_num, R1, R2
endmodule

module \理想流水线  (
  output RegWrite,
  output MemWrite,
  output [31:0] IF_PC,
  output [31:0] ID_PC,
  output [31:0] EX_PC,
  output [31:0] M_PC,
  output [31:0] WB_PC,
  output [31:0] RDin,
  output [31:0] MDin,
  output [31:0] LedData
);

  wire and_1_out, and_2_out, and_3_out, and_4_out, and_5_out, CLK, clock_2_out, comparator_1_eq,
       comparator_1_lt, comparator_2_eq, controlled_buffer_1_out, d_ff_1_q, EX_AluSrcB, EX_Beq, EX_BLEZ,
       EX_Bne, EX_LBU, EX_MemToReg, EX_MemWrite, EX_RegWrite, EX_SIGNEDEXT, EX_SRLV, EX_Syscall, Go, Halt,
       ID_AluSrcB, ID_Beq, ID_BLEZ, ID_Bne, ID_LBU, ID_MemToReg, ID_MemWrite, ID_RegWrite, ID_SIGNEDEXT,
       ID_SRLV, ID_Syscall, IR1, IR2, IR3, JAL, JMP, JR, MEM_LBU, MEM_MemToReg, MEM_RegWrite, MEM_Syscall,
       mips_alu_1_equal, nand_1_out, not_1_out, not_2_out, not_3_out, not_4_out, or_1_out, PCSrc, RegDst,
       Reset, RST, W1, W2, W3, WB_MemToReg, WB_Syscall;
  wire [3:0] EX_AluOP, ID_AluOP;
  wire [4:0] EX_REG, EX_shamt, ID_REG, MEM_REG, multiplexer_3_out, multiplexer_4_out, multiplexer_5_out,
       multiplexer_8_out, WB_REG;
  wire [12:0] CNT_num;
  wire [15:0] \LoadUse次数 , \总周期数 , \插入气泡数 , \无条件分支数 , \条件分支成功数 ;
  wire [25:0] addr;
  wire [31:0] a0, EX_EXT, EX_IR, EX_PC_4, EX_RESULT, EX_RS, EX_UEXT, EXT, ID_EXT, ID_PC_4, ID_RS, ID_RT,
       ID_UEXT, IF_IR, IF_PC_4, MEM_ALU, MEM_IR, MEM_RAM, MEM_RS, MEM_RT, multiplexer_1_out,
       multiplexer_7_out, PC_imm, ram_1_data, shifter_1_out, WB_ALU, WB_IR, WB_RAM, WB_RS, WB_RT,
       WriteBackData;
  wire [31:26] ID_IR;

  Button \u_总复位  (.out(RST));
  Button _1 (.out(IR1));
  Button _2 (.out(IR2));
  Button _3 (.out(IR3));
  // Probe on \总周期数 
  // Probe on \总周期数 
  Button \u_继续运行  (.out(Go));
  LED #(.active("true")) led_1 (.in(W1));
  LED #(.active("true")) led_2 (.in(W2));
  LED #(.active("true")) led_3 (.in(W3));
  Hex_Digit_Display hex_digit_display_1 (.value(LedData[31:28]));  // open: dp
  // Probe on IF_PC[19:0]
  // Mips_Probe mips_probe_1: pin names not known; wires that end beside it: IF_IR
  Hex_Digit_Display hex_digit_display_2 (.value(LedData[23:20]));  // open: dp
  Hex_Digit_Display hex_digit_display_3 (.value(LedData[27:24]));  // open: dp
  // Probe on ID_PC[19:0]
  // Mips_Probe mips_probe_2: pin names not known; wires that end beside it: {ID_IR, addr}
  Multiplexer #(.select(3), .width(32), .disabled("Z"), .enable("false")) multiplexer_1 (
    .in0(IF_PC_4), .in1(PC_imm), .in2({ID_PC[31:28], addr, 2'b00}), .in6(EX_RS), .out(multiplexer_1_out),
    .sel({JR, JMP, PCSrc}));  // open: in3, in4, in5, in7
  not not_1 (not_1_out, Halt);
  Hex_Digit_Display hex_digit_display_4 (.value(LedData[19:16]));  // open: dp
  Hex_Digit_Display hex_digit_display_5 (.value(LedData[15:12]));  // open: dp
  Register #(.width(32), .trigger("rising"), .Select("low")) PC (
    .D(multiplexer_1_out), .en(not_1_out), .Q(IF_PC), .clk(CLK), .clr(RST));
  Hex_Digit_Display hex_digit_display_6 (.value(LedData[11:8]));  // open: dp
  Hex_Digit_Display hex_digit_display_7 (.value(LedData[7:4]));  // open: dp
  Clock #(.highDuration(1), .lowDuration(1)) clock_1 (.out(CLK));
  // Probe on EX_PC[19:0]
  // Mips_Probe mips_probe_3: pin names not known; wires that end beside it: EX_IR
  Adder #(.width(32)) adder_1 (.a(IF_PC), .b(32'h4), .out(IF_PC_4));  // open: cin, cout
  Hex_Digit_Display hex_digit_display_8 (.value(LedData[3:0]));  // open: dp
  ROM #(.addrWidth(10), .dataWidth(32), .Select("high")) rom_1 (.addr(IF_PC[11:2]), .data(IF_IR));
  // Probe on \总周期数 
  // Probe on M_PC[19:0]
  // Mips_Probe mips_probe_4: pin names not known; wires that end beside it: MEM_IR
  // Mips_Probe mips_probe_5: pin names not known; wires that end beside it: IF_IR
  // Probe on \总周期数 
  // Probe on \无条件分支数 
  // Probe on \条件分支成功数 
  // Probe on \插入气泡数 
  // Probe on \LoadUse次数 
  \理想IF_ID  \u_理想if_id_1  (
    .PC(IF_PC), .IR(IF_IR), .PC_2(ID_PC), .IR_2({ID_IR, addr}), .in_1(CLK), .PC_4(IF_PC_4), .PC_4_2(ID_PC_4));
  // Probe on IF_PC[11:0]
  // Probe on WB_PC[19:0]
  // Mips_Probe mips_probe_6: pin names not known; wires that end beside it: IF_PC, IF_IR, WB_IR
  // Probe on ID_PC[11:0]
  // Probe on EX_PC[11:0]
  // Probe on M_PC[11:0]
  D_Flip_Flop #(.trigger("high"), .Pre_Clr_Positions("LEGACY"), .NegatePresetClear("false"), .enable("true"), .NewFFLayout("false")) d_ff_1 (.Q(d_ff_1_q));  // open: clk, D, Qn, preset, en, reset
  // Probe on 13'hc
  Multiplexer #(.select(1), .width(5), .disabled("Z"), .enable("false")) multiplexer_2 (
    .in0(addr[20:16]), .in1(addr[15:11]), .out(ID_REG), .sel(RegDst));
  // Probe on WB_PC[11:0]
  Comparator #(.width(13), .mode("twosComplement")) comparator_1 (
    .a(CNT_num), .b(13'hc), .eq(comparator_1_eq), .lt(comparator_1_lt));  // open: gt
  Clock #(.highDuration(1), .lowDuration(1)) clock_2 (.out(clock_2_out));
  \单周期硬布线控制器  \u_单周期硬布线控制器_1  (
    .Func(addr[5:0]), .OP(ID_IR), .ALU_OP(ID_AluOP), .MemToReg(ID_MemToReg), .MemWrite(ID_MemWrite),
    .ALU_SRC(ID_AluSrcB), .RegWrite(ID_RegWrite), .SysCALL(ID_Syscall), .SignedExt(ID_SIGNEDEXT),
    .RegDst(RegDst), .JR(JR), .JMP(JMP), .Beq(ID_Beq), .JAL(JAL), .Bne(ID_Bne), .BLEZ(ID_BLEZ),
    .SRLV(ID_SRLV), .LBU(ID_LBU));
  Multiplexer #(.select(1), .width(5), .disabled("Z"), .enable("false")) multiplexer_3 (
    .in0(addr[25:21]), .in1(5'b00010), .out(multiplexer_3_out), .sel(ID_Syscall));
  Multiplexer #(.select(1), .width(5), .disabled("Z"), .enable("false")) multiplexer_4 (
    .in0(addr[20:16]), .in1(5'b00100), .out(multiplexer_4_out), .sel(ID_Syscall));
  assign ID_UEXT = {{16{1'b0}}, addr[15:0]};  // Bit_Extender bit_extender_1
  assign ID_EXT = {{16{addr[15]}}, addr[15:0]};  // Bit_Extender bit_extender_2
  nand nand_1 (nand_1_out, d_ff_1_q, comparator_1_eq);
  Counter #(.width(13), .max('h1fff), .ongoal("stay"), .trigger("rising"), .behavior("old")) counter_1 (
    .count(comparator_1_lt), .Q(CNT_num), .clk(clock_2_out));  // open: load, D, carry, clr, preset
  Multiplexer #(.select(1), .width(5), .disabled("Z"), .enable("false")) multiplexer_5 (
    .in0(WB_REG), .in1({5{1'b1}}), .out(multiplexer_5_out), .sel(JAL));
  Multiplexer #(.select(1), .width(32), .disabled("Z"), .enable("false")) multiplexer_6 (
    .in0(WriteBackData), .in1(ID_PC_4), .out(RDin), .sel(JAL));
  assign controlled_buffer_1_out = nand_1_out ? clock_2_out : 1'bz;  // Controlled_Buffer controlled_buffer_1
  Pull_Resistor #(.pull(1)) pull_resistor_1 (.node(controlled_buffer_1_out));
  MIPS_Regifile mips_regifile_1 (
    .Din(RDin), .Clk(CLK), .R1(ID_RS), .R2(ID_RT), .WE(RegWrite), .W_num(multiplexer_5_out),
    .R1_num(multiplexer_3_out), .R2_num(multiplexer_4_out));
  \理想ID_EX  \u_理想id_ex_1  (
    .in_1(CLK), .PC(ID_PC), .REGWRITE(ID_RegWrite), .MEMTOREG(ID_MemToReg), .MEMWRITE(ID_MemWrite),
    .ALUOP(ID_AluOP), .BNE(ID_Bne), .BEQ(ID_Beq), .ALUSRC(ID_AluSrcB), .RS(ID_RS), .RT(ID_RT),
    .WRITEREG(ID_REG), .SIGNEXT(ID_EXT), .PC_4(ID_PC_4), .out_23(EX_PC), .out_25(EX_RegWrite),
    .out_26(EX_MemToReg), .out_27(EX_MemWrite), .out_28(EX_AluOP), .out_29(EX_Bne), .out_30(EX_Beq),
    .out_31(EX_AluSrcB), .out_37(EX_RS), .out_38(a0), .out_39(EX_REG), .out_41(EX_EXT), .out_43(EX_PC_4),
    .SIGNEXTU(ID_UEXT), .out_42(EX_UEXT), .SIGH(ID_SIGNEDEXT), .out_40(EX_SIGNEDEXT), .LBU(ID_LBU),
    .out_32(EX_LBU), .BLEZ(ID_BLEZ), .out_33(EX_BLEZ), .SRLV(ID_SRLV), .out_34(EX_SRLV), .SHAMT(addr[10:6]),
    .out_35(EX_shamt), .IR({ID_IR, addr}), .out_24(EX_IR), .SYSCALL(ID_Syscall), .out_36(EX_Syscall));
  Button button_1 (.out(Reset));
  Counter #(.width(16), .max('hffff), .ongoal("wrap"), .trigger("rising"), .behavior("old")) counter_2 (
    .count(not_2_out), .Q(\总周期数 ), .clk(CLK));  // open: load, D, carry, clr, preset
  not not_2 (not_2_out, Halt);
  Shifter #(.width(32), .shift("ll")) shifter_1 (.in(EX_EXT), .\dist (5'b00010), .out(shifter_1_out));
  Multiplexer #(.select(1), .width(32), .disabled("Z"), .enable("false")) multiplexer_7 (
    .in0(a0), .in1(EXT), .out(multiplexer_7_out), .sel(EX_AluSrcB));
  Multiplexer #(.select(1), .width(5), .disabled("Z"), .enable("false")) multiplexer_8 (
    .in0(EX_shamt), .in1(EX_RS[4:0]), .out(multiplexer_8_out), .sel(EX_SRLV));
  Multiplexer #(.select(1), .width(32), .disabled("Z"), .enable("false")) multiplexer_9 (
    .in0(EX_UEXT), .in1(EX_EXT), .out(EXT), .sel(EX_SIGNEDEXT));
  not not_3 (not_3_out, mips_alu_1_equal);
  and and_1 (and_1_out, not_3_out, EX_Bne);
  and and_2 (and_2_out, EX_Beq, mips_alu_1_equal);
  or or_1 (or_1_out, mips_alu_1_equal, EX_RESULT[0]);
  MIPS_ALU mips_alu_1 (
    .X(EX_RS), .Y(multiplexer_7_out), .AluOP(EX_AluOP), .Equal(mips_alu_1_equal), .Result(EX_RESULT),
    .shamt(multiplexer_8_out));  // open: Result_2
  Adder #(.width(32)) adder_2 (.a(shifter_1_out), .b(EX_PC_4), .out(PC_imm));  // open: cin, cout
  or or_2 (PCSrc, and_1_out, and_2_out, and_3_out);
  and and_3 (and_3_out, EX_BLEZ, or_1_out);
  Comparator #(.width(32), .mode("twosComplement")) comparator_2 (
    .a(WB_RS), .b(32'h22), .eq(comparator_2_eq));  // open: gt, lt
  not not_4 (not_4_out, comparator_2_eq);
  \理想EX_MEM  \u_理想ex_mem_1  (
    .in_1(CLK), .PC(EX_PC), .REGWRITE(EX_RegWrite), .MEMTOREG(EX_MemToReg), .MEMWRITE(EX_MemWrite),
    .RESULT(EX_RESULT), .WRITEDATA(a0), .WRITEREG(EX_REG), .out_14(M_PC), .out_16(MEM_RegWrite),
    .out_17(MEM_MemToReg), .out_18(MemWrite), .out_21(MEM_ALU), .out_22(MDin), .out_24(MEM_REG),
    .LBU(EX_LBU), .out_19(MEM_LBU), .IR(EX_IR), .out_15(MEM_IR), .SYSTEM(EX_Syscall), .out_20(MEM_Syscall),
    .RS(EX_RS), .out_23(MEM_RS), .RT(a0), .out_25(MEM_RT));
  and and_4 (and_4_out, WB_Syscall, comparator_2_eq);
  and and_5 (and_5_out, WB_Syscall, not_4_out);
  Register #(.width(1), .trigger("rising"), .Select("low")) register_1 (
    .D(and_5_out), .en(and_5_out), .Q(Halt), .clk(CLK), .clr(Go));
  Register #(.width(32), .trigger("rising"), .Select("low")) register_2 (
    .D(WB_RT), .en(and_4_out), .Q(LedData), .clk(CLK), .clr(Reset));
  RAM #(.addrWidth(10), .dataWidth(32), .bus("separate"), .Select("high")) ram_1 (
    .addr(MEM_ALU[11:2]), .din(MDin), .data(ram_1_data), .str(MemWrite), .clk(CLK), .clr(Reset));  // open: sel, ld
  Multiplexer #(.select(1), .width(32), .disabled("Z"), .enable("false")) multiplexer_10 (
    .in0(ram_1_data), .in1({{24{1'b0}}, ram_1_data[7:0]}), .out(MEM_RAM), .sel(MEM_LBU));
  \理想MEM_WB  \u_理想mem_wb_1  (
    .in_11(CLK), .PC(M_PC), .REGWRITE(MEM_RegWrite), .MEMTOREG(MEM_MemToReg), .ALU(MEM_ALU), .RAM(MEM_RAM),
    .WRITEREG(MEM_REG), .out_12(WB_PC), .out_14(RegWrite), .out_15(WB_MemToReg), .out_17(WB_ALU),
    .out_19(WB_RAM), .out_21(WB_REG), .IR(MEM_IR), .out_13(WB_IR), .SYSTEM(MEM_Syscall), .out_16(WB_Syscall),
    .RS(MEM_RS), .out_18(WB_RS), .RT(MEM_RT), .out_20(WB_RT));
  Multiplexer #(.select(1), .width(32), .disabled("Z"), .enable("false")) multiplexer_11 (
    .in0(WB_ALU), .in1(WB_RAM), .out(WriteBackData), .sel(WB_MemToReg));

  // Other names for the same wires on the sheet: EX_RT[31:0] = a0; EX_WRITEDATA[31:0] = a0; MEM_MemWrite = MemWrite;
  //   MEM_PC[31:0] = M_PC; MEM_RESULT[31:0] = MEM_ALU; MEM_WRITEDATA[31:0] = MDin; ID_IR[25:0] = addr;
  //   PC_J[31:2] = {ID_PC[31:28], addr}; ID_shamt[4:0] = addr[10:6]; PC_rst[31:0] = EX_RS; v0[31:0] = EX_RS;
  //   WB_RegWrite = RegWrite

  // Notes on the sheet:
  //   中断源
  //   时空图监测，可删除
  //   中断等待指示
  //   数码管输出
  //   指令存储器
  //   contents of rom_1 (hex, n*v repeats v):
  //   2011fff1 112020 20020022 c 22310001 1a20fffb 2002000a c
  //   指令字
  //   控制位
  //   OP
  //   rs
  //   rt
  //   rd
  //   流水调试日志用
  //   暂停节拍，不能为0
  //   JMP
  //   JR
  //   OP
  //   Func
  //   Func
  //   v0
  //   a0
  //   戳工具置1进入计数暂停模式，ctrl+k时钟自动运行到对应节拍暂停
  //   ctrl+k关闭时钟连续运行，将控制位置零，进入单步调试模式调试
  //   用这个时钟源需要去掉电路中的其他时钟源
  //   Beq
  //   Bne
  //   MemToReg
  //   MemWrite
  //   AluOP
  //   AluSrcB
  //   RegWrite
  //   JAL
  //   RegDst
  //   Syscall
  //   可计数暂停的时钟源
  //   为方便自动评测，需要输出流水线各段保存的PC值，注意是PC不是PC+4，另外ID段寄存器写入信息，Mem段内存写入信息也要输出
endmodule

module used (
  input  OP0,
  input  OP1,
  input  OP2,
  input  OP3,
  input  OP4,
  input  OP5,
  input  F0,
  input  F1,
  input  F2,
  input  F3,
  input  F4,
  input  F5,
  output RS,
  output RT
);

  wire and_1_out, and_2_out, and_3_out, and_4_out, and_5_out, and_6_out, and_7_out, and_8_out, and_9_out,
       and_10_out, and_11_out, and_12_out, and_13_out, and_14_out, and_15_out, and_16_out, and_17_out,
       and_18_out, and_19_out, and_20_out, and_21_out, and_22_out, and_23_out, and_24_out, and_25_out,
       and_26_out, and_27_out, not_1_out, not_2_out, not_3_out, not_4_out, not_5_out, not_6_out, not_7_out,
       not_8_out, not_9_out, not_10_out, not_11_out, not_12_out, not_13_out, not_14_out, not_15_out,
       not_16_out, not_17_out, not_18_out, not_19_out, not_20_out, not_21_out, not_22_out, not_23_out,
       not_24_out, not_25_out, not_26_out, not_27_out, not_28_out, not_29_out, not_30_out, not_31_out,
       not_32_out, not_33_out, not_34_out, not_35_out, not_36_out, not_37_out, not_38_out, not_39_out,
       not_40_out, not_41_out, not_42_out, not_43_out, not_44_out, not_45_out, not_46_out, not_47_out,
       not_48_out, not_49_out, not_50_out, not_51_out, not_52_out, not_53_out, not_54_out, not_55_out,
       not_56_out, not_57_out, not_58_out, not_59_out, not_60_out, not_61_out, not_62_out, not_63_out,
       not_64_out, not_65_out, not_66_out, not_67_out, not_68_out, not_69_out, not_70_out, not_71_out,
       not_72_out, not_73_out, not_74_out, not_75_out, not_76_out, not_77_out, not_78_out, not_79_out,
       not_80_out, not_81_out, not_82_out, not_83_out, not_84_out, not_85_out, not_86_out, not_87_out,
       not_88_out, not_89_out, not_90_out, not_91_out, not_92_out, not_93_out, not_94_out, not_95_out,
       not_96_out, not_97_out, not_98_out, not_99_out, not_100_out, not_101_out, not_102_out, not_103_out,
       not_104_out, not_105_out, not_106_out, not_107_out, not_108_out, not_109_out, not_110_out,
       not_111_out, not_112_out, not_113_out, not_114_out, not_115_out, not_116_out, not_117_out,
       not_118_out, not_119_out, not_120_out, not_121_out, not_122_out, not_123_out, not_124_out,
       not_125_out, not_126_out, not_127_out, not_128_out, not_129_out, not_130_out, not_131_out,
       not_132_out, not_133_out, not_134_out, not_135_out, not_136_out, not_137_out, not_138_out,
       not_139_out, not_140_out, not_141_out, not_142_out, not_143_out, not_144_out, not_145_out,
       not_146_out, not_147_out, not_148_out, not_149_out, not_150_out, not_151_out, not_152_out,
       not_153_out, not_154_out, not_155_out, not_156_out, not_157_out, not_158_out, not_159_out,
       not_160_out, not_161_out, not_162_out, not_163_out, not_164_out, not_165_out, not_166_out,
       not_167_out, not_168_out, not_169_out, not_170_out, not_171_out, not_172_out, not_173_out,
       not_174_out, not_175_out, not_176_out, not_177_out, not_178_out, not_179_out, not_180_out,
       not_181_out, not_182_out, not_183_out, not_184_out, not_185_out, not_186_out, not_187_out,
       not_188_out, not_189_out, not_190_out, not_191_out, not_192_out, not_193_out, not_194_out,
       not_195_out, not_196_out, not_197_out, not_198_out, not_199_out, not_200_out, not_201_out,
       not_202_out, not_203_out;

  not not_1 (not_1_out, OP0);
  not not_2 (not_2_out, OP1);
  not not_3 (not_3_out, OP4);
  not not_4 (not_4_out, OP5);
  not not_5 (not_5_out, F0);
  not not_6 (not_6_out, F2);
  not not_7 (not_7_out, F3);
  not not_8 (not_8_out, F4);
  not not_9 (not_9_out, OP0);
  not not_10 (not_10_out, OP1);
  not not_11 (not_11_out, OP4);
  not not_12 (not_12_out, OP5);
  not not_13 (not_13_out, F1);
  not not_14 (not_14_out, F3);
  not not_15 (not_15_out, F4);
  not not_16 (not_16_out, OP0);
  not not_17 (not_17_out, OP1);
  not not_18 (not_18_out, OP4);
  not not_19 (not_19_out, OP5);
  not not_20 (not_20_out, F0);
  not not_21 (not_21_out, F1);
  not not_22 (not_22_out, F4);
  not not_23 (not_23_out, F5);
  not not_24 (not_24_out, OP0);
  not not_25 (not_25_out, OP1);
  not not_26 (not_26_out, OP4);
  not not_27 (not_27_out, OP5);
  not not_28 (not_28_out, F2);
  not not_29 (not_29_out, F4);
  not not_30 (not_30_out, OP0);
  not not_31 (not_31_out, OP1);
  not not_32 (not_32_out, OP4);
  not not_33 (not_33_out, OP5);
  not not_34 (not_34_out, F0);
  not not_35 (not_35_out, F3);
  not not_36 (not_36_out, F4);
  not not_37 (not_37_out, F5);
  not not_38 (not_38_out, OP0);
  not not_39 (not_39_out, OP1);
  not not_40 (not_40_out, OP4);
  not not_41 (not_41_out, OP5);
  not not_42 (not_42_out, F3);
  not not_43 (not_43_out, F4);
  not not_44 (not_44_out, OP2);
  not not_45 (not_45_out, OP4);
  not not_46 (not_46_out, OP5);
  not not_47 (not_47_out, OP0);
  not not_48 (not_48_out, OP3);
  not not_49 (not_49_out, OP4);
  not not_50 (not_50_out, OP5);
  not not_51 (not_51_out, OP1);
  not not_52 (not_52_out, OP4);
  not not_53 (not_53_out, OP5);
  not not_54 (not_54_out, OP2);
  not not_55 (not_55_out, OP4);
  not not_56 (not_56_out, OP5);
  not not_57 (not_57_out, OP4);
  not not_58 (not_58_out, OP3);
  not not_59 (not_59_out, OP2);
  not not_60 (not_60_out, OP1);
  not not_61 (not_61_out, OP0);
  not not_62 (not_62_out, F5);
  not not_63 (not_63_out, F4);
  not not_64 (not_64_out, F3);
  not not_65 (not_65_out, F2);
  not not_66 (not_66_out, F1);
  not not_67 (not_67_out, F0);
  not not_68 (not_68_out, OP5);
  not not_69 (not_69_out, OP4);
  not not_70 (not_70_out, OP3);
  not not_71 (not_71_out, OP2);
  not not_72 (not_72_out, OP1);
  not not_73 (not_73_out, OP0);
  not not_74 (not_74_out, F5);
  not not_75 (not_75_out, F4);
  not not_76 (not_76_out, F3);
  not not_77 (not_77_out, F2);
  not not_78 (not_78_out, OP5);
  not not_79 (not_79_out, OP4);
  not not_80 (not_80_out, OP3);
  not not_81 (not_81_out, OP2);
  not not_82 (not_82_out, OP1);
  not not_83 (not_83_out, OP0);
  not not_84 (not_84_out, F5);
  not not_85 (not_85_out, F4);
  not not_86 (not_86_out, F3);
  not not_87 (not_87_out, F2);
  not not_88 (not_88_out, F0);
  not not_89 (not_89_out, OP5);
  not not_90 (not_90_out, OP4);
  not not_91 (not_91_out, OP3);
  not not_92 (not_92_out, OP2);
  not not_93 (not_93_out, OP1);
  not not_94 (not_94_out, OP0);
  not not_95 (not_95_out, F4);
  not not_96 (not_96_out, F3);
  not not_97 (not_97_out, F2);
  not not_98 (not_98_out, F1);
  not not_99 (not_99_out, F0);
  not not_100 (not_100_out, OP5);
  not not_101 (not_101_out, OP4);
  not not_102 (not_102_out, OP3);
  not not_103 (not_103_out, OP2);
  not not_104 (not_104_out, OP1);
  not not_105 (not_105_out, OP0);
  not not_106 (not_106_out, F4);
  not not_107 (not_107_out, F3);
  not not_108 (not_108_out, F2);
  not not_109 (not_109_out, F1);
  not not_110 (not_110_out, OP5);
  not not_111 (not_111_out, OP4);
  not not_112 (not_112_out, OP3);
  not not_113 (not_113_out, OP2);
  not not_114 (not_114_out, OP1);
  not not_115 (not_115_out, OP0);
  not not_116 (not_116_out, F4);
  not not_117 (not_117_out, F3);
  not not_118 (not_118_out, F2);
  not not_119 (not_119_out, F0);
  not not_120 (not_120_out, OP5);
  not not_121 (not_121_out, OP4);
  not not_122 (not_122_out, OP3);
  not not_123 (not_123_out, OP2);
  not not_124 (not_124_out, OP1);
  not not_125 (not_125_out, OP0);
  not not_126 (not_126_out, F4);
  not not_127 (not_127_out, F3);
  not not_128 (not_128_out, F1);
  not not_129 (not_129_out, F0);
  not not_130 (not_130_out, OP5);
  not not_131 (not_131_out, OP4);
  not not_132 (not_132_out, OP3);
  not not_133 (not_133_out, OP2);
  not not_134 (not_134_out, OP1);
  not not_135 (not_135_out, OP0);
  not not_136 (not_136_out, F4);
  not not_137 (not_137_out, F3);
  not not_138 (not_138_out, F1);
  not not_139 (not_139_out, OP5);
  not not_140 (not_140_out, OP4);
  not not_141 (not_141_out, OP3);
  not not_142 (not_142_out, OP2);
  not not_143 (not_143_out, OP1);
  not not_144 (not_144_out, OP0);
  not not_145 (not_145_out, F4);
  not not_146 (not_146_out, F3);
  not not_147 (not_147_out, OP5);
  not not_148 (not_148_out, OP4);
  not not_149 (not_149_out, OP3);
  not not_150 (not_150_out, OP2);
  not not_151 (not_151_out, OP1);
  not not_152 (not_152_out, OP0);
  not not_153 (not_153_out, F4);
  not not_154 (not_154_out, F2);
  not not_155 (not_155_out, F0);
  not not_156 (not_156_out, OP5);
  not not_157 (not_157_out, OP4);
  not not_158 (not_158_out, OP3);
  not not_159 (not_159_out, OP2);
  not not_160 (not_160_out, OP1);
  not not_161 (not_161_out, OP0);
  not not_162 (not_162_out, F4);
  not not_163 (not_163_out, F2);
  not not_164 (not_164_out, OP5);
  not not_165 (not_165_out, OP4);
  not not_166 (not_166_out, OP3);
  not not_167 (not_167_out, OP2);
  not not_168 (not_168_out, OP1);
  not not_169 (not_169_out, OP0);
  not not_170 (not_170_out, F5);
  not not_171 (not_171_out, F4);
  not not_172 (not_172_out, F1);
  not not_173 (not_173_out, F0);
  not not_174 (not_174_out, OP5);
  not not_175 (not_175_out, OP4);
  not not_176 (not_176_out, OP3);
  not not_177 (not_177_out, OP1);
  not not_178 (not_178_out, OP0);
  not not_179 (not_179_out, OP5);
  not not_180 (not_180_out, OP4);
  not not_181 (not_181_out, OP3);
  not not_182 (not_182_out, OP1);
  not not_183 (not_183_out, OP4);
  not not_184 (not_184_out, OP2);
  not not_185 (not_185_out, OP5);
  not not_186 (not_186_out, OP3);
  not not_187 (not_187_out, OP2);
  not not_188 (not_188_out, OP1);
  not not_189 (not_189_out, OP0);
  not not_190 (not_190_out, F5);
  not not_191 (not_191_out, F2);
  not not_192 (not_192_out, F1);
  not not_193 (not_193_out, F0);
  not not_194 (not_194_out, OP5);
  not not_195 (not_195_out, OP4);
  not not_196 (not_196_out, OP3);
  not not_197 (not_197_out, OP2);
  not not_198 (not_198_out, OP1);
  not not_199 (not_199_out, OP0);
  not not_200 (not_200_out, F5);
  not not_201 (not_201_out, F4);
  not not_202 (not_202_out, F3);
  not not_203 (not_203_out, F0);
  and and_1 (and_1_out, not_1_out, not_2_out, not_3_out, not_4_out, not_5_out, not_6_out, not_7_out, not_8_out, F5);
  and and_2 (and_2_out, not_9_out, not_10_out, not_11_out, not_12_out, not_13_out, not_14_out, not_15_out, F5);
  and and_3 (and_3_out, not_16_out, not_17_out, not_18_out, not_19_out, not_20_out, not_21_out, F3, not_22_out, not_23_out);
  and and_4 (and_4_out, not_24_out, not_25_out, not_26_out, not_27_out, F1, not_28_out, F3, not_29_out, F5);
  and and_5 (and_5_out, not_30_out, not_31_out, not_32_out, not_33_out, not_34_out, F1, F2, not_35_out, not_36_out, not_37_out);
  and and_6 (and_6_out, not_38_out, not_39_out, not_40_out, not_41_out, F0, F2, not_42_out, not_43_out, F5);
  and and_7 (and_7_out, not_44_out, OP3, not_45_out, not_46_out);
  and and_8 (and_8_out, not_47_out, OP2, not_48_out, not_49_out, not_50_out);
  and and_9 (and_9_out, not_51_out, OP2, not_52_out, not_53_out);
  and and_10 (and_10_out, OP0, OP1, not_54_out, not_55_out, OP5);
  and and_11 (and_11_out, not_56_out, not_57_out, not_58_out, not_59_out, not_60_out, not_61_out, not_62_out, not_63_out, not_64_out, not_65_out, not_66_out, not_67_out);
  and and_12 (and_12_out, not_68_out, not_69_out, not_70_out, not_71_out, not_72_out, not_73_out, not_74_out, not_75_out, not_76_out, not_77_out, F1, F0);
  and and_13 (and_13_out, not_78_out, not_79_out, not_80_out, not_81_out, not_82_out, not_83_out, not_84_out, not_85_out, not_86_out, not_87_out, F1, not_88_out);
  and and_14 (and_14_out, not_89_out, not_90_out, not_91_out, not_92_out, not_93_out, not_94_out, F5, not_95_out, not_96_out, not_97_out, not_98_out, not_99_out);
  and and_15 (and_15_out, not_100_out, not_101_out, not_102_out, not_103_out, not_104_out, not_105_out, F5, not_106_out, not_107_out, not_108_out, not_109_out, F0);
  and and_16 (and_16_out, not_110_out, not_111_out, not_112_out, not_113_out, not_114_out, not_115_out, F5, not_116_out, not_117_out, not_118_out, F1, not_119_out);
  and and_17 (and_17_out, not_120_out, not_121_out, not_122_out, not_123_out, not_124_out, not_125_out, F5, not_126_out, not_127_out, F2, not_128_out, not_129_out);
  and and_18 (and_18_out, not_130_out, not_131_out, not_132_out, not_133_out, not_134_out, not_135_out, F5, not_136_out, not_137_out, F2, not_138_out, F0);
  and and_19 (and_19_out, not_139_out, not_140_out, not_141_out, not_142_out, not_143_out, not_144_out, F5, not_145_out, not_146_out, F2, F1, F0);
  and and_20 (and_20_out, not_147_out, not_148_out, not_149_out, not_150_out, not_151_out, not_152_out, F5, not_153_out, F3, not_154_out, F1, not_155_out);
  and and_21 (and_21_out, not_156_out, not_157_out, not_158_out, not_159_out, not_160_out, not_161_out, F5, not_162_out, F3, not_163_out, F1, F0);
  and and_22 (and_22_out, not_164_out, not_165_out, not_166_out, not_167_out, not_168_out, not_169_out, not_170_out, not_171_out, F3, F2, not_172_out, not_173_out);
  and and_23 (and_23_out, not_174_out, not_175_out, not_176_out, OP2, not_177_out, not_178_out);
  and and_24 (and_24_out, not_179_out, not_180_out, not_181_out, OP2, not_182_out, OP0);
  and and_25 (and_25_out, OP5, not_183_out, OP3, not_184_out, OP1, OP0);
  and and_26 (and_26_out, not_185_out, OP4, not_186_out, not_187_out, not_188_out, not_189_out, not_190_out, F4, F3, not_191_out, not_192_out, not_193_out);
  and and_27 (and_27_out, not_194_out, not_195_out, not_196_out, not_197_out, not_198_out, not_199_out, not_200_out, not_201_out, not_202_out, F2, F1, not_203_out);
  or or_1 (RS, and_1_out, and_2_out, and_3_out, and_4_out, and_5_out, and_6_out, and_7_out, and_8_out, and_9_out, and_10_out);
  or or_2 (RT, and_11_out, and_12_out, and_13_out, and_14_out, and_15_out, and_16_out, and_17_out, and_18_out, and_19_out, and_20_out, and_21_out, and_22_out, and_23_out, and_24_out, and_25_out, and_26_out, and_27_out);
endmodule

module \气泡流水线  (
  output RegWrite,
  output MemWrite,
  output [31:0] IF_PC,
  output [31:0] ID_PC,
  output [31:0] EX_PC,
  output [31:0] M_PC,
  output [31:0] WB_PC,
  output [31:0] RDin,
  output [31:0] MDin,
  output [31:0] LedData
);

  wire and_1_out, and_2_out, and_3_out, and_4_out, and_5_out, and_6_out, and_7_out, and_8_out, CLK,
       clock_2_out, comparator_1_eq, comparator_1_lt, comparator_2_eq, controlled_buffer_1_out, d_ff_1_q,
       EX_AluSrcB, EX_Beq, EX_BLEZ, EX_Bne, EX_CLR, EX_JAL, EX_JMP, EX_JR, EX_LBU, EX_MemToReg, EX_MemWrite,
       EX_RegWrite, EX_SRLV, EX_Syscall, Go, Halt, ID_AluSrcB, ID_Beq, ID_BLEZ, ID_Bne, ID_JAL, ID_JMP,
       ID_JR, ID_LBU, ID_MemToReg, ID_MemWrite, ID_RegWrite, ID_SIGNEDEXT, ID_SRLV, ID_Syscall, IR1, IR2,
       IR3, MEM_JAL, MEM_LBU, MEM_MemToReg, MEM_RegWrite, MEM_Syscall, mips_alu_1_equal, nand_1_out,
       not_1_out, not_2_out, not_3_out, not_4_out, not_5_out, not_6_out, not_7_out, not_8_out, or_1_out,
       or_2_out, or_4_out, PCSrc, RegDst, Reset, RST, STALL, W1, W2, W3, WB_JAL, WB_MemToReg, WB_Syscall;
  wire [3:0] EX_AluOP, ID_AluOP;
  wire [4:0] EX_REG, EX_shamt, ID_REG, MEM_REG, multiplexer_5_out, multiplexer_9_out, RS, RT, WB_REG;
  wire [5:0] FUNC;
  wire [12:0] CNT_num;
  wire [15:0] \LoadUse次数 , \总周期数 , \插入气泡数 , \无条件分支数 , \条件分支成功数 ;
  wire [25:0] EX_addr;
  wire [25:6] ID_addr;
  wire [31:0] a0, bit_extender_1_out, bit_extender_2_out, EX_EXT, EX_IR, EX_PC_4, EX_RESULT, EX_RS, EX_RT,
       ID_EXT, ID_PC_4, ID_RS, ID_RT, IF_IR, IF_PC_4, MEM_ALU, MEM_IR, MEM_PC_4, MEM_RAM, MEM_RS,
       multiplexer_1_out, PC_imm, ram_1_data, shifter_1_out, WB_ALU, WB_IR, WB_PC_4, WB_RAM, WB_RS, WB_RT,
       WriteBackData;
  wire [31:26] ID_IR;

  Button \u_总复位  (.out(RST));
  Button _1 (.out(IR1));
  Button _2 (.out(IR2));
  Button _3 (.out(IR3));
  // Probe on \总周期数 
  // Probe on \总周期数 
  Button \u_继续运行  (.out(Go));
  LED #(.active("true")) led_1 (.in(W1));
  LED #(.active("true")) led_2 (.in(W2));
  LED #(.active("true")) led_3 (.in(W3));
  and and_1 (and_1_out, CLK, not_1_out);
  not not_1 (not_1_out, Halt);
  and and_2 (and_2_out, CLK, not_2_out);
  not not_2 (not_2_out, Halt);
  Hex_Digit_Display hex_digit_display_1 (.value(LedData[31:28]));  // open: dp
  // Probe on IF_PC[19:0]
  // Mips_Probe mips_probe_1: pin names not known; wires that end beside it: IF_IR
  Counter #(.width(16), .max('hffff), .ongoal("wrap"), .trigger("rising"), .behavior("old")) counter_1 (
    .count(EX_JMP), .Q(\无条件分支数 ), .clk(and_1_out));  // open: load, D, carry, clr, preset
  Counter #(.width(16), .max('hffff), .ongoal("wrap"), .trigger("rising"), .behavior("old")) counter_2 (
    .count(STALL), .Q(\插入气泡数 ), .clk(and_2_out));  // open: load, D, carry, clr, preset
  Hex_Digit_Display hex_digit_display_2 (.value(LedData[23:20]));  // open: dp
  Hex_Digit_Display hex_digit_display_3 (.value(LedData[27:24]));  // open: dp
  // Probe on ID_PC[19:0]
  // Mips_Probe mips_probe_2: pin names not known; wires that end beside it: {ID_IR, ID_addr, FUNC}
  Multiplexer #(.select(3), .width(32), .disabled("Z"), .enable("false")) multiplexer_1 (
    .in0(IF_PC_4), .in1(PC_imm), .in2({EX_PC[31:28], EX_addr, 2'b00}), .in6(EX_RS), .out(multiplexer_1_out),
    .sel({EX_JR, EX_JMP, PCSrc}));  // open: in3, in4, in5, in7
  not not_3 (not_3_out, or_1_out);
  or or_1 (or_1_out, STALL, Halt);
  Hex_Digit_Display hex_digit_display_4 (.value(LedData[15:12]));  // open: dp
  Hex_Digit_Display hex_digit_display_5 (.value(LedData[19:16]));  // open: dp
  Register #(.width(32), .trigger("rising"), .Select("low")) PC (
    .D(multiplexer_1_out), .en(not_3_out), .Q(IF_PC), .clk(CLK), .clr(RST));
  Hex_Digit_Display hex_digit_display_6 (.value(LedData[7:4]));  // open: dp
  Hex_Digit_Display hex_digit_display_7 (.value(LedData[11:8]));  // open: dp
  Clock #(.highDuration(1), .lowDuration(1)) clock_1 (.out(CLK));
  // Probe on EX_PC[19:0]
  // Mips_Probe mips_probe_3: pin names not known; wires that end beside it: EX_IR
  Counter #(.width(16), .max('hffff), .ongoal("wrap"), .trigger("rising"), .behavior("old")) counter_3 (
    .count(PCSrc), .Q(\条件分支成功数 ), .clk(and_3_out));  // open: load, D, carry, clr, preset
  and and_3 (and_3_out, CLK, not_4_out);
  not not_4 (not_4_out, Halt);
  Adder #(.width(32)) adder_1 (.a(IF_PC), .b(32'h4), .out(IF_PC_4));  // open: cin, cout
  Hex_Digit_Display hex_digit_display_8 (.value(LedData[3:0]));  // open: dp
  ROM #(.addrWidth(10), .dataWidth(32), .Select("high")) rom_1 (.addr(IF_PC[11:2]), .data(IF_IR));
  // Probe on \总周期数 
  // Probe on M_PC[19:0]
  // Mips_Probe mips_probe_4: pin names not known; wires that end beside it: MEM_IR
  // Mips_Probe mips_probe_5: pin names not known; wires that end beside it: IF_IR
  // Probe on \总周期数 
  // Probe on \无条件分支数 
  // Probe on \条件分支成功数 
  // Probe on \插入气泡数 
  // Probe on \LoadUse次数 
  not not_5 (not_5_out, STALL);
  \气泡IF_ID  \u_气泡if_id_1  (
    .PC(IF_PC), .IR(IF_IR), .PC_2(ID_PC), .IR_2({ID_IR, ID_addr, FUNC}), .in_1(CLK), .PC_4(IF_PC_4),
    .PC_4_2(ID_PC_4), .BRANCH(EX_CLR), .EN(not_5_out));
  // Probe on IF_PC[11:0]
  // Probe on WB_PC[19:0]
  // Mips_Probe mips_probe_6: pin names not known; wires that end beside it: IF_PC, IF_IR, WB_IR
  // Probe on ID_PC[11:0]
  // Probe on EX_PC[11:0]
  // Probe on M_PC[11:0]
  D_Flip_Flop #(.trigger("high"), .Pre_Clr_Positions("LEGACY"), .NegatePresetClear("false"), .enable("true"), .NewFFLayout("false")) d_ff_1 (.Q(d_ff_1_q));  // open: clk, D, Qn, preset, en, reset
  // Probe on 13'h610
  Multiplexer #(.select(1), .width(5), .disabled("Z"), .enable("false")) multiplexer_2 (
    .in0(ID_addr[20:16]), .in1(ID_addr[15:11]), .out(ID_REG), .sel(RegDst));
  // Probe on WB_PC[11:0]
  Comparator #(.width(13), .mode("twosComplement")) comparator_1 (
    .a(CNT_num), .b(13'h610), .eq(comparator_1_eq), .lt(comparator_1_lt));  // open: gt
  Clock #(.highDuration(1), .lowDuration(1)) clock_2 (.out(clock_2_out));
  \单周期硬布线控制器  \u_单周期硬布线控制器_1  (
    .Func(FUNC), .OP(ID_IR), .ALU_OP(ID_AluOP), .MemToReg(ID_MemToReg), .MemWrite(ID_MemWrite),
    .ALU_SRC(ID_AluSrcB), .RegWrite(ID_RegWrite), .SysCALL(ID_Syscall), .SignedExt(ID_SIGNEDEXT),
    .RegDst(RegDst), .JR(ID_JR), .JMP(ID_JMP), .Beq(ID_Beq), .JAL(ID_JAL), .Bne(ID_Bne), .BLEZ(ID_BLEZ),
    .SRLV(ID_SRLV), .LBU(ID_LBU));
  Multiplexer #(.select(1), .width(5), .disabled("Z"), .enable("false")) multiplexer_3 (
    .in0(ID_addr[25:21]), .in1(5'b00010), .out(RS), .sel(ID_Syscall));
  Multiplexer #(.select(1), .width(5), .disabled("Z"), .enable("false")) multiplexer_4 (
    .in0(ID_addr[20:16]), .in1(5'b00100), .out(RT), .sel(ID_Syscall));
  assign bit_extender_1_out = {{16{1'b0}}, {ID_addr[15:6], FUNC}};  // Bit_Extender bit_extender_1
  assign bit_extender_2_out = {{16{ID_addr[15]}}, {ID_addr[15:6], FUNC}};  // Bit_Extender bit_extender_2
  nand nand_1 (nand_1_out, d_ff_1_q, comparator_1_eq);
  Counter #(.width(13), .max('h1fff), .ongoal("stay"), .trigger("rising"), .behavior("old")) counter_4 (
    .count(comparator_1_lt), .Q(CNT_num), .clk(clock_2_out));  // open: load, D, carry, clr, preset
  Multiplexer #(.select(1), .width(5), .disabled("Z"), .enable("false")) multiplexer_5 (
    .in0(WB_REG), .in1({5{1'b1}}), .out(multiplexer_5_out), .sel(WB_JAL));
  Multiplexer #(.select(1), .width(32), .disabled("Z"), .enable("false")) multiplexer_6 (
    .in0(WriteBackData), .in1(WB_PC_4), .out(RDin), .sel(WB_JAL));
  Multiplexer #(.select(1), .width(32), .disabled("Z"), .enable("false")) multiplexer_7 (
    .in0(bit_extender_1_out), .in1(bit_extender_2_out), .out(ID_EXT), .sel(ID_SIGNEDEXT));
  assign controlled_buffer_1_out = nand_1_out ? clock_2_out : 1'bz;  // Controlled_Buffer controlled_buffer_1
  Pull_Resistor #(.pull(1)) pull_resistor_1 (.node(controlled_buffer_1_out));
  MIPS_Regifile mips_regifile_1 (
    .Din(RDin), .Clk(CLK), .R1(ID_RS), .R2(ID_RT), .WE(RegWrite), .W_num(multiplexer_5_out), .R1_num(RS),
    .R2_num(RT));
  or or_2 (or_2_out, STALL, EX_CLR);
  \气泡ID_EX  \u_气泡id_ex_1  (
    .in_1(CLK), .PC(ID_PC), .REGWRITE(ID_RegWrite), .MEMTOREG(ID_MemToReg), .MEMWRITE(ID_MemWrite),
    .ALUOP(ID_AluOP), .BNE(ID_Bne), .BEQ(ID_Beq), .ALUSRC(ID_AluSrcB), .RS(ID_RS), .RT(ID_RT),
    .WRITEREG(ID_REG), .SIGNEXT(ID_EXT), .PC_4(ID_PC_4), .out_27(EX_PC), .out_28(EX_RegWrite),
    .out_29(EX_MemToReg), .out_30(EX_MemWrite), .out_31(EX_AluOP), .out_32(EX_Bne), .out_33(EX_Beq),
    .out_34(EX_AluSrcB), .out_43(EX_RS), .out_44(EX_RT), .out_45(EX_REG), .out_46(EX_EXT), .out_47(EX_PC_4),
    .LBU(ID_LBU), .out_35(EX_LBU), .BLEZ(ID_BLEZ), .out_37(EX_BLEZ), .SRLV(ID_SRLV), .out_39(EX_SRLV),
    .SHAMT(ID_addr[10:6]), .out_42(EX_shamt), .IR({ID_IR, ID_addr, FUNC}), .out_26(EX_IR),
    .SYSCALL(ID_Syscall), .out_40(EX_Syscall), .CLR(or_2_out), .JR(ID_JR), .out_38(EX_JR), .JMP(ID_JMP),
    .out_36(EX_JMP), .addr({ID_addr, FUNC}), .out_48(EX_addr), .JAL(ID_JAL), .out_41(EX_JAL));
  Multiplexer #(.select(1), .width(32), .disabled("Z"), .enable("false")) multiplexer_8 (
    .in0(EX_RT), .in1(EX_EXT), .out(a0), .sel(EX_AluSrcB));
  Multiplexer #(.select(1), .width(5), .disabled("Z"), .enable("false")) multiplexer_9 (
    .in0(EX_shamt), .in1(EX_RS[4:0]), .out(multiplexer_9_out), .sel(EX_SRLV));
  Shifter #(.width(32), .shift("ll")) shifter_1 (.in(EX_EXT), .\dist (5'b00010), .out(shifter_1_out));
  \数据相关处理  \u_数据相关处理_1  (
    .OP(ID_IR), .FUNC(FUNC), .EX_REGWRITE(EX_RegWrite), .MEM_REGWRITE(MEM_RegWrite), .EX_WRITEREG(EX_REG),
    .MEM_WRITEREG(MEM_REG), .RS(RS), .RT(RT), .STALL(STALL));
  or or_3 (EX_CLR, EX_JMP, PCSrc);
  not not_6 (not_6_out, mips_alu_1_equal);
  and and_4 (and_4_out, not_6_out, EX_Bne);
  and and_5 (and_5_out, EX_Beq, mips_alu_1_equal);
  or or_4 (or_4_out, mips_alu_1_equal, EX_RESULT[0]);
  MIPS_ALU mips_alu_1 (
    .X(EX_RS), .Y(a0), .AluOP(EX_AluOP), .Equal(mips_alu_1_equal), .Result(EX_RESULT),
    .shamt(multiplexer_9_out));  // open: Result_2
  Adder #(.width(32)) adder_2 (.a(shifter_1_out), .b(EX_PC_4), .out(PC_imm));  // open: cin, cout
  or or_5 (PCSrc, and_4_out, and_5_out, and_6_out);
  and and_6 (and_6_out, EX_BLEZ, or_4_out);
  Button button_1 (.out(Reset));
  Counter #(.width(16), .max('hffff), .ongoal("wrap"), .trigger("rising"), .behavior("old")) counter_5 (
    .count(not_7_out), .Q(\总周期数 ), .clk(CLK));  // open: load, D, carry, clr, preset
  not not_7 (not_7_out, Halt);
  \气泡EX_MEM  \u_气泡ex_mem_1  (
    .in_1(CLK), .PC(EX_PC), .REGWRITE(EX_RegWrite), .MEMTOREG(EX_MemToReg), .MEMWRITE(EX_MemWrite),
    .RESULT(EX_RESULT), .WRITEDATA(EX_RT), .WRITEREG(EX_REG), .out_15(M_PC), .out_17(MEM_RegWrite),
    .out_18(MEM_MemToReg), .out_20(MemWrite), .out_23(MEM_ALU), .out_24(MDin), .out_26(MEM_REG),
    .LBU(EX_LBU), .out_21(MEM_LBU), .IR(EX_IR), .out_16(MEM_IR), .SYSTEM(EX_Syscall), .out_22(MEM_Syscall),
    .JAL(EX_JAL), .out_19(MEM_JAL), .PC_4(EX_PC_4), .out_25(MEM_PC_4), .RS(EX_RS), .out_27(MEM_RS));
  Comparator #(.width(32), .mode("twosComplement")) comparator_2 (
    .a(WB_RS), .b(32'h22), .eq(comparator_2_eq));  // open: gt, lt
  RAM #(.addrWidth(10), .dataWidth(32), .bus("separate"), .Select("high")) ram_1 (
    .addr(MEM_ALU[11:2]), .din(MDin), .data(ram_1_data), .str(MemWrite), .clk(CLK), .clr(Reset));  // open: sel, ld
  not not_8 (not_8_out, comparator_2_eq);
  Multiplexer #(.select(1), .width(32), .disabled("Z"), .enable("false")) multiplexer_10 (
    .in0(ram_1_data), .in1({{24{1'b0}}, ram_1_data[7:0]}), .out(MEM_RAM), .sel(MEM_LBU));
  and and_7 (and_7_out, WB_Syscall, comparator_2_eq);
  and and_8 (and_8_out, WB_Syscall, not_8_out);
  Register #(.width(1), .trigger("rising"), .Select("low")) register_1 (
    .D(and_8_out), .en(and_8_out), .Q(Halt), .clk(CLK), .clr(Go));
  \气泡MEM_WB  \u_气泡mem_wb_1  (
    .in_12(CLK), .PC(M_PC), .REGWRITE(MEM_RegWrite), .MEMTOREG(MEM_MemToReg), .ALU(MEM_ALU), .RAM(MEM_RAM),
    .WRITEREG(MEM_REG), .out_14(WB_PC), .out_16(RegWrite), .out_18(WB_MemToReg), .out_20(WB_ALU),
    .out_21(WB_RAM), .out_23(WB_REG), .IR(MEM_IR), .out_15(WB_IR), .SYSTEM(MEM_Syscall), .out_19(WB_Syscall),
    .JAL(MEM_JAL), .out_17(WB_JAL), .PC_4(MEM_PC_4), .out_22(WB_PC_4), .RS(MEM_RS), .out_24(WB_RS),
    .RT(MDin), .out_25(WB_RT));
  Register #(.width(32), .trigger("rising"), .Select("low")) register_2 (
    .D(WB_RT), .en(and_7_out), .Q(LedData), .clk(CLK), .clr(Reset));
  Multiplexer #(.select(1), .width(32), .disabled("Z"), .enable("false")) multiplexer_11 (
    .in0(WB_ALU), .in1(WB_RAM), .out(WriteBackData), .sel(WB_MemToReg));

  // Other names for the same wires on the sheet: ID_addr[5:0] = FUNC; ID_IR[25:0] = {ID_addr, FUNC};
  //   ID_shamt[4:0] = ID_addr[10:6]; OP[5:0] = ID_IR; MEM_MemWrite = MemWrite; MEM_PC[31:0] = M_PC;
  //   MEM_RESULT[31:0] = MEM_ALU; MEM_WRITEDATA[31:0] = MDin; PC_J[31:2] = {EX_PC[31:28], EX_addr};
  //   PC_rst[31:0] = EX_RS; v0[31:0] = EX_RS; WB_RegWrite = RegWrite

  // Notes on the sheet:
  //   中断源
  //   时空图监测，可删除
  //   中断等待指示
  //   数码管输出
  //   指令存储器
  //   contents of rom_1 (hex, n*v repeats v):
  //   20090000 200b0020 34118483 20120401 118c00 129400 36318281 22520401 ad310000 2328820 21290004
  //   216bffff 1560fffb 20020022 200b0020 20090000 91310000 112020 20020022 c 21290004 216bffff 1560fff9
  //   2002000a c
  //   指令字
  //   控制位
  //   OP
  //   rs
  //   rt
  //   rd
  //   流水调试日志用
  //   暂停节拍，不能为0
  //   JMP
  //   JR
  //   OP
  //   Func
  //   Func
  //   v0
  //   a0
  //   戳工具置1进入计数暂停模式，ctrl+k时钟自动运行到对应节拍暂停
  //   ctrl+k关闭时钟连续运行，将控制位置零，进入单步调试模式调试
  //   Beq
  //   Bne
  //   MemToReg
  //   MemWrite
  //   AluOP
  //   AluSrcB
  //   RegWrite
  //   JAL
  //   RegDst
  //   Syscall
  //   可计数暂停的时钟源
  //   为方便自动评测，需要输出流水线各段保存的PC值，注意是PC不是PC+4，另外ID段寄存器写入信息，Mem段内存写入信息也要输出
endmodule

module \数据相关处理  (
  input  [5:0] OP,
  input  [5:0] FUNC,
  input  EX_REGWRITE,
  input  MEM_REGWRITE,
  input  [4:0] EX_WRITEREG,
  input  [4:0] MEM_WRITEREG,
  input  [4:0] RS,
  input  [4:0] RT,
  output STALL
);

  wire _1, _2, _3, _4, comparator_1_eq, comparator_4_eq, RS__0, RS_EX, RS_MEM, RSUSED, RT__0, RT_EX, RT_MEM,
       RTUSED;

  used used_1 (
    .OP0(OP[0]), .OP1(OP[1]), .OP2(OP[2]), .OP3(OP[3]), .OP4(OP[4]), .OP5(OP[5]), .F0(FUNC[0]), .F1(FUNC[1]),
    .F2(FUNC[2]), .F3(FUNC[3]), .F4(FUNC[4]), .F5(FUNC[5]), .RS(RSUSED), .RT(RTUSED));
  Comparator #(.width(5), .mode("twosComplement")) comparator_1 (
    .a(RS), .b({5{1'b0}}), .eq(comparator_1_eq));  // open: gt, lt
  Comparator #(.width(5), .mode("twosComplement")) comparator_2 (.a(RS), .b(EX_WRITEREG), .eq(RS_EX));  // open: gt, lt
  Comparator #(.width(5), .mode("twosComplement")) comparator_3 (
    .a(RS), .b(MEM_WRITEREG), .eq(RS_MEM));  // open: gt, lt
  Comparator #(.width(5), .mode("twosComplement")) comparator_4 (
    .a(RT), .b({5{1'b0}}), .eq(comparator_4_eq));  // open: gt, lt
  Comparator #(.width(5), .mode("twosComplement")) comparator_5 (.a(RT), .b(EX_WRITEREG), .eq(RT_EX));  // open: gt, lt
  Comparator #(.width(5), .mode("twosComplement")) comparator_6 (
    .a(RT), .b(MEM_WRITEREG), .eq(RT_MEM));  // open: gt, lt
  not not_1 (RS__0, comparator_1_eq);
  not not_2 (RT__0, comparator_4_eq);
  or or_1 (STALL, _1, _2, _3, _4);
  and and_1 (_1, RSUSED, RS__0, EX_REGWRITE, RS_EX);
  and and_2 (_2, RTUSED, RT__0, EX_REGWRITE, RT_EX);
  and and_3 (_3, RSUSED, RS__0, MEM_REGWRITE, RS_MEM);
  and and_4 (_4, RTUSED, RT__0, MEM_REGWRITE, RT_MEM);
endmodule
module \重定向流水线  (
  output RegWrite,
  output MemWrite,
  output [31:0] IF_PC,
  output [31:0] ID_PC,
  output [31:0] EX_PC,
  output [31:0] M_PC,
  output [31:0] WB_PC,
  output [31:0] RDin,
  output [31:0] MDin,
  output [31:0] LedData
);

  wire and_1_out, and_2_out, and_3_out, and_4_out, and_5_out, and_6_out, and_7_out, and_8_out, and_9_out,
       and_10_out, CLK, clock_1_out, clock_2_out, comparator_1_eq, comparator_1_lt, comparator_2_eq,
       d_ff_1_q, EX_AluSrcB, EX_Beq, EX_BLEZ, EX_Bne, EX_CLR, EX_JAL, EX_JMP, EX_JR, EX_LBU, EX_MemToReg,
       EX_MemWrite, EX_RegWrite, EX_SRLV, EX_Syscall, Go, Halt, ID_AluSrcB, ID_Beq, ID_BLEZ, ID_Bne, ID_JAL,
       ID_JMP, ID_JR, ID_LBU, ID_MemToReg, ID_MemWrite, ID_RegWrite, ID_SIGNEDEXT, ID_SRLV, ID_Syscall, IR1,
       IR2, IR3, MEM_JAL, MEM_LBU, MEM_MemToReg, MEM_RegWrite, MEM_Syscall, mips_alu_1_equal, nand_1_out,
       not_1_out, not_2_out, not_3_out, not_4_out, not_5_out, not_6_out, not_7_out, not_8_out, not_9_out,
       not_10_out, or_1_out, or_2_out, or_3_out, PCSrc, RegDst, Reset, RST, STALL, W1, W2, W3, WB_JAL,
       WB_MemToReg, WB_Syscall;
  wire [1:0] EX_RSFOWARD, EX_RTFOWARD, ID_RSFOWARD, ID_RTFOWARD;
  wire [3:0] EX_AluOP, ID_AluOP;
  wire [4:0] EX_REG, EX_shamt, ID_REG, MEM_REG, multiplexer_5_out, multiplexer_9_out, RS, RT, WB_REG;
  wire [5:0] FUNC;
  wire [12:0] CNT_num;
  wire [15:0] \LoadUse次数 , \总周期数 , \插入气泡数 , \无条件分支数 , \条件分支成功数 ;
  wire [25:0] EX_addr;
  wire [25:6] ID_addr;
  wire [31:0] a0, bit_extender_1_out, bit_extender_2_out, EX_EXT, EX_IR, EX_PC_4, EX_RESULT, EX_RS, EX_RT,
       FWDA, FWDB, ID_EXT, ID_PC_4, ID_RS, ID_RT, IF_IR, IF_PC_4, MEM_ALU, MEM_IR, MEM_PC_4, MEM_RAM, MEM_RS,
       multiplexer_1_out, PC_imm, ram_1_data, shifter_1_out, WB_ALU, WB_IR, WB_PC_4, WB_RAM, WB_RS, WB_RT,
       WriteBackData;
  wire [31:26] ID_IR;

  Button \u_总复位  (.out(RST));
  Button _1 (.out(IR1));
  Button _2 (.out(IR2));
  Button _3 (.out(IR3));
  // Probe on \总周期数 
  // Probe on \总周期数 
  Button \u_继续运行  (.out(Go));
  LED #(.active("true")) led_1 (.in(W1));
  LED #(.active("true")) led_2 (.in(W2));
  LED #(.active("true")) led_3 (.in(W3));
  and and_1 (and_1_out, CLK, not_1_out);
  not not_1 (not_1_out, Halt);
  and and_2 (and_2_out, CLK, not_2_out);
  not not_2 (not_2_out, Halt);
  Hex_Digit_Display hex_digit_display_1 (.value(LedData[31:28]));  // open: dp
  // Probe on IF_PC[19:0]
  // Mips_Probe mips_probe_1: pin names not known; wires that end beside it: IF_IR
  Counter #(.width(16), .max('hffff), .ongoal("wrap"), .trigger("rising"), .behavior("old")) counter_1 (
    .count(EX_JMP), .Q(\无条件分支数 ), .clk(and_1_out));  // open: load, D, carry, clr, preset
  Counter #(.width(16), .max('hffff), .ongoal("wrap"), .trigger("rising"), .behavior("old")) counter_2 (
    .count(STALL), .Q(\插入气泡数 ), .clk(and_2_out));  // open: load, D, carry, clr, preset
  Hex_Digit_Display hex_digit_display_2 (.value(LedData[27:24]));  // open: dp
  Hex_Digit_Display hex_digit_display_3 (.value(LedData[23:20]));  // open: dp
  // Probe on ID_PC[19:0]
  // Mips_Probe mips_probe_2: pin names not known; wires that end beside it: {ID_IR, ID_addr, FUNC}
  Multiplexer #(.select(3), .width(32), .disabled("Z"), .enable("false")) multiplexer_1 (
    .in0(IF_PC_4), .in1(PC_imm), .in2({EX_PC[31:28], EX_addr, 2'b00}), .in6(FWDA), .out(multiplexer_1_out),
    .sel({EX_JR, EX_JMP, PCSrc}));  // open: in3, in4, in5, in7
  not not_3 (not_3_out, or_1_out);
  or or_1 (or_1_out, STALL, Halt);
  Hex_Digit_Display hex_digit_display_4 (.value(LedData[15:12]));  // open: dp
  Hex_Digit_Display hex_digit_display_5 (.value(LedData[19:16]));  // open: dp
  Register #(.width(32), .trigger("rising"), .Select("low")) PC (
    .D(multiplexer_1_out), .en(not_3_out), .Q(IF_PC), .clk(CLK), .clr(RST));
  Hex_Digit_Display hex_digit_display_6 (.value(LedData[7:4]));  // open: dp
  Hex_Digit_Display hex_digit_display_7 (.value(LedData[11:8]));  // open: dp
  Clock #(.highDuration(1), .lowDuration(1)) clock_1 (.out(clock_1_out));
  // Probe on EX_PC[19:0]
  // Mips_Probe mips_probe_3: pin names not known; wires that end beside it: EX_IR, clock_1_out, CLK
  Counter #(.width(16), .max('hffff), .ongoal("wrap"), .trigger("rising"), .behavior("old")) counter_3 (
    .count(PCSrc), .Q(\条件分支成功数 ), .clk(and_3_out));  // open: load, D, carry, clr, preset
  and and_3 (and_3_out, CLK, not_4_out);
  not not_4 (not_4_out, Halt);
  Counter #(.width(16), .max('hffff), .ongoal("wrap"), .trigger("rising"), .behavior("old")) counter_4 (
    .count(STALL), .Q(\LoadUse次数 ), .clk(and_4_out));  // open: load, D, carry, clr, preset
  and and_4 (and_4_out, CLK, not_5_out);
  not not_5 (not_5_out, Halt);
  Adder #(.width(32)) adder_1 (.a(IF_PC), .b(32'h4), .out(IF_PC_4));  // open: cin, cout
  Hex_Digit_Display hex_digit_display_8 (.value(LedData[3:0]));  // open: dp
  ROM #(.addrWidth(10), .dataWidth(32), .Select("high")) rom_1 (.addr(IF_PC[11:2]), .data(IF_IR));
  // Probe on \总周期数 
  // Probe on M_PC[19:0]
  // Mips_Probe mips_probe_4: pin names not known; wires that end beside it: MEM_IR
  // Mips_Probe mips_probe_5: pin names not known; wires that end beside it: IF_IR
  // Probe on \总周期数 
  // Probe on \无条件分支数 
  // Probe on \条件分支成功数 
  // Probe on \插入气泡数 
  // Probe on \LoadUse次数 
  not not_6 (not_6_out, STALL);
  \气泡IF_ID  \u_气泡if_id_1  (
    .PC(IF_PC), .IR(IF_IR), .PC_2(ID_PC), .IR_2({ID_IR, ID_addr, FUNC}), .in_1(CLK), .PC_4(IF_PC_4),
    .PC_4_2(ID_PC_4), .BRANCH(EX_CLR), .EN(not_6_out));
  // Probe on IF_PC[11:0]
  // Probe on WB_PC[19:0]
  // Mips_Probe mips_probe_6: pin names not known; wires that end beside it: IF_PC, IF_IR, WB_IR
  // Probe on EX_PC[11:0]
  // Probe on ID_PC[11:0]
  // Probe on M_PC[11:0]
  D_Flip_Flop #(.trigger("high"), .Pre_Clr_Positions("LEGACY"), .NegatePresetClear("false"), .enable("true"), .NewFFLayout("false")) d_ff_1 (.Q(d_ff_1_q));  // open: clk, D, Qn, preset, en, reset
  // Probe on 13'hea
  Multiplexer #(.select(1), .width(5), .disabled("Z"), .enable("false")) multiplexer_2 (
    .in0(ID_addr[20:16]), .in1(ID_addr[15:11]), .out(ID_REG), .sel(RegDst));
  // Probe on WB_PC[11:0]
  Comparator #(.width(13), .mode("twosComplement")) comparator_1 (
    .a(CNT_num), .b(13'hea), .eq(comparator_1_eq), .lt(comparator_1_lt));  // open: gt
  Clock #(.highDuration(1), .lowDuration(1)) clock_2 (.out(clock_2_out));
  \单周期硬布线控制器  \u_单周期硬布线控制器_1  (
    .Func(FUNC), .OP(ID_IR), .ALU_OP(ID_AluOP), .MemToReg(ID_MemToReg), .MemWrite(ID_MemWrite),
    .ALU_SRC(ID_AluSrcB), .RegWrite(ID_RegWrite), .SysCALL(ID_Syscall), .SignedExt(ID_SIGNEDEXT),
    .RegDst(RegDst), .JR(ID_JR), .JMP(ID_JMP), .Beq(ID_Beq), .JAL(ID_JAL), .Bne(ID_Bne), .BLEZ(ID_BLEZ),
    .SRLV(ID_SRLV), .LBU(ID_LBU));
  Multiplexer #(.select(1), .width(5), .disabled("Z"), .enable("false")) multiplexer_3 (
    .in0(ID_addr[25:21]), .in1(5'b00010), .out(RS), .sel(ID_Syscall));
  Multiplexer #(.select(1), .width(5), .disabled("Z"), .enable("false")) multiplexer_4 (
    .in0(ID_addr[20:16]), .in1(5'b00100), .out(RT), .sel(ID_Syscall));
  assign bit_extender_1_out = {{16{1'b0}}, {ID_addr[15:6], FUNC}};  // Bit_Extender bit_extender_1
  assign bit_extender_2_out = {{16{ID_addr[15]}}, {ID_addr[15:6], FUNC}};  // Bit_Extender bit_extender_2
  nand nand_1 (nand_1_out, d_ff_1_q, comparator_1_eq);
  Counter #(.width(13), .max('h1fff), .ongoal("stay"), .trigger("rising"), .behavior("old")) counter_5 (
    .count(comparator_1_lt), .Q(CNT_num), .clk(clock_2_out));  // open: load, D, carry, clr, preset
  Multiplexer #(.select(1), .width(5), .disabled("Z"), .enable("false")) multiplexer_5 (
    .in0(WB_REG), .in1({5{1'b1}}), .out(multiplexer_5_out), .sel(WB_JAL));
  Multiplexer #(.select(1), .width(32), .disabled("Z"), .enable("false")) multiplexer_6 (
    .in0(WriteBackData), .in1(WB_PC_4), .out(RDin), .sel(WB_JAL));
  Multiplexer #(.select(1), .width(32), .disabled("Z"), .enable("false")) multiplexer_7 (
    .in0(bit_extender_1_out), .in1(bit_extender_2_out), .out(ID_EXT), .sel(ID_SIGNEDEXT));
  assign CLK = nand_1_out ? clock_2_out : 1'bz;  // Controlled_Buffer controlled_buffer_1
  Pull_Resistor #(.pull(1)) pull_resistor_1 (.node(CLK));
  MIPS_Regifile mips_regifile_1 (
    .Din(RDin), .Clk(CLK), .R1(ID_RS), .R2(ID_RT), .WE(RegWrite), .W_num(multiplexer_5_out), .R1_num(RS),
    .R2_num(RT));
  or or_2 (or_2_out, EX_CLR, STALL);
  \重定向ID_EX  \u_重定向id_ex_1  (
    .in_1(CLK), .PC(ID_PC), .REGWRITE(ID_RegWrite), .MEMTOREG(ID_MemToReg), .MEMWRITE(ID_MemWrite),
    .ALUOP(ID_AluOP), .BNE(ID_Bne), .BEQ(ID_Beq), .ALUSRC(ID_AluSrcB), .RS(ID_RS), .RT(ID_RT),
    .WRITEREG(ID_REG), .SIGNEXT(ID_EXT), .PC_4(ID_PC_4), .out_29(EX_PC), .out_30(EX_RegWrite),
    .out_31(EX_MemToReg), .out_32(EX_MemWrite), .out_33(EX_AluOP), .out_34(EX_Bne), .out_35(EX_Beq),
    .out_36(EX_AluSrcB), .out_46(EX_RS), .out_48(EX_RT), .out_49(EX_REG), .out_50(EX_EXT), .out_51(EX_PC_4),
    .LBU(ID_LBU), .out_37(EX_LBU), .BLEZ(ID_BLEZ), .out_39(EX_BLEZ), .SRLV(ID_SRLV), .out_41(EX_SRLV),
    .SHAMT(ID_addr[10:6]), .out_44(EX_shamt), .IR({ID_IR, ID_addr, FUNC}), .out_28(EX_IR),
    .SYSCALL(ID_Syscall), .out_42(EX_Syscall), .CLR(or_2_out), .JR(ID_JR), .out_40(EX_JR), .JMP(ID_JMP),
    .out_38(EX_JMP), .addr({ID_addr, FUNC}), .out_52(EX_addr), .JAL(ID_JAL), .out_43(EX_JAL),
    .RSFORWARD(ID_RSFOWARD), .out_45(EX_RSFOWARD), .RTFORWARD(ID_RTFOWARD), .out_47(EX_RTFOWARD));
  Multiplexer #(.select(1), .width(32), .disabled("Z"), .enable("false")) multiplexer_8 (
    .in0(FWDB), .in1(EX_EXT), .out(a0), .sel(EX_AluSrcB));
  Multiplexer #(.select(1), .width(5), .disabled("Z"), .enable("false")) multiplexer_9 (
    .in0(EX_shamt), .in1(FWDA[4:0]), .out(multiplexer_9_out), .sel(EX_SRLV));
  Shifter #(.width(32), .shift("ll")) shifter_1 (.in(EX_EXT), .\dist (5'b00010), .out(shifter_1_out));
  Loaduse loaduse_1 (
    .OP(ID_IR), .FUNC(FUNC), .EX_MEMTOREG(EX_MemToReg), .MEM_MEMTOREG(MemWrite), .EX_REGWRITE(EX_RegWrite),
    .MEM_REGWRITE(MEM_RegWrite), .EX_WRITEREG(EX_REG), .MEM_WRITEREG(MEM_REG), .RS(RS), .RT(RT),
    .STALL(STALL), .RSFOWARD(ID_RSFOWARD), .RTFOWARD(ID_RTFOWARD));
  not not_7 (not_7_out, mips_alu_1_equal);
  and and_5 (and_5_out, not_7_out, EX_Bne);
  and and_6 (and_6_out, EX_Beq, mips_alu_1_equal);
  or or_3 (or_3_out, mips_alu_1_equal, EX_RESULT[0]);
  MIPS_ALU mips_alu_1 (
    .X(FWDA), .Y(a0), .AluOP(EX_AluOP), .Equal(mips_alu_1_equal), .Result(EX_RESULT),
    .shamt(multiplexer_9_out));  // open: Result_2
  Multiplexer #(.select(2), .width(32), .disabled("Z"), .enable("false")) multiplexer_10 (
    .in0(EX_RS), .in1(WriteBackData), .in2(MEM_ALU), .out(FWDA), .sel(EX_RSFOWARD));  // open: in3
  Multiplexer #(.select(2), .width(32), .disabled("Z"), .enable("false")) multiplexer_11 (
    .in0(EX_RT), .in1(WriteBackData), .in2(MEM_ALU), .out(FWDB), .sel(EX_RTFOWARD));  // open: in3
  Adder #(.width(32)) adder_2 (.a(shifter_1_out), .b(EX_PC_4), .out(PC_imm));  // open: cin, cout
  or or_4 (EX_CLR, PCSrc, EX_JMP);
  or or_5 (PCSrc, and_5_out, and_6_out, and_7_out);
  and and_7 (and_7_out, EX_BLEZ, or_3_out);
  Button button_1 (.out(Reset));
  Counter #(.width(16), .max('hffff), .ongoal("wrap"), .trigger("rising"), .behavior("old")) counter_6 (
    .count(not_8_out), .Q(\总周期数 ), .clk(CLK));  // open: load, D, carry, clr, preset
  not not_8 (not_8_out, Halt);
  \气泡EX_MEM  \u_气泡ex_mem_1  (
    .in_1(CLK), .PC(EX_PC), .REGWRITE(EX_RegWrite), .MEMTOREG(EX_MemToReg), .MEMWRITE(EX_MemWrite),
    .RESULT(EX_RESULT), .WRITEDATA(FWDB), .WRITEREG(EX_REG), .out_15(M_PC), .out_17(MEM_RegWrite),
    .out_18(MEM_MemToReg), .out_20(MemWrite), .out_23(MEM_ALU), .out_24(MDin), .out_26(MEM_REG),
    .LBU(EX_LBU), .out_21(MEM_LBU), .IR(EX_IR), .out_16(MEM_IR), .SYSTEM(EX_Syscall), .out_22(MEM_Syscall),
    .JAL(EX_JAL), .out_19(MEM_JAL), .PC_4(EX_PC_4), .out_25(MEM_PC_4), .RS(FWDA), .out_27(MEM_RS));
  Comparator #(.width(32), .mode("twosComplement")) comparator_2 (
    .a(WB_RS), .b(32'h22), .eq(comparator_2_eq));  // open: gt, lt
  RAM #(.addrWidth(10), .dataWidth(32), .bus("separate"), .Select("high")) ram_1 (
    .addr(MEM_ALU[11:2]), .din(MDin), .data(ram_1_data), .str(MemWrite), .clk(CLK), .clr(Reset));  // open: sel, ld
  not not_9 (not_9_out, comparator_2_eq);
  Multiplexer #(.select(1), .width(32), .disabled("Z"), .enable("false")) multiplexer_12 (
    .in0(ram_1_data), .in1({{24{1'b0}}, ram_1_data[7:0]}), .out(MEM_RAM), .sel(MEM_LBU));
  and and_8 (and_8_out, WB_Syscall, comparator_2_eq);
  and and_9 (and_9_out, WB_Syscall, not_9_out);
  Register #(.width(1), .trigger("rising"), .Select("low")) register_1 (
    .D(and_9_out), .en(and_9_out), .Q(Halt), .clk(CLK), .clr(Go));
  \气泡MEM_WB  \u_气泡mem_wb_1  (
    .in_12(CLK), .PC(M_PC), .REGWRITE(MEM_RegWrite), .MEMTOREG(MEM_MemToReg), .ALU(MEM_ALU), .RAM(MEM_RAM),
    .WRITEREG(MEM_REG), .out_14(WB_PC), .out_16(RegWrite), .out_18(WB_MemToReg), .out_20(WB_ALU),
    .out_21(WB_RAM), .out_23(WB_REG), .IR(MEM_IR), .out_15(WB_IR), .SYSTEM(MEM_Syscall), .out_19(WB_Syscall),
    .JAL(MEM_JAL), .out_17(WB_JAL), .PC_4(MEM_PC_4), .out_22(WB_PC_4), .RS(MEM_RS), .out_24(WB_RS),
    .RT(MDin), .out_25(WB_RT));
  Register #(.width(32), .trigger("rising"), .Select("low")) register_2 (
    .D(WB_RT), .en(and_8_out), .Q(LedData), .clk(and_10_out), .clr(Reset));
  and and_10 (and_10_out, CLK, not_10_out);
  not not_10 (not_10_out, Halt);
  Multiplexer #(.select(1), .width(32), .disabled("Z"), .enable("false")) multiplexer_13 (
    .in0(WB_ALU), .in1(WB_RAM), .out(WriteBackData), .sel(WB_MemToReg));

  // Other names for the same wires on the sheet: ID_addr[5:0] = FUNC; ID_IR[25:0] = {ID_addr, FUNC};
  //   ID_shamt[4:0] = ID_addr[10:6]; OP[5:0] = ID_IR; MEM_MemWrite = MemWrite; MEM_PC[31:0] = M_PC;
  //   MEM_RESULT[31:0] = MEM_ALU; MEM_WRITEDATA[31:0] = MDin; PC_J[31:2] = {EX_PC[31:28], EX_addr};
  //   PC_rst[31:0] = FWDA; v0[31:0] = FWDA; WB_RegWrite = RegWrite

  // Notes on the sheet:
  //   中断源
  //   时空图监测，可删除
  //   中断等待指示
  //   数码管输出
  //   指令存储器
  //   contents of rom_1 (hex, n*v repeats v):
  //   2011fff1 112020 20020022 c 22310001 1a20fffb 2002000a c
  //   指令字
  //   控制位
  //   OP
  //   rs
  //   rt
  //   rd
  //   流水调试日志用
  //   暂停节拍，不能为0
  //   JMP
  //   JR
  //   OP
  //   Func
  //   Func
  //   v0
  //   a0
  //   戳工具置1进入计数暂停模式，ctrl+k时钟自动运行到对应节拍暂停
  //   ctrl+k关闭时钟连续运行，将控制位置零，进入单步调试模式调试
  //   Beq
  //   Bne
  //   MemToReg
  //   MemWrite
  //   AluOP
  //   AluSrcB
  //   RegWrite
  //   JAL
  //   RegDst
  //   Syscall
  //   可计数暂停的时钟源
  //   为方便自动评测，需要输出流水线各段保存的PC值，注意是PC不是PC+4，另外ID段寄存器写入信息，Mem段内存写入信息也要输出
endmodule

module Loaduse (
  input  [5:0] OP,
  input  [5:0] FUNC,
  input  EX_MEMTOREG,
  input  MEM_MEMTOREG,
  input  EX_REGWRITE,
  input  MEM_REGWRITE,
  input  [4:0] EX_WRITEREG,
  input  [4:0] MEM_WRITEREG,
  input  [4:0] RS,
  input  [4:0] RT,
  output STALL,
  output [1:0] RSFOWARD,
  output [1:0] RTFOWARD
);

  wire _1, _2, comparator_1_eq, comparator_4_eq, RS_1, RS_2, RS__0, RS_EX, RS_MEM, RSUSED, RT_1, RT_2, RT__0,
       RT_EX, RT_MEM, RTUSED;

  used used_1 (
    .OP0(OP[0]), .OP1(OP[1]), .OP2(OP[2]), .OP3(OP[3]), .OP4(OP[4]), .OP5(OP[5]), .F0(FUNC[0]), .F1(FUNC[1]),
    .F2(FUNC[2]), .F3(FUNC[3]), .F4(FUNC[4]), .F5(FUNC[5]), .RS(RSUSED), .RT(RTUSED));
  Comparator #(.width(5), .mode("twosComplement")) comparator_1 (
    .a(RS), .b({5{1'b0}}), .eq(comparator_1_eq));  // open: gt, lt
  Comparator #(.width(5), .mode("twosComplement")) comparator_2 (.a(RS), .b(EX_WRITEREG), .eq(RS_EX));  // open: gt, lt
  Comparator #(.width(5), .mode("twosComplement")) comparator_3 (
    .a(RS), .b(MEM_WRITEREG), .eq(RS_MEM));  // open: gt, lt
  Comparator #(.width(5), .mode("twosComplement")) comparator_4 (
    .a(RT), .b({5{1'b0}}), .eq(comparator_4_eq));  // open: gt, lt
  Comparator #(.width(5), .mode("twosComplement")) comparator_5 (.a(RT), .b(EX_WRITEREG), .eq(RT_EX));  // open: gt, lt
  Comparator #(.width(5), .mode("twosComplement")) comparator_6 (
    .a(RT), .b(MEM_WRITEREG), .eq(RT_MEM));  // open: gt, lt
  not not_1 (RS__0, comparator_1_eq);
  not not_2 (RT__0, comparator_4_eq);
  and and_1 (_1, RSUSED, RS__0, EX_MEMTOREG, RS_EX);
  and and_2 (_2, RTUSED, RT__0, EX_MEMTOREG, RT_EX);
  and and_3 (RS_2, RSUSED, RS__0, EX_REGWRITE, RS_EX);
  and and_4 (RS_1, RSUSED, RS__0, MEM_REGWRITE, RS_MEM);
  Priority_Encoder #(.select(2), .disabled("Z")) priority_encoder_1 (
    .in0(1'b1), .in1(RS_1), .in2(RS_2), .out(RSFOWARD));  // open: in3, gs, en_out, en_in
  and and_5 (RT_2, RTUSED, RT__0, EX_REGWRITE, RT_EX);
  and and_6 (RT_1, RTUSED, RT__0, MEM_REGWRITE, RT_MEM);
  Priority_Encoder #(.select(2), .disabled("Z")) priority_encoder_2 (
    .in0(1'b1), .in1(RT_1), .in2(RT_2), .out(RTFOWARD));  // open: in3, gs, en_out, en_in
  or or_1 (STALL, _1, _2);

  // Other names for the same wires on the sheet: EX_MEMREAD = EX_MEMTOREG; LOADUSE = STALL;
  //   MEM_MEMREAD = MEM_MEMTOREG
endmodule

module \中断按键参考电路  (
  input  \同步清零信号 ,
  output \与中断屏蔽位与 
);

  wire \_1号中断_out , and_1_out, clock_1_out, d_ff_1_q, or_1_out, or_2_out;

  Clock #(.highDuration(1), .lowDuration(1)) clock_1 (.out(clock_1_out));
  Button \_1号中断  (.out(\_1号中断_out ));
  or or_1 (or_1_out, \与中断屏蔽位与 , d_ff_1_q);
  LED #(.active("true")) \_1号中断等待指示灯  (.in(or_1_out));
  D_Flip_Flop #(.trigger("rising"), .Pre_Clr_Positions("LEGACY"), .NegatePresetClear("false"), .enable("true"), .NewFFLayout("false")) d_ff_1 (
    .clk(\_1号中断_out ), .D(1'b1), .Q(d_ff_1_q), .reset(\与中断屏蔽位与 ));  // open: Qn, preset, en
  or or_2 (or_2_out, d_ff_1_q, \与中断屏蔽位与 );
  and and_1 (and_1_out, or_2_out, ~\同步清零信号 );  // AND_Gate
  D_Flip_Flop #(.trigger("rising"), .Pre_Clr_Positions("LEGACY"), .NegatePresetClear("false"), .enable("true"), .NewFFLayout("false")) IR1 (
    .clk(clock_1_out), .D(and_1_out), .Q(\与中断屏蔽位与 ));  // open: Qn, preset, en, reset
  \单周期硬布线控制器  \u_单周期硬布线控制器_1  ();  // open: Func, OP, ALU_OP, MemToReg, MemWrite, ALU_SRC, RegWrite, SysCALL, SignedExt, RegDst, JR, JMP, Beq, JAL, Bne, BLEZ, SRLV, LBU

  // Notes on the sheet:
  //   中断信号采样参考电路
  //   Reset 
endmodule

module \单周期MIPS_单级中断  (
  input  IR1,
  input  IR2,
  input  IR3,
  output RegWrite,
  output MemWrite,
  output [31:0] PC,
  output [31:0] IR,
  output [31:0] RDin,
  output [31:0] MDin,
  output [31:0] LedData
);

  wire CLK, comparator_1_eq, comparator_2_eq, comparator_3_eq, comparator_4_eq, Go, IR1_t, IR2_t, IR3_t, IRA,
       IRB, IRC, or_1_out, W1, W2, W3;
  wire [15:0] \总周期数 ;

  Clock #(.highDuration(1), .lowDuration(1)) clock_1 (.out(CLK));
  Button _1 ();  // open: out
  Button _2 ();  // open: out
  Button _3 ();  // open: out
  Button \u_继续运行  (.out(Go));
  LED #(.active("true")) led_1 (.in(W1));
  LED #(.active("true")) led_2 (.in(W2));
  LED #(.active("true")) led_3 (.in(W3));
  Hex_Digit_Display hex_digit_display_1 (.value(LedData[31:28]));  // open: dp
  Comparator #(.width(16), .mode("twosComplement")) comparator_1 (
    .a(16'h23b), .b(\总周期数 ), .eq(comparator_1_eq));  // open: gt, lt
  Comparator #(.width(16), .mode("twosComplement")) comparator_2 (
    .a(\总周期数 ), .b(16'h1), .eq(comparator_2_eq));  // open: gt, lt
  Comparator #(.width(16), .mode("twosComplement")) comparator_3 (
    .a(\总周期数 ), .b(16'h4), .eq(comparator_3_eq));  // open: gt, lt
  Comparator #(.width(16), .mode("twosComplement")) comparator_4 (
    .a(\总周期数 ), .b(16'h7), .eq(comparator_4_eq));  // open: gt, lt
  Hex_Digit_Display hex_digit_display_2 (.value(LedData[27:24]));  // open: dp
  Hex_Digit_Display hex_digit_display_3 (.value(LedData[23:20]));  // open: dp
  or or_1 (or_1_out, comparator_1_eq, comparator_2_eq);
  assign IRA = or_1_out ? ~CLK : 1'bz;  // Controlled_Inverter controlled_inverter_1
  assign IRB = comparator_3_eq ? ~CLK : 1'bz;  // Controlled_Inverter controlled_inverter_2
  assign IRC = comparator_4_eq ? ~CLK : 1'bz;  // Controlled_Inverter controlled_inverter_3
  Hex_Digit_Display hex_digit_display_4 (.value(LedData[15:12]));  // open: dp
  Hex_Digit_Display hex_digit_display_5 (.value(LedData[19:16]));  // open: dp
  Pull_Resistor #(.pull(0)) pull_resistor_1 (.node(IRA));
  Pull_Resistor #(.pull(0)) pull_resistor_2 (.node(IRB));
  Pull_Resistor #(.pull(0)) pull_resistor_3 (.node(IRC));
  Hex_Digit_Display hex_digit_display_6 (.value(LedData[11:8]));  // open: dp
  Hex_Digit_Display hex_digit_display_7 (.value(LedData[7:4]));  // open: dp
  // Probe on \总周期数 
  Hex_Digit_Display hex_digit_display_8 (.value(LedData[3:0]));  // open: dp
  or or_2 (IR1_t, IR1, IRA);
  or or_3 (IR2_t, IR2, IRB);
  or or_4 (IR3_t, IR3, IRC);

  // Notes on the sheet:
  //   中断源
  //   中断等待指示
  //   总复位信号应将除ROM以外所有存储组件全部清零
  //   单级中断测试信号模拟器
  //   数码管输出
  //   数码管输出应该用寄存器锁存，否则显示数据只能一闪而过
  //   为方便自动评测，需要输出PC，IR，寄存器堆写如数据RDin
  //   RAM写使能MemWrite、RAM写入数据MDin等信号
endmodule

module \单周期MIPS_多级中断  (
  input  IR1,
  input  IR2,
  input  IR3,
  output RegWrite,
  output MemWrite,
  output [31:0] PC,
  output [31:0] IR,
  output [31:0] RDin,
  output [31:0] MDin,
  output [31:0] LedData
);

  wire CLK, comparator_1_eq, comparator_2_eq, comparator_3_eq, comparator_4_eq, comparator_5_eq, Go, IR1_t,
       IR2_t, IR3_t, IRA, IRB, IRC, or_1_out, or_2_out, W1, W2, W3;
  wire [15:0] \总周期数 ;

  Clock #(.highDuration(1), .lowDuration(1)) clock_1 (.out(CLK));
  Button _1 ();  // open: out
  Button _2 ();  // open: out
  Button _3 ();  // open: out
  Button \u_继续运行  (.out(Go));
  LED #(.active("true")) led_1 (.in(W1));
  LED #(.active("true")) led_2 (.in(W2));
  LED #(.active("true")) led_3 (.in(W3));
  Hex_Digit_Display hex_digit_display_1 (.value(LedData[31:28]));  // open: dp
  Comparator #(.width(16), .mode("twosComplement")) comparator_1 (
    .a(\总周期数 ), .b(16'h7), .eq(comparator_1_eq));  // open: gt, lt
  Comparator #(.width(16), .mode("twosComplement")) comparator_2 (
    .a(\总周期数 ), .b(16'h241), .eq(comparator_2_eq));  // open: gt, lt
  Hex_Digit_Display hex_digit_display_2 (.value(LedData[27:24]));  // open: dp
  Hex_Digit_Display hex_digit_display_3 (.value(LedData[23:20]));  // open: dp
  Comparator #(.width(16), .mode("twosComplement")) comparator_3 (
    .a(16'h258), .b(\总周期数 ), .eq(comparator_3_eq));  // open: gt, lt
  or or_1 (or_1_out, comparator_3_eq, comparator_4_eq);
  Comparator #(.width(16), .mode("twosComplement")) comparator_4 (
    .a(\总周期数 ), .b(16'h1), .eq(comparator_4_eq));  // open: gt, lt
  Comparator #(.width(16), .mode("twosComplement")) comparator_5 (
    .a(\总周期数 ), .b(16'h4), .eq(comparator_5_eq));  // open: gt, lt
  or or_2 (or_2_out, comparator_1_eq, comparator_2_eq);
  Hex_Digit_Display hex_digit_display_4 (.value(LedData[15:12]));  // open: dp
  Hex_Digit_Display hex_digit_display_5 (.value(LedData[19:16]));  // open: dp
  Pull_Resistor #(.pull(0)) pull_resistor_1 (.node(IRA));
  assign IRA = or_1_out ? ~CLK : 1'bz;  // Controlled_Inverter controlled_inverter_1
  Pull_Resistor #(.pull(0)) pull_resistor_2 (.node(IRB));
  assign IRB = comparator_5_eq ? ~CLK : 1'bz;  // Controlled_Inverter controlled_inverter_2
  Pull_Resistor #(.pull(0)) pull_resistor_3 (.node(IRC));
  assign IRC = or_2_out ? ~CLK : 1'bz;  // Controlled_Inverter controlled_inverter_3
  Hex_Digit_Display hex_digit_display_6 (.value(LedData[7:4]));  // open: dp
  Hex_Digit_Display hex_digit_display_7 (.value(LedData[11:8]));  // open: dp
  // Probe on \总周期数 
  Hex_Digit_Display hex_digit_display_8 (.value(LedData[3:0]));  // open: dp
  or or_3 (IR1_t, IR1, IRA);
  or or_4 (IR2_t, IR2, IRB);
  or or_5 (IR3_t, IR3, IRC);

  // Notes on the sheet:
  //   中断源
  //   中断等待指示
  //   总复位信号应将除ROM以外所有存储组件全部清零
  //   多级中断测试信号模拟器
  //   数码管输出
  //   数码管输出应该用寄存器锁存，否则显示数据只能一闪而过
  //   为方便自动评测，需要输出PC，IR，寄存器堆写如数据RDin
  //   RAM写使能MemWrite、RAM写入数据MDin等信号
endmodule

module \封装正确性测试  (
);

  wire IR1, IR2, IR3, MemW, RegW;
  wire [31:0] EX_PC, ID_PC, IF_PC, IR, LED, MDin, MDinr, MEM_PC, PC, RDin, RDinr, WB_PC;

  \单周期MIPS  \u_单周期mips_1  (
    .RegWrite(RegW), .MemWrite(MemW), .PC(PC), .IR(IR), .RDin(RDin), .MDin(MDin), .LedData(LED));  // open: IR1, IR2, IR3
  \气泡流水线  \u_气泡流水线_1  (
    .RegWrite(RegW), .MemWrite(MemW), .IF_PC(IF_PC), .ID_PC(ID_PC), .EX_PC(EX_PC), .M_PC(MEM_PC),
    .WB_PC(WB_PC), .RDin(RDinr), .MDin(MDinr), .LedData(LED));
  \单周期MIPS_单级中断  \u_单周期mips_单级中断_1  (
    .IR1(IR1), .IR2(IR2), .IR3(IR3), .RegWrite(RegW), .MemWrite(MemW), .PC(PC), .IR(IR), .RDin(RDin),
    .MDin(MDin), .LedData(LED));
  \理想流水线  \u_理想流水线_1  (
    .RegWrite(RegW), .MemWrite(MemW), .IF_PC(IF_PC), .ID_PC(ID_PC), .EX_PC(EX_PC), .M_PC(MEM_PC),
    .WB_PC(WB_PC), .RDin(RDinr), .MDin(MDinr), .LedData(LED));
  \重定向流水线  \u_重定向流水线_1  (
    .RegWrite(RegW), .MemWrite(MemW), .IF_PC(IF_PC), .ID_PC(ID_PC), .EX_PC(EX_PC), .M_PC(MEM_PC),
    .WB_PC(WB_PC), .RDin(RDinr), .MDin(MDinr), .LedData(LED));
  \单周期MIPS_多级中断  \u_单周期mips_多级中断_1  (
    .IR1(IR1), .IR2(IR2), .IR3(IR3), .RegWrite(RegW), .MemWrite(MemW), .PC(PC), .IR(IR), .RDin(RDin),
    .MDin(MDin), .LedData(LED));

  // Notes on the sheet:
  //   单周期封装测试
  //   气泡流水封装测试
  //   单周期+单级中断封装测试
  //   请检查上面封装有无位宽不匹配，引脚标签是否和连接的标签相对应，否则无法在educoder平台上正确测试
  //   理想流水封装测试
  //   重定向流水封装测试
  //   单周期+多级中断封装测试
endmodule

module \理想IF_ID  (
  input  in_1,
  input  [31:0] PC,
  input  [31:0] IR,
  input  [31:0] PC_4,
  output [31:0] PC_2,
  output [31:0] IR_2,
  output [31:0] PC_4_2
);

  Register #(.width(32), .trigger("rising"), .Select("low")) register_1 (
    .D(PC), .Q(PC_2), .clk(in_1));  // open: en, clr
  Register #(.width(32), .trigger("rising"), .Select("low")) register_2 (
    .D(IR), .Q(IR_2), .clk(in_1));  // open: en, clr
  Register #(.width(32), .trigger("rising"), .Select("low")) register_3 (
    .D(PC_4), .Q(PC_4_2), .clk(in_1));  // open: en, clr

  // Other names for the same wires on the sheet: clk = in_1
endmodule

module \理想ID_EX  (
  input  in_1,
  input  [31:0] PC,
  input  [31:0] IR,
  input  REGWRITE,
  input  MEMTOREG,
  input  MEMWRITE,
  input  [3:0] ALUOP,
  input  BNE,
  input  BEQ,
  input  ALUSRC,
  input  LBU,
  input  BLEZ,
  input  SRLV,
  input  [4:0] SHAMT,
  input  SYSCALL,
  input  [31:0] RS,
  input  [31:0] RT,
  input  [4:0] WRITEREG,
  input  SIGH,
  input  [31:0] SIGNEXT,
  input  [31:0] SIGNEXTU,
  input  [31:0] PC_4,
  output [31:0] out_23,
  output [31:0] out_24,
  output out_25,
  output out_26,
  output out_27,
  output [3:0] out_28,
  output out_29,
  output out_30,
  output out_31,
  output out_32,
  output out_33,
  output out_34,
  output [4:0] out_35,
  output out_36,
  output [31:0] out_37,
  output [31:0] out_38,
  output [4:0] out_39,
  output out_40,
  output [31:0] out_41,
  output [31:0] out_42,
  output [31:0] out_43
);

  Register #(.width(32), .trigger("rising"), .Select("low")) register_1 (
    .D(PC), .Q(out_23), .clk(in_1));  // open: en, clr
  Register #(.width(1), .trigger("rising"), .Select("low")) register_2 (
    .D(REGWRITE), .Q(out_25), .clk(in_1));  // open: en, clr
  Register #(.width(1), .trigger("rising"), .Select("low")) register_3 (
    .D(MEMTOREG), .Q(out_26), .clk(in_1));  // open: en, clr
  Register #(.width(1), .trigger("rising"), .Select("low")) register_4 (
    .D(MEMWRITE), .Q(out_27), .clk(in_1));  // open: en, clr
  Register #(.width(4), .trigger("rising"), .Select("low")) register_5 (
    .D(ALUOP), .Q(out_28), .clk(in_1));  // open: en, clr
  Register #(.width(1), .trigger("rising"), .Select("low")) register_6 (
    .D(BNE), .Q(out_29), .clk(in_1));  // open: en, clr
  Register #(.width(1), .trigger("rising"), .Select("low")) register_7 (
    .D(BEQ), .Q(out_30), .clk(in_1));  // open: en, clr
  Register #(.width(1), .trigger("rising"), .Select("low")) register_8 (
    .D(ALUSRC), .Q(out_31), .clk(in_1));  // open: en, clr
  Register #(.width(32), .trigger("rising"), .Select("low")) register_9 (
    .D(RS), .Q(out_37), .clk(in_1));  // open: en, clr
  Register #(.width(32), .trigger("rising"), .Select("low")) register_10 (
    .D(RT), .Q(out_38), .clk(in_1));  // open: en, clr
  Register #(.width(5), .trigger("rising"), .Select("low")) register_11 (
    .D(WRITEREG), .Q(out_39), .clk(in_1));  // open: en, clr
  Register #(.width(32), .trigger("rising"), .Select("low")) register_12 (
    .D(SIGNEXT), .Q(out_41), .clk(in_1));  // open: en, clr
  Register #(.width(32), .trigger("rising"), .Select("low")) register_13 (
    .D(PC_4), .Q(out_43), .clk(in_1));  // open: en, clr
  Register #(.width(32), .trigger("rising"), .Select("low")) register_14 (
    .D(IR), .Q(out_24), .clk(in_1));  // open: en, clr
  Register #(.width(1), .trigger("rising"), .Select("low")) register_15 (
    .D(LBU), .Q(out_32), .clk(in_1));  // open: en, clr
  Register #(.width(1), .trigger("rising"), .Select("low")) register_16 (
    .D(SIGH), .Q(out_40), .clk(in_1));  // open: en, clr
  Register #(.width(32), .trigger("rising"), .Select("low")) register_17 (
    .D(SIGNEXTU), .Q(out_42), .clk(in_1));  // open: en, clr
  Register #(.width(1), .trigger("rising"), .Select("low")) register_18 (
    .D(BLEZ), .Q(out_33), .clk(in_1));  // open: en, clr
  Register #(.width(1), .trigger("rising"), .Select("low")) register_19 (
    .D(SRLV), .Q(out_34), .clk(in_1));  // open: en, clr
  Register #(.width(1), .trigger("rising"), .Select("low")) register_20 (
    .D(SYSCALL), .Q(out_36), .clk(in_1));  // open: en, clr
  Register #(.width(5), .trigger("rising"), .Select("low")) register_21 (
    .D(SHAMT), .Q(out_35), .clk(in_1));  // open: en, clr

  // Other names for the same wires on the sheet: CLK = in_1
endmodule

module \理想EX_MEM  (
  input  in_1,
  input  [31:0] PC,
  input  [31:0] IR,
  input  REGWRITE,
  input  MEMTOREG,
  input  MEMWRITE,
  input  LBU,
  input  SYSTEM,
  input  [31:0] RESULT,
  input  [31:0] WRITEDATA,
  input  [31:0] RS,
  input  [4:0] WRITEREG,
  input  [31:0] RT,
  output [31:0] out_14,
  output [31:0] out_15,
  output out_16,
  output out_17,
  output out_18,
  output out_19,
  output out_20,
  output [31:0] out_21,
  output [31:0] out_22,
  output [31:0] out_23,
  output [4:0] out_24,
  output [31:0] out_25
);

  Register #(.width(32), .trigger("rising"), .Select("low")) register_1 (
    .D(PC), .Q(out_14), .clk(in_1));  // open: en, clr
  Register #(.width(1), .trigger("rising"), .Select("low")) register_2 (
    .D(REGWRITE), .Q(out_16), .clk(in_1));  // open: en, clr
  Register #(.width(1), .trigger("rising"), .Select("low")) register_3 (
    .D(MEMTOREG), .Q(out_17), .clk(in_1));  // open: en, clr
  Register #(.width(1), .trigger("rising"), .Select("low")) register_4 (
    .D(MEMWRITE), .Q(out_18), .clk(in_1));  // open: en, clr
  Register #(.width(32), .trigger("rising"), .Select("low")) register_5 (
    .D(RESULT), .Q(out_21), .clk(in_1));  // open: en, clr
  Register #(.width(32), .trigger("rising"), .Select("low")) register_6 (
    .D(WRITEDATA), .Q(out_22), .clk(in_1));  // open: en, clr
  Register #(.width(5), .trigger("rising"), .Select("low")) register_7 (
    .D(WRITEREG), .Q(out_24), .clk(in_1));  // open: en, clr
  Register #(.width(1), .trigger("rising"), .Select("low")) register_8 (
    .D(LBU), .Q(out_19), .clk(in_1));  // open: en, clr
  Register #(.width(1), .trigger("rising"), .Select("low")) register_9 (
    .D(SYSTEM), .Q(out_20), .clk(in_1));  // open: en, clr
  Register #(.width(32), .trigger("rising"), .Select("low")) register_10 (
    .D(RS), .Q(out_23), .clk(in_1));  // open: en, clr
  Register #(.width(32), .trigger("rising"), .Select("low")) register_11 (
    .D(RT), .Q(out_25), .clk(in_1));  // open: en, clr
  Register #(.width(32), .trigger("rising"), .Select("low")) register_12 (
    .D(IR), .Q(out_15), .clk(in_1));  // open: en, clr

  // Other names for the same wires on the sheet: CLK = in_1
endmodule

module \理想MEM_WB  (
  input  [31:0] PC,
  input  [31:0] IR,
  input  REGWRITE,
  input  MEMTOREG,
  input  SYSTEM,
  input  [31:0] ALU,
  input  [31:0] RS,
  input  [31:0] RAM,
  input  [31:0] RT,
  input  [4:0] WRITEREG,
  input  in_11,
  output [31:0] out_12,
  output [31:0] out_13,
  output out_14,
  output out_15,
  output out_16,
  output [31:0] out_17,
  output [31:0] out_18,
  output [31:0] out_19,
  output [31:0] out_20,
  output [4:0] out_21
);

  Register #(.width(32), .trigger("rising"), .Select("low")) register_1 (
    .D(PC), .Q(out_12), .clk(in_11));  // open: en, clr
  Register #(.width(1), .trigger("rising"), .Select("low")) register_2 (
    .D(REGWRITE), .Q(out_14), .clk(in_11));  // open: en, clr
  Register #(.width(1), .trigger("rising"), .Select("low")) register_3 (
    .D(MEMTOREG), .Q(out_15), .clk(in_11));  // open: en, clr
  Register #(.width(32), .trigger("rising"), .Select("low")) register_4 (
    .D(ALU), .Q(out_17), .clk(in_11));  // open: en, clr
  Register #(.width(32), .trigger("rising"), .Select("low")) register_5 (
    .D(RAM), .Q(out_19), .clk(in_11));  // open: en, clr
  Register #(.width(5), .trigger("rising"), .Select("low")) register_6 (
    .D(WRITEREG), .Q(out_21), .clk(in_11));  // open: en, clr
  Register #(.width(32), .trigger("rising"), .Select("low")) register_7 (
    .D(IR), .Q(out_13), .clk(in_11));  // open: en, clr
  Register #(.width(1), .trigger("rising"), .Select("low")) register_8 (
    .D(SYSTEM), .Q(out_16), .clk(in_11));  // open: en, clr
  Register #(.width(32), .trigger("rising"), .Select("low")) register_9 (
    .D(RS), .Q(out_18), .clk(in_11));  // open: en, clr
  Register #(.width(32), .trigger("rising"), .Select("low")) register_10 (
    .D(RT), .Q(out_20), .clk(in_11));  // open: en, clr

  // Other names for the same wires on the sheet: CLK = in_11
endmodule

module \气泡IF_ID  (
  input  in_1,
  input  BRANCH,
  input  EN,
  input  [31:0] PC,
  input  [31:0] IR,
  input  [31:0] PC_4,
  output [31:0] PC_2,
  output [31:0] IR_2,
  output [31:0] PC_4_2
);

  wire [31:0] multiplexer_1_out, multiplexer_2_out, multiplexer_3_out;

  Multiplexer #(.select(1), .width(32), .disabled("Z"), .enable("false")) multiplexer_1 (
    .in0(PC), .in1({32{1'b0}}), .out(multiplexer_1_out), .sel(BRANCH));
  Multiplexer #(.select(1), .width(32), .disabled("Z"), .enable("false")) multiplexer_2 (
    .in0(IR), .in1({32{1'b0}}), .out(multiplexer_2_out), .sel(BRANCH));
  Multiplexer #(.select(1), .width(32), .disabled("Z"), .enable("false")) multiplexer_3 (
    .in0(PC_4), .in1({32{1'b0}}), .out(multiplexer_3_out), .sel(BRANCH));
  Register #(.width(32), .trigger("rising"), .Select("low")) register_1 (
    .D(multiplexer_1_out), .en(EN), .Q(PC_2), .clk(in_1));  // open: clr
  Register #(.width(32), .trigger("rising"), .Select("low")) register_2 (
    .D(multiplexer_2_out), .en(EN), .Q(IR_2), .clk(in_1));  // open: clr
  Register #(.width(32), .trigger("rising"), .Select("low")) register_3 (
    .D(multiplexer_3_out), .en(EN), .Q(PC_4_2), .clk(in_1));  // open: clr

  // Other names for the same wires on the sheet: clk = in_1; CLR = BRANCH
endmodule

module \气泡ID_EX  (
  input  in_1,
  input  CLR,
  input  [31:0] IR,
  input  [31:0] PC,
  input  REGWRITE,
  input  MEMTOREG,
  input  MEMWRITE,
  input  [3:0] ALUOP,
  input  BNE,
  input  BEQ,
  input  ALUSRC,
  input  LBU,
  input  JMP,
  input  BLEZ,
  input  JR,
  input  SRLV,
  input  SYSCALL,
  input  JAL,
  input  [4:0] SHAMT,
  input  [31:0] RS,
  input  [31:0] RT,
  input  [4:0] WRITEREG,
  input  [31:0] SIGNEXT,
  input  [31:0] PC_4,
  input  [25:0] addr,
  output [31:0] out_26,
  output [31:0] out_27,
  output out_28,
  output out_29,
  output out_30,
  output [3:0] out_31,
  output out_32,
  output out_33,
  output out_34,
  output out_35,
  output out_36,
  output out_37,
  output out_38,
  output out_39,
  output out_40,
  output out_41,
  output [4:0] out_42,
  output [31:0] out_43,
  output [31:0] out_44,
  output [4:0] out_45,
  output [31:0] out_46,
  output [31:0] out_47,
  output [25:0] out_48
);

  wire multiplexer_3_out, multiplexer_4_out, multiplexer_5_out, multiplexer_7_out, multiplexer_8_out,
       multiplexer_9_out, multiplexer_10_out, multiplexer_11_out, multiplexer_12_out, multiplexer_13_out,
       multiplexer_14_out, multiplexer_15_out, multiplexer_16_out;
  wire [3:0] multiplexer_6_out;
  wire [4:0] multiplexer_17_out, multiplexer_20_out;
  wire [25:0] multiplexer_23_out;
  wire [31:0] multiplexer_1_out, multiplexer_2_out, multiplexer_18_out, multiplexer_19_out,
       multiplexer_21_out, multiplexer_22_out;

  Multiplexer #(.select(1), .width(32), .disabled("Z"), .enable("false")) multiplexer_1 (
    .in0(IR), .in1({32{1'b0}}), .out(multiplexer_1_out), .sel(CLR));
  Multiplexer #(.select(1), .width(32), .disabled("Z"), .enable("false")) multiplexer_2 (
    .in0(PC), .in1({32{1'b0}}), .out(multiplexer_2_out), .sel(CLR));
  Multiplexer #(.select(1), .width(1), .disabled("Z"), .enable("false")) multiplexer_3 (
    .in0(REGWRITE), .in1(1'b0), .out(multiplexer_3_out), .sel(CLR));
  Multiplexer #(.select(1), .width(1), .disabled("Z"), .enable("false")) multiplexer_4 (
    .in0(MEMTOREG), .in1(1'b0), .out(multiplexer_4_out), .sel(CLR));
  Multiplexer #(.select(1), .width(1), .disabled("Z"), .enable("false")) multiplexer_5 (
    .in0(MEMWRITE), .in1(1'b0), .out(multiplexer_5_out), .sel(CLR));
  Multiplexer #(.select(1), .width(4), .disabled("Z"), .enable("false")) multiplexer_6 (
    .in0(ALUOP), .in1(4'b0000), .out(multiplexer_6_out), .sel(CLR));
  Multiplexer #(.select(1), .width(1), .disabled("Z"), .enable("false")) multiplexer_7 (
    .in0(BNE), .in1(1'b0), .out(multiplexer_7_out), .sel(CLR));
  Multiplexer #(.select(1), .width(1), .disabled("Z"), .enable("false")) multiplexer_8 (
    .in0(BEQ), .in1(1'b0), .out(multiplexer_8_out), .sel(CLR));
  Multiplexer #(.select(1), .width(1), .disabled("Z"), .enable("false")) multiplexer_9 (
    .in0(ALUSRC), .in1(1'b0), .out(multiplexer_9_out), .sel(CLR));
  Multiplexer #(.select(1), .width(1), .disabled("Z"), .enable("false")) multiplexer_10 (
    .in0(LBU), .in1(1'b0), .out(multiplexer_10_out), .sel(CLR));
  Multiplexer #(.select(1), .width(1), .disabled("Z"), .enable("false")) multiplexer_11 (
    .in0(JMP), .in1(1'b0), .out(multiplexer_11_out), .sel(CLR));
  Multiplexer #(.select(1), .width(1), .disabled("Z"), .enable("false")) multiplexer_12 (
    .in0(BLEZ), .in1(1'b0), .out(multiplexer_12_out), .sel(CLR));
  Multiplexer #(.select(1), .width(1), .disabled("Z"), .enable("false")) multiplexer_13 (
    .in0(JR), .in1(1'b0), .out(multiplexer_13_out), .sel(CLR));
  Multiplexer #(.select(1), .width(1), .disabled("Z"), .enable("false")) multiplexer_14 (
    .in0(SRLV), .in1(1'b0), .out(multiplexer_14_out), .sel(CLR));
  Multiplexer #(.select(1), .width(1), .disabled("Z"), .enable("false")) multiplexer_15 (
    .in0(SYSCALL), .in1(1'b0), .out(multiplexer_15_out), .sel(CLR));
  Multiplexer #(.select(1), .width(1), .disabled("Z"), .enable("false")) multiplexer_16 (
    .in0(JAL), .in1(1'b0), .out(multiplexer_16_out), .sel(CLR));
  Multiplexer #(.select(1), .width(5), .disabled("Z"), .enable("false")) multiplexer_17 (
    .in0(SHAMT), .in1({5{1'b0}}), .out(multiplexer_17_out), .sel(CLR));
  Multiplexer #(.select(1), .width(32), .disabled("Z"), .enable("false")) multiplexer_18 (
    .in0(RS), .in1({32{1'b0}}), .out(multiplexer_18_out), .sel(CLR));
  Multiplexer #(.select(1), .width(32), .disabled("Z"), .enable("false")) multiplexer_19 (
    .in0(RT), .in1({32{1'b0}}), .out(multiplexer_19_out), .sel(CLR));
  Multiplexer #(.select(1), .width(5), .disabled("Z"), .enable("false")) multiplexer_20 (
    .in0(WRITEREG), .in1({5{1'b0}}), .out(multiplexer_20_out), .sel(CLR));
  Multiplexer #(.select(1), .width(32), .disabled("Z"), .enable("false")) multiplexer_21 (
    .in0(SIGNEXT), .in1({32{1'b0}}), .out(multiplexer_21_out), .sel(CLR));
  Multiplexer #(.select(1), .width(32), .disabled("Z"), .enable("false")) multiplexer_22 (
    .in0(PC_4), .in1({32{1'b0}}), .out(multiplexer_22_out), .sel(CLR));
  Multiplexer #(.select(1), .width(26), .disabled("Z"), .enable("false")) multiplexer_23 (
    .in0(addr), .in1({26{1'b0}}), .out(multiplexer_23_out), .sel(CLR));
  Register #(.width(32), .trigger("rising"), .Select("low")) register_1 (
    .D(multiplexer_1_out), .Q(out_26), .clk(in_1));  // open: en, clr
  Register #(.width(32), .trigger("rising"), .Select("low")) register_2 (
    .D(multiplexer_2_out), .Q(out_27), .clk(in_1));  // open: en, clr
  Register #(.width(1), .trigger("rising"), .Select("low")) register_3 (
    .D(multiplexer_3_out), .Q(out_28), .clk(in_1));  // open: en, clr
  Register #(.width(1), .trigger("rising"), .Select("low")) register_4 (
    .D(multiplexer_4_out), .Q(out_29), .clk(in_1));  // open: en, clr
  Register #(.width(1), .trigger("rising"), .Select("low")) register_5 (
    .D(multiplexer_5_out), .Q(out_30), .clk(in_1));  // open: en, clr
  Register #(.width(4), .trigger("rising"), .Select("low")) register_6 (
    .D(multiplexer_6_out), .Q(out_31), .clk(in_1));  // open: en, clr
  Register #(.width(1), .trigger("rising"), .Select("low")) register_7 (
    .D(multiplexer_7_out), .Q(out_32), .clk(in_1));  // open: en, clr
  Register #(.width(1), .trigger("rising"), .Select("low")) register_8 (
    .D(multiplexer_8_out), .Q(out_33), .clk(in_1));  // open: en, clr
  Register #(.width(1), .trigger("rising"), .Select("low")) register_9 (
    .D(multiplexer_9_out), .Q(out_34), .clk(in_1));  // open: en, clr
  Register #(.width(1), .trigger("rising"), .Select("low")) register_10 (
    .D(multiplexer_10_out), .Q(out_35), .clk(in_1));  // open: en, clr
  Register #(.width(1), .trigger("rising"), .Select("low")) register_11 (
    .D(multiplexer_11_out), .Q(out_36), .clk(in_1));  // open: en, clr
  Register #(.width(1), .trigger("rising"), .Select("low")) register_12 (
    .D(multiplexer_12_out), .Q(out_37), .clk(in_1));  // open: en, clr
  Register #(.width(1), .trigger("rising"), .Select("low")) register_13 (
    .D(multiplexer_13_out), .Q(out_38), .clk(in_1));  // open: en, clr
  Register #(.width(1), .trigger("rising"), .Select("low")) register_14 (
    .D(multiplexer_14_out), .Q(out_39), .clk(in_1));  // open: en, clr
  Register #(.width(1), .trigger("rising"), .Select("low")) register_15 (
    .D(multiplexer_15_out), .Q(out_40), .clk(in_1));  // open: en, clr
  Register #(.width(1), .trigger("rising"), .Select("low")) register_16 (
    .D(multiplexer_16_out), .Q(out_41), .clk(in_1));  // open: en, clr
  Register #(.width(5), .trigger("rising"), .Select("low")) register_17 (
    .D(multiplexer_17_out), .Q(out_42), .clk(in_1));  // open: en, clr
  Register #(.width(32), .trigger("rising"), .Select("low")) register_18 (
    .D(multiplexer_18_out), .Q(out_43), .clk(in_1));  // open: en, clr
  Register #(.width(32), .trigger("rising"), .Select("low")) register_19 (
    .D(multiplexer_19_out), .Q(out_44), .clk(in_1));  // open: en, clr
  Register #(.width(5), .trigger("rising"), .Select("low")) register_20 (
    .D(multiplexer_20_out), .Q(out_45), .clk(in_1));  // open: en, clr
  Register #(.width(32), .trigger("rising"), .Select("low")) register_21 (
    .D(multiplexer_21_out), .Q(out_46), .clk(in_1));  // open: en, clr
  Register #(.width(32), .trigger("rising"), .Select("low")) register_22 (
    .D(multiplexer_22_out), .Q(out_47), .clk(in_1));  // open: en, clr
  Register #(.width(26), .trigger("rising"), .Select("low")) register_23 (
    .D(multiplexer_23_out), .Q(out_48), .clk(in_1));  // open: en, clr

  // Other names for the same wires on the sheet: CLK = in_1
endmodule

module \气泡EX_MEM  (
  input  in_1,
  input  [31:0] PC,
  input  [31:0] IR,
  input  REGWRITE,
  input  MEMTOREG,
  input  JAL,
  input  MEMWRITE,
  input  LBU,
  input  SYSTEM,
  input  [31:0] RESULT,
  input  [31:0] WRITEDATA,
  input  [31:0] PC_4,
  input  [4:0] WRITEREG,
  input  [31:0] RS,
  output [31:0] out_15,
  output [31:0] out_16,
  output out_17,
  output out_18,
  output out_19,
  output out_20,
  output out_21,
  output out_22,
  output [31:0] out_23,
  output [31:0] out_24,
  output [31:0] out_25,
  output [4:0] out_26,
  output [31:0] out_27
);

  Register #(.width(32), .trigger("rising"), .Select("low")) register_1 (
    .D(PC), .Q(out_15), .clk(in_1));  // open: en, clr
  Register #(.width(1), .trigger("rising"), .Select("low")) register_2 (
    .D(REGWRITE), .Q(out_17), .clk(in_1));  // open: en, clr
  Register #(.width(1), .trigger("rising"), .Select("low")) register_3 (
    .D(MEMTOREG), .Q(out_18), .clk(in_1));  // open: en, clr
  Register #(.width(1), .trigger("rising"), .Select("low")) register_4 (
    .D(MEMWRITE), .Q(out_20), .clk(in_1));  // open: en, clr
  Register #(.width(32), .trigger("rising"), .Select("low")) register_5 (
    .D(RESULT), .Q(out_23), .clk(in_1));  // open: en, clr
  Register #(.width(32), .trigger("rising"), .Select("low")) register_6 (
    .D(WRITEDATA), .Q(out_24), .clk(in_1));  // open: en, clr
  Register #(.width(5), .trigger("rising"), .Select("low")) register_7 (
    .D(WRITEREG), .Q(out_26), .clk(in_1));  // open: en, clr
  Register #(.width(1), .trigger("rising"), .Select("low")) register_8 (
    .D(JAL), .Q(out_19), .clk(in_1));  // open: en, clr
  Register #(.width(1), .trigger("rising"), .Select("low")) register_9 (
    .D(LBU), .Q(out_21), .clk(in_1));  // open: en, clr
  Register #(.width(1), .trigger("rising"), .Select("low")) register_10 (
    .D(SYSTEM), .Q(out_22), .clk(in_1));  // open: en, clr
  Register #(.width(32), .trigger("rising"), .Select("low")) register_11 (
    .D(PC_4), .Q(out_25), .clk(in_1));  // open: en, clr
  Register #(.width(32), .trigger("rising"), .Select("low")) register_12 (
    .D(RS), .Q(out_27), .clk(in_1));  // open: en, clr
  Register #(.width(32), .trigger("rising"), .Select("low")) register_13 (
    .D(IR), .Q(out_16), .clk(in_1));  // open: en, clr

  // Other names for the same wires on the sheet: CLK = in_1
endmodule

module \气泡MEM_WB  (
  input  [31:0] PC,
  input  [31:0] IR,
  input  REGWRITE,
  input  JAL,
  input  MEMTOREG,
  input  SYSTEM,
  input  [31:0] ALU,
  input  [31:0] RAM,
  input  [31:0] PC_4,
  input  [4:0] WRITEREG,
  input  [31:0] RS,
  input  in_12,
  input  [31:0] RT,
  output [31:0] out_14,
  output [31:0] out_15,
  output out_16,
  output out_17,
  output out_18,
  output out_19,
  output [31:0] out_20,
  output [31:0] out_21,
  output [31:0] out_22,
  output [4:0] out_23,
  output [31:0] out_24,
  output [31:0] out_25
);

  Register #(.width(32), .trigger("rising"), .Select("low")) register_1 (
    .D(PC), .Q(out_14), .clk(in_12));  // open: en, clr
  Register #(.width(1), .trigger("rising"), .Select("low")) register_2 (
    .D(REGWRITE), .Q(out_16), .clk(in_12));  // open: en, clr
  Register #(.width(1), .trigger("rising"), .Select("low")) register_3 (
    .D(MEMTOREG), .Q(out_18), .clk(in_12));  // open: en, clr
  Register #(.width(32), .trigger("rising"), .Select("low")) register_4 (
    .D(ALU), .Q(out_20), .clk(in_12));  // open: en, clr
  Register #(.width(32), .trigger("rising"), .Select("low")) register_5 (
    .D(RAM), .Q(out_21), .clk(in_12));  // open: en, clr
  Register #(.width(5), .trigger("rising"), .Select("low")) register_6 (
    .D(WRITEREG), .Q(out_23), .clk(in_12));  // open: en, clr
  Register #(.width(32), .trigger("rising"), .Select("low")) register_7 (
    .D(IR), .Q(out_15), .clk(in_12));  // open: en, clr
  Register #(.width(1), .trigger("rising"), .Select("low")) register_8 (
    .D(JAL), .Q(out_17), .clk(in_12));  // open: en, clr
  Register #(.width(32), .trigger("rising"), .Select("low")) register_9 (
    .D(PC_4), .Q(out_22), .clk(in_12));  // open: en, clr
  Register #(.width(32), .trigger("rising"), .Select("low")) register_10 (
    .D(RS), .Q(out_24), .clk(in_12));  // open: en, clr
  Register #(.width(32), .trigger("rising"), .Select("low")) register_11 (
    .D(RT), .Q(out_25), .clk(in_12));  // open: en, clr
  Register #(.width(1), .trigger("rising"), .Select("low")) register_12 (
    .D(SYSTEM), .Q(out_19), .clk(in_12));  // open: en, clr

  // Other names for the same wires on the sheet: CLK = in_12
endmodule

module \重定向ID_EX  (
  input  in_1,
  input  CLR,
  input  [31:0] IR,
  input  [31:0] PC,
  input  REGWRITE,
  input  MEMTOREG,
  input  MEMWRITE,
  input  [3:0] ALUOP,
  input  BNE,
  input  BEQ,
  input  ALUSRC,
  input  LBU,
  input  JMP,
  input  BLEZ,
  input  JR,
  input  SRLV,
  input  SYSCALL,
  input  JAL,
  input  [4:0] SHAMT,
  input  [1:0] RSFORWARD,
  input  [31:0] RS,
  input  [1:0] RTFORWARD,
  input  [31:0] RT,
  input  [4:0] WRITEREG,
  input  [31:0] SIGNEXT,
  input  [31:0] PC_4,
  input  [25:0] addr,
  output [31:0] out_28,
  output [31:0] out_29,
  output out_30,
  output out_31,
  output out_32,
  output [3:0] out_33,
  output out_34,
  output out_35,
  output out_36,
  output out_37,
  output out_38,
  output out_39,
  output out_40,
  output out_41,
  output out_42,
  output out_43,
  output [4:0] out_44,
  output [1:0] out_45,
  output [31:0] out_46,
  output [1:0] out_47,
  output [31:0] out_48,
  output [4:0] out_49,
  output [31:0] out_50,
  output [31:0] out_51,
  output [25:0] out_52
);

  wire multiplexer_3_out, multiplexer_4_out, multiplexer_5_out, multiplexer_7_out, multiplexer_8_out,
       multiplexer_9_out, multiplexer_10_out, multiplexer_11_out, multiplexer_12_out, multiplexer_13_out,
       multiplexer_14_out, multiplexer_15_out, multiplexer_16_out;
  wire [1:0] multiplexer_24_out, multiplexer_25_out;
  wire [3:0] multiplexer_6_out;
  wire [4:0] multiplexer_17_out, multiplexer_20_out;
  wire [25:0] multiplexer_23_out;
  wire [31:0] multiplexer_1_out, multiplexer_2_out, multiplexer_18_out, multiplexer_19_out,
       multiplexer_21_out, multiplexer_22_out;

  Multiplexer #(.select(1), .width(32), .disabled("Z"), .enable("false")) multiplexer_1 (
    .in0(IR), .in1({32{1'b0}}), .out(multiplexer_1_out), .sel(CLR));
  Multiplexer #(.select(1), .width(32), .disabled("Z"), .enable("false")) multiplexer_2 (
    .in0(PC), .in1({32{1'b0}}), .out(multiplexer_2_out), .sel(CLR));
  Multiplexer #(.select(1), .width(1), .disabled("Z"), .enable("false")) multiplexer_3 (
    .in0(REGWRITE), .in1(1'b0), .out(multiplexer_3_out), .sel(CLR));
  Multiplexer #(.select(1), .width(1), .disabled("Z"), .enable("false")) multiplexer_4 (
    .in0(MEMTOREG), .in1(1'b0), .out(multiplexer_4_out), .sel(CLR));
  Multiplexer #(.select(1), .width(1), .disabled("Z"), .enable("false")) multiplexer_5 (
    .in0(MEMWRITE), .in1(1'b0), .out(multiplexer_5_out), .sel(CLR));
  Multiplexer #(.select(1), .width(4), .disabled("Z"), .enable("false")) multiplexer_6 (
    .in0(ALUOP), .in1(4'b0000), .out(multiplexer_6_out), .sel(CLR));
  Multiplexer #(.select(1), .width(1), .disabled("Z"), .enable("false")) multiplexer_7 (
    .in0(BNE), .in1(1'b0), .out(multiplexer_7_out), .sel(CLR));
  Multiplexer #(.select(1), .width(1), .disabled("Z"), .enable("false")) multiplexer_8 (
    .in0(BEQ), .in1(1'b0), .out(multiplexer_8_out), .sel(CLR));
  Multiplexer #(.select(1), .width(1), .disabled("Z"), .enable("false")) multiplexer_9 (
    .in0(ALUSRC), .in1(1'b0), .out(multiplexer_9_out), .sel(CLR));
  Multiplexer #(.select(1), .width(1), .disabled("Z"), .enable("false")) multiplexer_10 (
    .in0(LBU), .in1(1'b0), .out(multiplexer_10_out), .sel(CLR));
  Multiplexer #(.select(1), .width(1), .disabled("Z"), .enable("false")) multiplexer_11 (
    .in0(JMP), .in1(1'b0), .out(multiplexer_11_out), .sel(CLR));
  Multiplexer #(.select(1), .width(1), .disabled("Z"), .enable("false")) multiplexer_12 (
    .in0(BLEZ), .in1(1'b0), .out(multiplexer_12_out), .sel(CLR));
  Multiplexer #(.select(1), .width(1), .disabled("Z"), .enable("false")) multiplexer_13 (
    .in0(JR), .in1(1'b0), .out(multiplexer_13_out), .sel(CLR));
  Multiplexer #(.select(1), .width(1), .disabled("Z"), .enable("false")) multiplexer_14 (
    .in0(SRLV), .in1(1'b0), .out(multiplexer_14_out), .sel(CLR));
  Multiplexer #(.select(1), .width(1), .disabled("Z"), .enable("false")) multiplexer_15 (
    .in0(SYSCALL), .in1(1'b0), .out(multiplexer_15_out), .sel(CLR));
  Multiplexer #(.select(1), .width(1), .disabled("Z"), .enable("false")) multiplexer_16 (
    .in0(JAL), .in1(1'b0), .out(multiplexer_16_out), .sel(CLR));
  Multiplexer #(.select(1), .width(5), .disabled("Z"), .enable("false")) multiplexer_17 (
    .in0(SHAMT), .in1({5{1'b0}}), .out(multiplexer_17_out), .sel(CLR));
  Multiplexer #(.select(1), .width(32), .disabled("Z"), .enable("false")) multiplexer_18 (
    .in0(RS), .in1({32{1'b0}}), .out(multiplexer_18_out), .sel(CLR));
  Multiplexer #(.select(1), .width(32), .disabled("Z"), .enable("false")) multiplexer_19 (
    .in0(RT), .in1({32{1'b0}}), .out(multiplexer_19_out), .sel(CLR));
  Multiplexer #(.select(1), .width(5), .disabled("Z"), .enable("false")) multiplexer_20 (
    .in0(WRITEREG), .in1({5{1'b0}}), .out(multiplexer_20_out), .sel(CLR));
  Multiplexer #(.select(1), .width(32), .disabled("Z"), .enable("false")) multiplexer_21 (
    .in0(SIGNEXT), .in1({32{1'b0}}), .out(multiplexer_21_out), .sel(CLR));
  Multiplexer #(.select(1), .width(32), .disabled("Z"), .enable("false")) multiplexer_22 (
    .in0(PC_4), .in1({32{1'b0}}), .out(multiplexer_22_out), .sel(CLR));
  Multiplexer #(.select(1), .width(26), .disabled("Z"), .enable("false")) multiplexer_23 (
    .in0(addr), .in1({26{1'b0}}), .out(multiplexer_23_out), .sel(CLR));
  Register #(.width(32), .trigger("rising"), .Select("low")) register_1 (
    .D(multiplexer_1_out), .Q(out_28), .clk(in_1));  // open: en, clr
  Register #(.width(32), .trigger("rising"), .Select("low")) register_2 (
    .D(multiplexer_2_out), .Q(out_29), .clk(in_1));  // open: en, clr
  Register #(.width(1), .trigger("rising"), .Select("low")) register_3 (
    .D(multiplexer_3_out), .Q(out_30), .clk(in_1));  // open: en, clr
  Register #(.width(1), .trigger("rising"), .Select("low")) register_4 (
    .D(multiplexer_4_out), .Q(out_31), .clk(in_1));  // open: en, clr
  Register #(.width(1), .trigger("rising"), .Select("low")) register_5 (
    .D(multiplexer_5_out), .Q(out_32), .clk(in_1));  // open: en, clr
  Register #(.width(4), .trigger("rising"), .Select("low")) register_6 (
    .D(multiplexer_6_out), .Q(out_33), .clk(in_1));  // open: en, clr
  Register #(.width(1), .trigger("rising"), .Select("low")) register_7 (
    .D(multiplexer_7_out), .Q(out_34), .clk(in_1));  // open: en, clr
  Register #(.width(1), .trigger("rising"), .Select("low")) register_8 (
    .D(multiplexer_8_out), .Q(out_35), .clk(in_1));  // open: en, clr
  Register #(.width(1), .trigger("rising"), .Select("low")) register_9 (
    .D(multiplexer_9_out), .Q(out_36), .clk(in_1));  // open: en, clr
  Register #(.width(1), .trigger("rising"), .Select("low")) register_10 (
    .D(multiplexer_10_out), .Q(out_37), .clk(in_1));  // open: en, clr
  Register #(.width(1), .trigger("rising"), .Select("low")) register_11 (
    .D(multiplexer_11_out), .Q(out_38), .clk(in_1));  // open: en, clr
  Register #(.width(1), .trigger("rising"), .Select("low")) register_12 (
    .D(multiplexer_12_out), .Q(out_39), .clk(in_1));  // open: en, clr
  Register #(.width(1), .trigger("rising"), .Select("low")) register_13 (
    .D(multiplexer_13_out), .Q(out_40), .clk(in_1));  // open: en, clr
  Register #(.width(1), .trigger("rising"), .Select("low")) register_14 (
    .D(multiplexer_14_out), .Q(out_41), .clk(in_1));  // open: en, clr
  Register #(.width(1), .trigger("rising"), .Select("low")) register_15 (
    .D(multiplexer_15_out), .Q(out_42), .clk(in_1));  // open: en, clr
  Register #(.width(1), .trigger("rising"), .Select("low")) register_16 (
    .D(multiplexer_16_out), .Q(out_43), .clk(in_1));  // open: en, clr
  Register #(.width(5), .trigger("rising"), .Select("low")) register_17 (
    .D(multiplexer_17_out), .Q(out_44), .clk(in_1));  // open: en, clr
  Register #(.width(32), .trigger("rising"), .Select("low")) register_18 (
    .D(multiplexer_18_out), .Q(out_46), .clk(in_1));  // open: en, clr
  Register #(.width(32), .trigger("rising"), .Select("low")) register_19 (
    .D(multiplexer_19_out), .Q(out_48), .clk(in_1));  // open: en, clr
  Register #(.width(5), .trigger("rising"), .Select("low")) register_20 (
    .D(multiplexer_20_out), .Q(out_49), .clk(in_1));  // open: en, clr
  Register #(.width(32), .trigger("rising"), .Select("low")) register_21 (
    .D(multiplexer_21_out), .Q(out_50), .clk(in_1));  // open: en, clr
  Register #(.width(32), .trigger("rising"), .Select("low")) register_22 (
    .D(multiplexer_22_out), .Q(out_51), .clk(in_1));  // open: en, clr
  Register #(.width(26), .trigger("rising"), .Select("low")) register_23 (
    .D(multiplexer_23_out), .Q(out_52), .clk(in_1));  // open: en, clr
  Multiplexer #(.select(1), .width(2), .disabled("Z"), .enable("false")) multiplexer_24 (
    .in0(RSFORWARD), .in1(2'b00), .out(multiplexer_24_out), .sel(CLR));
  Multiplexer #(.select(1), .width(2), .disabled("Z"), .enable("false")) multiplexer_25 (
    .in0(RTFORWARD), .in1(2'b00), .out(multiplexer_25_out), .sel(CLR));
  Register #(.width(2), .trigger("rising"), .Select("low")) register_24 (
    .D(multiplexer_24_out), .Q(out_45), .clk(in_1));  // open: en, clr
  Register #(.width(2), .trigger("rising"), .Select("low")) register_25 (
    .D(multiplexer_25_out), .Q(out_47), .clk(in_1));  // open: en, clr

  // Other names for the same wires on the sheet: CLK = in_1
endmodule
