// Logisim project cpu24多级中断内存.circ as structural Verilog: 13 circuits, main circuit ◇单周期MIPS
module \单周期MIPS  (
  input  IR1,
  input  IR2,
  input  IR3,
  output RegWrite,
  output MemWrite,
  output [31:0] PC,
  output [31:0] IR,
  output [31:0] RDin,
  output [31:0] MDin,
  output [31:0] LedData
);

  wire AluSrcB, and_1_out, and_2_out, and_3_out, Beq, Bne, CLK, clock_2_out, comparator_1_eq,
       comparator_1_lt, comparator_2_eq, controlled_buffer_1_out, d_ff_1_q, Go, Halt, IR1_t, IR2_t, IR3_t,
       IRA, IRB, IRC, JAL, JMP, JR, MemToReg, mips_alu_1_equal, nand_1_out, not_1_out, not_2_out, not_3_out,
       not_4_out, or_1_out, PCSrc, RegDst, Reset, SignedExt, Syscall, W1, W2, W3;
  wire [3:0] AluOP;
  wire [4:0] multiplexer_2_out, multiplexer_3_out, multiplexer_4_out, multiplexer_5_out;
  wire [12:0] CNT_num;
  wire [15:0] \总周期数 ;
  wire [31:0] bit_extender_1_out, bit_extender_2_out, mips_alu_1_result, multiplexer_1_out,
       multiplexer_7_out, multiplexer_8_out, PC_4, PC_imm, PC_rst, ram_1_data, shifter_1_out, WriteBackData;

  Clock #(.highDuration(1), .lowDuration(1)) clock_1 (.out(CLK));
  Button _1 (.out(IRA));
  Button _2 (.out(IRB));
  Button _3 (.out(IRC));
  Button \u_继续运行  (.out(Go));
  LED #(.active("true")) led_1 (.in(W1));
  LED #(.active("true")) led_2 (.in(W2));
  LED #(.active("true")) led_3 (.in(W3));
  D_Flip_Flop #(.trigger("high"), .Pre_Clr_Positions("LEGACY"), .NegatePresetClear("false"), .enable("true"), .NewFFLayout("false")) d_ff_1 (.Q(d_ff_1_q));  // open: clk, D, Qn, preset, en, reset
  Hex_Digit_Display hex_digit_display_1 (.value(LedData[31:28]));  // open: dp
  Button button_1 (.out(Reset));
  Multiplexer #(.select(3), .width(32), .disabled("Z"), .enable("false")) multiplexer_1 (
    .in0(PC_4), .in1(PC_imm), .in2({PC[31:28], IR[25:0], 2'b00}), .in6(PC_rst), .out(multiplexer_1_out),
    .sel({JR, JMP, PCSrc}));  // open: in3, in4, in5, in7
  or or_1 (or_1_out, not_1_out, Go);
  not not_1 (not_1_out, Halt);
  // Probe on 13'hc
  Hex_Digit_Display hex_digit_display_2 (.value(LedData[27:24]));  // open: dp
  Hex_Digit_Display hex_digit_display_3 (.value(LedData[23:20]));  // open: dp
  Register #(.width(32), .trigger("rising"), .Select("low")) u_PC (
    .D(multiplexer_1_out), .en(or_1_out), .Q(PC), .clk(CLK), .clr(Reset));
  Comparator #(.width(13), .mode("twosComplement")) comparator_1 (
    .a(CNT_num), .b(13'hc), .eq(comparator_1_eq), .lt(comparator_1_lt));  // open: gt
  Clock #(.highDuration(1), .lowDuration(1)) clock_2 (.out(clock_2_out));
  Hex_Digit_Display hex_digit_display_4 (.value(LedData[15:12]));  // open: dp
  Hex_Digit_Display hex_digit_display_5 (.value(LedData[19:16]));  // open: dp
  Counter #(.width(16), .max('hffff), .ongoal("wrap"), .trigger("rising"), .behavior("old")) counter_1 (
    .count(not_2_out), .Q(\总周期数 ), .clk(CLK));  // open: load, D, carry, clr, preset
  not not_2 (not_2_out, Halt);
  Adder #(.width(32)) adder_1 (.a(PC), .b(32'h4), .out(PC_4));  // open: cin, cout
  nand nand_1 (nand_1_out, d_ff_1_q, comparator_1_eq);
  Counter #(.width(13), .max('h1fff), .ongoal("stay"), .trigger("rising"), .behavior("old")) counter_2 (
    .count(comparator_1_lt), .Q(CNT_num), .clk(clock_2_out));  // open: load, D, carry, clr, preset
  Hex_Digit_Display hex_digit_display_6 (.value(LedData[11:8]));  // open: dp
  Hex_Digit_Display hex_digit_display_7 (.value(LedData[7:4]));  // open: dp
  // Probe on \总周期数 
  assign controlled_buffer_1_out = nand_1_out ? clock_2_out : 1'bz;  // Controlled_Buffer controlled_buffer_1
  Pull_Resistor #(.pull(1)) pull_resistor_1 (.node(controlled_buffer_1_out));
  Hex_Digit_Display hex_digit_display_8 (.value(LedData[3:0]));  // open: dp
  // Mips_Probe mips_probe_1: pin names not known; wires that end beside it: IR
  ROM #(.addrWidth(10), .dataWidth(32), .Select("high")) rom_1 (.addr(PC[11:2]), .data(IR));
  or or_2 (IR1_t, IR1, IRA);
  \单周期硬布线控制器  \u_单周期硬布线控制器_1  (
    .Func(IR[5:0]), .OP(IR[31:26]), .ALU_OP(AluOP), .MemToReg(MemToReg), .MemWrite(MemWrite),
    .ALU_SRC(AluSrcB), .SysCALL(Syscall), .SignedExt(SignedExt), .RegDst(RegDst), .JR(JR), .JMP(JMP),
    .Beq(Beq), .JAL(JAL), .Bne(Bne), .RegWrite(RegWrite));  // open: ERET, in_3, MTC0, MFC0
  Multiplexer #(.select(1), .width(5), .disabled("Z"), .enable("false")) multiplexer_2 (
    .in0(IR[25:21]), .in1(5'b00010), .out(multiplexer_2_out), .sel(Syscall));
  Multiplexer #(.select(1), .width(5), .disabled("Z"), .enable("false")) multiplexer_3 (
    .in0(IR[20:16]), .in1(5'b00100), .out(multiplexer_3_out), .sel(Syscall));
  Multiplexer #(.select(1), .width(5), .disabled("Z"), .enable("false")) multiplexer_4 (
    .in0(IR[20:16]), .in1(IR[15:11]), .out(multiplexer_4_out), .sel(RegDst));
  Multiplexer #(.select(1), .width(5), .disabled("Z"), .enable("false")) multiplexer_5 (
    .in0(multiplexer_4_out), .in1({5{1'b1}}), .out(multiplexer_5_out), .sel(JAL));
  assign bit_extender_1_out = {{16{1'b0}}, IR[15:0]};  // Bit_Extender bit_extender_1
  assign bit_extender_2_out = {{16{IR[15]}}, IR[15:0]};  // Bit_Extender bit_extender_2
  or or_3 (IR2_t, IR2, IRB);
  Multiplexer #(.select(1), .width(32), .disabled("Z"), .enable("false")) multiplexer_6 (
    .in0(WriteBackData), .in1(PC_4), .out(RDin), .sel(JAL));
  Multiplexer #(.select(1), .width(32), .disabled("Z"), .enable("false")) multiplexer_7 (
    .in0(bit_extender_1_out), .in1(bit_extender_2_out), .out(multiplexer_7_out), .sel(SignedExt));
  MIPS_Regifile mips_regifile_1 (
    .Din(RDin), .Clk(CLK), .R1(PC_rst), .R2(MDin), .WE(RegWrite), .W_num(multiplexer_5_out),
    .R1_num(multiplexer_2_out), .R2_num(multiplexer_3_out));
  Shifter #(.width(32), .shift("ll")) shifter_1 (.in(bit_extender_2_out), .\dist (5'b00010), .out(shifter_1_out));
  or or_4 (IR3_t, IR3, IRC);
  Adder #(.width(32)) adder_2 (.a(shifter_1_out), .b(PC_4), .out(PC_imm));  // open: cin, cout
  Comparator #(.width(32), .mode("twosComplement")) comparator_2 (
    .a(PC_rst), .b(32'h22), .eq(comparator_2_eq));  // open: gt, lt
  not not_3 (not_3_out, mips_alu_1_equal);
  Multiplexer #(.select(1), .width(32), .disabled("Z"), .enable("false")) multiplexer_8 (
    .in0(MDin), .in1(multiplexer_7_out), .out(multiplexer_8_out), .sel(AluSrcB));
  not not_4 (not_4_out, comparator_2_eq);
  and and_1 (and_1_out, not_3_out, Bne);
  and and_2 (and_2_out, Beq, mips_alu_1_equal);
  MIPS_ALU mips_alu_1 (
    .X(PC_rst), .Y(multiplexer_8_out), .AluOP(AluOP), .Equal(mips_alu_1_equal), .Result(mips_alu_1_result),
    .shamt(IR[10:6]));  // open: Result_2
  and and_3 (and_3_out, Syscall, comparator_2_eq);
  and and_4 (Halt, Syscall, not_4_out);
  or or_5 (PCSrc, and_1_out, and_2_out);
  Register #(.width(32), .trigger("rising"), .Select("low")) register_1 (
    .D(MDin), .en(and_3_out), .Q(LedData), .clk(CLK), .clr(Reset));
  RAM #(.addrWidth(10), .dataWidth(32), .bus("separate"), .Select("high")) ram_1 (
    .addr(mips_alu_1_result[11:2]), .din(MDin), .data(ram_1_data), .str(MemWrite), .clk(CLK), .clr(Reset));  // open: sel, ld
  Multiplexer #(.select(1), .width(32), .disabled("Z"), .enable("false")) multiplexer_9 (
    .in0(mips_alu_1_result), .in1(ram_1_data), .out(WriteBackData), .sel(MemToReg));

  // Other names for the same wires on the sheet: a0[31:0] = MDin; addr[25:0] = IR[25:0];
  //   PC_J[31:2] = {PC[31:28], IR[25:0]}; shamt[4:0] = IR[10:6]; v0[31:0] = PC_rst

  // Notes on the sheet:
  //   中断源
  //   中断等待指示
  //   总复位信号应将除ROM以外所有存储组件全部清零
  //   控制位
  //   暂停节拍，不能为0
  //   用这个时钟源需要去掉电路中的其他时钟源
  //   戳工具置1进入计数暂停模式，ctrl+k时钟自动运行到对应节拍暂停
  //   ctrl+k关闭时钟连续运行，将控制位置零，进入单步调试模式调试
  //   数码管输出
  //   数码管输出应该用寄存器锁存，否则显示数据只能一闪而过
  //   指令存储器
  //   可计数暂停的时钟源
  //   指令字
  //   contents of rom_1 (hex, n*v repeats v):
  //   201d07d0 20100001 109fc0 139fc3 8021 2012000c 24160008 26100001 3210000f 20080008 20090001 139900
  //   2709825 132020 20020022 c 1094022 1500fff9 22100001 2018000f 2188024 108700 20080008 20090001 139902
  //   2709825 132021 20020022 c 1094022 1500fff9 108702 2c9b022 12c00001 8000c07 4020 1084027 84400
  //   3508ffff 82021 20020022 c 8000c01 afa20000 23bd0004 afa40000 23bd0004 afb00000 23bd0004 afb30000
  //   23bd0004 afb40000 23bd0004 afb50000 23bd0004 afb60000 23bd0004 20160001 20140003 20150001 168020
  //   108100 2149825 132020 20020022 c 1600fffa 295a022 1680fff7 23bdfffc 8fb60000 23bdfffc 8fb50000
  //   23bdfffc 8fb40000 23bdfffc 8fb30000 23bdfffc 8fb00000 23bdfffc 8fa40000 23bdfffc 8fa20000 42000018
  //   afa20000 23bd0004 afa40000 23bd0004 afb00000 23bd0004 afb30000 23bd0004 afb40000 23bd0004 afb50000
  //   23bd0004 afb60000 23bd0004 20160002 20140003 20150001 168020 108100 2149825 132020 20020022 c
  //   1600fffa 295a022 1680fff7 23bdfffc 8fb60000 23bdfffc 8fb50000 23bdfffc 8fb40000 23bdfffc 8fb30000
  //   23bdfffc 8fb00000 23bdfffc 8fa40000 23bdfffc 8fa20000 42000018 afa20000 23bd0004 afa40000 23bd0004
  //   afb00000 23bd0004 afb30000 23bd0004 afb40000 23bd0004 afb50000 23bd0004 afb60000 23bd0004 20160003
  //   20140003 20150001 168020 108100 2149825 132020 20020022 c 1600fffa 295a022 1680fff7 23bdfffc
  //   8fb60000 23bdfffc 8fb50000 23bdfffc 8fb40000 23bdfffc 8fb30000 23bdfffc 8fb00000 23bdfffc 8fa40000
  //   23bdfffc 8fa20000 42000018
  //   OP
  //   Func
  //   rs
  //   rt
  //   rd
  //   Beq
  //   JMP
  //   JR
  //   Bne
  //   OP
  //   JAL
  //   Func
  //   Syscall
  //   v0
  //   a0
  //   MemToReg
  //   MemWrite
  //   AluOP
  //   AluSrcB
  //   RegWrite
  //   RegDst
  //   为方便自动评测，需要输出PC，IR，寄存器堆写如数据RDin
  //   RAM写使能MemWrite、RAM写入数据MDin等信号
endmodule

// 单周期硬布线控制器
module \单周期硬布线控制器  (
  input  [5:0] OP,
  input  [5:0] Func,
  input  [4:0] in_3,
  output [3:0] ALU_OP,
  output MemToReg,
  output MemWrite,
  output ALU_SRC,
  output SysCALL,
  output SignedExt,
  output RegDst,
  output Beq,
  output Bne,
  output JR,
  output JMP,
  output JAL,
  output ERET,
  output MTC0,
  output RegWrite,
  output MFC0
);

  wire not_1_out, not_2_out, not_3_out, not_4_out, not_5_out, not_6_out, not_7_out, not_8_out, not_9_out,
       not_10_out, not_11_out, not_12_out, not_13_out, not_14_out, not_15_out, not_16_out, not_17_out,
       not_18_out, not_19_out, RegW0;

  \运算控制器自动生成  \u_运算控制器自动生成_1  (
    .OP0(OP[0]), .OP1(OP[1]), .OP2(OP[2]), .OP3(OP[3]), .OP4(OP[4]), .OP5(OP[5]), .F0(Func[0]), .F1(Func[1]),
    .F2(Func[2]), .F3(Func[3]), .F4(Func[4]), .F5(Func[5]), .S0(ALU_OP[0]), .S1(ALU_OP[1]), .S2(ALU_OP[2]),
    .S3(ALU_OP[3]));
  \控制信号自动生成  \u_控制信号自动生成_1  (
    .OP0(OP[0]), .MemToReg(MemToReg), .OP1(OP[1]), .OP2(OP[2]), .MemWrite(MemWrite), .OP3(OP[3]),
    .OP4(OP[4]), .OP5(OP[5]), .F0(Func[0]), .F1(Func[1]), .ALU_SRC(ALU_SRC), .F2(Func[2]), .F3(Func[3]),
    .F4(Func[4]), .F5(Func[5]), .RegWrite(RegW0), .SysCALL(SysCALL), .SignedExt(SignedExt), .RegDst(RegDst),
    .BEQ(Beq), .BNE(Bne), .JR(JR), .JUMP(JMP), .JAL(JAL), .ERET(ERET));
  not not_1 (not_1_out, OP[0]);
  not not_2 (not_2_out, OP[1]);
  not not_3 (not_3_out, OP[2]);
  not not_4 (not_4_out, OP[3]);
  and and_1 (MTC0, not_1_out, not_2_out, not_3_out, not_4_out, OP[4], not_5_out, not_6_out, not_7_out, in_3[2], not_8_out, not_9_out);
  not not_5 (not_5_out, OP[5]);
  not not_6 (not_6_out, in_3[0]);
  not not_7 (not_7_out, in_3[1]);
  not not_8 (not_8_out, in_3[3]);
  not not_9 (not_9_out, in_3[4]);
  not not_10 (not_10_out, OP[0]);
  not not_11 (not_11_out, OP[1]);
  not not_12 (not_12_out, OP[2]);
  not not_13 (not_13_out, OP[3]);
  and and_2 (MFC0, not_10_out, not_11_out, not_12_out, not_13_out, OP[4], not_14_out, not_15_out, not_16_out, not_17_out, not_18_out, not_19_out);
  not not_14 (not_14_out, OP[5]);
  not not_15 (not_15_out, in_3[0]);
  not not_16 (not_16_out, in_3[1]);
  not not_17 (not_17_out, in_3[2]);
  not not_18 (not_18_out, in_3[3]);
  not not_19 (not_19_out, in_3[4]);
  or or_1 (RegWrite, RegW0, MFC0);

  // Other names for the same wires on the sheet: MF[4:0] = in_3; MT[4:0] = in_3; OP_CODE[5:0] = OP; RegW1 = MFC0

  // Notes on the sheet:
  //   运算器控制器，根据指令生成运算器功能选择信号
  //   控制信号生成，产生数据通路需要的其他控制信号
endmodule

// 运算器控制器
module \运算控制器自动生成  (
  input  OP0,
  input  OP1,
  input  OP2,
  input  OP3,
  input  OP4,
  input  OP5,
  input  F0,
  input  F1,
  input  F2,
  input  F3,
  input  F4,
  input  F5,
  output S0,
  output S1,
  output S2,
  output S3
);

  wire and_1_out, and_2_out, and_3_out, and_4_out, and_5_out, and_6_out, and_7_out, and_8_out, and_9_out,
       and_10_out, and_11_out, and_12_out, and_13_out, and_14_out, and_15_out, and_16_out, and_17_out,
       and_18_out, and_19_out, and_20_out, and_21_out, and_22_out, and_23_out, and_24_out, and_25_out,
       and_26_out, and_27_out, and_28_out, and_29_out, and_30_out, and_31_out, and_32_out, and_33_out,
       and_34_out, not_1_out, not_2_out, not_3_out, not_4_out, not_5_out, not_6_out, not_7_out, not_8_out,
       not_9_out, not_10_out, not_11_out, not_12_out, not_13_out, not_14_out, not_15_out, not_16_out,
       not_17_out, not_18_out, not_19_out, not_20_out, not_21_out, not_22_out, not_23_out, not_24_out,
       not_25_out, not_26_out, not_27_out, not_28_out, not_29_out, not_30_out, not_31_out, not_32_out,
       not_33_out, not_34_out, not_35_out, not_36_out, not_37_out, not_38_out, not_39_out, not_40_out,
       not_41_out, not_42_out, not_43_out, not_44_out, not_45_out, not_46_out, not_47_out, not_48_out,
       not_49_out, not_50_out, not_51_out, not_52_out, not_53_out, not_54_out, not_55_out, not_56_out,
       not_57_out, not_58_out, not_59_out, not_60_out, not_61_out, not_62_out, not_63_out, not_64_out,
       not_65_out, not_66_out, not_67_out, not_68_out, not_69_out, not_70_out, not_71_out, not_72_out,
       not_73_out, not_74_out, not_75_out, not_76_out, not_77_out, not_78_out, not_79_out, not_80_out,
       not_81_out, not_82_out, not_83_out, not_84_out, not_85_out, not_86_out, not_87_out, not_88_out,
       not_89_out, not_90_out, not_91_out, not_92_out, not_93_out, not_94_out, not_95_out, not_96_out,
       not_97_out, not_98_out, not_99_out, not_100_out, not_101_out, not_102_out, not_103_out, not_104_out,
       not_105_out, not_106_out, not_107_out, not_108_out, not_109_out, not_110_out, not_111_out,
       not_112_out, not_113_out, not_114_out, not_115_out, not_116_out, not_117_out, not_118_out,
       not_119_out, not_120_out, not_121_out, not_122_out, not_123_out, not_124_out, not_125_out,
       not_126_out, not_127_out, not_128_out, not_129_out, not_130_out, not_131_out, not_132_out,
       not_133_out, not_134_out, not_135_out, not_136_out, not_137_out, not_138_out, not_139_out,
       not_140_out, not_141_out, not_142_out, not_143_out, not_144_out, not_145_out, not_146_out,
       not_147_out, not_148_out, not_149_out, not_150_out, not_151_out, not_152_out, not_153_out,
       not_154_out, not_155_out, not_156_out, not_157_out, not_158_out, not_159_out, not_160_out,
       not_161_out, not_162_out, not_163_out, not_164_out, not_165_out, not_166_out, not_167_out,
       not_168_out, not_169_out, not_170_out, not_171_out, not_172_out, not_173_out, not_174_out,
       not_175_out, not_176_out, not_177_out, not_178_out, not_179_out, not_180_out, not_181_out,
       not_182_out, not_183_out, not_184_out, not_185_out, not_186_out, not_187_out, not_188_out,
       not_189_out, not_190_out, not_191_out, not_192_out, not_193_out, not_194_out, not_195_out,
       not_196_out, not_197_out, not_198_out, not_199_out, not_200_out, not_201_out, not_202_out,
       not_203_out, not_204_out, not_205_out, not_206_out, not_207_out, not_208_out, not_209_out,
       not_210_out, not_211_out, not_212_out, not_213_out, not_214_out, not_215_out, not_216_out,
       not_217_out, not_218_out, not_219_out, not_220_out, not_221_out, not_222_out, not_223_out,
       not_224_out, not_225_out, not_226_out, not_227_out, not_228_out, not_229_out, not_230_out,
       not_231_out, not_232_out, not_233_out, not_234_out, not_235_out, not_236_out;

  not not_1 (not_1_out, OP5);
  not not_2 (not_2_out, OP4);
  not not_3 (not_3_out, OP3);
  not not_4 (not_4_out, OP2);
  not not_5 (not_5_out, OP1);
  not not_6 (not_6_out, OP0);
  not not_7 (not_7_out, F5);
  not not_8 (not_8_out, F4);
  not not_9 (not_9_out, F3);
  not not_10 (not_10_out, F2);
  not not_11 (not_11_out, OP5);
  not not_12 (not_12_out, OP4);
  not not_13 (not_13_out, OP3);
  not not_14 (not_14_out, OP2);
  not not_15 (not_15_out, OP1);
  not not_16 (not_16_out, OP0);
  not not_17 (not_17_out, F4);
  not not_18 (not_18_out, F3);
  not not_19 (not_19_out, F2);
  not not_20 (not_20_out, F1);
  not not_21 (not_21_out, F0);
  not not_22 (not_22_out, OP5);
  not not_23 (not_23_out, OP4);
  not not_24 (not_24_out, OP3);
  not not_25 (not_25_out, OP2);
  not not_26 (not_26_out, OP1);
  not not_27 (not_27_out, OP0);
  not not_28 (not_28_out, F4);
  not not_29 (not_29_out, F3);
  not not_30 (not_30_out, F2);
  not not_31 (not_31_out, F1);
  not not_32 (not_32_out, OP5);
  not not_33 (not_33_out, OP4);
  not not_34 (not_34_out, OP3);
  not not_35 (not_35_out, OP2);
  not not_36 (not_36_out, OP1);
  not not_37 (not_37_out, OP0);
  not not_38 (not_38_out, F4);
  not not_39 (not_39_out, F3);
  not not_40 (not_40_out, F1);
  not not_41 (not_41_out, F0);
  not not_42 (not_42_out, OP5);
  not not_43 (not_43_out, OP4);
  not not_44 (not_44_out, OP3);
  not not_45 (not_45_out, OP2);
  not not_46 (not_46_out, OP1);
  not not_47 (not_47_out, OP0);
  not not_48 (not_48_out, F4);
  not not_49 (not_49_out, F2);
  not not_50 (not_50_out, F0);
  not not_51 (not_51_out, OP5);
  not not_52 (not_52_out, OP4);
  not not_53 (not_53_out, OP2);
  not not_54 (not_54_out, OP1);
  not not_55 (not_55_out, OP0);
  not not_56 (not_56_out, OP5);
  not not_57 (not_57_out, OP4);
  not not_58 (not_58_out, OP1);
  not not_59 (not_59_out, OP0);
  not not_60 (not_60_out, OP5);
  not not_61 (not_61_out, OP4);
  not not_62 (not_62_out, OP2);
  not not_63 (not_63_out, OP1);
  not not_64 (not_64_out, OP5);
  not not_65 (not_65_out, OP4);
  not not_66 (not_66_out, OP2);
  not not_67 (not_67_out, OP0);
  not not_68 (not_68_out, OP4);
  not not_69 (not_69_out, OP3);
  not not_70 (not_70_out, OP2);
  not not_71 (not_71_out, OP4);
  not not_72 (not_72_out, OP2);
  not not_73 (not_73_out, OP5);
  not not_74 (not_74_out, OP4);
  not not_75 (not_75_out, OP3);
  not not_76 (not_76_out, OP2);
  not not_77 (not_77_out, OP1);
  not not_78 (not_78_out, OP0);
  not not_79 (not_79_out, F5);
  not not_80 (not_80_out, F4);
  not not_81 (not_81_out, F3);
  not not_82 (not_82_out, F2);
  not not_83 (not_83_out, F0);
  not not_84 (not_84_out, OP5);
  not not_85 (not_85_out, OP4);
  not not_86 (not_86_out, OP3);
  not not_87 (not_87_out, OP2);
  not not_88 (not_88_out, OP1);
  not not_89 (not_89_out, OP0);
  not not_90 (not_90_out, F4);
  not not_91 (not_91_out, F3);
  not not_92 (not_92_out, F2);
  not not_93 (not_93_out, F0);
  not not_94 (not_94_out, OP5);
  not not_95 (not_95_out, OP4);
  not not_96 (not_96_out, OP3);
  not not_97 (not_97_out, OP2);
  not not_98 (not_98_out, OP1);
  not not_99 (not_99_out, OP0);
  not not_100 (not_100_out, F4);
  not not_101 (not_101_out, F3);
  not not_102 (not_102_out, F1);
  not not_103 (not_103_out, F0);
  not not_104 (not_104_out, OP5);
  not not_105 (not_105_out, OP4);
  not not_106 (not_106_out, OP3);
  not not_107 (not_107_out, OP2);
  not not_108 (not_108_out, OP1);
  not not_109 (not_109_out, OP0);
  not not_110 (not_110_out, F4);
  not not_111 (not_111_out, F3);
  not not_112 (not_112_out, OP5);
  not not_113 (not_113_out, OP4);
  not not_114 (not_114_out, OP3);
  not not_115 (not_115_out, OP2);
  not not_116 (not_116_out, OP1);
  not not_117 (not_117_out, OP0);
  not not_118 (not_118_out, F4);
  not not_119 (not_119_out, F2);
  not not_120 (not_120_out, F0);
  not not_121 (not_121_out, OP5);
  not not_122 (not_122_out, OP4);
  not not_123 (not_123_out, OP1);
  not not_124 (not_124_out, OP0);
  not not_125 (not_125_out, OP5);
  not not_126 (not_126_out, OP4);
  not not_127 (not_127_out, OP2);
  not not_128 (not_128_out, OP0);
  not not_129 (not_129_out, OP5);
  not not_130 (not_130_out, OP4);
  not not_131 (not_131_out, OP3);
  not not_132 (not_132_out, OP2);
  not not_133 (not_133_out, OP1);
  not not_134 (not_134_out, OP0);
  not not_135 (not_135_out, F4);
  not not_136 (not_136_out, F3);
  not not_137 (not_137_out, F2);
  not not_138 (not_138_out, F1);
  not not_139 (not_139_out, F0);
  not not_140 (not_140_out, OP5);
  not not_141 (not_141_out, OP4);
  not not_142 (not_142_out, OP3);
  not not_143 (not_143_out, OP2);
  not not_144 (not_144_out, OP1);
  not not_145 (not_145_out, OP0);
  not not_146 (not_146_out, F4);
  not not_147 (not_147_out, F3);
  not not_148 (not_148_out, F2);
  not not_149 (not_149_out, F1);
  not not_150 (not_150_out, OP5);
  not not_151 (not_151_out, OP4);
  not not_152 (not_152_out, OP3);
  not not_153 (not_153_out, OP2);
  not not_154 (not_154_out, OP1);
  not not_155 (not_155_out, OP0);
  not not_156 (not_156_out, F4);
  not not_157 (not_157_out, F3);
  not not_158 (not_158_out, F2);
  not not_159 (not_159_out, F0);
  not not_160 (not_160_out, OP5);
  not not_161 (not_161_out, OP4);
  not not_162 (not_162_out, OP3);
  not not_163 (not_163_out, OP2);
  not not_164 (not_164_out, OP1);
  not not_165 (not_165_out, OP0);
  not not_166 (not_166_out, F4);
  not not_167 (not_167_out, F3);
  not not_168 (not_168_out, F1);
  not not_169 (not_169_out, F0);
  not not_170 (not_170_out, OP5);
  not not_171 (not_171_out, OP4);
  not not_172 (not_172_out, OP3);
  not not_173 (not_173_out, OP2);
  not not_174 (not_174_out, OP1);
  not not_175 (not_175_out, OP0);
  not not_176 (not_176_out, F4);
  not not_177 (not_177_out, F2);
  not not_178 (not_178_out, OP5);
  not not_179 (not_179_out, OP4);
  not not_180 (not_180_out, OP2);
  not not_181 (not_181_out, OP1);
  not not_182 (not_182_out, OP0);
  not not_183 (not_183_out, OP5);
  not not_184 (not_184_out, OP4);
  not not_185 (not_185_out, OP1);
  not not_186 (not_186_out, OP0);
  not not_187 (not_187_out, OP5);
  not not_188 (not_188_out, OP4);
  not not_189 (not_189_out, OP2);
  not not_190 (not_190_out, OP1);
  not not_191 (not_191_out, OP4);
  not not_192 (not_192_out, OP3);
  not not_193 (not_193_out, OP2);
  not not_194 (not_194_out, OP4);
  not not_195 (not_195_out, OP2);
  not not_196 (not_196_out, OP5);
  not not_197 (not_197_out, OP4);
  not not_198 (not_198_out, OP3);
  not not_199 (not_199_out, OP2);
  not not_200 (not_200_out, OP1);
  not not_201 (not_201_out, OP0);
  not not_202 (not_202_out, F4);
  not not_203 (not_203_out, F3);
  not not_204 (not_204_out, F1);
  not not_205 (not_205_out, OP5);
  not not_206 (not_206_out, OP4);
  not not_207 (not_207_out, OP3);
  not not_208 (not_208_out, OP2);
  not not_209 (not_209_out, OP1);
  not not_210 (not_210_out, OP0);
  not not_211 (not_211_out, F4);
  not not_212 (not_212_out, F3);
  not not_213 (not_213_out, OP5);
  not not_214 (not_214_out, OP4);
  not not_215 (not_215_out, OP3);
  not not_216 (not_216_out, OP2);
  not not_217 (not_217_out, OP1);
  not not_218 (not_218_out, OP0);
  not not_219 (not_219_out, F4);
  not not_220 (not_220_out, F2);
  not not_221 (not_221_out, F0);
  not not_222 (not_222_out, OP5);
  not not_223 (not_223_out, OP4);
  not not_224 (not_224_out, OP3);
  not not_225 (not_225_out, OP2);
  not not_226 (not_226_out, OP1);
  not not_227 (not_227_out, OP0);
  not not_228 (not_228_out, F4);
  not not_229 (not_229_out, F2);
  not not_230 (not_230_out, OP5);
  not not_231 (not_231_out, OP4);
  not not_232 (not_232_out, OP2);
  not not_233 (not_233_out, OP0);
  not not_234 (not_234_out, OP5);
  not not_235 (not_235_out, OP4);
  not not_236 (not_236_out, OP1);
  and and_1 (and_1_out, not_1_out, not_2_out, not_3_out, not_4_out, not_5_out, not_6_out, not_7_out, not_8_out, not_9_out, not_10_out, F1, F0);
  and and_2 (and_2_out, not_11_out, not_12_out, not_13_out, not_14_out, not_15_out, not_16_out, F5, not_17_out, not_18_out, not_19_out, not_20_out, not_21_out);
  and and_3 (and_3_out, not_22_out, not_23_out, not_24_out, not_25_out, not_26_out, not_27_out, F5, not_28_out, not_29_out, not_30_out, not_31_out, F0);
  and and_4 (and_4_out, not_32_out, not_33_out, not_34_out, not_35_out, not_36_out, not_37_out, F5, not_38_out, not_39_out, F2, not_40_out, not_41_out);
  and and_5 (and_5_out, not_42_out, not_43_out, not_44_out, not_45_out, not_46_out, not_47_out, F5, not_48_out, F3, not_49_out, F1, not_50_out);
  and and_6 (and_6_out, not_51_out, not_52_out, OP3, not_53_out, not_54_out, not_55_out);
  and and_7 (and_7_out, not_56_out, not_57_out, OP3, OP2, not_58_out, not_59_out);
  and and_8 (and_8_out, not_60_out, not_61_out, OP3, not_62_out, not_63_out, OP0);
  and and_9 (and_9_out, not_64_out, not_65_out, OP3, not_66_out, OP1, not_67_out);
  and and_10 (and_10_out, OP5, not_68_out, not_69_out, not_70_out, OP1, OP0);
  and and_11 (and_11_out, OP5, not_71_out, OP3, not_72_out, OP1, OP0);
  and and_12 (and_12_out, not_73_out, not_74_out, not_75_out, not_76_out, not_77_out, not_78_out, not_79_out, not_80_out, not_81_out, not_82_out, F1, not_83_out);
  and and_13 (and_13_out, not_84_out, not_85_out, not_86_out, not_87_out, not_88_out, not_89_out, F5, not_90_out, not_91_out, not_92_out, F1, not_93_out);
  and and_14 (and_14_out, not_94_out, not_95_out, not_96_out, not_97_out, not_98_out, not_99_out, F5, not_100_out, not_101_out, F2, not_102_out, not_103_out);
  and and_15 (and_15_out, not_104_out, not_105_out, not_106_out, not_107_out, not_108_out, not_109_out, F5, not_110_out, not_111_out, F2, F1, F0);
  and and_16 (and_16_out, not_112_out, not_113_out, not_114_out, not_115_out, not_116_out, not_117_out, F5, not_118_out, F3, not_119_out, F1, not_120_out);
  and and_17 (and_17_out, not_121_out, not_122_out, OP3, OP2, not_123_out, not_124_out);
  and and_18 (and_18_out, not_125_out, not_126_out, OP3, not_127_out, OP1, not_128_out);
  and and_19 (and_19_out, not_129_out, not_130_out, not_131_out, not_132_out, not_133_out, not_134_out, F5, not_135_out, not_136_out, not_137_out, not_138_out, not_139_out);
  and and_20 (and_20_out, not_140_out, not_141_out, not_142_out, not_143_out, not_144_out, not_145_out, F5, not_146_out, not_147_out, not_148_out, not_149_out, F0);
  and and_21 (and_21_out, not_150_out, not_151_out, not_152_out, not_153_out, not_154_out, not_155_out, F5, not_156_out, not_157_out, not_158_out, F1, not_159_out);
  and and_22 (and_22_out, not_160_out, not_161_out, not_162_out, not_163_out, not_164_out, not_165_out, F5, not_166_out, not_167_out, F2, not_168_out, not_169_out);
  and and_23 (and_23_out, not_170_out, not_171_out, not_172_out, not_173_out, not_174_out, not_175_out, F5, not_176_out, F3, not_177_out, F1, F0);
  and and_24 (and_24_out, not_178_out, not_179_out, OP3, not_180_out, not_181_out, not_182_out);
  and and_25 (and_25_out, not_183_out, not_184_out, OP3, OP2, not_185_out, not_186_out);
  and and_26 (and_26_out, not_187_out, not_188_out, OP3, not_189_out, not_190_out, OP0);
  and and_27 (and_27_out, OP5, not_191_out, not_192_out, not_193_out, OP1, OP0);
  and and_28 (and_28_out, OP5, not_194_out, OP3, not_195_out, OP1, OP0);
  and and_29 (and_29_out, not_196_out, not_197_out, not_198_out, not_199_out, not_200_out, not_201_out, F5, not_202_out, not_203_out, F2, not_204_out, F0);
  and and_30 (and_30_out, not_205_out, not_206_out, not_207_out, not_208_out, not_209_out, not_210_out, F5, not_211_out, not_212_out, F2, F1, F0);
  and and_31 (and_31_out, not_213_out, not_214_out, not_215_out, not_216_out, not_217_out, not_218_out, F5, not_219_out, F3, not_220_out, F1, not_221_out);
  and and_32 (and_32_out, not_222_out, not_223_out, not_224_out, not_225_out, not_226_out, not_227_out, F5, not_228_out, F3, not_229_out, F1, F0);
  and and_33 (and_33_out, not_230_out, not_231_out, OP3, not_232_out, OP1, not_233_out);
  and and_34 (and_34_out, not_234_out, not_235_out, OP3, OP2, not_236_out, OP0);
  or or_1 (S0, and_1_out, and_2_out, and_3_out, and_4_out, and_5_out, and_6_out, and_7_out, and_8_out, and_9_out, and_10_out, and_11_out);
  or or_2 (S1, and_12_out, and_13_out, and_14_out, and_15_out, and_16_out, and_17_out, and_18_out);
  or or_3 (S2, and_19_out, and_20_out, and_21_out, and_22_out, and_23_out, and_24_out, and_25_out, and_26_out, and_27_out, and_28_out);
  or or_4 (S3, and_29_out, and_30_out, and_31_out, and_32_out, and_33_out, and_34_out);
endmodule

// 控制信号生成
module \控制信号自动生成  (
  input  OP0,
  input  OP1,
  input  OP2,
  input  OP3,
  input  OP4,
  input  OP5,
  input  F0,
  input  F1,
  input  F2,
  input  F3,
  input  F4,
  input  F5,
  output MemToReg,
  output MemWrite,
  output ALU_SRC,
  output RegWrite,
  output SysCALL,
  output SignedExt,
  output RegDst,
  output BEQ,
  output BNE,
  output JR,
  output JUMP,
  output JAL,
  output ERET
);

  wire and_3_out, and_4_out, and_5_out, and_6_out, and_7_out, and_8_out, and_9_out, and_10_out, and_11_out,
       and_12_out, and_13_out, and_15_out, and_16_out, and_17_out, and_18_out, and_19_out, and_20_out,
       and_21_out, and_25_out, and_26_out, not_1_out, not_2_out, not_3_out, not_4_out, not_5_out, not_6_out,
       not_7_out, not_8_out, not_9_out, not_10_out, not_11_out, not_12_out, not_13_out, not_14_out,
       not_15_out, not_16_out, not_17_out, not_18_out, not_19_out, not_20_out, not_21_out, not_22_out,
       not_23_out, not_24_out, not_25_out, not_26_out, not_27_out, not_28_out, not_29_out, not_30_out,
       not_31_out, not_32_out, not_33_out, not_34_out, not_35_out, not_36_out, not_37_out, not_38_out,
       not_39_out, not_40_out, not_41_out, not_42_out, not_43_out, not_44_out, not_45_out, not_46_out,
       not_47_out, not_48_out, not_49_out, not_50_out, not_51_out, not_52_out, not_53_out, not_54_out,
       not_55_out, not_56_out, not_57_out, not_58_out, not_59_out, not_60_out, not_61_out, not_62_out,
       not_63_out, not_64_out, not_65_out, not_66_out, not_67_out, not_68_out, not_69_out, not_70_out,
       not_71_out, not_72_out, not_73_out, not_74_out, not_75_out, not_76_out, not_77_out, not_78_out,
       not_79_out, not_80_out, not_81_out, not_82_out, not_83_out, not_84_out, not_85_out, not_86_out,
       not_87_out, not_88_out, not_89_out, not_90_out, not_91_out, not_92_out, not_93_out, not_94_out,
       not_95_out, not_96_out, not_97_out, not_98_out, not_99_out, not_100_out, not_101_out, not_102_out,
       not_103_out, not_104_out, not_105_out, not_106_out, not_107_out, not_108_out, not_109_out,
       not_110_out, not_111_out, not_112_out, not_113_out, not_114_out, not_115_out, not_116_out,
       not_117_out, not_118_out, not_119_out, not_120_out, not_121_out, not_122_out, not_123_out,
       not_124_out, not_125_out, not_126_out, not_127_out, not_128_out, not_129_out, not_130_out,
       not_131_out, not_132_out, not_133_out, not_134_out, not_135_out, not_136_out, not_137_out,
       not_138_out, not_139_out, not_140_out, not_141_out, not_142_out, not_143_out, not_144_out,
       not_145_out, not_146_out, not_147_out, not_148_out, not_149_out, not_150_out, not_151_out,
       not_152_out, not_153_out, not_154_out, not_155_out, not_156_out, not_157_out, not_158_out,
       not_159_out, not_160_out, not_161_out, not_162_out, not_163_out, not_164_out, not_165_out,
       not_166_out, not_167_out, not_168_out, not_169_out, not_170_out, not_171_out, not_172_out,
       not_173_out, not_174_out;

  not not_1 (not_1_out, OP2);
  not not_2 (not_2_out, OP3);
  not not_3 (not_3_out, OP4);
  not not_4 (not_4_out, OP2);
  not not_5 (not_5_out, OP4);
  not not_6 (not_6_out, OP0);
  not not_7 (not_7_out, OP2);
  not not_8 (not_8_out, OP4);
  not not_9 (not_9_out, OP5);
  not not_10 (not_10_out, OP1);
  not not_11 (not_11_out, OP4);
  not not_12 (not_12_out, OP5);
  not not_13 (not_13_out, OP2);
  not not_14 (not_14_out, OP4);
  not not_15 (not_15_out, OP0);
  not not_16 (not_16_out, OP1);
  not not_17 (not_17_out, OP2);
  not not_18 (not_18_out, OP4);
  not not_19 (not_19_out, OP5);
  not not_20 (not_20_out, F0);
  not not_21 (not_21_out, F2);
  not not_22 (not_22_out, F3);
  not not_23 (not_23_out, F4);
  not not_24 (not_24_out, OP0);
  not not_25 (not_25_out, OP1);
  not not_26 (not_26_out, OP2);
  not not_27 (not_27_out, OP4);
  not not_28 (not_28_out, OP5);
  not not_29 (not_29_out, F1);
  not not_30 (not_30_out, F3);
  not not_31 (not_31_out, F4);
  not not_32 (not_32_out, OP0);
  not not_33 (not_33_out, OP1);
  not not_34 (not_34_out, OP2);
  not not_35 (not_35_out, OP4);
  not not_36 (not_36_out, OP5);
  not not_37 (not_37_out, F2);
  not not_38 (not_38_out, F3);
  not not_39 (not_39_out, F4);
  not not_40 (not_40_out, F5);
  not not_41 (not_41_out, OP0);
  not not_42 (not_42_out, OP1);
  not not_43 (not_43_out, OP2);
  not not_44 (not_44_out, OP4);
  not not_45 (not_45_out, OP5);
  not not_46 (not_46_out, F2);
  not not_47 (not_47_out, F4);
  not not_48 (not_48_out, OP0);
  not not_49 (not_49_out, OP1);
  not not_50 (not_50_out, OP2);
  not not_51 (not_51_out, OP4);
  not not_52 (not_52_out, OP5);
  not not_53 (not_53_out, F3);
  not not_54 (not_54_out, F4);
  not not_55 (not_55_out, OP0);
  not not_56 (not_56_out, OP2);
  not not_57 (not_57_out, OP4);
  not not_58 (not_58_out, OP5);
  not not_59 (not_59_out, OP1);
  not not_60 (not_60_out, OP4);
  not not_61 (not_61_out, OP5);
  not not_62 (not_62_out, OP2);
  not not_63 (not_63_out, OP3);
  not not_64 (not_64_out, OP4);
  not not_65 (not_65_out, OP0);
  not not_66 (not_66_out, OP1);
  not not_67 (not_67_out, OP2);
  not not_68 (not_68_out, OP3);
  not not_69 (not_69_out, OP4);
  not not_70 (not_70_out, OP5);
  not not_71 (not_71_out, F0);
  not not_72 (not_72_out, F1);
  not not_73 (not_73_out, F4);
  not not_74 (not_74_out, F5);
  not not_75 (not_75_out, OP0);
  not not_76 (not_76_out, OP2);
  not not_77 (not_77_out, OP4);
  not not_78 (not_78_out, OP5);
  not not_79 (not_79_out, OP1);
  not not_80 (not_80_out, OP2);
  not not_81 (not_81_out, OP4);
  not not_82 (not_82_out, OP5);
  not not_83 (not_83_out, OP0);
  not not_84 (not_84_out, OP1);
  not not_85 (not_85_out, OP2);
  not not_86 (not_86_out, OP3);
  not not_87 (not_87_out, OP4);
  not not_88 (not_88_out, OP5);
  not not_89 (not_89_out, F0);
  not not_90 (not_90_out, F2);
  not not_91 (not_91_out, F3);
  not not_92 (not_92_out, F4);
  not not_93 (not_93_out, OP0);
  not not_94 (not_94_out, OP1);
  not not_95 (not_95_out, OP2);
  not not_96 (not_96_out, OP3);
  not not_97 (not_97_out, OP4);
  not not_98 (not_98_out, OP5);
  not not_99 (not_99_out, F1);
  not not_100 (not_100_out, F3);
  not not_101 (not_101_out, F4);
  not not_102 (not_102_out, OP0);
  not not_103 (not_103_out, OP1);
  not not_104 (not_104_out, OP2);
  not not_105 (not_105_out, OP3);
  not not_106 (not_106_out, OP4);
  not not_107 (not_107_out, OP5);
  not not_108 (not_108_out, F2);
  not not_109 (not_109_out, F3);
  not not_110 (not_110_out, F4);
  not not_111 (not_111_out, F5);
  not not_112 (not_112_out, OP0);
  not not_113 (not_113_out, OP1);
  not not_114 (not_114_out, OP2);
  not not_115 (not_115_out, OP3);
  not not_116 (not_116_out, OP4);
  not not_117 (not_117_out, OP5);
  not not_118 (not_118_out, F2);
  not not_119 (not_119_out, F4);
  not not_120 (not_120_out, OP0);
  not not_121 (not_121_out, OP1);
  not not_122 (not_122_out, OP2);
  not not_123 (not_123_out, OP3);
  not not_124 (not_124_out, OP4);
  not not_125 (not_125_out, OP5);
  not not_126 (not_126_out, F3);
  not not_127 (not_127_out, F4);
  not not_128 (not_128_out, OP0);
  not not_129 (not_129_out, OP1);
  not not_130 (not_130_out, OP3);
  not not_131 (not_131_out, OP4);
  not not_132 (not_132_out, OP5);
  not not_133 (not_133_out, OP1);
  not not_134 (not_134_out, OP3);
  not not_135 (not_135_out, OP4);
  not not_136 (not_136_out, OP5);
  not not_137 (not_137_out, OP0);
  not not_138 (not_138_out, OP1);
  not not_139 (not_139_out, OP2);
  not not_140 (not_140_out, OP3);
  not not_141 (not_141_out, OP4);
  not not_142 (not_142_out, OP5);
  not not_143 (not_143_out, F0);
  not not_144 (not_144_out, F1);
  not not_145 (not_145_out, F2);
  not not_146 (not_146_out, F4);
  not not_147 (not_147_out, F5);
  not not_148 (not_148_out, OP0);
  not not_149 (not_149_out, OP2);
  not not_150 (not_150_out, OP3);
  not not_151 (not_151_out, OP4);
  not not_152 (not_152_out, OP5);
  not not_153 (not_153_out, F0);
  not not_154 (not_154_out, F1);
  not not_155 (not_155_out, F2);
  not not_156 (not_156_out, F4);
  not not_157 (not_157_out, F5);
  not not_158 (not_158_out, OP2);
  not not_159 (not_159_out, OP3);
  not not_160 (not_160_out, OP4);
  not not_161 (not_161_out, OP5);
  not not_162 (not_162_out, OP2);
  not not_163 (not_163_out, OP3);
  not not_164 (not_164_out, OP4);
  not not_165 (not_165_out, OP5);
  not not_166 (not_166_out, OP5);
  not not_167 (not_167_out, OP3);
  not not_168 (not_168_out, OP2);
  not not_169 (not_169_out, OP1);
  not not_170 (not_170_out, OP0);
  not not_171 (not_171_out, F5);
  not not_172 (not_172_out, F2);
  not not_173 (not_173_out, F1);
  not not_174 (not_174_out, F0);
  and and_1 (MemToReg, OP0, OP1, not_1_out, not_2_out, not_3_out, OP5);
  and and_2 (MemWrite, OP0, OP1, not_4_out, OP3, not_5_out, OP5);
  and and_3 (and_3_out, not_6_out, not_7_out, OP3, not_8_out, not_9_out);
  and and_4 (and_4_out, not_10_out, OP3, not_11_out, not_12_out);
  or or_1 (ALU_SRC, and_3_out, and_4_out, and_5_out);
  and and_5 (and_5_out, OP0, OP1, not_13_out, not_14_out, OP5);
  and and_6 (and_6_out, not_15_out, not_16_out, not_17_out, not_18_out, not_19_out, not_20_out, not_21_out, not_22_out, not_23_out);
  and and_7 (and_7_out, not_24_out, not_25_out, not_26_out, not_27_out, not_28_out, not_29_out, not_30_out, not_31_out, F5);
  and and_8 (and_8_out, not_32_out, not_33_out, not_34_out, not_35_out, not_36_out, F1, not_37_out, not_38_out, not_39_out, not_40_out);
  and and_9 (and_9_out, not_41_out, not_42_out, not_43_out, not_44_out, not_45_out, F1, not_46_out, F3, not_47_out, F5);
  and and_10 (and_10_out, not_48_out, not_49_out, not_50_out, not_51_out, not_52_out, F0, F2, not_53_out, not_54_out, F5);
  and and_11 (and_11_out, not_55_out, not_56_out, OP3, not_57_out, not_58_out);
  and and_12 (and_12_out, not_59_out, OP3, not_60_out, not_61_out);
  and and_13 (and_13_out, OP0, OP1, not_62_out, not_63_out, not_64_out);
  and and_14 (SysCALL, not_65_out, not_66_out, not_67_out, not_68_out, not_69_out, not_70_out, not_71_out, not_72_out, F2, F3, not_73_out, not_74_out);
  and and_15 (and_15_out, not_75_out, not_76_out, OP3, not_77_out, not_78_out);
  or or_2 (SignedExt, and_15_out, and_16_out);
  and and_16 (and_16_out, not_79_out, not_80_out, OP3, not_81_out, not_82_out);
  and and_17 (and_17_out, not_83_out, not_84_out, not_85_out, not_86_out, not_87_out, not_88_out, not_89_out, not_90_out, not_91_out, not_92_out);
  and and_18 (and_18_out, not_93_out, not_94_out, not_95_out, not_96_out, not_97_out, not_98_out, not_99_out, not_100_out, not_101_out, F5);
  and and_19 (and_19_out, not_102_out, not_103_out, not_104_out, not_105_out, not_106_out, not_107_out, F1, not_108_out, not_109_out, not_110_out, not_111_out);
  and and_20 (and_20_out, not_112_out, not_113_out, not_114_out, not_115_out, not_116_out, not_117_out, F1, not_118_out, F3, not_119_out, F5);
  and and_21 (and_21_out, not_120_out, not_121_out, not_122_out, not_123_out, not_124_out, not_125_out, F0, F2, not_126_out, not_127_out, F5);
  and and_22 (BEQ, not_128_out, not_129_out, OP2, not_130_out, not_131_out, not_132_out);
  and and_23 (BNE, OP0, not_133_out, OP2, not_134_out, not_135_out, not_136_out);
  and and_24 (JR, not_137_out, not_138_out, not_139_out, not_140_out, not_141_out, not_142_out, not_143_out, not_144_out, not_145_out, F3, not_146_out, not_147_out);
  and and_25 (and_25_out, not_148_out, not_149_out, not_150_out, not_151_out, not_152_out, not_153_out, not_154_out, not_155_out, F3, not_156_out, not_157_out);
  and and_26 (and_26_out, OP1, not_158_out, not_159_out, not_160_out, not_161_out);
  and and_27 (JAL, OP0, OP1, not_162_out, not_163_out, not_164_out, not_165_out);
  and and_28 (ERET, not_166_out, OP4, not_167_out, not_168_out, not_169_out, not_170_out, not_171_out, F4, F3, not_172_out, not_173_out, not_174_out);
  or or_3 (RegWrite, and_6_out, and_7_out, and_8_out, and_9_out, and_10_out, and_11_out, and_12_out, and_13_out);
  or or_4 (RegDst, and_17_out, and_18_out, and_19_out, and_20_out, and_21_out);
  or or_5 (JUMP, and_25_out, and_26_out);
endmodule

// ALU
module MIPS_ALU (
  input  [4:0] shamt,
  input  [31:0] X,
  input  [31:0] Y,
  input  [3:0] AluOP,
  output Equal,
  output [31:0] Result,
  output [31:0] Result_2
);

  wire [0:0] comparator_1_lt, comparator_2_lt;
  wire [31:0] adder_1_out, AND_out, divider_1_out, divider_1_rem, multiplier_1_cout, multiplier_1_out,
       NOR_out, OR_out, shifter_1_out, shifter_2_out, shifter_3_out, subtractor_1_out, XOR_out;

  assign AND_out = X & Y;  // AND_Gate AND, 32 bits wide
  assign OR_out = X | Y;  // OR_Gate OR, 32 bits wide
  Shifter #(.width(32), .shift("ll")) shifter_1 (.in(Y), .\dist (shamt), .out(shifter_1_out));
  Shifter #(.width(32), .shift("ar")) shifter_2 (.in(Y), .\dist (shamt), .out(shifter_2_out));
  Shifter #(.width(32), .shift("lr")) shifter_3 (.in(Y), .\dist (shamt), .out(shifter_3_out));
  Multiplier #(.width(32)) multiplier_1 (.a(X), .b(Y), .out(multiplier_1_out), .cout(multiplier_1_cout));  // open: cin
  Divider #(.width(32)) divider_1 (.a(X), .b(Y), .out(divider_1_out), .rem(divider_1_rem));  // open: upper
  Adder #(.width(32)) adder_1 (.a(X), .b(Y), .out(adder_1_out));  // open: cin, cout
  Subtractor #(.width(32)) subtractor_1 (.a(X), .b(Y), .out(subtractor_1_out));  // open: bin, bout
  assign XOR_out = X ^ Y;  // XOR_Gate XOR, 32 bits wide
  assign NOR_out = ~(X | Y);  // NOR_Gate NOR, 32 bits wide
  Comparator #(.width(32), .mode("twosComplement")) comparator_1 (
    .a(X), .b(Y), .eq(Equal), .lt(comparator_1_lt[0]));  // open: gt
  Comparator #(.width(32), .mode("unsigned")) comparator_2 (.a(X), .b(Y), .lt(comparator_2_lt[0]));  // open: gt, eq
  Multiplexer #(.select(4), .width(32), .disabled("Z"), .enable("false")) multiplexer_1 (
    .in0(shifter_1_out), .in1(shifter_2_out), .in2(shifter_3_out), .in3(multiplier_1_out),
    .in4(divider_1_out), .in5(adder_1_out), .in6(subtractor_1_out), .in7(AND_out), .in8(OR_out),
    .in9(XOR_out), .in10(NOR_out), .in11({{31{1'b0}}, comparator_1_lt[0]}),
    .in12({{31{1'b0}}, comparator_2_lt[0]}), .in13({32{1'b0}}), .in14({32{1'b0}}), .in15({32{1'b0}}),
    .out(Result), .sel(AluOP));
  Multiplexer #(.select(4), .width(32), .disabled("Z"), .enable("false")) multiplexer_2 (
    .in0({32{1'b0}}), .in1({32{1'b0}}), .in2({32{1'b0}}), .in3(multiplier_1_cout), .in4(divider_1_rem),
    .in5({32{1'b0}}), .in6({32{1'b0}}), .in7({32{1'b0}}), .in8({32{1'b0}}), .in9({32{1'b0}}),
    .in10({32{1'b0}}), .in11({32{1'b0}}), .in12({32{1'b0}}), .in13({32{1'b0}}), .in14({32{1'b0}}),
    .in15({32{1'b0}}), .out(Result_2), .sel(AluOP));

  // Other names for the same wires on the sheet: Result2[31:0] = Result_2; S[3:0] = AluOP

  // Notes on the sheet:
  //   不要改变此引脚区域内容，也不要改变ALU封装形式
  //   输入引脚
  //   输出引脚
endmodule

module MIPS_Regifile (
  input  [31:0] Din,
  input  Clk,
  input  WE,
  input  [4:0] R1_num,
  input  [4:0] W_num,
  input  [4:0] R2_num,
  output [31:0] R1,
  output [31:0] R2
);

  // RegisterFile registerfile_1: pin names not known; wires that end beside it: Din, Clk, WE, W_num, R1_num, R2_num, R1, R2
endmodule

module \理想流水线  (
  output RegWrite,
  output MemWrite,
  output [31:0] IF_PC,
  output [31:0] ID_PC,
  output [31:0] EX_PC,
  output [31:0] M_PC,
  output [31:0] WB_PC,
  output [31:0] RDin,
  output [31:0] MDin,
  output [31:0] LedData
);

  wire CLK, clock_1_out, clock_2_out, comparator_1_eq, comparator_1_lt, d_ff_1_q, Go, IR1, IR2, IR3,
       nand_1_out, RST, W1, W2, W3;
  wire [12:0] CNT_num;
  wire [15:0] \LoadUse次数 , \总周期数 , \插入气泡数 , \无条件分支数 , \条件分支成功数 ;
  wire [31:0] EX_IR, ID_IR, IF_IR, MEM_IR, WB_IR;

  Button \u_总复位  (.out(RST));
  Button _1 (.out(IR1));
  Button _2 (.out(IR2));
  Button _3 (.out(IR3));
  // Probe on \总周期数 
  // Probe on \总周期数 
  Button \u_继续运行  (.out(Go));
  LED #(.active("true")) led_1 (.in(W1));
  LED #(.active("true")) led_2 (.in(W2));
  LED #(.active("true")) led_3 (.in(W3));
  Hex_Digit_Display hex_digit_display_1 (.value(LedData[31:28]));  // open: dp
  // Probe on IF_PC[19:0]
  // Mips_Probe mips_probe_1: pin names not known; wires that end beside it: IF_IR
  Hex_Digit_Display hex_digit_display_2 (.value(LedData[27:24]));  // open: dp
  Hex_Digit_Display hex_digit_display_3 (.value(LedData[23:20]));  // open: dp
  // Probe on ID_PC[19:0]
  // Mips_Probe mips_probe_2: pin names not known; wires that end beside it: ID_IR
  Hex_Digit_Display hex_digit_display_4 (.value(LedData[15:12]));  // open: dp
  Hex_Digit_Display hex_digit_display_5 (.value(LedData[19:16]));  // open: dp
  Hex_Digit_Display hex_digit_display_6 (.value(LedData[7:4]));  // open: dp
  Hex_Digit_Display hex_digit_display_7 (.value(LedData[11:8]));  // open: dp
  Clock #(.highDuration(1), .lowDuration(1)) clock_1 (.out(clock_1_out));
  // Probe on EX_PC[19:0]
  // Mips_Probe mips_probe_3: pin names not known; wires that end beside it: clock_1_out, EX_IR, CLK
  Hex_Digit_Display hex_digit_display_8 (.value(LedData[3:0]));  // open: dp
  // Probe on \总周期数 
  // Probe on M_PC[19:0]
  // Mips_Probe mips_probe_4: pin names not known; wires that end beside it: MEM_IR
  // Probe on \总周期数 
  // Probe on \无条件分支数 
  // Probe on \条件分支成功数 
  // Probe on \插入气泡数 
  // Probe on \LoadUse次数 
  // Probe on IF_PC[11:0]
  // Probe on WB_PC[19:0]
  // Mips_Probe mips_probe_5: pin names not known; wires that end beside it: WB_IR
  // Probe on EX_PC[11:0]
  // Probe on ID_PC[11:0]
  // Probe on M_PC[11:0]
  D_Flip_Flop #(.trigger("high"), .Pre_Clr_Positions("LEGACY"), .NegatePresetClear("false"), .enable("true"), .NewFFLayout("false")) d_ff_1 (.Q(d_ff_1_q));  // open: clk, D, Qn, preset, en, reset
  // Probe on 13'hc
  // Probe on WB_PC[11:0]
  Comparator #(.width(13), .mode("twosComplement")) comparator_1 (
    .a(CNT_num), .b(13'hc), .eq(comparator_1_eq), .lt(comparator_1_lt));  // open: gt
  Clock #(.highDuration(1), .lowDuration(1)) clock_2 (.out(clock_2_out));
  nand nand_1 (nand_1_out, d_ff_1_q, comparator_1_eq);
  Counter #(.width(13), .max('h1fff), .ongoal("stay"), .trigger("rising"), .behavior("old")) counter_1 (
    .count(comparator_1_lt), .Q(CNT_num), .clk(clock_2_out));  // open: load, D, carry, clr, preset
  assign CLK = nand_1_out ? clock_2_out : 1'bz;  // Controlled_Buffer controlled_buffer_1
  Pull_Resistor #(.pull(1)) pull_resistor_1 (.node(CLK));

  // Other names for the same wires on the sheet: MEM_PC[31:0] = M_PC

  // Notes on the sheet:
  //   中断源
  //   时空图监测，可删除
  //   中断等待指示
  //   数码管输出
  //   控制位
  //   流水调试日志用
  //   暂停节拍，不能为0
  //   戳工具置1进入计数暂停模式，ctrl+k时钟自动运行到对应节拍暂停
  //   ctrl+k关闭时钟连续运行，将控制位置零，进入单步调试模式调试
  //   用这个时钟源需要去掉电路中的其他时钟源
  //   可计数暂停的时钟源
  //   为方便自动评测，需要输出流水线各段保存的PC值，注意是PC不是PC+4，另外ID段寄存器写入信息，Mem段内存写入信息也要输出
endmodule

module \气泡流水线  (
  output RegWrite,
  output MemWrite,
  output [31:0] IF_PC,
  output [31:0] ID_PC,
  output [31:0] EX_PC,
  output [31:0] M_PC,
  output [31:0] WB_PC,
  output [31:0] RDin,
  output [31:0] MDin,
  output [31:0] LedData
);

  wire CLK, clock_2_out, comparator_1_eq, comparator_1_lt, d_ff_1_q, Go, IR1, IR2, IR3, nand_1_out, RST, W1,
       W2, W3;
  wire [12:0] CNT_num;
  wire [15:0] \LoadUse次数 , \总周期数 , \插入气泡数 , \无条件分支数 , \条件分支成功数 ;
  wire [31:0] EX_IR, ID_IR, IF_IR, MEM_IR, WB_IR;

  Button \u_总复位  (.out(RST));
  Button _1 (.out(IR1));
  Button _2 (.out(IR2));
  Button _3 (.out(IR3));
  // Probe on \总周期数 
  // Probe on \总周期数 
  Button \u_继续运行  (.out(Go));
  LED #(.active("true")) led_1 (.in(W1));
  LED #(.active("true")) led_2 (.in(W2));
  LED #(.active("true")) led_3 (.in(W3));
  Hex_Digit_Display hex_digit_display_1 (.value(LedData[31:28]));  // open: dp
  // Probe on IF_PC[19:0]
  // Mips_Probe mips_probe_1: pin names not known; wires that end beside it: IF_IR
  Hex_Digit_Display hex_digit_display_2 (.value(LedData[23:20]));  // open: dp
  Hex_Digit_Display hex_digit_display_3 (.value(LedData[27:24]));  // open: dp
  // Probe on ID_PC[19:0]
  // Mips_Probe mips_probe_2: pin names not known; wires that end beside it: ID_IR
  Hex_Digit_Display hex_digit_display_4 (.value(LedData[15:12]));  // open: dp
  Hex_Digit_Display hex_digit_display_5 (.value(LedData[19:16]));  // open: dp
  Hex_Digit_Display hex_digit_display_6 (.value(LedData[11:8]));  // open: dp
  Hex_Digit_Display hex_digit_display_7 (.value(LedData[7:4]));  // open: dp
  Clock #(.highDuration(1), .lowDuration(1)) clock_1 (.out(CLK));
  // Probe on EX_PC[19:0]
  // Mips_Probe mips_probe_3: pin names not known; wires that end beside it: EX_IR
  Hex_Digit_Display hex_digit_display_8 (.value(LedData[3:0]));  // open: dp
  // Probe on \总周期数 
  // Probe on M_PC[19:0]
  // Mips_Probe mips_probe_4: pin names not known; wires that end beside it: MEM_IR
  // Probe on \总周期数 
  // Probe on \无条件分支数 
  // Probe on \条件分支成功数 
  // Probe on \插入气泡数 
  // Probe on \LoadUse次数 
  // Probe on IF_PC[11:0]
  // Probe on WB_PC[19:0]
  // Mips_Probe mips_probe_5: pin names not known; wires that end beside it: WB_IR
  // Probe on ID_PC[11:0]
  // Probe on EX_PC[11:0]
  // Probe on M_PC[11:0]
  D_Flip_Flop #(.trigger("high"), .Pre_Clr_Positions("LEGACY"), .NegatePresetClear("false"), .enable("true"), .NewFFLayout("false")) d_ff_1 (.Q(d_ff_1_q));  // open: clk, D, Qn, preset, en, reset
  // Probe on 13'hc
  // Probe on WB_PC[11:0]
  Comparator #(.width(13), .mode("twosComplement")) comparator_1 (
    .a(CNT_num), .b(13'hc), .eq(comparator_1_eq), .lt(comparator_1_lt));  // open: gt
  Clock #(.highDuration(1), .lowDuration(1)) clock_2 (.out(clock_2_out));
  nand nand_1 (nand_1_out, d_ff_1_q, comparator_1_eq);
  Counter #(.width(13), .max('h1fff), .ongoal("stay"), .trigger("rising"), .behavior("old")) counter_1 (
    .count(comparator_1_lt), .Q(CNT_num), .clk(clock_2_out));  // open: load, D, carry, clr, preset
  assign CLK = nand_1_out ? clock_2_out : 1'bz;  // Controlled_Buffer controlled_buffer_1
  Pull_Resistor #(.pull(1)) pull_resistor_1 (.node(CLK));

  // Other names for the same wires on the sheet: MEM_PC[31:0] = M_PC

  // Notes on the sheet:
  //   中断源
  //   时空图监测，可删除
  //   中断等待指示
  //   数码管输出
  //   控制位
  //   流水调试日志用
  //   暂停节拍，不能为0
  //   戳工具置1进入计数暂停模式，ctrl+k时钟自动运行到对应节拍暂停
  //   ctrl+k关闭时钟连续运行，将控制位置零，进入单步调试模式调试
  //   可计数暂停的时钟源
  //   为方便自动评测，需要输出流水线各段保存的PC值，注意是PC不是PC+4，另外ID段寄存器写入信息，Mem段内存写入信息也要输出
endmodule

module \重定向流水线  (
  output RegWrite,
  output MemWrite,
  output [31:0] IF_PC,
  output [31:0] ID_PC,
  output [31:0] EX_PC,
  output [31:0] M_PC,
  output [31:0] WB_PC,
  output [31:0] RDin,
  output [31:0] MDin,
  output [31:0] LedData
);

  wire CLK, clock_2_out, comparator_1_eq, comparator_1_lt, d_ff_1_q, Go, IR1, IR2, IR3, nand_1_out, RST, W1,
       W2, W3;
  wire [12:0] CNT_num;
  wire [15:0] \LoadUse次数 , \总周期数 , \插入气泡数 , \无条件分支数 , \条件分支成功数 ;
  wire [31:0] EX_IR, ID_IR, IF_IR, MEM_IR, WB_IR;

  Button \u_总复位  (.out(RST));
  Button _1 (.out(IR1));
  Button _2 (.out(IR2));
  Button _3 (.out(IR3));
  // Probe on \总周期数 
  // Probe on \总周期数 
  Button \u_继续运行  (.out(Go));
  LED #(.active("true")) led_1 (.in(W1));
  LED #(.active("true")) led_2 (.in(W2));
  LED #(.active("true")) led_3 (.in(W3));
  Hex_Digit_Display hex_digit_display_1 (.value(LedData[31:28]));  // open: dp
  // Probe on IF_PC[19:0]
  // Mips_Probe mips_probe_1: pin names not known; wires that end beside it: IF_IR
  Hex_Digit_Display hex_digit_display_2 (.value(LedData[23:20]));  // open: dp
  Hex_Digit_Display hex_digit_display_3 (.value(LedData[27:24]));  // open: dp
  // Probe on ID_PC[19:0]
  // Mips_Probe mips_probe_2: pin names not known; wires that end beside it: ID_IR
  Hex_Digit_Display hex_digit_display_4 (.value(LedData[19:16]));  // open: dp
  Hex_Digit_Display hex_digit_display_5 (.value(LedData[15:12]));  // open: dp
  Hex_Digit_Display hex_digit_display_6 (.value(LedData[11:8]));  // open: dp
  Hex_Digit_Display hex_digit_display_7 (.value(LedData[7:4]));  // open: dp
  Clock #(.highDuration(1), .lowDuration(1)) clock_1 (.out(CLK));
  // Probe on EX_PC[19:0]
  // Mips_Probe mips_probe_3: pin names not known; wires that end beside it: EX_IR
  Hex_Digit_Display hex_digit_display_8 (.value(LedData[3:0]));  // open: dp
  // Probe on \总周期数 
  // Probe on M_PC[19:0]
  // Mips_Probe mips_probe_4: pin names not known; wires that end beside it: MEM_IR
  // Probe on \总周期数 
  // Probe on \无条件分支数 
  // Probe on \条件分支成功数 
  // Probe on \插入气泡数 
  // Probe on \LoadUse次数 
  // Probe on IF_PC[11:0]
  // Probe on WB_PC[19:0]
  // Mips_Probe mips_probe_5: pin names not known; wires that end beside it: WB_IR
  // Probe on ID_PC[11:0]
  // Probe on EX_PC[11:0]
  // Probe on M_PC[11:0]
  D_Flip_Flop #(.trigger("high"), .Pre_Clr_Positions("LEGACY"), .NegatePresetClear("false"), .enable("true"), .NewFFLayout("false")) d_ff_1 (.Q(d_ff_1_q));  // open: clk, D, Qn, preset, en, reset
  // Probe on 13'hc
  // Probe on WB_PC[11:0]
  Comparator #(.width(13), .mode("twosComplement")) comparator_1 (
    .a(CNT_num), .b(13'hc), .eq(comparator_1_eq), .lt(comparator_1_lt));  // open: gt
  Clock #(.highDuration(1), .lowDuration(1)) clock_2 (.out(clock_2_out));
  nand nand_1 (nand_1_out, d_ff_1_q, comparator_1_eq);
  Counter #(.width(13), .max('h1fff), .ongoal("stay"), .trigger("rising"), .behavior("old")) counter_1 (
    .count(comparator_1_lt), .Q(CNT_num), .clk(clock_2_out));  // open: load, D, carry, clr, preset
  assign CLK = nand_1_out ? clock_2_out : 1'bz;  // Controlled_Buffer controlled_buffer_1
  Pull_Resistor #(.pull(1)) pull_resistor_1 (.node(CLK));

  // Other names for the same wires on the sheet: MEM_PC[31:0] = M_PC

  // Notes on the sheet:
  //   中断源
  //   时空图监测，可删除
  //   中断等待指示
  //   数码管输出
  //   控制位
  //   流水调试日志用
  //   暂停节拍，不能为0
  //   戳工具置1进入计数暂停模式，ctrl+k时钟自动运行到对应节拍暂停
  //   ctrl+k关闭时钟连续运行，将控制位置零，进入单步调试模式调试
  //   可计数暂停的时钟源
  //   为方便自动评测，需要输出流水线各段保存的PC值，注意是PC不是PC+4，另外ID段寄存器写入信息，Mem段内存写入信息也要输出
endmodule

module \中断按键参考电路  (
  input  \同步清零信号 ,
  output \与中断屏蔽位与 
);

  wire \_1号中断_out , and_1_out, clock_1_out, d_ff_1_q, or_1_out, or_2_out;

  Clock #(.highDuration(1), .lowDuration(1)) clock_1 (.out(clock_1_out));
  Button \_1号中断  (.out(\_1号中断_out ));
  or or_1 (or_1_out, \与中断屏蔽位与 , d_ff_1_q);
  LED #(.active("true")) \_1号中断等待指示灯  (.in(or_1_out));
  D_Flip_Flop #(.trigger("rising"), .Pre_Clr_Positions("LEGACY"), .NegatePresetClear("false"), .enable("true"), .NewFFLayout("false")) d_ff_1 (
    .clk(\_1号中断_out ), .D(1'b1), .Q(d_ff_1_q), .reset(\与中断屏蔽位与 ));  // open: Qn, preset, en
  or or_2 (or_2_out, d_ff_1_q, \与中断屏蔽位与 );
  and and_1 (and_1_out, or_2_out, ~\同步清零信号 );  // AND_Gate
  D_Flip_Flop #(.trigger("rising"), .Pre_Clr_Positions("LEGACY"), .NegatePresetClear("false"), .enable("true"), .NewFFLayout("false")) IR1 (
    .clk(clock_1_out), .D(and_1_out), .Q(\与中断屏蔽位与 ));  // open: Qn, preset, en, reset
  \单周期硬布线控制器  \u_单周期硬布线控制器_1  ();  // open: Func, OP, ALU_OP, MemToReg, MemWrite, ALU_SRC, SysCALL, SignedExt, RegDst, JR, JMP, Beq, JAL, Bne, ERET, in_3, MTC0, MFC0, RegWrite

  // Notes on the sheet:
  //   中断信号采样参考电路
  //   Reset 
endmodule

module \单周期MIPS_单级中断  (
  input  IR1,
  input  IR2,
  input  IR3,
  output RegWrite,
  output MemWrite,
  output [31:0] PC,
  output [31:0] IR,
  output [31:0] RDin,
  output [31:0] MDin,
  output [31:0] LedData
);

  wire _1_out, _2_out, _3_out, AluSrcB, and_1_out, and_2_out, and_3_out, and_5_out, and_6_out, and_7_out,
       and_8_out, Beq, Bne, clear1, clear2, clear3, CLK, clock_2_out, comparator_1_eq, comparator_1_lt,
       comparator_2_eq, comparator_3_eq, comparator_4_eq, comparator_5_eq, comparator_6_eq,
       controlled_buffer_1_out, d_ff_1_q, d_ff_2_q, d_ff_3_q, d_ff_4_q, Eret, Go, Halt, IE, INT, Int1, Int2,
       Int3, IntAll, IR1_t, IR2_t, IR3_t, IRA, IRB, IRC, JAL, JMP, JR, MemToReg, mips_alu_1_equal,
       nand_1_out, not_1_out, not_2_out, not_3_out, not_4_out, not_5_out, or_1_out, or_4_out, or_10_out,
       or_11_out, or_12_out, PCSrc, RegDst, Reset, SignedExt, Syscall, W1, W2, W3;
  wire [1:0] priority_encoder_1_out, register_2_q;
  wire [3:0] AluOP;
  wire [4:0] multiplexer_6_out, multiplexer_7_out, multiplexer_8_out, multiplexer_9_out;
  wire [12:0] CNT_num;
  wire [15:0] \总周期数 ;
  wire [31:0] bit_extender_1_out, bit_extender_2_out, BreakAddr, EPCAddr, IntAddr, mips_alu_1_result,
       multiplexer_1_out, multiplexer_2_out, multiplexer_4_out, multiplexer_5_out, multiplexer_11_out,
       multiplexer_12_out, PC_4, PC_imm, PC_rst, ram_1_data, shifter_1_out, WriteBackData;

  Clock #(.highDuration(1), .lowDuration(1)) clock_1 (.out(CLK));
  Button _1 (.out(_1_out));
  Button _2 (.out(_2_out));
  Button _3 (.out(_3_out));
  Multiplexer #(.select(1), .width(32), .disabled("Z"), .enable("false")) multiplexer_1 (
    .in0(PC_4), .in1(PC_imm), .out(multiplexer_1_out), .sel(PCSrc));
  Multiplexer #(.select(1), .width(32), .disabled("Z"), .enable("false")) multiplexer_2 (
    .in0(multiplexer_1_out), .in1({PC[31:28], IR[25:0], 2'b00}), .out(multiplexer_2_out), .sel(JMP));
  Multiplexer #(.select(1), .width(32), .disabled("Z"), .enable("false")) multiplexer_3 (
    .in0(multiplexer_2_out), .in1(PC_rst), .out(BreakAddr), .sel(JR));
  Button \u_继续运行  (.out(Go));
  LED #(.active("true")) led_1 (.in(W1));
  LED #(.active("true")) led_2 (.in(W2));
  LED #(.active("true")) led_3 (.in(W3));
  Multiplexer #(.select(1), .width(32), .disabled("Z"), .enable("false")) multiplexer_4 (
    .in0(BreakAddr), .in1(IntAddr), .out(multiplexer_4_out), .sel(INT));
  Hex_Digit_Display hex_digit_display_1 (.value(LedData[31:28]));  // open: dp
  Multiplexer #(.select(1), .width(32), .disabled("Z"), .enable("false")) multiplexer_5 (
    .in0(multiplexer_4_out), .in1(EPCAddr), .out(multiplexer_5_out), .sel(Eret));
  or or_1 (or_1_out, not_1_out, Go);
  not not_1 (not_1_out, Halt);
  D_Flip_Flop #(.trigger("high"), .Pre_Clr_Positions("LEGACY"), .NegatePresetClear("false"), .enable("true"), .NewFFLayout("false")) d_ff_1 (.Q(d_ff_1_q));  // open: clk, D, Qn, preset, en, reset
  // Probe on 13'hc
  Hex_Digit_Display hex_digit_display_2 (.value(LedData[27:24]));  // open: dp
  Hex_Digit_Display hex_digit_display_3 (.value(LedData[23:20]));  // open: dp
  Register #(.width(32), .trigger("rising"), .Select("low")) u_PC (
    .D(multiplexer_5_out), .en(or_1_out), .Q(PC), .clk(CLK), .clr(Reset));
  Comparator #(.width(13), .mode("twosComplement")) comparator_1 (
    .a(CNT_num), .b(13'hc), .eq(comparator_1_eq), .lt(comparator_1_lt));  // open: gt
  Clock #(.highDuration(1), .lowDuration(1)) clock_2 (.out(clock_2_out));
  Hex_Digit_Display hex_digit_display_4 (.value(LedData[15:12]));  // open: dp
  Hex_Digit_Display hex_digit_display_5 (.value(LedData[19:16]));  // open: dp
  Button button_1 (.out(Reset));
  Counter #(.width(16), .max('hffff), .ongoal("wrap"), .trigger("rising"), .behavior("old")) counter_1 (
    .count(not_2_out), .Q(\总周期数 ), .clk(CLK));  // open: load, D, carry, clr, preset
  not not_2 (not_2_out, Halt);
  Adder #(.width(32)) adder_1 (.a(PC), .b(32'h4), .out(PC_4));  // open: cin, cout
  nand nand_1 (nand_1_out, d_ff_1_q, comparator_1_eq);
  Counter #(.width(13), .max('h1fff), .ongoal("stay"), .trigger("rising"), .behavior("old")) counter_2 (
    .count(comparator_1_lt), .Q(CNT_num), .clk(clock_2_out));  // open: load, D, carry, clr, preset
  Hex_Digit_Display hex_digit_display_6 (.value(LedData[11:8]));  // open: dp
  Hex_Digit_Display hex_digit_display_7 (.value(LedData[7:4]));  // open: dp
  // Probe on \总周期数 
  assign controlled_buffer_1_out = nand_1_out ? clock_2_out : 1'bz;  // Controlled_Buffer controlled_buffer_1
  Hex_Digit_Display hex_digit_display_8 (.value(LedData[3:0]));  // open: dp
  // Mips_Probe mips_probe_1: pin names not known; wires that end beside it: IR
  ROM #(.addrWidth(10), .dataWidth(32), .Select("high")) rom_1 (.addr(PC[11:2]), .data(IR));
  Pull_Resistor #(.pull(1)) pull_resistor_1 (.node(controlled_buffer_1_out));
  or or_2 (IR1_t, IR1, IRA);
  \单周期硬布线控制器  \u_单周期硬布线控制器_1  (
    .Func(IR[5:0]), .OP(IR[31:26]), .ALU_OP(AluOP), .MemToReg(MemToReg), .MemWrite(MemWrite),
    .ALU_SRC(AluSrcB), .SysCALL(Syscall), .SignedExt(SignedExt), .RegDst(RegDst), .JR(JR), .JMP(JMP),
    .Beq(Beq), .JAL(JAL), .Bne(Bne), .ERET(Eret), .RegWrite(RegWrite));  // open: in_3, MTC0, MFC0
  Multiplexer #(.select(1), .width(5), .disabled("Z"), .enable("false")) multiplexer_6 (
    .in0(IR[25:21]), .in1(5'b00010), .out(multiplexer_6_out), .sel(Syscall));
  Multiplexer #(.select(1), .width(5), .disabled("Z"), .enable("false")) multiplexer_7 (
    .in0(IR[20:16]), .in1(5'b00100), .out(multiplexer_7_out), .sel(Syscall));
  Multiplexer #(.select(1), .width(5), .disabled("Z"), .enable("false")) multiplexer_8 (
    .in0(IR[20:16]), .in1(IR[15:11]), .out(multiplexer_8_out), .sel(RegDst));
  Multiplexer #(.select(1), .width(5), .disabled("Z"), .enable("false")) multiplexer_9 (
    .in0(multiplexer_8_out), .in1({5{1'b1}}), .out(multiplexer_9_out), .sel(JAL));
  assign bit_extender_1_out = {{16{1'b0}}, IR[15:0]};  // Bit_Extender bit_extender_1
  assign bit_extender_2_out = {{16{IR[15]}}, IR[15:0]};  // Bit_Extender bit_extender_2
  or or_3 (IR2_t, IR2, IRB);
  Multiplexer #(.select(1), .width(32), .disabled("Z"), .enable("false")) multiplexer_10 (
    .in0(WriteBackData), .in1(PC_4), .out(RDin), .sel(JAL));
  Multiplexer #(.select(1), .width(32), .disabled("Z"), .enable("false")) multiplexer_11 (
    .in0(bit_extender_1_out), .in1(bit_extender_2_out), .out(multiplexer_11_out), .sel(SignedExt));
  MIPS_Regifile mips_regifile_1 (
    .Din(RDin), .Clk(CLK), .R1(PC_rst), .R2(MDin), .WE(RegWrite), .W_num(multiplexer_9_out),
    .R1_num(multiplexer_6_out), .R2_num(multiplexer_7_out));
  Shifter #(.width(32), .shift("ll")) shifter_1 (.in(bit_extender_2_out), .\dist (5'b00010), .out(shifter_1_out));
  Comparator #(.width(16), .mode("twosComplement")) comparator_2 (
    .a(16'h23b), .b(\总周期数 ), .eq(comparator_2_eq));  // open: gt, lt
  or or_4 (or_4_out, comparator_2_eq, comparator_3_eq);
  Comparator #(.width(16), .mode("twosComplement")) comparator_3 (
    .a(\总周期数 ), .b(16'h1), .eq(comparator_3_eq));  // open: gt, lt
  Comparator #(.width(16), .mode("twosComplement")) comparator_4 (
    .a(\总周期数 ), .b(16'h4), .eq(comparator_4_eq));  // open: gt, lt
  Comparator #(.width(16), .mode("twosComplement")) comparator_5 (
    .a(\总周期数 ), .b(16'h7), .eq(comparator_5_eq));  // open: gt, lt
  or or_5 (IR3_t, IR3, IRC);
  Adder #(.width(32)) adder_2 (.a(shifter_1_out), .b(PC_4), .out(PC_imm));  // open: cin, cout
  Pull_Resistor #(.pull(0)) pull_resistor_2 (.node(IRA));
  assign IRA = or_4_out ? ~CLK : 1'bz;  // Controlled_Inverter controlled_inverter_1
  Pull_Resistor #(.pull(0)) pull_resistor_3 (.node(IRB));
  assign IRB = comparator_4_eq ? ~CLK : 1'bz;  // Controlled_Inverter controlled_inverter_2
  Pull_Resistor #(.pull(0)) pull_resistor_4 (.node(IRC));
  assign IRC = comparator_5_eq ? ~CLK : 1'bz;  // Controlled_Inverter controlled_inverter_3
  Comparator #(.width(32), .mode("twosComplement")) comparator_6 (
    .a(PC_rst), .b(32'h22), .eq(comparator_6_eq));  // open: gt, lt
  not not_3 (not_3_out, mips_alu_1_equal);
  Multiplexer #(.select(1), .width(32), .disabled("Z"), .enable("false")) multiplexer_12 (
    .in0(MDin), .in1(multiplexer_11_out), .out(multiplexer_12_out), .sel(AluSrcB));
  not not_4 (not_4_out, comparator_6_eq);
  and and_1 (and_1_out, not_3_out, Bne);
  and and_2 (and_2_out, Beq, mips_alu_1_equal);
  MIPS_ALU mips_alu_1 (
    .X(PC_rst), .Y(multiplexer_12_out), .AluOP(AluOP), .Equal(mips_alu_1_equal), .Result(mips_alu_1_result),
    .shamt(IR[10:6]));  // open: Result_2
  and and_3 (and_3_out, Syscall, comparator_6_eq);
  and and_4 (Halt, Syscall, not_4_out);
  or or_6 (PCSrc, and_1_out, and_2_out);
  Register #(.width(32), .trigger("rising"), .Select("low")) register_1 (
    .D(MDin), .en(and_3_out), .Q(LedData), .clk(CLK), .clr(Reset));
  RAM #(.addrWidth(10), .dataWidth(32), .bus("separate"), .Select("high")) ram_1 (
    .addr(mips_alu_1_result[11:2]), .din(MDin), .data(ram_1_data), .str(MemWrite), .clk(CLK), .clr(Reset));  // open: sel, ld
  Multiplexer #(.select(1), .width(32), .disabled("Z"), .enable("false")) multiplexer_13 (
    .in0(mips_alu_1_result), .in1(ram_1_data), .out(WriteBackData), .sel(MemToReg));
  or or_7 (W1, Int1, d_ff_2_q);
  or or_8 (W2, Int2, d_ff_3_q);
  or or_9 (W3, Int3, d_ff_4_q);
  D_Flip_Flop #(.trigger("rising"), .Pre_Clr_Positions("LEGACY"), .NegatePresetClear("false"), .enable("true"), .NewFFLayout("false")) d_ff_2 (
    .clk(IR1_t), .D(1'b1), .Q(d_ff_2_q), .reset(Int1));  // open: Qn, preset, en
  D_Flip_Flop #(.trigger("rising"), .Pre_Clr_Positions("LEGACY"), .NegatePresetClear("false"), .enable("true"), .NewFFLayout("false")) d_ff_3 (
    .clk(IR2_t), .D(1'b1), .Q(d_ff_3_q), .reset(Int2));  // open: Qn, preset, en
  D_Flip_Flop #(.trigger("rising"), .Pre_Clr_Positions("LEGACY"), .NegatePresetClear("false"), .enable("true"), .NewFFLayout("false")) d_ff_4 (
    .clk(IR3_t), .D(1'b1), .Q(d_ff_4_q), .reset(Int3));  // open: Qn, preset, en
  or or_10 (or_10_out, d_ff_2_q, Int1);
  or or_11 (or_11_out, d_ff_3_q, Int2);
  or or_12 (or_12_out, d_ff_4_q, Int3);
  and and_5 (and_5_out, or_10_out, ~clear1);  // AND_Gate
  and and_6 (and_6_out, or_11_out, ~clear2);  // AND_Gate
  and and_7 (and_7_out, or_12_out, ~clear3);  // AND_Gate
  D_Flip_Flop #(.trigger("rising"), .Pre_Clr_Positions("LEGACY"), .NegatePresetClear("false"), .enable("true"), .NewFFLayout("false")) u_IR1 (
    .clk(CLK), .D(and_5_out), .Q(Int1));  // open: Qn, preset, en, reset
  D_Flip_Flop #(.trigger("rising"), .Pre_Clr_Positions("LEGACY"), .NegatePresetClear("false"), .enable("true"), .NewFFLayout("false")) u_IR2 (
    .clk(CLK), .D(and_6_out), .Q(Int2));  // open: Qn, preset, en, reset
  D_Flip_Flop #(.trigger("rising"), .Pre_Clr_Positions("LEGACY"), .NegatePresetClear("false"), .enable("true"), .NewFFLayout("false")) u_IR3 (
    .clk(CLK), .D(and_7_out), .Q(Int3));  // open: Qn, preset, en, reset
  not not_5 (not_5_out, Eret);
  and and_8 (and_8_out, not_5_out, IntAll);
  and and_9 (INT, IE, IntAll);
  or or_13 (IntAll, Int1, Int2, Int3);
  Priority_Encoder #(.select(2), .disabled("Z")) priority_encoder_1 (
    .in0(Int1), .in1(Int2), .in2(Int3), .out(priority_encoder_1_out));  // open: in3, gs, en_out, en_in
  Multiplexer #(.select(2), .width(32), .disabled("Z"), .enable("false")) multiplexer_14 (
    .in0(32'h30ac), .in1(32'h3150), .in2(32'h31f4), .out(IntAddr), .sel(priority_encoder_1_out));  // open: in3
  D_Flip_Flop #(.trigger("rising"), .Pre_Clr_Positions("ABOVE_BELOW"), .NegatePresetClear("false"), .enable("false"), .NewFFLayout("true")) d_ff_5 (
    .clk(CLK), .D(and_8_out), .Qn(IE));  // open: Q, preset, reset
  Register #(.width(2), .trigger("rising"), .Select("low")) register_2 (
    .D(priority_encoder_1_out), .en(INT), .Q(register_2_q), .clk(CLK));  // open: clr
  Demultiplexer #(.select(2), .width(1), .tristate("false"), .disabled("Z"), .enable("false")) demultiplexer_1 (
    .out0(clear1), .out1(clear2), .out2(clear3), .in(Eret), .sel(register_2_q));  // open: out3
  Register #(.width(32), .trigger("rising"), .Select("low")) register_3 (
    .D(BreakAddr), .en(INT), .Q(EPCAddr), .clk(CLK));  // open: clr

  // Other names for the same wires on the sheet: a0[31:0] = MDin; addr[25:0] = IR[25:0];
  //   PC_J[31:2] = {PC[31:28], IR[25:0]}; shamt[4:0] = IR[10:6]; v0[31:0] = PC_rst

  // Notes on the sheet:
  //   中断源
  //   中断等待指示
  //   总复位信号应将除ROM以外所有存储组件全部清零
  //   控制位
  //   暂停节拍，不能为0
  //   数码管输出
  //   数码管输出应该用寄存器锁存，否则显示数据只能一闪而过
  //   指令存储器
  //   可计数暂停的时钟源
  //   指令字
  //   contents of rom_1 (hex, n*v repeats v):
  //   201d07d0 20100001 109fc0 139fc3 8021 2012000c 24160008 26100001 3210000f 20080008 20090001 139900
  //   2709825 132020 20020022 c 1094022 1500fff9 22100001 2018000f 2188024 108700 20080008 20090001 139902
  //   2709825 132021 20020022 c 1094022 1500fff9 108702 2c9b022 12c00001 8000c07 4020 1084027 84400
  //   3508ffff 82021 20020022 c 8000c01 afa20000 23bd0004 afa40000 23bd0004 afb00000 23bd0004 afb30000
  //   23bd0004 afb40000 23bd0004 afb50000 23bd0004 afb60000 23bd0004 40167000 afb60000 23bd0004 40806000
  //   20160001 20140003 20150001 168020 108100 2149825 132020 20020022 c 1600fffa 295a022 1680fff7
  //   20160001 40966000 23bdfffc 8fb60000 40967000 23bdfffc 8fb60000 23bdfffc 8fb50000 23bdfffc 8fb40000
  //   23bdfffc 8fb30000 23bdfffc 8fb00000 23bdfffc 8fa40000 23bdfffc 8fa20000 42000018 afa20000 23bd0004
  //   afa40000 23bd0004 afb00000 23bd0004 afb30000 23bd0004 afb40000 23bd0004 afb50000 23bd0004 afb60000
  //   23bd0004 40167000 afb60000 23bd0004 40806000 20160002 20140003 20150001 168020 108100 2149825 132020
  //   20020022 c 1600fffa 295a022 1680fff7 20160001 40966000 23bdfffc 8fb60000 40967000 23bdfffc 8fb60000
  //   23bdfffc 8fb50000 23bdfffc 8fb40000 23bdfffc 8fb30000 23bdfffc 8fb00000 23bdfffc 8fa40000 23bdfffc
  //   8fa20000 42000018 afa20000 23bd0004 afa40000 23bd0004 afb00000 23bd0004 afb30000 23bd0004 afb40000
  //   23bd0004 afb50000 23bd0004 afb60000 23bd0004 40167000 afb60000 23bd0004 40806000 20160003 20140003
  //   20150001 168020 108100 2149825 132020 20020022 c 1600fffa 295a022 1680fff7 20160001 40966000
  //   23bdfffc 8fb60000 40967000 23bdfffc 8fb60000 23bdfffc 8fb50000 23bdfffc 8fb40000 23bdfffc 8fb30000
  //   23bdfffc 8fb00000 23bdfffc 8fa40000 23bdfffc 8fa20000 42000018
  //   OP
  //   Func
  //   rs
  //   rt
  //   rd
  //   Beq
  //   JMP
  //   JR
  //   Bne
  //   OP
  //   JAL
  //   Func
  //   Syscall
  //   Eret
  //   v0
  //   a0
  //   MemToReg
  //   MemWrite
  //   AluOP
  //   AluSrcB
  //   RegWrite
  //   RegDst
  //   单级中断测试信号模拟器
  //   为方便自动评测，需要输出PC，IR，寄存器堆写如数据RDin
  //   RAM写使能MemWrite、RAM写入数据MDin等信号
  //   Reset 
  //   Reset 
  //   Reset 
endmodule

module \单周期MIPS_多级中断  (
  input  IR1,
  input  IR2,
  input  IR3,
  output RegWrite,
  output MemWrite,
  output [31:0] PC,
  output [31:0] IR,
  output [31:0] RDin,
  output [31:0] MDin,
  output [31:0] LedData
);

  wire AluSrcB, and_1_out, and_3_out, and_4_out, and_5_out, and_6_out, and_7_out, and_8_out, Beq, Bne,
       ChangeInt, clear1, clear2, clear3, CLK, clock_2_out, comparator_1_eq, comparator_2_eq,
       comparator_3_eq, comparator_4_eq, comparator_5_eq, comparator_6_lt, comparator_7_eq,
       controlled_buffer_1_out, d_ff_1_q, d_ff_2_q, d_ff_3_q, d_ff_4_q, Equal, Eret, Go, Halt, Higher, INT,
       Int1, Int2, Int3, IR1_t, IR2_t, IR3_t, IRA, IRB, IRC, JAL, JMP, JR, MemToReg, MFC0, mips_alu_1_equal,
       MTC0, nand_1_out, nIE_q, not_1_out, not_2_out, not_3_out, not_4_out, not_5_out, not_6_out, not_7_out,
       or_1_out, or_2_out, or_3_out, or_11_out, or_12_out, or_13_out, or_14_out, or_15_out, PCSrc, RegDst,
       Reset, SignedExt, Syscall, W1, W2, W3;
  wire [1:0] HighestInt, multiplexer_15_out, multiplexer_18_out, multiplexer_20_out, NowInt, SecInt, ThrInt;
  wire [3:0] AluOP;
  wire [4:0] multiplexer_6_out, multiplexer_7_out, multiplexer_8_out, multiplexer_9_out;
  wire [12:0] CNT_num;
  wire [15:0] \总周期数 ;
  wire [31:0] bit_extender_1_out, bit_extender_2_out, BreakAddr, EPCAddr, IntAddr, mips_alu_1_result,
       multiplexer_1_out, multiplexer_2_out, multiplexer_4_out, multiplexer_10_out, multiplexer_12_out,
       multiplexer_13_out, multiplexer_16_out, multiplexer_19_out, multiplexer_21_out, PC_4, PC_imm, PC_rst,
       pcnext, ram_1_data, SecAddr, shifter_1_out, ThrAddr, WriteBackData;

  Clock #(.highDuration(1), .lowDuration(1)) clock_1 (.out(CLK));
  Button _1 ();  // open: out
  Button _2 ();  // open: out
  Button _3 ();  // open: out
  Multiplexer #(.select(1), .width(32), .disabled("Z"), .enable("false")) multiplexer_1 (
    .in0(PC_4), .in1(PC_imm), .out(multiplexer_1_out), .sel(PCSrc));
  Button \u_继续运行  (.out(Go));
  LED #(.active("true")) led_1 (.in(W1));
  LED #(.active("true")) led_2 (.in(W2));
  LED #(.active("true")) led_3 (.in(W3));
  Multiplexer #(.select(1), .width(32), .disabled("Z"), .enable("false")) multiplexer_2 (
    .in0(multiplexer_1_out), .in1({PC[31:28], IR[25:0], 2'b00}), .out(multiplexer_2_out), .sel(JMP));
  Multiplexer #(.select(1), .width(32), .disabled("Z"), .enable("false")) multiplexer_3 (
    .in0(multiplexer_2_out), .in1(PC_rst), .out(BreakAddr), .sel(JR));
  Hex_Digit_Display hex_digit_display_1 (.value(LedData[31:28]));  // open: dp
  Multiplexer #(.select(1), .width(32), .disabled("Z"), .enable("false")) multiplexer_4 (
    .in0(BreakAddr), .in1(IntAddr), .out(multiplexer_4_out), .sel(INT));
  Hex_Digit_Display hex_digit_display_2 (.value(LedData[23:20]));  // open: dp
  Hex_Digit_Display hex_digit_display_3 (.value(LedData[27:24]));  // open: dp
  Multiplexer #(.select(1), .width(32), .disabled("Z"), .enable("false")) multiplexer_5 (
    .in0(multiplexer_4_out), .in1(EPCAddr), .out(pcnext), .sel(Eret));
  or or_1 (or_1_out, not_1_out, Go);
  not not_1 (not_1_out, Halt);
  Comparator #(.width(16), .mode("twosComplement")) comparator_1 (
    .a(16'h258), .b(\总周期数 ), .eq(comparator_1_eq));  // open: gt, lt
  Comparator #(.width(16), .mode("twosComplement")) comparator_2 (
    .a(\总周期数 ), .b(16'h1), .eq(comparator_2_eq));  // open: gt, lt
  Comparator #(.width(16), .mode("twosComplement")) comparator_3 (
    .a(\总周期数 ), .b(16'h4), .eq(comparator_3_eq));  // open: gt, lt
  Comparator #(.width(16), .mode("twosComplement")) comparator_4 (
    .a(\总周期数 ), .b(16'h7), .eq(comparator_4_eq));  // open: gt, lt
  Comparator #(.width(16), .mode("twosComplement")) comparator_5 (
    .a(\总周期数 ), .b(16'h241), .eq(comparator_5_eq));  // open: gt, lt
  Hex_Digit_Display hex_digit_display_4 (.value(LedData[15:12]));  // open: dp
  Hex_Digit_Display hex_digit_display_5 (.value(LedData[19:16]));  // open: dp
  Button button_1 (.out(Reset));
  not not_2 (not_2_out, Halt);
  Register #(.width(32), .trigger("rising"), .Select("low")) u_PC (
    .D(pcnext), .en(or_1_out), .Q(PC), .clk(CLK), .clr(Reset));
  or or_2 (or_2_out, comparator_1_eq, comparator_2_eq);
  assign IRA = or_2_out ? ~CLK : 1'bz;  // Controlled_Inverter controlled_inverter_1
  assign IRB = comparator_3_eq ? ~CLK : 1'bz;  // Controlled_Inverter controlled_inverter_2
  or or_3 (or_3_out, comparator_4_eq, comparator_5_eq);
  assign IRC = or_3_out ? ~CLK : 1'bz;  // Controlled_Inverter controlled_inverter_3
  Hex_Digit_Display hex_digit_display_6 (.value(LedData[11:8]));  // open: dp
  Hex_Digit_Display hex_digit_display_7 (.value(LedData[7:4]));  // open: dp
  // Probe on \总周期数 
  Counter #(.width(16), .max('hffff), .ongoal("wrap"), .trigger("rising"), .behavior("old")) counter_1 (
    .count(not_2_out), .Q(\总周期数 ), .clk(CLK), .clr(Reset));  // open: load, D, carry, preset
  Adder #(.width(32)) adder_1 (.a(PC), .b(32'h4), .out(PC_4));  // open: cin, cout
  Pull_Resistor #(.pull(0)) pull_resistor_1 (.node(IRA));
  Pull_Resistor #(.pull(0)) pull_resistor_2 (.node(IRB));
  Pull_Resistor #(.pull(0)) pull_resistor_3 (.node(IRC));
  Hex_Digit_Display hex_digit_display_8 (.value(LedData[3:0]));  // open: dp
  ROM #(.addrWidth(10), .dataWidth(32), .Select("high")) rom_1 (.addr(PC[11:2]), .data(IR));
  // Mips_Probe mips_probe_1: pin names not known; wires that end beside it: IR, IR
  or or_4 (IR1_t, IR1, IRA);
  Multiplexer #(.select(1), .width(5), .disabled("Z"), .enable("false")) multiplexer_6 (
    .in0(IR[20:16]), .in1(IR[15:11]), .out(multiplexer_6_out), .sel(RegDst));
  D_Flip_Flop #(.trigger("high"), .Pre_Clr_Positions("LEGACY"), .NegatePresetClear("false"), .enable("true"), .NewFFLayout("false")) d_ff_1 (.Q(d_ff_1_q));  // open: clk, D, Qn, preset, en, reset
  // Probe on 13'h248
  or or_5 (IR2_t, IR2, IRB);
  \单周期硬布线控制器  \u_单周期硬布线控制器_1  (
    .Func(IR[5:0]), .OP(IR[31:26]), .ALU_OP(AluOP), .MemToReg(MemToReg), .MemWrite(MemWrite),
    .ALU_SRC(AluSrcB), .SysCALL(Syscall), .SignedExt(SignedExt), .RegDst(RegDst), .JR(JR), .JMP(JMP),
    .Beq(Beq), .JAL(JAL), .Bne(Bne), .ERET(Eret), .in_3(IR[25:21]), .MTC0(MTC0), .MFC0(MFC0),
    .RegWrite(RegWrite));
  Multiplexer #(.select(1), .width(5), .disabled("Z"), .enable("false")) multiplexer_7 (
    .in0(IR[25:21]), .in1(5'b00010), .out(multiplexer_7_out), .sel(Syscall));
  Multiplexer #(.select(1), .width(5), .disabled("Z"), .enable("false")) multiplexer_8 (
    .in0(IR[20:16]), .in1(5'b00100), .out(multiplexer_8_out), .sel(Syscall));
  Multiplexer #(.select(1), .width(5), .disabled("Z"), .enable("false")) multiplexer_9 (
    .in0(multiplexer_6_out), .in1({5{1'b1}}), .out(multiplexer_9_out), .sel(JAL));
  Multiplexer #(.select(1), .width(32), .disabled("Z"), .enable("false")) multiplexer_10 (
    .in0(WriteBackData), .in1(PC_4), .out(multiplexer_10_out), .sel(JAL));
  assign bit_extender_1_out = {{16{1'b0}}, IR[15:0]};  // Bit_Extender bit_extender_1
  assign bit_extender_2_out = {{16{IR[15]}}, IR[15:0]};  // Bit_Extender bit_extender_2
  not not_3 (not_3_out, d_ff_1_q);
  Comparator #(.width(13), .mode("twosComplement")) comparator_6 (
    .a(CNT_num), .b(13'h248), .eq(Equal), .lt(comparator_6_lt));  // open: gt
  Clock #(.highDuration(1), .lowDuration(1)) clock_2 (.out(clock_2_out));
  Multiplexer #(.select(1), .width(32), .disabled("Z"), .enable("false")) multiplexer_11 (
    .in0(multiplexer_10_out), .in1(EPCAddr), .out(RDin), .sel(MFC0));
  Multiplexer #(.select(1), .width(32), .disabled("Z"), .enable("false")) multiplexer_12 (
    .in0(bit_extender_1_out), .in1(bit_extender_2_out), .out(multiplexer_12_out), .sel(SignedExt));
  Shifter #(.width(32), .shift("ll")) shifter_1 (.in(bit_extender_2_out), .\dist (5'b00010), .out(shifter_1_out));
  nand nand_1 (nand_1_out, not_3_out, Equal);
  Counter #(.width(13), .max('h1fff), .ongoal("stay"), .trigger("rising"), .behavior("old")) counter_2 (
    .count(comparator_6_lt), .Q(CNT_num), .clk(clock_2_out));  // open: load, D, carry, clr, preset
  or or_6 (IR3_t, IR3, IRC);
  MIPS_Regifile mips_regifile_1 (
    .Din(RDin), .Clk(CLK), .R1(PC_rst), .R2(MDin), .WE(RegWrite), .W_num(multiplexer_9_out),
    .R1_num(multiplexer_7_out), .R2_num(multiplexer_8_out));
  assign controlled_buffer_1_out = nand_1_out ? clock_2_out : 1'bz;  // Controlled_Buffer controlled_buffer_1
  Multiplexer #(.select(1), .width(32), .disabled("Z"), .enable("false")) multiplexer_13 (
    .in0(MDin), .in1(multiplexer_12_out), .out(multiplexer_13_out), .sel(AluSrcB));
  Adder #(.width(32)) adder_2 (.a(shifter_1_out), .b(PC_4), .out(PC_imm));  // open: cin, cout
  Pull_Resistor #(.pull(1)) pull_resistor_4 (.node(controlled_buffer_1_out));
  Comparator #(.width(32), .mode("twosComplement")) comparator_7 (
    .a(PC_rst), .b(32'h22), .eq(comparator_7_eq));  // open: gt, lt
  not not_4 (not_4_out, mips_alu_1_equal);
  MIPS_ALU mips_alu_1 (
    .X(PC_rst), .Y(multiplexer_13_out), .AluOP(AluOP), .Equal(mips_alu_1_equal), .Result(mips_alu_1_result),
    .shamt(IR[10:6]));  // open: Result_2
  and and_1 (and_1_out, Syscall, comparator_7_eq);
  and and_2 (Halt, Syscall, not_5_out);
  not not_5 (not_5_out, comparator_7_eq);
  and and_3 (and_3_out, not_4_out, Bne);
  or or_7 (PCSrc, and_3_out, and_4_out);
  and and_4 (and_4_out, Beq, mips_alu_1_equal);
  Register #(.width(32), .trigger("rising"), .Select("low")) register_1 (
    .D(MDin), .en(and_1_out), .Q(LedData), .clk(CLK), .clr(Reset));
  Multiplexer #(.select(1), .width(32), .disabled("Z"), .enable("false")) multiplexer_14 (
    .in0(mips_alu_1_result), .in1(ram_1_data), .out(WriteBackData), .sel(MemToReg));
  RAM #(.addrWidth(10), .dataWidth(32), .bus("separate"), .Select("high")) ram_1 (
    .addr(mips_alu_1_result[11:2]), .din(MDin), .data(ram_1_data), .str(MemWrite), .clk(CLK), .clr(Reset));  // open: sel, ld
  or or_8 (W1, Int1, d_ff_2_q);
  or or_9 (W2, Int2, d_ff_3_q);
  or or_10 (W3, Int3, d_ff_4_q);
  D_Flip_Flop #(.trigger("rising"), .Pre_Clr_Positions("LEGACY"), .NegatePresetClear("false"), .enable("true"), .NewFFLayout("false")) d_ff_2 (
    .clk(IR1_t), .D(1'b1), .Q(d_ff_2_q), .reset(Int1));  // open: Qn, preset, en
  D_Flip_Flop #(.trigger("rising"), .Pre_Clr_Positions("LEGACY"), .NegatePresetClear("false"), .enable("true"), .NewFFLayout("false")) d_ff_3 (
    .clk(IR2_t), .D(1'b1), .Q(d_ff_3_q), .reset(Int2));  // open: Qn, preset, en
  D_Flip_Flop #(.trigger("rising"), .Pre_Clr_Positions("LEGACY"), .NegatePresetClear("false"), .enable("true"), .NewFFLayout("false")) d_ff_4 (
    .clk(IR3_t), .D(1'b1), .Q(d_ff_4_q), .reset(Int3));  // open: Qn, preset, en
  or or_11 (or_11_out, d_ff_2_q, Int1);
  or or_12 (or_12_out, d_ff_3_q, Int2);
  or or_13 (or_13_out, d_ff_4_q, Int3);
  and and_5 (and_5_out, or_11_out, ~clear1);  // AND_Gate
  and and_6 (and_6_out, or_12_out, ~clear2);  // AND_Gate
  and and_7 (and_7_out, or_13_out, ~clear3);  // AND_Gate
  D_Flip_Flop #(.trigger("rising"), .Pre_Clr_Positions("LEGACY"), .NegatePresetClear("false"), .enable("true"), .NewFFLayout("false")) u_IR1 (
    .clk(CLK), .D(and_5_out), .Q(Int1));  // open: Qn, preset, en, reset
  D_Flip_Flop #(.trigger("rising"), .Pre_Clr_Positions("LEGACY"), .NegatePresetClear("false"), .enable("true"), .NewFFLayout("false")) u_IR2 (
    .clk(CLK), .D(and_6_out), .Q(Int2));  // open: Qn, preset, en, reset
  D_Flip_Flop #(.trigger("rising"), .Pre_Clr_Positions("LEGACY"), .NegatePresetClear("false"), .enable("true"), .NewFFLayout("false")) u_IR3 (
    .clk(CLK), .D(and_7_out), .Q(Int3));  // open: Qn, preset, en, reset
  not not_6 (not_6_out, Higher);
  Priority_Encoder #(.select(2), .disabled("Z")) priority_encoder_1 (
    .in0(1'b1), .in1(Int1), .in2(Int2), .in3(Int3), .out(HighestInt));  // open: gs, en_out, en_in
  and and_8 (and_8_out, MTC0, not_6_out);
  Multiplexer #(.select(1), .width(2), .disabled("Z"), .enable("false")) multiplexer_15 (
    .in0(HighestInt), .in1(SecInt), .out(multiplexer_15_out), .sel(Eret));
  Multiplexer #(.select(1), .width(32), .disabled("Z"), .enable("false")) multiplexer_16 (
    .in0(BreakAddr), .in1(SecAddr), .out(multiplexer_16_out), .sel(Eret));
  Multiplexer #(.select(2), .width(32), .disabled("Z"), .enable("false")) multiplexer_17 (
    .in1(32'h30ac), .in2(32'h3174), .in3(32'h323c), .out(IntAddr), .sel(HighestInt));  // open: in0
  or or_14 (or_14_out, INT, and_8_out, MFC0);
  or or_15 (or_15_out, INT, MFC0, MTC0, Eret);
  Register #(.width(2), .trigger("rising"), .Select("low")) register_2 (
    .D(multiplexer_15_out), .en(ChangeInt), .Q(NowInt), .clk(CLK));  // open: clr
  Register #(.width(32), .trigger("rising"), .Select("low")) register_3 (
    .D(multiplexer_16_out), .en(ChangeInt), .Q(EPCAddr), .clk(CLK));  // open: clr
  Register #(.width(1), .trigger("rising"), .Select("low")) nIE (
    .D(or_14_out), .en(or_15_out), .Q(nIE_q), .clk(CLK));  // open: clr
  Comparator #(.width(2), .mode("unsigned")) comparator_8 (.a(HighestInt), .b(NowInt), .gt(Higher));  // open: eq, lt
  Demultiplexer #(.select(2), .width(1), .tristate("false"), .disabled(0), .enable("false")) demultiplexer_1 (
    .out1(clear1), .out2(clear2), .out3(clear3), .in(Eret), .sel(NowInt));  // open: out0
  not not_7 (not_7_out, nIE_q);
  and and_9 (INT, not_7_out, Higher);
  Multiplexer #(.select(1), .width(2), .disabled("Z"), .enable("false")) multiplexer_18 (
    .in0(NowInt), .in1(ThrInt), .out(multiplexer_18_out), .sel(Eret));
  Multiplexer #(.select(1), .width(32), .disabled("Z"), .enable("false")) multiplexer_19 (
    .in0(EPCAddr), .in1(ThrAddr), .out(multiplexer_19_out), .sel(Eret));
  Register #(.width(2), .trigger("rising"), .Select("low")) register_4 (
    .D(multiplexer_18_out), .en(ChangeInt), .Q(SecInt), .clk(CLK));  // open: clr
  Register #(.width(32), .trigger("rising"), .Select("low")) register_5 (
    .D(multiplexer_19_out), .en(ChangeInt), .Q(SecAddr), .clk(CLK));  // open: clr
  Multiplexer #(.select(1), .width(2), .disabled("Z"), .enable("false")) multiplexer_20 (
    .in0(SecInt), .in1(2'b00), .out(multiplexer_20_out), .sel(Eret));
  Multiplexer #(.select(1), .width(32), .disabled("Z"), .enable("false")) multiplexer_21 (
    .in0(SecAddr), .in1({32{1'b0}}), .out(multiplexer_21_out), .sel(Eret));
  or or_16 (ChangeInt, Eret, INT);
  Register #(.width(2), .trigger("rising"), .Select("low")) register_6 (
    .D(multiplexer_20_out), .en(ChangeInt), .Q(ThrInt), .clk(CLK));  // open: clr
  Register #(.width(32), .trigger("rising"), .Select("low")) register_7 (
    .D(multiplexer_21_out), .en(ChangeInt), .Q(ThrAddr), .clk(CLK));  // open: clr

  // Other names for the same wires on the sheet: a0[31:0] = MDin; addr[25:0] = IR[25:0];
  //   PC_J[31:2] = {PC[31:28], IR[25:0]}; shamt[4:0] = IR[10:6]; que[1:0] = HighestInt; v0[31:0] = PC_rst

  // Notes on the sheet:
  //   中断源
  //   中断等待指示
  //   总复位信号应将除ROM以外所有存储组件全部清零
  //   多级中断测试信号模拟器
  //   数码管输出
  //   数码管输出应该用寄存器锁存，否则显示数据只能一闪而过
  //   指令存储器
  //   contents of rom_1 (hex, n*v repeats v):
  //   201d07d0 20100001 109fc0 139fc3 8021 2012000c 24160008 26100001 3210000f 20080008 20090001 139900
  //   2709825 132020 20020022 c 1094022 1500fff9 22100001 2018000f 2188024 108700 20080008 20090001 139902
  //   2709825 132021 20020022 c 1094022 1500fff9 108702 2c9b022 12c00001 8000c07 4020 1084027 84400
  //   3508ffff 82021 20020022 c 8000c01 afa20000 23bd0004 afa40000 23bd0004 afb00000 23bd0004 afb30000
  //   23bd0004 afb40000 23bd0004 afb50000 23bd0004 afb60000 23bd0004 40167000 afb60000 23bd0004 40806000
  //   20160001 20140003 20150001 168020 108100 2149825 132020 20020022 c 1600fffa 295a022 1680fff7
  //   20160001 40966000 23bdfffc 8fb60000 40967000 23bdfffc 8fb60000 23bdfffc 8fb50000 23bdfffc 8fb40000
  //   23bdfffc 8fb30000 23bdfffc 8fb00000 23bdfffc 8fa40000 23bdfffc 8fa20000 42000018 afa20000 23bd0004
  //   afa40000 23bd0004 afb00000 23bd0004 afb30000 23bd0004 afb40000 23bd0004 afb50000 23bd0004 afb60000
  //   23bd0004 40167000 afb60000 23bd0004 40806000 20160002 20140003 20150001 168020 108100 2149825 132020
  //   20020022 c 1600fffa 295a022 1680fff7 20160001 40966000 23bdfffc 8fb60000 40967000 23bdfffc 8fb60000
  //   23bdfffc 8fb50000 23bdfffc 8fb40000 23bdfffc 8fb30000 23bdfffc 8fb00000 23bdfffc 8fa40000 23bdfffc
  //   8fa20000 42000018 afa20000 23bd0004 afa40000 23bd0004 afb00000 23bd0004 afb30000 23bd0004 afb40000
  //   23bd0004 afb50000 23bd0004 afb60000 23bd0004 40167000 afb60000 23bd0004 40806000 20160003 20140003
  //   20150001 168020 108100 2149825 132020 20020022 c 1600fffa 295a022 1680fff7 20160001 40966000
  //   23bdfffc 8fb60000 40967000 23bdfffc 8fb60000 23bdfffc 8fb50000 23bdfffc 8fb40000 23bdfffc 8fb30000
  //   23bdfffc 8fb00000 23bdfffc 8fa40000 23bdfffc 8fa20000 42000018
  //   OP
  //   Func
  //   rs
  //   指令字
  //   rt
  //   rd
  //   控制位
  //   JMP
  //   JR
  //   OP
  //   Func
  //   MT/MF
  //   v0
  //   a0
  //   暂停节拍，不能为0
  //   Beq
  //   Bne
  //   MemToReg
  //   MemWrite
  //   AluOP
  //   AluSrcB
  //   RegWrite
  //   JAL
  //   RegDst
  //   Eret
  //   Syscall
  //   可计数暂停的时钟源
  //   为方便自动评测，需要输出PC，IR，寄存器堆写如数据RDin
  //   RAM写使能MemWrite、RAM写入数据MDin等信号
  //   Reset 
  //   Reset 
  //   Reset 
endmodule

module \封装正确性测试  (
);

  wire IR1, IR2, IR3, MemW, RegW;
  wire [31:0] EX_PC, ID_PC, IF_PC, IR, LED, MDin, MDinr, MEM_PC, PC, RDin, RDinr, WB_PC;

  \单周期MIPS  \u_单周期mips_1  (
    .RegWrite(RegW), .MemWrite(MemW), .PC(PC), .IR(IR), .RDin(RDin), .MDin(MDin), .LedData(LED));  // open: IR1, IR2, IR3
  \气泡流水线  \u_气泡流水线_1  (
    .RegWrite(RegW), .MemWrite(MemW), .IF_PC(IF_PC), .ID_PC(ID_PC), .EX_PC(EX_PC), .M_PC(MEM_PC),
    .WB_PC(WB_PC), .RDin(RDinr), .MDin(MDinr), .LedData(LED));
  \单周期MIPS_单级中断  \u_单周期mips_单级中断_1  (
    .IR1(IR1), .IR2(IR2), .IR3(IR3), .RegWrite(RegW), .MemWrite(MemW), .PC(PC), .IR(IR), .RDin(RDin),
    .MDin(MDin), .LedData(LED));
  \理想流水线  \u_理想流水线_1  (
    .RegWrite(RegW), .MemWrite(MemW), .IF_PC(IF_PC), .ID_PC(ID_PC), .EX_PC(EX_PC), .M_PC(MEM_PC),
    .WB_PC(WB_PC), .RDin(RDinr), .MDin(MDinr), .LedData(LED));
  \重定向流水线  \u_重定向流水线_1  (
    .RegWrite(RegW), .MemWrite(MemW), .IF_PC(IF_PC), .ID_PC(ID_PC), .EX_PC(EX_PC), .M_PC(MEM_PC),
    .WB_PC(WB_PC), .RDin(RDinr), .MDin(MDinr), .LedData(LED));
  \单周期MIPS_多级中断  \u_单周期mips_多级中断_1  (
    .IR1(IR1), .IR2(IR2), .IR3(IR3), .RegWrite(RegW), .MemWrite(MemW), .PC(PC), .IR(IR), .RDin(RDin),
    .MDin(MDin), .LedData(LED));

  // Notes on the sheet:
  //   单周期封装测试
  //   气泡流水封装测试
  //   单周期+单级中断封装测试
  //   请检查上面封装有无位宽不匹配，引脚标签是否和连接的标签相对应，否则无法在educoder平台上正确测试
  //   理想流水封装测试
  //   重定向流水封装测试
  //   单周期+多级中断封装测试
endmodule
